// Logisim project cpu21-riscv.circ as structural Verilog: 38 circuits, main circuit ◇单周期RISC-V
module \单周期RISC_V  (
  input  IR1,
  input  IR2,
  input  IR3,
  output RegWrite,
  output MemWrite,
  output [31:0] PC,
  output [31:0] IR,
  output [31:0] RDin,
  output [31:0] MDin,
  output [31:0] LedData
);

  wire alu_1_equal, alu_1_out_6, and_3_out, and_5_out, and_6_out, and_7_out, B_signal, blt, Branch, CLK,
       clock_1_out, comparator_1_eq, comparator_2_eq, comparator_2_lt, d_ff_2_q, ecall, Go, halt, IR1_t,
       IR2_t, IR3_t, IRA, IRB, IRC, J_signal, Jalr_signal, Ledout, nand_1_out, not_1_out, not_2_out,
       not_3_out, or_1_out, or_2_out, or_3_out, or_9_out, riscv_probe_1_p2, RST, S_signal, sb, sltiu, W1, W2,
       W3, \单周期硬布线控制器_1_alu_src , \单周期硬布线控制器_1_beq , \单周期硬布线控制器_1_bne , \单周期硬布线控制器_1_memtoreg ;
  wire [1:0] Imm_Sel;
  wire [3:0] decoder_1_out0, RAM_Sel, \单周期硬布线控制器_1_alu_op ;
  wire [4:0] bit_extender_6_out, multiplexer_3_out, multiplexer_4_out, multiplier_1_out;
  wire [12:0] CNT_num;
  wire [15:0] \总周期数 ;
  wire [31:0] adder_2_out, ALU_Res, bit_extender_1_out, bit_extender_2_out, bit_extender_3_out,
       bit_extender_4_out, bit_extender_5_out, MemData, mips_ram_1_p8, multiplexer_1_out, multiplexer_2_out,
       multiplexer_5_out, multiplexer_6_out, multiplexer_7_out, multiplexer_8_out, PC_4, R1_Data,
       shifter_1_out, shifter_2_out;

  Button \u_继续运行  (.out(Go));
  Button _1 (.out(IRA));
  Button _2 (.out(IRB));
  Button _3 (.out(IRC));
  Button button_1 (.out(RST));
  LED #(.active("true")) led_1 (.in(W1));
  LED #(.active("true")) led_2 (.in(W2));
  LED #(.active("true")) led_3 (.in(W3));
  or or_1 (or_1_out, Branch, J_signal);
  Multiplexer #(.select(1), .width(32), .disabled("Z"), .enable("false")) multiplexer_1 (
    .in0(PC_4), .in1(adder_2_out), .out(multiplexer_1_out), .sel(or_1_out));
  Hex_Digit_Display hex_digit_display_1 (.value(LedData[31:28]));  // open: dp
  Hex_Digit_Display hex_digit_display_2 (.value(LedData[27:24]));  // open: dp
  Hex_Digit_Display hex_digit_display_3 (.value(LedData[23:20]));  // open: dp
  Multiplexer #(.select(1), .width(32), .disabled("Z"), .enable("false")) multiplexer_2 (
    .in0(multiplexer_1_out), .in1(ALU_Res), .out(multiplexer_2_out), .sel(Jalr_signal));
  not not_1 (not_1_out, halt);
  or or_2 (or_2_out, B_signal, J_signal);
  or or_3 (or_3_out, J_signal, S_signal);
  Hex_Digit_Display hex_digit_display_4 (.value(LedData[15:12]));  // open: dp
  Hex_Digit_Display hex_digit_display_5 (.value(LedData[19:16]));  // open: dp
  Register #(.width(32), .trigger("rising"), .Select("low")) u_PC (
    .D(multiplexer_2_out), .en(not_1_out), .Q(PC), .clk(CLK), .clr(RST));
  and and_1 (Imm_Sel[1], ~S_signal, or_2_out);  // AND_Gate
  and and_2 (Imm_Sel[0], or_3_out, ~B_signal);  // AND_Gate
  Hex_Digit_Display hex_digit_display_6 (.value(LedData[11:8]));  // open: dp
  Hex_Digit_Display hex_digit_display_7 (.value(LedData[7:4]));  // open: dp
  // Probe on \总周期数 
  Adder #(.width(32)) adder_1 (.a(PC), .b(32'h4), .out(PC_4));  // open: cin, cout
  Hex_Digit_Display hex_digit_display_8 (.value(LedData[3:0]));  // open: dp
  // RiscV_Probe riscv_probe_1: pin names not known; wires that end beside it: IR, riscv_probe_1_p2
  ROM #(.addrWidth(10), .dataWidth(32), .Select("high")) rom_1 (.addr(PC[11:2]), .data(IR));
  or or_4 (IR1_t, IR1, IRA);
  Comparator #(.width(32), .mode("unsigned")) comparator_1 (
    .a(R1_Data), .b(32'h22), .eq(comparator_1_eq));  // open: gt, lt
  or or_5 (IR2_t, IR2, IRB);
  \单周期硬布线控制器  \u_单周期硬布线控制器_1  (
    .Funct({IR[30], IR[25], IR[14:12]}), .OP(IR[6:2]), .ALU_OP(\单周期硬布线控制器_1_alu_op ),
    .MemToReg(\单周期硬布线控制器_1_memtoreg ), .MemWrite(MemWrite), .ALU_SRC(\单周期硬布线控制器_1_alu_src ),
    .RegWrite(RegWrite), .ecall(ecall), .S_type(S_signal), .Jalr(Jalr_signal), .Beq(\单周期硬布线控制器_1_beq ),
    .JAL(J_signal), .Bne(\单周期硬布线控制器_1_bne ), .in_3(IR[21]), .uret(riscv_probe_1_p2), .Sltiu(sltiu), .Sb(sb),
    .Blt(blt));
  Multiplexer #(.select(1), .width(5), .disabled("Z"), .enable("false")) multiplexer_3 (
    .in0(IR[19:15]), .in1(5'b10001), .out(multiplexer_3_out), .sel(ecall));
  Multiplexer #(.select(1), .width(5), .disabled("Z"), .enable("false")) multiplexer_4 (
    .in0(IR[24:20]), .in1(5'b01010), .out(multiplexer_4_out), .sel(ecall));
  assign bit_extender_1_out = {{20{IR[31]}}, IR[31:20]};  // Bit_Extender bit_extender_1
  assign bit_extender_2_out = {{20{1'b0}}, IR[31:20]};  // Bit_Extender bit_extender_2
  assign bit_extender_3_out = {{20{IR[31]}}, {IR[31:25], IR[11:7]}};  // Bit_Extender bit_extender_3
  assign bit_extender_4_out = {{20{IR[31]}}, {IR[31], IR[7], IR[30:25], IR[11:8]}};  // Bit_Extender bit_extender_4
  assign bit_extender_5_out = {{12{IR[31]}}, {IR[31], IR[19:12], IR[20], IR[30:21]}};  // Bit_Extender bit_extender_5
  and and_3 (and_3_out, ecall, ~comparator_1_eq);  // AND_Gate
  and and_4 (Ledout, comparator_1_eq, ecall);
  or or_6 (B_signal, \单周期硬布线控制器_1_beq , blt, \单周期硬布线控制器_1_bne );
  Multiplexer #(.select(1), .width(32), .disabled("Z"), .enable("false")) multiplexer_5 (
    .in0(bit_extender_1_out), .in1(bit_extender_2_out), .out(multiplexer_5_out), .sel(sltiu));
  D_Flip_Flop #(.trigger("rising"), .Pre_Clr_Positions("ABOVE_BELOW"), .NegatePresetClear("false"), .enable("true"), .NewFFLayout("true")) d_ff_1 (
    .clk(CLK), .D(and_3_out), .Q(halt), .en(ecall), .reset(Go));  // open: Qn, preset
  or or_7 (IR3_t, IR3, IRC);
  \Regifile_上升沿  \regifile_上升沿_1  (
    .Din(RDin), .Clk(CLK), .R1(R1_Data), .R2(MDin), .WE(RegWrite), .W_num(IR[11:7]),
    .R1_num(multiplexer_3_out), .R2_num(multiplexer_4_out));
  Multiplexer #(.select(2), .width(32), .disabled("Z"), .enable("false")) multiplexer_6 (
    .in0(multiplexer_5_out), .in1(bit_extender_3_out), .in2(bit_extender_4_out), .in3(bit_extender_5_out),
    .out(multiplexer_6_out), .sel(Imm_Sel));
  Multiplexer #(.select(1), .width(32), .disabled("Z"), .enable("false")) multiplexer_7 (
    .in0(MDin), .in1(multiplexer_6_out), .out(multiplexer_7_out), .sel(\单周期硬布线控制器_1_alu_src ));
  Register #(.width(32), .trigger("rising"), .Select("low")) register_1 (
    .D(MDin), .en(Ledout), .Q(LedData), .clk(CLK), .clr(RST));
  ALU alu_1 (
    .X(R1_Data), .Y(multiplexer_7_out), .AluOP(\单周期硬布线控制器_1_alu_op ), .Equal(alu_1_equal), .Result(ALU_Res),
    .out_6(alu_1_out_6));  // open: Result_2, out_4
  Shifter #(.width(32), .shift("ll")) shifter_1 (.in(multiplexer_6_out), .\dist (5'b00001), .out(shifter_1_out));
  and and_5 (and_5_out, blt, alu_1_out_6);
  and and_6 (and_6_out, alu_1_equal, \单周期硬布线控制器_1_beq );
  and and_7 (and_7_out, ~alu_1_equal, \单周期硬布线控制器_1_bne );  // AND_Gate
  Adder #(.width(32)) adder_2 (.a(PC), .b(shifter_1_out), .out(adder_2_out));  // open: cin, cout
  or or_8 (Branch, and_5_out, and_6_out, and_7_out);
  not not_2 (not_2_out, halt);
  not not_3 (not_3_out, MemWrite);
  Counter #(.width(16), .max('hffff), .ongoal("stay"), .trigger("rising"), .behavior("old")) counter_1 (
    .count(not_2_out), .Q(\总周期数 ), .clk(CLK));  // open: load, D, carry, clr, preset
  D_Flip_Flop #(.trigger("high"), .Pre_Clr_Positions("LEGACY"), .NegatePresetClear("false"), .enable("true"), .NewFFLayout("false")) d_ff_2 (.Q(d_ff_2_q));  // open: clk, D, Qn, preset, en, reset
  // Probe on 13'hc
  // cs3410_MIPS_RAM mips_ram_1: pin names not known; wires that end beside it: ALU_Res[21:2], MemData, MemWrite, RAM_Sel, CLK, not_3_out, RST, mips_ram_1_p8
  Comparator #(.width(13), .mode("twosComplement")) comparator_2 (
    .a(CNT_num), .b(13'hc), .eq(comparator_2_eq), .lt(comparator_2_lt));  // open: gt
  Clock #(.highDuration(1), .lowDuration(1)) clock_1 (.out(clock_1_out));
  Multiplexer #(.select(1), .width(32), .disabled("Z"), .enable("false")) multiplexer_8 (
    .in0(ALU_Res), .in1(mips_ram_1_p8), .out(multiplexer_8_out), .sel(\单周期硬布线控制器_1_memtoreg ));
  Decoder #(.select(2), .tristate("false"), .disabled("Z"), .enable("false")) decoder_1 (
    .out0(decoder_1_out0[0]), .out1(decoder_1_out0[1]), .out2(decoder_1_out0[2]), .out3(decoder_1_out0[3]),
    .sel(ALU_Res[1:0]));
  Counter #(.width(13), .max('h1fff), .ongoal("stay"), .trigger("rising"), .behavior("old")) counter_2 (
    .count(comparator_2_lt), .Q(CNT_num), .clk(clock_1_out));  // open: load, D, carry, clr, preset
  or or_9 (or_9_out, J_signal, Jalr_signal);
  Multiplexer #(.select(1), .width(32), .disabled("Z"), .enable("false")) multiplexer_9 (
    .in0(multiplexer_8_out), .in1(PC_4), .out(RDin), .sel(or_9_out));
  assign bit_extender_6_out = {{3{1'b0}}, ALU_Res[1:0]};  // Bit_Extender bit_extender_6
  nand nand_1 (nand_1_out, d_ff_2_q, comparator_2_eq);
  Multiplier #(.width(5)) multiplier_1 (
    .a(bit_extender_6_out), .b(5'b01000), .out(multiplier_1_out));  // open: cin, cout
  Multiplexer #(.select(1), .width(4), .disabled("Z"), .enable("false")) multiplexer_10 (
    .in0(4'b1111), .in1(decoder_1_out0), .out(RAM_Sel), .sel(sb));
  assign CLK = nand_1_out ? clock_1_out : 1'bz;  // Controlled_Buffer controlled_buffer_1
  Pull_Resistor #(.pull(1)) pull_resistor_1 (.node(CLK));
  Shifter #(.width(32), .shift("ll")) shifter_2 (.in(MDin), .\dist (multiplier_1_out), .out(shifter_2_out));
  Multiplexer #(.select(1), .width(32), .disabled("Z"), .enable("false")) multiplexer_11 (
    .in0(MDin), .in1(shifter_2_out), .out(MemData), .sel(sb));

  // Other names for the same wires on the sheet: Bit_Sel[1:0] = ALU_Res[1:0]

  // Notes on the sheet:
  //   中断源
  //   中断等待指示
  //   数码管输出应该用寄存器锁存，否则显示数据只能一闪而过
  //   生成立即数选择信号
  //   数码管输出
  //   指令探针
  //   指令存储器
  //   contents of rom_1 (hex, n*v repeats v):
  //   100493 100006f 100493 200913 300993 100006f 100493 200913 300993 100006f 100493 200913 300993
  //   100006f 100493 200913 300993 29c000ef 100413 100493 1f49493 900533 2200893 73 24d493 48463 fedff06f
  //   900533 2200893 73 100493 249493 900533 2200893 73 48463 fedff06f 100493 1f49493 900533 2200893 73
  //   4034d493 900533 2200893 73 4044d493 900533 2200893 73 4044d493 900533 2200893 73 4044d493 900533
  //   2200893 73 4044d493 900533 2200893 73 4044d493 900533 2200893 73 4044d493 900533 2200893 73 4044d493
  //   900533 2200893 73 100413 1f41993 41f9d993 433 c00913 300b13 140413 f47413 800293 100313 499993
  //   89e9b3 1300533 2200893 73 406282b3 fe0294e3 140413 f00f93 1f47433 1c41413 800293 100313 49d993
  //   89e9b3 1300533 2200893 73 406282b3 fe0294e3 1c45413 406b0b33 b0463 f95ff06f 2b3 fff2c293 829293
  //   ff2e293 500533 2200893 73 fff00413 493 84a023 140413 448493 84a023 140413 448493 84a023 140413
  //   448493 84a023 140413 448493 84a023 140413 448493 84a023 140413 448493 84a023 140413 448493 84a023
  //   140413 448493 84a023 140413 448493 84a023 140413 448493 84a023 140413 448493 84a023 140413 448493
  //   84a023 140413 448493 84a023 140413 448493 84a023 140413 448493 84a023 140413 448493 140413 433
  //   3c00493 42983 4aa03 149a2b3 28663 134a023 1442023 ffc48493 fe9412e3 800533 2200893 73 440413 3c00493
  //   fc9416e3 a00893 73 413 140413 800533 2200893 73 240413 800533 2200893 73 340413 800533 2200893 73
  //   440413 800533 2200893 73 540413 800533 2200893 73 640413 800533 2200893 73 740413 800533 2200893 73
  //   840413 800533 2200893 2200893 73 8067
  //   指令字
  //   I型指令立即数
  //   S型指令立即数
  //   B型指令立即数
  //   J型指令立即数
  //   JAL
  //   JALR
  //   URET
  //   Sltiu
  //   Sb
  //   rs1
  //   rs2
  //   rd
  //   Beq
  //   Bne
  //   MemToReg
  //   MemWrite
  //   AluOP
  //   AluSrcB
  //   RegWrite
  //   Blt
  //   生成停机信号halt和LED显示信号Ledout
  //   LedData显示控制
  //   为方便自动评测，需要输出PC，IR，寄存器堆写如数据RDin
  //   RAM写使能MemWrite、RAM写入数据MDin等信号
  //   数据存储器
  //   周期信号显示控制
  //   控制位
  //   暂停节拍，不能为0
  //   戳工具置1进入计数暂停模式，ctrl+k时钟自动运行到对应节拍暂停
  //   ctrl+k关闭时钟连续运行，将控制位置零，进入单步调试模式调试
  //   计算Sb对应的MemData
  //   可计数暂停的时钟源
endmodule

// 单周期硬布线控制器
module \单周期硬布线控制器  (
  input  [4:0] OP,
  input  [4:0] Funct,
  input  in_3,
  output [3:0] ALU_OP,
  output uret,
  output MemToReg,
  output ecall,
  output MemWrite,
  output ALU_SRC,
  output RegWrite,
  output S_type,
  output Beq,
  output Bne,
  output Jalr,
  output JAL,
  output Sltiu,
  output Sb,
  output Blt
);

  wire \控制信号自动生成_1_ecall ;

  \运算控制器自动生成  \u_运算控制器自动生成_1  (
    .OP2(OP[0]), .OP3(OP[1]), .OP4(OP[2]), .OP5(OP[3]), .OP6(OP[4]), .F12(Funct[0]), .F13(Funct[1]),
    .F14(Funct[2]), .F25(Funct[3]), .F30(Funct[4]), .S0(ALU_OP[0]), .S1(ALU_OP[1]), .S2(ALU_OP[2]),
    .S3(ALU_OP[3]));
  \控制信号自动生成  \u_控制信号自动生成_1  (
    .OP2(OP[0]), .OP3(OP[1]), .MemToReg(MemToReg), .OP4(OP[2]), .OP5(OP[3]), .OP6(OP[4]), .F12(Funct[0]),
    .MemWrite(MemWrite), .F13(Funct[1]), .F14(Funct[2]), .F25(Funct[3]), .F30(Funct[4]), .ALU_SRC(ALU_SRC),
    .RegWrite(RegWrite), .ecall(\控制信号自动生成_1_ecall ), .S_Type(S_type), .BEQ(Beq), .BNE(Bne), .JALR(Jalr),
    .JAL(JAL), .Sltiu(Sltiu), .Sb(Sb), .Blt(Blt));
  and and_1 (uret, in_3, \控制信号自动生成_1_ecall );
  and and_2 (ecall, ~in_3, \控制信号自动生成_1_ecall );  // AND_Gate

  // Other names for the same wires on the sheet: IR21 = in_3; OP_CODE[4:0] = OP

  // Notes on the sheet:
  //   控制信号生成，产生数据通路需要的其他控制信号
  //   运算器控制器，根据指令生成运算器功能选择信号
endmodule

// 运算器控制器
module \运算控制器自动生成  (
  input  OP2,
  input  OP3,
  input  OP4,
  input  OP5,
  input  OP6,
  input  F12,
  input  F13,
  input  F14,
  input  F25,
  input  F30,
  output S0,
  output S1,
  output S2,
  output S3
);

  wire and_1_out, and_2_out, and_3_out, and_4_out, and_5_out, and_6_out, and_7_out, and_8_out, and_9_out,
       and_10_out, and_11_out, and_12_out, and_13_out, and_14_out, and_15_out, and_16_out, and_17_out,
       and_18_out, and_19_out, and_20_out, and_21_out, and_22_out, and_23_out, and_24_out, and_25_out,
       and_26_out, and_27_out, and_28_out, and_29_out, and_30_out, and_31_out, and_32_out, and_33_out,
       and_34_out, and_35_out, and_36_out, and_37_out, and_38_out, and_39_out, and_40_out, not_1_out,
       not_2_out, not_3_out, not_4_out, not_5_out, not_6_out, not_7_out, not_8_out, not_9_out, not_10_out,
       not_11_out, not_12_out, not_13_out, not_14_out, not_15_out, not_16_out, not_17_out, not_18_out,
       not_19_out, not_20_out, not_21_out, not_22_out, not_23_out, not_24_out, not_25_out, not_26_out,
       not_27_out, not_28_out, not_29_out, not_30_out, not_31_out, not_32_out, not_33_out, not_34_out,
       not_35_out, not_36_out, not_37_out, not_38_out, not_39_out, not_40_out, not_41_out, not_42_out,
       not_43_out, not_44_out, not_45_out, not_46_out, not_47_out, not_48_out, not_49_out, not_50_out,
       not_51_out, not_52_out, not_53_out, not_54_out, not_55_out, not_56_out, not_57_out, not_58_out,
       not_59_out, not_60_out, not_61_out, not_62_out, not_63_out, not_64_out, not_65_out, not_66_out,
       not_67_out, not_68_out, not_69_out, not_70_out, not_71_out, not_72_out, not_73_out, not_74_out,
       not_75_out, not_76_out, not_77_out, not_78_out, not_79_out, not_80_out, not_81_out, not_82_out,
       not_83_out, not_84_out, not_85_out, not_86_out, not_87_out, not_88_out, not_89_out, not_90_out,
       not_91_out, not_92_out, not_93_out, not_94_out, not_95_out, not_96_out, not_97_out, not_98_out,
       not_99_out, not_100_out, not_101_out, not_102_out, not_103_out, not_104_out, not_105_out, not_106_out,
       not_107_out, not_108_out, not_109_out, not_110_out, not_111_out, not_112_out, not_113_out,
       not_114_out, not_115_out, not_116_out, not_117_out, not_118_out, not_119_out, not_120_out,
       not_121_out, not_122_out, not_123_out, not_124_out, not_125_out, not_126_out, not_127_out,
       not_128_out, not_129_out, not_130_out, not_131_out, not_132_out, not_133_out, not_134_out,
       not_135_out, not_136_out, not_137_out, not_138_out, not_139_out, not_140_out, not_141_out,
       not_142_out, not_143_out, not_144_out, not_145_out, not_146_out, not_147_out, not_148_out,
       not_149_out, not_150_out, not_151_out, not_152_out, not_153_out, not_154_out, not_155_out,
       not_156_out, not_157_out, not_158_out, not_159_out, not_160_out, not_161_out, not_162_out,
       not_163_out, not_164_out, not_165_out, not_166_out, not_167_out, not_168_out, not_169_out,
       not_170_out, not_171_out, not_172_out, not_173_out, not_174_out, not_175_out, not_176_out,
       not_177_out, not_178_out, not_179_out, not_180_out, not_181_out, not_182_out, not_183_out,
       not_184_out, not_185_out, not_186_out, not_187_out, not_188_out, not_189_out, not_190_out,
       not_191_out, not_192_out, not_193_out, not_194_out, not_195_out, not_196_out, not_197_out,
       not_198_out, not_199_out, not_200_out, not_201_out, not_202_out, not_203_out, not_204_out,
       not_205_out, not_206_out, not_207_out, not_208_out, not_209_out, not_210_out, not_211_out,
       not_212_out, not_213_out, not_214_out, not_215_out, not_216_out, not_217_out, not_218_out,
       not_219_out, not_220_out, not_221_out, not_222_out, not_223_out, not_224_out, not_225_out,
       not_226_out, not_227_out, not_228_out, not_229_out, not_230_out, not_231_out, not_232_out, not_233_out;

  not not_1 (not_1_out, F30);
  not not_2 (not_2_out, F25);
  not not_3 (not_3_out, F14);
  not not_4 (not_4_out, F13);
  not not_5 (not_5_out, F12);
  not not_6 (not_6_out, OP6);
  not not_7 (not_7_out, OP3);
  not not_8 (not_8_out, OP2);
  not not_9 (not_9_out, F30);
  not not_10 (not_10_out, F25);
  not not_11 (not_11_out, OP6);
  not not_12 (not_12_out, OP3);
  not not_13 (not_13_out, OP2);
  not not_14 (not_14_out, F30);
  not not_15 (not_15_out, F25);
  not not_16 (not_16_out, F14);
  not not_17 (not_17_out, F12);
  not not_18 (not_18_out, OP6);
  not not_19 (not_19_out, OP3);
  not not_20 (not_20_out, OP2);
  not not_21 (not_21_out, F14);
  not not_22 (not_22_out, F13);
  not not_23 (not_23_out, F12);
  not not_24 (not_24_out, OP6);
  not not_25 (not_25_out, OP5);
  not not_26 (not_26_out, OP3);
  not not_27 (not_27_out, OP2);
  not not_28 (not_28_out, OP6);
  not not_29 (not_29_out, OP5);
  not not_30 (not_30_out, OP3);
  not not_31 (not_31_out, OP2);
  not not_32 (not_32_out, F13);
  not not_33 (not_33_out, F12);
  not not_34 (not_34_out, OP6);
  not not_35 (not_35_out, OP5);
  not not_36 (not_36_out, OP3);
  not not_37 (not_37_out, OP2);
  not not_38 (not_38_out, F14);
  not not_39 (not_39_out, F12);
  not not_40 (not_40_out, OP6);
  not not_41 (not_41_out, OP5);
  not not_42 (not_42_out, OP3);
  not not_43 (not_43_out, OP2);
  not not_44 (not_44_out, F25);
  not not_45 (not_45_out, F13);
  not not_46 (not_46_out, OP6);
  not not_47 (not_47_out, OP5);
  not not_48 (not_48_out, OP3);
  not not_49 (not_49_out, OP2);
  not not_50 (not_50_out, F14);
  not not_51 (not_51_out, F12);
  not not_52 (not_52_out, OP6);
  not not_53 (not_53_out, OP5);
  not not_54 (not_54_out, OP4);
  not not_55 (not_55_out, OP3);
  not not_56 (not_56_out, OP2);
  not not_57 (not_57_out, F14);
  not not_58 (not_58_out, F12);
  not not_59 (not_59_out, OP6);
  not not_60 (not_60_out, OP4);
  not not_61 (not_61_out, OP3);
  not not_62 (not_62_out, OP2);
  not not_63 (not_63_out, OP4);
  not not_64 (not_64_out, OP3);
  not not_65 (not_65_out, F14);
  not not_66 (not_66_out, F13);
  not not_67 (not_67_out, F12);
  not not_68 (not_68_out, OP6);
  not not_69 (not_69_out, OP4);
  not not_70 (not_70_out, OP3);
  not not_71 (not_71_out, OP2);
  not not_72 (not_72_out, F13);
  not not_73 (not_73_out, F12);
  not not_74 (not_74_out, OP4);
  not not_75 (not_75_out, OP3);
  not not_76 (not_76_out, OP2);
  not not_77 (not_77_out, F25);
  not not_78 (not_78_out, F14);
  not not_79 (not_79_out, F13);
  not not_80 (not_80_out, F12);
  not not_81 (not_81_out, OP6);
  not not_82 (not_82_out, OP3);
  not not_83 (not_83_out, OP2);
  not not_84 (not_84_out, F30);
  not not_85 (not_85_out, F25);
  not not_86 (not_86_out, OP6);
  not not_87 (not_87_out, OP3);
  not not_88 (not_88_out, OP2);
  not not_89 (not_89_out, F30);
  not not_90 (not_90_out, F25);
  not not_91 (not_91_out, F14);
  not not_92 (not_92_out, F12);
  not not_93 (not_93_out, OP6);
  not not_94 (not_94_out, OP3);
  not not_95 (not_95_out, OP2);
  not not_96 (not_96_out, OP6);
  not not_97 (not_97_out, OP5);
  not not_98 (not_98_out, OP3);
  not not_99 (not_99_out, OP2);
  not not_100 (not_100_out, F14);
  not not_101 (not_101_out, F12);
  not not_102 (not_102_out, OP6);
  not not_103 (not_103_out, OP5);
  not not_104 (not_104_out, OP3);
  not not_105 (not_105_out, OP2);
  not not_106 (not_106_out, F30);
  not not_107 (not_107_out, F25);
  not not_108 (not_108_out, F13);
  not not_109 (not_109_out, OP6);
  not not_110 (not_110_out, OP5);
  not not_111 (not_111_out, OP3);
  not not_112 (not_112_out, OP2);
  not not_113 (not_113_out, F30);
  not not_114 (not_114_out, F25);
  not not_115 (not_115_out, F13);
  not not_116 (not_116_out, OP6);
  not not_117 (not_117_out, OP3);
  not not_118 (not_118_out, OP2);
  not not_119 (not_119_out, F13);
  not not_120 (not_120_out, F12);
  not not_121 (not_121_out, OP4);
  not not_122 (not_122_out, OP3);
  not not_123 (not_123_out, OP2);
  not not_124 (not_124_out, F30);
  not not_125 (not_125_out, F25);
  not not_126 (not_126_out, F14);
  not not_127 (not_127_out, F13);
  not not_128 (not_128_out, F12);
  not not_129 (not_129_out, OP6);
  not not_130 (not_130_out, OP3);
  not not_131 (not_131_out, OP2);
  not not_132 (not_132_out, F25);
  not not_133 (not_133_out, F14);
  not not_134 (not_134_out, F13);
  not not_135 (not_135_out, F12);
  not not_136 (not_136_out, OP6);
  not not_137 (not_137_out, OP3);
  not not_138 (not_138_out, OP2);
  not not_139 (not_139_out, F30);
  not not_140 (not_140_out, F25);
  not not_141 (not_141_out, OP6);
  not not_142 (not_142_out, OP3);
  not not_143 (not_143_out, OP2);
  not not_144 (not_144_out, F30);
  not not_145 (not_145_out, F25);
  not not_146 (not_146_out, F14);
  not not_147 (not_147_out, OP6);
  not not_148 (not_148_out, OP3);
  not not_149 (not_149_out, OP2);
  not not_150 (not_150_out, F14);
  not not_151 (not_151_out, F13);
  not not_152 (not_152_out, F12);
  not not_153 (not_153_out, OP6);
  not not_154 (not_154_out, OP5);
  not not_155 (not_155_out, OP3);
  not not_156 (not_156_out, OP2);
  not not_157 (not_157_out, OP6);
  not not_158 (not_158_out, OP5);
  not not_159 (not_159_out, OP3);
  not not_160 (not_160_out, OP2);
  not not_161 (not_161_out, F14);
  not not_162 (not_162_out, F12);
  not not_163 (not_163_out, OP6);
  not not_164 (not_164_out, OP5);
  not not_165 (not_165_out, OP4);
  not not_166 (not_166_out, OP3);
  not not_167 (not_167_out, OP2);
  not not_168 (not_168_out, F14);
  not not_169 (not_169_out, F12);
  not not_170 (not_170_out, OP6);
  not not_171 (not_171_out, OP4);
  not not_172 (not_172_out, OP3);
  not not_173 (not_173_out, OP2);
  not not_174 (not_174_out, OP4);
  not not_175 (not_175_out, OP3);
  not not_176 (not_176_out, F14);
  not not_177 (not_177_out, OP6);
  not not_178 (not_178_out, OP5);
  not not_179 (not_179_out, OP3);
  not not_180 (not_180_out, OP2);
  not not_181 (not_181_out, F14);
  not not_182 (not_182_out, F13);
  not not_183 (not_183_out, F12);
  not not_184 (not_184_out, OP6);
  not not_185 (not_185_out, OP4);
  not not_186 (not_186_out, OP3);
  not not_187 (not_187_out, OP2);
  not not_188 (not_188_out, F30);
  not not_189 (not_189_out, F25);
  not not_190 (not_190_out, F12);
  not not_191 (not_191_out, OP6);
  not not_192 (not_192_out, OP3);
  not not_193 (not_193_out, OP2);
  not not_194 (not_194_out, F30);
  not not_195 (not_195_out, F25);
  not not_196 (not_196_out, F14);
  not not_197 (not_197_out, F12);
  not not_198 (not_198_out, OP6);
  not not_199 (not_199_out, OP3);
  not not_200 (not_200_out, OP2);
  not not_201 (not_201_out, F30);
  not not_202 (not_202_out, F25);
  not not_203 (not_203_out, F14);
  not not_204 (not_204_out, OP6);
  not not_205 (not_205_out, OP3);
  not not_206 (not_206_out, OP2);
  not not_207 (not_207_out, F12);
  not not_208 (not_208_out, OP6);
  not not_209 (not_209_out, OP5);
  not not_210 (not_210_out, OP3);
  not not_211 (not_211_out, OP2);
  not not_212 (not_212_out, F13);
  not not_213 (not_213_out, F12);
  not not_214 (not_214_out, OP6);
  not not_215 (not_215_out, OP5);
  not not_216 (not_216_out, OP3);
  not not_217 (not_217_out, OP2);
  not not_218 (not_218_out, F14);
  not not_219 (not_219_out, F12);
  not not_220 (not_220_out, OP6);
  not not_221 (not_221_out, OP5);
  not not_222 (not_222_out, OP3);
  not not_223 (not_223_out, OP2);
  not not_224 (not_224_out, F14);
  not not_225 (not_225_out, OP6);
  not not_226 (not_226_out, OP5);
  not not_227 (not_227_out, OP3);
  not not_228 (not_228_out, OP2);
  not not_229 (not_229_out, F13);
  not not_230 (not_230_out, F12);
  not not_231 (not_231_out, OP4);
  not not_232 (not_232_out, OP3);
  not not_233 (not_233_out, OP2);
  and and_1 (and_1_out, not_1_out, not_2_out, not_3_out, not_4_out, not_5_out, not_6_out, OP5, OP4, not_7_out, not_8_out);
  and and_2 (and_2_out, not_9_out, not_10_out, F14, F13, F12, not_11_out, OP5, OP4, not_12_out, not_13_out);
  and and_3 (and_3_out, not_14_out, not_15_out, not_16_out, F13, not_17_out, not_18_out, OP5, OP4, not_19_out, not_20_out);
  and and_4 (and_4_out, not_21_out, not_22_out, not_23_out, not_24_out, not_25_out, OP4, not_26_out, not_27_out);
  and and_5 (and_5_out, F14, F13, F12, not_28_out, not_29_out, OP4, not_30_out, not_31_out);
  and and_6 (and_6_out, F14, not_32_out, not_33_out, not_34_out, not_35_out, OP4, not_36_out, not_37_out);
  and and_7 (and_7_out, not_38_out, F13, not_39_out, not_40_out, not_41_out, OP4, not_42_out, not_43_out);
  and and_8 (and_8_out, F30, not_44_out, F14, not_45_out, F12, not_46_out, not_47_out, OP4, not_48_out, not_49_out);
  and and_9 (and_9_out, not_50_out, F13, not_51_out, not_52_out, not_53_out, not_54_out, not_55_out, not_56_out);
  and and_10 (and_10_out, not_57_out, F13, not_58_out, not_59_out, OP5, not_60_out, not_61_out, not_62_out);
  and and_11 (and_11_out, OP6, OP5, not_63_out, not_64_out, OP2);
  and and_12 (and_12_out, not_65_out, not_66_out, not_67_out, not_68_out, OP5, not_69_out, not_70_out, not_71_out);
  and and_13 (and_13_out, F14, not_72_out, not_73_out, OP6, OP5, not_74_out, not_75_out, not_76_out);
  and and_14 (and_14_out, F30, not_77_out, not_78_out, not_79_out, not_80_out, not_81_out, OP5, OP4, not_82_out, not_83_out);
  and and_15 (and_15_out, not_84_out, not_85_out, F14, F13, F12, not_86_out, OP5, OP4, not_87_out, not_88_out);
  and and_16 (and_16_out, not_89_out, not_90_out, not_91_out, F13, not_92_out, not_93_out, OP5, OP4, not_94_out, not_95_out);
  and and_17 (and_17_out, F14, F13, F12, not_96_out, not_97_out, OP4, not_98_out, not_99_out);
  and and_18 (and_18_out, not_100_out, F13, not_101_out, not_102_out, not_103_out, OP4, not_104_out, not_105_out);
  and and_19 (and_19_out, not_106_out, not_107_out, F14, not_108_out, F12, not_109_out, not_110_out, OP4, not_111_out, not_112_out);
  and and_20 (and_20_out, not_113_out, not_114_out, F14, not_115_out, F12, not_116_out, OP5, OP4, not_117_out, not_118_out);
  and and_21 (and_21_out, F14, not_119_out, not_120_out, OP6, OP5, not_121_out, not_122_out, not_123_out);
  and and_22 (and_22_out, not_124_out, not_125_out, not_126_out, not_127_out, not_128_out, not_129_out, OP5, OP4, not_130_out, not_131_out);
  and and_23 (and_23_out, F30, not_132_out, not_133_out, not_134_out, not_135_out, not_136_out, OP5, OP4, not_137_out, not_138_out);
  and and_24 (and_24_out, not_139_out, not_140_out, F14, F13, F12, not_141_out, OP5, OP4, not_142_out, not_143_out);
  and and_25 (and_25_out, not_144_out, not_145_out, not_146_out, F13, F12, not_147_out, OP5, OP4, not_148_out, not_149_out);
  and and_26 (and_26_out, not_150_out, not_151_out, not_152_out, not_153_out, not_154_out, OP4, not_155_out, not_156_out);
  and and_27 (and_27_out, F14, F13, F12, not_157_out, not_158_out, OP4, not_159_out, not_160_out);
  and and_28 (and_28_out, not_161_out, F13, not_162_out, not_163_out, not_164_out, not_165_out, not_166_out, not_167_out);
  and and_29 (and_29_out, not_168_out, F13, not_169_out, not_170_out, OP5, not_171_out, not_172_out, not_173_out);
  and and_30 (and_30_out, OP6, OP5, not_174_out, not_175_out, OP2);
  and and_31 (and_31_out, not_176_out, F13, F12, not_177_out, not_178_out, OP4, not_179_out, not_180_out);
  and and_32 (and_32_out, not_181_out, not_182_out, not_183_out, not_184_out, OP5, not_185_out, not_186_out, not_187_out);
  and and_33 (and_33_out, not_188_out, not_189_out, F14, F13, not_190_out, not_191_out, OP5, OP4, not_192_out, not_193_out);
  and and_34 (and_34_out, not_194_out, not_195_out, not_196_out, F13, not_197_out, not_198_out, OP5, OP4, not_199_out, not_200_out);
  and and_35 (and_35_out, not_201_out, not_202_out, not_203_out, F13, F12, not_204_out, OP5, OP4, not_205_out, not_206_out);
  and and_36 (and_36_out, F14, F13, not_207_out, not_208_out, not_209_out, OP4, not_210_out, not_211_out);
  and and_37 (and_37_out, F14, not_212_out, not_213_out, not_214_out, not_215_out, OP4, not_216_out, not_217_out);
  and and_38 (and_38_out, not_218_out, F13, not_219_out, not_220_out, not_221_out, OP4, not_222_out, not_223_out);
  and and_39 (and_39_out, not_224_out, F13, F12, not_225_out, not_226_out, OP4, not_227_out, not_228_out);
  and and_40 (and_40_out, F14, not_229_out, not_230_out, OP6, OP5, not_231_out, not_232_out, not_233_out);
  or or_1 (S0, and_1_out, and_2_out, and_3_out, and_4_out, and_5_out, and_6_out, and_7_out, and_8_out, and_9_out, and_10_out, and_11_out, and_12_out, and_13_out);
  or or_2 (S1, and_14_out, and_15_out, and_16_out, and_17_out, and_18_out, and_19_out, and_20_out, and_21_out);
  or or_3 (S2, and_22_out, and_23_out, and_24_out, and_25_out, and_26_out, and_27_out, and_28_out, and_29_out, and_30_out, and_31_out, and_32_out);
  or or_4 (S3, and_33_out, and_34_out, and_35_out, and_36_out, and_37_out, and_38_out, and_39_out, and_40_out);
endmodule

// 控制信号生成
module \控制信号自动生成  (
  input  OP2,
  input  OP3,
  input  OP4,
  input  OP5,
  input  OP6,
  input  F12,
  input  F13,
  input  F14,
  input  F25,
  input  F30,
  output MemToReg,
  output MemWrite,
  output ALU_SRC,
  output RegWrite,
  output ecall,
  output S_Type,
  output BEQ,
  output BNE,
  output JALR,
  output JAL,
  output Sltiu,
  output Sb,
  output Blt
);

  wire and_3_out, and_4_out, and_5_out, and_6_out, and_7_out, and_8_out, and_9_out, and_10_out, and_11_out,
       and_12_out, and_13_out, and_14_out, and_15_out, and_16_out, and_17_out, and_18_out, and_19_out,
       and_20_out, not_1_out, not_2_out, not_3_out, not_4_out, not_5_out, not_6_out, not_7_out, not_8_out,
       not_9_out, not_10_out, not_11_out, not_12_out, not_13_out, not_14_out, not_15_out, not_16_out,
       not_17_out, not_18_out, not_19_out, not_20_out, not_21_out, not_22_out, not_23_out, not_24_out,
       not_25_out, not_26_out, not_27_out, not_28_out, not_29_out, not_30_out, not_31_out, not_32_out,
       not_33_out, not_34_out, not_35_out, not_36_out, not_37_out, not_38_out, not_39_out, not_40_out,
       not_41_out, not_42_out, not_43_out, not_44_out, not_45_out, not_46_out, not_47_out, not_48_out,
       not_49_out, not_50_out, not_51_out, not_52_out, not_53_out, not_54_out, not_55_out, not_56_out,
       not_57_out, not_58_out, not_59_out, not_60_out, not_61_out, not_62_out, not_63_out, not_64_out,
       not_65_out, not_66_out, not_67_out, not_68_out, not_69_out, not_70_out, not_71_out, not_72_out,
       not_73_out, not_74_out, not_75_out, not_76_out, not_77_out, not_78_out, not_79_out, not_80_out,
       not_81_out, not_82_out, not_83_out, not_84_out, not_85_out, not_86_out, not_87_out, not_88_out,
       not_89_out, not_90_out, not_91_out, not_92_out, not_93_out, not_94_out, not_95_out, not_96_out,
       not_97_out, not_98_out, not_99_out, not_100_out, not_101_out, not_102_out, not_103_out, not_104_out,
       not_105_out, not_106_out, not_107_out, not_108_out, not_109_out, not_110_out, not_111_out,
       not_112_out, not_113_out, not_114_out, not_115_out, not_116_out, not_117_out, not_118_out,
       not_119_out, not_120_out, not_121_out, not_122_out, not_123_out, not_124_out, not_125_out,
       not_126_out, not_127_out, not_128_out, not_129_out, not_130_out, not_131_out, not_132_out,
       not_133_out, not_134_out, not_135_out, not_136_out, not_137_out, not_138_out;

  not not_1 (not_1_out, OP2);
  not not_2 (not_2_out, OP3);
  not not_3 (not_3_out, OP4);
  not not_4 (not_4_out, OP5);
  not not_5 (not_5_out, OP6);
  not not_6 (not_6_out, F12);
  not not_7 (not_7_out, F14);
  not not_8 (not_8_out, OP2);
  not not_9 (not_9_out, OP3);
  not not_10 (not_10_out, OP4);
  not not_11 (not_11_out, OP6);
  not not_12 (not_12_out, F12);
  not not_13 (not_13_out, F14);
  not not_14 (not_14_out, OP2);
  not not_15 (not_15_out, OP3);
  not not_16 (not_16_out, OP5);
  not not_17 (not_17_out, OP6);
  not not_18 (not_18_out, F12);
  not not_19 (not_19_out, F14);
  not not_20 (not_20_out, OP2);
  not not_21 (not_21_out, OP3);
  not not_22 (not_22_out, OP4);
  not not_23 (not_23_out, OP6);
  not not_24 (not_24_out, F12);
  not not_25 (not_25_out, F14);
  not not_26 (not_26_out, OP2);
  not not_27 (not_27_out, OP3);
  not not_28 (not_28_out, OP5);
  not not_29 (not_29_out, OP6);
  not not_30 (not_30_out, F12);
  not not_31 (not_31_out, OP2);
  not not_32 (not_32_out, OP3);
  not not_33 (not_33_out, OP5);
  not not_34 (not_34_out, OP6);
  not not_35 (not_35_out, F25);
  not not_36 (not_36_out, F30);
  not not_37 (not_37_out, OP2);
  not not_38 (not_38_out, OP3);
  not not_39 (not_39_out, OP5);
  not not_40 (not_40_out, OP6);
  not not_41 (not_41_out, F25);
  not not_42 (not_42_out, OP2);
  not not_43 (not_43_out, OP3);
  not not_44 (not_44_out, OP5);
  not not_45 (not_45_out, OP6);
  not not_46 (not_46_out, OP3);
  not not_47 (not_47_out, OP4);
  not not_48 (not_48_out, OP2);
  not not_49 (not_49_out, OP3);
  not not_50 (not_50_out, OP5);
  not not_51 (not_51_out, OP6);
  not not_52 (not_52_out, F12);
  not not_53 (not_53_out, F14);
  not not_54 (not_54_out, OP2);
  not not_55 (not_55_out, OP3);
  not not_56 (not_56_out, OP5);
  not not_57 (not_57_out, OP6);
  not not_58 (not_58_out, F12);
  not not_59 (not_59_out, OP2);
  not not_60 (not_60_out, OP3);
  not not_61 (not_61_out, OP5);
  not not_62 (not_62_out, OP6);
  not not_63 (not_63_out, F25);
  not not_64 (not_64_out, F30);
  not not_65 (not_65_out, OP2);
  not not_66 (not_66_out, OP3);
  not not_67 (not_67_out, OP6);
  not not_68 (not_68_out, F12);
  not not_69 (not_69_out, F13);
  not not_70 (not_70_out, F14);
  not not_71 (not_71_out, F25);
  not not_72 (not_72_out, OP2);
  not not_73 (not_73_out, OP3);
  not not_74 (not_74_out, OP5);
  not not_75 (not_75_out, OP6);
  not not_76 (not_76_out, F25);
  not not_77 (not_77_out, OP2);
  not not_78 (not_78_out, OP3);
  not not_79 (not_79_out, OP5);
  not not_80 (not_80_out, OP6);
  not not_81 (not_81_out, OP2);
  not not_82 (not_82_out, OP3);
  not not_83 (not_83_out, OP6);
  not not_84 (not_84_out, F25);
  not not_85 (not_85_out, F30);
  not not_86 (not_86_out, OP2);
  not not_87 (not_87_out, OP3);
  not not_88 (not_88_out, OP6);
  not not_89 (not_89_out, F25);
  not not_90 (not_90_out, F30);
  not not_91 (not_91_out, OP4);
  not not_92 (not_92_out, F14);
  not not_93 (not_93_out, F13);
  not not_94 (not_94_out, F12);
  not not_95 (not_95_out, OP3);
  not not_96 (not_96_out, OP2);
  not not_97 (not_97_out, F14);
  not not_98 (not_98_out, F13);
  not not_99 (not_99_out, F12);
  not not_100 (not_100_out, OP3);
  not not_101 (not_101_out, OP2);
  not not_102 (not_102_out, OP2);
  not not_103 (not_103_out, OP3);
  not not_104 (not_104_out, OP4);
  not not_105 (not_105_out, OP6);
  not not_106 (not_106_out, F12);
  not not_107 (not_107_out, F14);
  not not_108 (not_108_out, OP2);
  not not_109 (not_109_out, OP3);
  not not_110 (not_110_out, OP4);
  not not_111 (not_111_out, F12);
  not not_112 (not_112_out, F13);
  not not_113 (not_113_out, F14);
  not not_114 (not_114_out, OP2);
  not not_115 (not_115_out, OP3);
  not not_116 (not_116_out, OP4);
  not not_117 (not_117_out, F13);
  not not_118 (not_118_out, F14);
  not not_119 (not_119_out, OP3);
  not not_120 (not_120_out, OP4);
  not not_121 (not_121_out, OP4);
  not not_122 (not_122_out, OP2);
  not not_123 (not_123_out, OP3);
  not not_124 (not_124_out, OP5);
  not not_125 (not_125_out, OP6);
  not not_126 (not_126_out, F14);
  not not_127 (not_127_out, OP2);
  not not_128 (not_128_out, OP3);
  not not_129 (not_129_out, OP4);
  not not_130 (not_130_out, OP6);
  not not_131 (not_131_out, F12);
  not not_132 (not_132_out, F13);
  not not_133 (not_133_out, F14);
  not not_134 (not_134_out, OP2);
  not not_135 (not_135_out, OP3);
  not not_136 (not_136_out, OP4);
  not not_137 (not_137_out, F12);
  not not_138 (not_138_out, F13);
  and and_1 (MemToReg, not_1_out, not_2_out, not_3_out, not_4_out, not_5_out, not_6_out, F13, not_7_out);
  and and_2 (MemWrite, not_8_out, not_9_out, not_10_out, OP5, not_11_out, not_12_out, not_13_out);
  and and_3 (and_3_out, not_14_out, not_15_out, not_16_out, not_17_out, not_18_out, F13, not_19_out);
  and and_4 (and_4_out, not_20_out, not_21_out, not_22_out, OP5, not_23_out, not_24_out, not_25_out);
  and and_5 (and_5_out, not_26_out, not_27_out, OP4, not_28_out, not_29_out, not_30_out);
  and and_6 (and_6_out, not_31_out, not_32_out, OP4, not_33_out, not_34_out, not_35_out, not_36_out);
  and and_7 (and_7_out, not_37_out, not_38_out, OP4, not_39_out, not_40_out, F14, not_41_out);
  and and_8 (and_8_out, not_42_out, not_43_out, OP4, not_44_out, not_45_out, F13);
  and and_9 (and_9_out, OP2, not_46_out, not_47_out, OP5, OP6);
  and and_10 (and_10_out, not_48_out, not_49_out, not_50_out, not_51_out, not_52_out, F13, not_53_out);
  and and_11 (and_11_out, not_54_out, not_55_out, OP4, not_56_out, not_57_out, not_58_out);
  and and_12 (and_12_out, not_59_out, not_60_out, OP4, not_61_out, not_62_out, not_63_out, not_64_out);
  and and_13 (and_13_out, not_65_out, not_66_out, OP4, not_67_out, not_68_out, not_69_out, not_70_out, not_71_out);
  and and_14 (and_14_out, not_72_out, not_73_out, OP4, not_74_out, not_75_out, F14, not_76_out);
  and and_15 (and_15_out, not_77_out, not_78_out, OP4, not_79_out, not_80_out, F13);
  and and_16 (and_16_out, not_81_out, not_82_out, OP4, not_83_out, F13, not_84_out, not_85_out);
  and and_17 (and_17_out, not_86_out, not_87_out, OP4, not_88_out, F12, F14, not_89_out, not_90_out);
  and and_18 (and_18_out, OP2, not_91_out, OP5, OP6);
  and and_19 (and_19_out, not_92_out, not_93_out, not_94_out, OP6, OP5, OP4, not_95_out, not_96_out);
  and and_20 (and_20_out, not_97_out, not_98_out, not_99_out, OP6, OP5, OP4, not_100_out, not_101_out);
  and and_21 (S_Type, not_102_out, not_103_out, not_104_out, OP5, not_105_out, not_106_out, not_107_out);
  and and_22 (BEQ, not_108_out, not_109_out, not_110_out, OP5, OP6, not_111_out, not_112_out, not_113_out);
  and and_23 (BNE, not_114_out, not_115_out, not_116_out, OP5, OP6, F12, not_117_out, not_118_out);
  and and_24 (JALR, OP2, not_119_out, not_120_out, OP5, OP6);
  and and_25 (JAL, OP2, OP3, not_121_out, OP5, OP6);
  and and_26 (Sltiu, not_122_out, not_123_out, OP4, not_124_out, not_125_out, F12, F13, not_126_out);
  and and_27 (Sb, not_127_out, not_128_out, not_129_out, OP5, not_130_out, not_131_out, not_132_out, not_133_out);
  and and_28 (Blt, not_134_out, not_135_out, not_136_out, OP5, OP6, not_137_out, not_138_out, F14);
  or or_1 (ALU_SRC, and_3_out, and_4_out, and_5_out, and_6_out, and_7_out, and_8_out, and_9_out);
  or or_2 (ecall, and_19_out, and_20_out);
  or or_3 (RegWrite, and_10_out, and_11_out, and_12_out, and_13_out, and_14_out, and_15_out, and_16_out, and_17_out, and_18_out);
endmodule

// ALU
module ALU (
  input  [31:0] X,
  input  [31:0] Y,
  input  [3:0] AluOP,
  output out_4,
  output Equal,
  output out_6,
  output [31:0] Result,
  output [31:0] Result_2
);

  wire [0:0] comparator_1_lt, comparator_2_lt;
  wire [31:0] adder_1_out, AND_out, divider_1_out, divider_1_rem, multiplier_1_cout, multiplier_1_out,
       NOR_out, OR_out, shifter_1_out, shifter_2_out, shifter_3_out, subtractor_1_out, XOR_out;

  assign AND_out = X & Y;  // AND_Gate AND, 32 bits wide
  assign OR_out = X | Y;  // OR_Gate OR, 32 bits wide
  Shifter #(.width(32), .shift("ll")) shifter_1 (.in(X), .\dist (Y[4:0]), .out(shifter_1_out));
  Shifter #(.width(32), .shift("ar")) shifter_2 (.in(X), .\dist (Y[4:0]), .out(shifter_2_out));
  Shifter #(.width(32), .shift("lr")) shifter_3 (.in(X), .\dist (Y[4:0]), .out(shifter_3_out));
  Multiplier #(.width(32)) multiplier_1 (.a(X), .b(Y), .out(multiplier_1_out), .cout(multiplier_1_cout));  // open: cin
  Divider #(.width(32)) divider_1 (.a(X), .b(Y), .out(divider_1_out), .rem(divider_1_rem));  // open: upper
  Adder #(.width(32)) adder_1 (.a(X), .b(Y), .out(adder_1_out));  // open: cin, cout
  Subtractor #(.width(32)) subtractor_1 (.a(X), .b(Y), .out(subtractor_1_out));  // open: bin, bout
  assign XOR_out = X ^ Y;  // XOR_Gate XOR, 32 bits wide
  assign NOR_out = ~(X | Y);  // NOR_Gate NOR, 32 bits wide
  Comparator #(.width(32), .mode("twosComplement")) comparator_1 (
    .a(X), .b(Y), .eq(Equal), .lt(comparator_1_lt[0]));  // open: gt
  Comparator #(.width(32), .mode("unsigned")) comparator_2 (.a(X), .b(Y), .lt(comparator_2_lt[0]));  // open: gt, eq
  Multiplexer #(.select(4), .width(32), .disabled("Z"), .enable("false")) multiplexer_1 (
    .in0(shifter_1_out), .in1(shifter_2_out), .in2(shifter_3_out), .in3(multiplier_1_out),
    .in4(divider_1_out), .in5(adder_1_out), .in6(subtractor_1_out), .in7(AND_out), .in8(OR_out),
    .in9(XOR_out), .in10(NOR_out), .in11({{31{1'b0}}, comparator_1_lt[0]}),
    .in12({{31{1'b0}}, comparator_2_lt[0]}), .in13({32{1'b0}}), .in14({32{1'b0}}), .in15({32{1'b0}}),
    .out(Result), .sel(AluOP));
  Multiplexer #(.select(4), .width(32), .disabled("Z"), .enable("false")) multiplexer_2 (
    .in0({32{1'b0}}), .in1({32{1'b0}}), .in2({32{1'b0}}), .in3(multiplier_1_cout), .in4(divider_1_rem),
    .in5({32{1'b0}}), .in6({32{1'b0}}), .in7({32{1'b0}}), .in8({32{1'b0}}), .in9({32{1'b0}}),
    .in10({32{1'b0}}), .in11({32{1'b0}}), .in12({32{1'b0}}), .in13({32{1'b0}}), .in14({32{1'b0}}),
    .in15({32{1'b0}}), .out(Result_2), .sel(AluOP));
  Multiplexer #(.select(4), .width(1), .disabled("Z"), .enable("false")) multiplexer_3 (
    .in0(1'b0), .in1(1'b0), .in2(1'b0), .in3(1'b0), .in4(1'b0), .in5(1'b0), .in6(1'b0), .in7(1'b0),
    .in8(1'b0), .in9(1'b0), .in10(1'b0), .in11(comparator_1_lt[0]), .in12(comparator_2_lt[0]), .in13(1'b0),
    .in14(1'b0), .in15(1'b0), .out(out_6), .sel(AluOP));
  not not_1 (out_4, out_6);

  // Other names for the same wires on the sheet: Result2[31:0] = Result_2; S[3:0] = AluOP; tunnel = out_6;
  //   tunnel_t = out_4

  // Notes on the sheet:
  //   不要改变此引脚区域内容，也不要改变ALU封装形式
  //   输入引脚
  //   输出引脚
endmodule

module \Regifile_上升沿  (
  input  [31:0] Din,
  input  Clk,
  input  WE,
  input  [4:0] W_num,
  input  [4:0] R1_num,
  input  [4:0] R2_num,
  output [31:0] R1,
  output [31:0] R2
);

  // RegisterFile registerfile_1: pin names not known; wires that end beside it: Din, Clk, WE, W_num, R1_num, R2_num, R1, R2
endmodule

module \Regifile_下降沿  (
  input  [31:0] Din,
  input  Clk,
  input  WE,
  input  [4:0] R1_num,
  input  [4:0] W_num,
  input  [4:0] R2_num,
  output [31:0] R1,
  output [31:0] R2
);

  // RegisterFile registerfile_1: pin names not known; wires that end beside it: Din, Clk, WE, W_num, R1_num, R2_num, R1, R2
endmodule

module \理想流水线  (
  output RegWrite,
  output MemWrite,
  output [31:0] IF_PC,
  output [31:0] ID_PC,
  output [31:0] EX_PC,
  output [31:0] M_PC,
  output [31:0] WB_PC,
  output [31:0] RDin,
  output [31:0] MDin,
  output [31:0] LedData
);

  wire alu_1_equal, alu_1_out_6, and_3_out, and_5_out, and_6_out, and_7_out, CLK, clock_1_out, clock_2_out,
       comparator_1_eq, comparator_2_eq, comparator_2_lt, d_ff_1_q, ecall, EX_B_signal, EX_J_signal,
       ex_mem_1_ecall_2, ex_mem_1_jal_2, ex_mem_1_jalr_2, ex_mem_1_memtoreg_2, ex_mem_1_regwrite_2,
       EX_S_signal, Go, halt, id_ex_1_alusrcb_2, id_ex_1_beq_2, id_ex_1_blt_2, id_ex_1_bne_2,
       id_ex_1_ecall_2, id_ex_1_jalr_2, id_ex_1_memtoreg_2, id_ex_1_memwrite_2, id_ex_1_regwrite_2,
       id_ex_1_sb_2, id_ex_1_sltiu_2, IR1, IR2, IR3, Ledout, mem_wb_1_jal_2, mem_wb_1_jalr_2,
       mem_wb_1_memtoreg_2, mips_ram_1_p6, nand_1_out, not_1_out, not_2_out, or_1_out, or_2_out, or_3_out,
       or_5_out, or_6_out, RST, sb, W1, W2, W3, \单周期硬布线控制器_1_alu_src , \单周期硬布线控制器_1_beq , \单周期硬布线控制器_1_blt ,
       \单周期硬布线控制器_1_bne , \单周期硬布线控制器_1_ecall , \单周期硬布线控制器_1_jal , \单周期硬布线控制器_1_jalr , \单周期硬布线控制器_1_memtoreg ,
       \单周期硬布线控制器_1_memwrite , \单周期硬布线控制器_1_regwrite , \单周期硬布线控制器_1_s_type , \单周期硬布线控制器_1_sb ,
       \单周期硬布线控制器_1_sltiu , \单周期硬布线控制器_1_uret ;
  wire [1:0] Bit_Sel, EX_Imm_Sel;
  wire [3:0] decoder_1_out0, id_ex_1_aluop_2, RAM_Sel, \单周期硬布线控制器_1_alu_op ;
  wire [4:0] bit_extender_6_out, multiplexer_3_out, multiplexer_4_out, multiplier_1_out;
  wire [11:0] id_ex_1_imm_b_2, id_ex_1_imm_i_2, id_ex_1_imm_s_2;
  wire [12:0] CNT_num;
  wire [15:0] \LoadUse次数 , \总周期数 , \插入气泡数 , \无条件分支数 , \条件分支成功数 ;
  wire [19:0] id_ex_1_imm_j_2;
  wire [31:0] adder_2_out, bit_extender_1_out, bit_extender_2_out, bit_extender_3_out, bit_extender_4_out,
       bit_extender_5_out, EX_AluData, EX_IR, ex_mem_1_pc_4_2, EX_R1Data, EX_R2Data, id_ex_1_pc_4_2, ID_IR,
       ID_R1Data, if_id_1_pc_4_2, IF_IR, IF_PC_4, MEM_IR, MEM_R1Data, mem_wb_1_aludata_2, mem_wb_1_memdata_2,
       MemData, mips_ram_1_p8, multiplexer_1_out, multiplexer_2_out, multiplexer_5_out, multiplexer_6_out,
       multiplexer_7_out, multiplexer_10_out, \regifile_上升沿_1_r2 , shifter_1_out, shifter_2_out, WB_IR,
       WB_PC_4, WB_R1Data, WB_R2Data;
  wire [31:2] ex_mem_1_aludata_2;

  Button \u_总复位  (.out(RST));
  Button _1 (.out(IR1));
  Button _2 (.out(IR2));
  Button _3 (.out(IR3));
  // Probe on \总周期数 
  // Probe on \总周期数 
  Button \u_继续运行  (.out(Go));
  LED #(.active("true")) led_1 (.in(W1));
  LED #(.active("true")) led_2 (.in(W2));
  LED #(.active("true")) led_3 (.in(W3));
  or or_1 (or_1_out, or_5_out, EX_J_signal);
  Hex_Digit_Display hex_digit_display_1 (.value(LedData[31:28]));  // open: dp
  // Probe on IF_PC[19:0]
  // RiscV_Probe riscv_probe_1: pin names not known; wires that end beside it: IF_IR
  Multiplexer #(.select(1), .width(32), .disabled("Z"), .enable("false")) multiplexer_1 (
    .in0(IF_PC_4), .in1(adder_2_out), .out(multiplexer_1_out), .sel(or_1_out));
  Multiplexer #(.select(1), .width(32), .disabled("Z"), .enable("false")) multiplexer_2 (
    .in0(multiplexer_1_out), .in1(EX_AluData), .out(multiplexer_2_out), .sel(id_ex_1_jalr_2));
  or or_2 (or_2_out, EX_B_signal, EX_J_signal);
  or or_3 (or_3_out, EX_J_signal, EX_S_signal);
  Hex_Digit_Display hex_digit_display_2 (.value(LedData[27:24]));  // open: dp
  Hex_Digit_Display hex_digit_display_3 (.value(LedData[23:20]));  // open: dp
  // Probe on ID_PC[19:0]
  // RiscV_Probe riscv_probe_2: pin names not known; wires that end beside it: ID_IR
  Register #(.width(32), .trigger("rising"), .Select("low")) PC (
    .D(multiplexer_2_out), .en(not_1_out), .Q(IF_PC), .clk(CLK), .clr(RST));
  not not_1 (not_1_out, halt);
  Hex_Digit_Display hex_digit_display_4 (.value(LedData[19:16]));  // open: dp
  Hex_Digit_Display hex_digit_display_5 (.value(LedData[15:12]));  // open: dp
  Adder #(.width(32)) adder_1 (.a(IF_PC), .b(32'h4), .out(IF_PC_4));  // open: cin, cout
  and and_1 (EX_Imm_Sel[1], ~EX_S_signal, or_2_out);  // AND_Gate
  and and_2 (EX_Imm_Sel[0], or_3_out, ~EX_B_signal);  // AND_Gate
  Hex_Digit_Display hex_digit_display_6 (.value(LedData[7:4]));  // open: dp
  Hex_Digit_Display hex_digit_display_7 (.value(LedData[11:8]));  // open: dp
  Clock #(.highDuration(1), .lowDuration(1)) clock_1 (.out(clock_1_out));
  // Probe on EX_PC[19:0]
  // RiscV_Probe riscv_probe_3: pin names not known; wires that end beside it: clock_1_out, EX_IR, CLK
  Hex_Digit_Display hex_digit_display_8 (.value(LedData[3:0]));  // open: dp
  ROM #(.addrWidth(10), .dataWidth(32), .Select("high")) rom_1 (.addr(IF_PC[11:2]), .data(IF_IR));
  // Probe on \总周期数 
  // Probe on M_PC[19:0]
  // RiscV_Probe riscv_probe_4: pin names not known; wires that end beside it: MEM_IR
  // RiscV_Probe riscv_probe_5: pin names not known; wires that end beside it: IF_IR
  // Probe on \总周期数 
  // Probe on \无条件分支数 
  // Probe on \条件分支成功数 
  // Probe on \插入气泡数 
  // Probe on \LoadUse次数 
  Comparator #(.width(32), .mode("unsigned")) comparator_1 (
    .a(WB_R1Data), .b(32'h22), .eq(comparator_1_eq));  // open: gt, lt
  // Probe on IF_PC[11:0]
  // Probe on WB_PC[19:0]
  // RiscV_Probe riscv_probe_6: pin names not known; wires that end beside it: WB_IR
  IF_ID if_id_1 (
    .CLK(CLK), .\RST_高电平有效 (RST), .\en_低电平有效 (1'b0), .IR(IF_IR), .PC(IF_PC), .PC_4(IF_PC_4), .IR_2(ID_IR),
    .PC_2(ID_PC), .PC_4_2(if_id_1_pc_4_2));
  // Probe on ID_PC[11:0]
  // Probe on EX_PC[11:0]
  and and_3 (and_3_out, ecall, ~comparator_1_eq);  // AND_Gate
  and and_4 (Ledout, comparator_1_eq, ecall);
  // Probe on M_PC[11:0]
  D_Flip_Flop #(.trigger("high"), .Pre_Clr_Positions("LEGACY"), .NegatePresetClear("false"), .enable("true"), .NewFFLayout("false")) d_ff_1 (.Q(d_ff_1_q));  // open: clk, D, Qn, preset, en, reset
  // Probe on 13'hc
  \单周期硬布线控制器  \u_单周期硬布线控制器_1  (
    .Funct({ID_IR[30], ID_IR[25], ID_IR[14:12]}), .OP(ID_IR[6:2]), .ALU_OP(\单周期硬布线控制器_1_alu_op ),
    .MemToReg(\单周期硬布线控制器_1_memtoreg ), .MemWrite(\单周期硬布线控制器_1_memwrite ), .ALU_SRC(\单周期硬布线控制器_1_alu_src ),
    .RegWrite(\单周期硬布线控制器_1_regwrite ), .ecall(\单周期硬布线控制器_1_ecall ), .S_type(\单周期硬布线控制器_1_s_type ),
    .Jalr(\单周期硬布线控制器_1_jalr ), .Beq(\单周期硬布线控制器_1_beq ), .JAL(\单周期硬布线控制器_1_jal ), .Bne(\单周期硬布线控制器_1_bne ),
    .in_3(ID_IR[21]), .uret(\单周期硬布线控制器_1_uret ), .Sltiu(\单周期硬布线控制器_1_sltiu ), .Sb(\单周期硬布线控制器_1_sb ),
    .Blt(\单周期硬布线控制器_1_blt ));
  Multiplexer #(.select(1), .width(5), .disabled("Z"), .enable("false")) multiplexer_3 (
    .in0(ID_IR[19:15]), .in1(5'b10001), .out(multiplexer_3_out), .sel(\单周期硬布线控制器_1_ecall ));
  Multiplexer #(.select(1), .width(5), .disabled("Z"), .enable("false")) multiplexer_4 (
    .in0(ID_IR[24:20]), .in1(5'b01010), .out(multiplexer_4_out), .sel(\单周期硬布线控制器_1_ecall ));
  D_Flip_Flop #(.trigger("falling"), .Pre_Clr_Positions("ABOVE_BELOW"), .NegatePresetClear("false"), .enable("true"), .NewFFLayout("true")) d_ff_2 (
    .clk(CLK), .D(and_3_out), .Q(halt), .en(ecall), .reset(Go));  // open: Qn, preset
  // Probe on WB_PC[11:0]
  Comparator #(.width(13), .mode("twosComplement")) comparator_2 (
    .a(CNT_num), .b(13'hc), .eq(comparator_2_eq), .lt(comparator_2_lt));  // open: gt
  Clock #(.highDuration(1), .lowDuration(1)) clock_2 (.out(clock_2_out));
  nand nand_1 (nand_1_out, d_ff_1_q, comparator_2_eq);
  Counter #(.width(13), .max('h1fff), .ongoal("stay"), .trigger("rising"), .behavior("old")) counter_1 (
    .count(comparator_2_lt), .Q(CNT_num), .clk(clock_2_out));  // open: load, D, carry, clr, preset
  \Regifile_上升沿  \regifile_上升沿_1  (
    .Din(RDin), .Clk(CLK), .R1(ID_R1Data), .R2(\regifile_上升沿_1_r2 ), .WE(RegWrite), .W_num(WB_IR[11:7]),
    .R1_num(multiplexer_3_out), .R2_num(multiplexer_4_out));
  assign CLK = nand_1_out ? clock_2_out : 1'bz;  // Controlled_Buffer controlled_buffer_1
  ID_EX id_ex_1 (
    .CLK(CLK), .\RST_高电平有效 (RST), .\en_低电平有效 (1'b0), .RegWrite(\单周期硬布线控制器_1_regwrite ), .IR(ID_IR),
    .AluSrcB(\单周期硬布线控制器_1_alu_src ), .AluOP(\单周期硬布线控制器_1_alu_op ), .PC(ID_PC),
    .MemWrite(\单周期硬布线控制器_1_memwrite ), .MemToReg(\单周期硬布线控制器_1_memtoreg ), .PC_4(if_id_1_pc_4_2),
    .Bne(\单周期硬布线控制器_1_bne ), .Beq(\单周期硬布线控制器_1_beq ), .R1(ID_R1Data), .JAL(\单周期硬布线控制器_1_jal ),
    .R2(\regifile_上升沿_1_r2 ), .JALR(\单周期硬布线控制器_1_jalr ), .URET(\单周期硬布线控制器_1_uret ), .Imm_I(ID_IR[31:20]),
    .RegWrite_2(id_ex_1_regwrite_2), .IR_2(EX_IR), .AluSrcB_2(id_ex_1_alusrcb_2), .AluOP_2(id_ex_1_aluop_2),
    .PC_2(EX_PC), .MemWrite_2(id_ex_1_memwrite_2), .MemToReg_2(id_ex_1_memtoreg_2), .PC_4_2(id_ex_1_pc_4_2),
    .Bne_2(id_ex_1_bne_2), .Beq_2(id_ex_1_beq_2), .R1_2(EX_R1Data), .JAL_2(EX_J_signal), .R2_2(EX_R2Data),
    .JALR_2(id_ex_1_jalr_2), .Imm_I_2(id_ex_1_imm_i_2), .Sltiu(\单周期硬布线控制器_1_sltiu ),
    .Sltiu_2(id_ex_1_sltiu_2), .Sb(\单周期硬布线控制器_1_sb ), .Sb_2(id_ex_1_sb_2), .Blt(\单周期硬布线控制器_1_blt ),
    .Blt_2(id_ex_1_blt_2), .ecall(\单周期硬布线控制器_1_ecall ), .ecall_2(id_ex_1_ecall_2),
    .Imm_S({ID_IR[31:25], ID_IR[11:7]}), .Imm_S_2(id_ex_1_imm_s_2),
    .Imm_B({ID_IR[31], ID_IR[7], ID_IR[30:25], ID_IR[11:8]}), .Imm_B_2(id_ex_1_imm_b_2),
    .Imm_J({ID_IR[31], ID_IR[19:12], ID_IR[20], ID_IR[30:21]}), .Imm_J_2(id_ex_1_imm_j_2),
    .S_Type(\单周期硬布线控制器_1_s_type ), .S_Type_2(EX_S_signal));  // open: URET_2
  Pull_Resistor #(.pull(1)) pull_resistor_1 (.node(CLK));
  Register #(.width(32), .trigger("rising"), .Select("low")) register_1 (
    .D(WB_R2Data), .en(Ledout), .Q(LedData), .clk(CLK), .clr(RST));
  or or_4 (EX_B_signal, id_ex_1_beq_2, id_ex_1_bne_2, id_ex_1_blt_2);
  assign bit_extender_1_out = {{20{id_ex_1_imm_i_2[11]}}, id_ex_1_imm_i_2};  // Bit_Extender bit_extender_1
  assign bit_extender_2_out = {{20{1'b0}}, id_ex_1_imm_i_2};  // Bit_Extender bit_extender_2
  assign bit_extender_3_out = {{20{id_ex_1_imm_s_2[11]}}, id_ex_1_imm_s_2};  // Bit_Extender bit_extender_3
  assign bit_extender_4_out = {{20{id_ex_1_imm_b_2[11]}}, id_ex_1_imm_b_2};  // Bit_Extender bit_extender_4
  assign bit_extender_5_out = {{12{id_ex_1_imm_j_2[19]}}, id_ex_1_imm_j_2};  // Bit_Extender bit_extender_5
  Multiplexer #(.select(1), .width(32), .disabled("Z"), .enable("false")) multiplexer_5 (
    .in0(bit_extender_1_out), .in1(bit_extender_2_out), .out(multiplexer_5_out), .sel(id_ex_1_sltiu_2));
  Multiplexer #(.select(1), .width(32), .disabled("Z"), .enable("false")) multiplexer_6 (
    .in0(EX_R2Data), .in1(multiplexer_7_out), .out(multiplexer_6_out), .sel(id_ex_1_alusrcb_2));
  Multiplexer #(.select(2), .width(32), .disabled("Z"), .enable("false")) multiplexer_7 (
    .in0(multiplexer_5_out), .in1(bit_extender_3_out), .in2(bit_extender_4_out), .in3(bit_extender_5_out),
    .out(multiplexer_7_out), .sel(EX_Imm_Sel));
  not not_2 (not_2_out, halt);
  ALU alu_1 (
    .X(EX_R1Data), .Y(multiplexer_6_out), .AluOP(id_ex_1_aluop_2), .Equal(alu_1_equal), .Result(EX_AluData),
    .out_6(alu_1_out_6));  // open: Result_2, out_4
  Shifter #(.width(32), .shift("ll")) shifter_1 (.in(multiplexer_7_out), .\dist (5'b00001), .out(shifter_1_out));
  Counter #(.width(16), .max('hffff), .ongoal("stay"), .trigger("rising"), .behavior("old")) counter_2 (
    .count(not_2_out), .Q(\总周期数 ), .clk(CLK));  // open: load, D, carry, clr, preset
  and and_5 (and_5_out, id_ex_1_beq_2, alu_1_equal);
  or or_5 (or_5_out, and_5_out, and_6_out, and_7_out);
  and and_6 (and_6_out, id_ex_1_bne_2, ~alu_1_equal);  // AND_Gate
  and and_7 (and_7_out, id_ex_1_blt_2, alu_1_out_6);
  Adder #(.width(32)) adder_2 (.a(EX_PC), .b(shifter_1_out), .out(adder_2_out));  // open: cin, cout
  EX_MEM ex_mem_1 (
    .CLK(CLK), .\RST_高电平有效 (RST), .\en_低电平有效 (1'b0), .RegWrite(id_ex_1_regwrite_2),
    .MemWrite(id_ex_1_memwrite_2), .IR(EX_IR), .MemToReg(id_ex_1_memtoreg_2), .JAL(EX_J_signal), .PC(EX_PC),
    .JALR(id_ex_1_jalr_2), .PC_4(id_ex_1_pc_4_2), .ecall(id_ex_1_ecall_2), .R1(EX_R1Data), .Sb(id_ex_1_sb_2),
    .R2(EX_R2Data), .AluData(EX_AluData), .RegWrite_2(ex_mem_1_regwrite_2), .MemWrite_2(MemWrite),
    .IR_2(MEM_IR), .MemToReg_2(ex_mem_1_memtoreg_2), .JAL_2(ex_mem_1_jal_2), .PC_2(M_PC),
    .JALR_2(ex_mem_1_jalr_2), .PC_4_2(ex_mem_1_pc_4_2), .ecall_2(ex_mem_1_ecall_2), .R1_2(MEM_R1Data),
    .Sb_2(sb), .R2_2(MDin), .AluData_2({ex_mem_1_aludata_2, Bit_Sel}));
  assign bit_extender_6_out = {{3{1'b0}}, Bit_Sel};  // Bit_Extender bit_extender_6
  Decoder #(.select(2), .tristate("false"), .disabled("Z"), .enable("false")) decoder_1 (
    .out0(decoder_1_out0[0]), .out1(decoder_1_out0[1]), .out2(decoder_1_out0[2]), .out3(decoder_1_out0[3]),
    .sel(Bit_Sel));
  Multiplier #(.width(5)) multiplier_1 (
    .a(bit_extender_6_out), .b(5'b01000), .out(multiplier_1_out));  // open: cin, cout
  Multiplexer #(.select(1), .width(4), .disabled("Z"), .enable("false")) multiplexer_8 (
    .in0(4'b1111), .in1(decoder_1_out0), .out(RAM_Sel), .sel(sb));
  Shifter #(.width(32), .shift("ll")) shifter_2 (.in(MDin), .\dist (multiplier_1_out), .out(shifter_2_out));
  // cs3410_MIPS_RAM mips_ram_1: pin names not known; wires that end beside it: ex_mem_1_aludata_2[21:2], MemData, MemWrite, RAM_Sel, CLK, mips_ram_1_p6, RST, mips_ram_1_p8
  not not_3 (mips_ram_1_p6, MemWrite);
  Multiplexer #(.select(1), .width(32), .disabled("Z"), .enable("false")) multiplexer_9 (
    .in0(MDin), .in1(shifter_2_out), .out(MemData), .sel(sb));
  MEM_WB mem_wb_1 (
    .CLK(CLK), .\RST_高电平有效 (RST), .\en_低电平有效 (1'b0), .RegWrite(ex_mem_1_regwrite_2), .IR(MEM_IR),
    .MemToReg(ex_mem_1_memtoreg_2), .JAL(ex_mem_1_jal_2), .PC(M_PC), .JALR(ex_mem_1_jalr_2),
    .PC_4(ex_mem_1_pc_4_2), .ecall(ex_mem_1_ecall_2), .R1(MEM_R1Data), .R2(MDin),
    .AluData({ex_mem_1_aludata_2, Bit_Sel}), .MemData(mips_ram_1_p8), .RegWrite_2(RegWrite), .IR_2(WB_IR),
    .MemToReg_2(mem_wb_1_memtoreg_2), .JAL_2(mem_wb_1_jal_2), .PC_2(WB_PC), .JALR_2(mem_wb_1_jalr_2),
    .PC_4_2(WB_PC_4), .ecall_2(ecall), .R1_2(WB_R1Data), .R2_2(WB_R2Data), .AluData_2(mem_wb_1_aludata_2),
    .MemData_2(mem_wb_1_memdata_2));
  Multiplexer #(.select(1), .width(32), .disabled("Z"), .enable("false")) multiplexer_10 (
    .in0(mem_wb_1_aludata_2), .in1(mem_wb_1_memdata_2), .out(multiplexer_10_out), .sel(mem_wb_1_memtoreg_2));
  or or_6 (or_6_out, mem_wb_1_jalr_2, mem_wb_1_jal_2);
  Multiplexer #(.select(1), .width(32), .disabled("Z"), .enable("false")) multiplexer_11 (
    .in0(multiplexer_10_out), .in1(WB_PC_4), .out(RDin), .sel(or_6_out));

  // Other names for the same wires on the sheet: MEM_PC[31:0] = M_PC; MEM_R2Data[31:0] = MDin

  // Notes on the sheet:
  //   中断源
  //   时空图监测，可删除
  //   中断等待指示
  //   EX阶段 生成立即数选择信号
  //   数码管输出
  //   指令存储器
  //   contents of rom_1 (hex, n*v repeats v):
  //   413 493 913 993 46413 14e493 296913 39e993 842023 942223 1242423 1342623 a00893 493 913 993 73
  //   指令探针
  //   生成停机信号halt和LED显示信号Ledout
  //   控制位
  //   JAL
  //   JALR
  //   URET
  //   Sltiu
  //   Sb
  //   rs1
  //   rs2
  //   流水调试日志用
  //   暂停节拍，不能为0
  //   Beq
  //   Bne
  //   MemToReg
  //   MemWrite
  //   AluOP
  //   AluSrcB
  //   RegWrite
  //   Blt
  //   I型指令立即数
  //   S型指令立即数
  //   B型指令立即数
  //   J型指令立即数
  //   戳工具置1进入计数暂停模式，ctrl+k时钟自动运行到对应节拍暂停
  //   ctrl+k关闭时钟连续运行，将控制位置零，进入单步调试模式调试
  //   用这个时钟源需要去掉电路中的其他时钟源
  //   可计数暂停的时钟源
  //   LedData显示控制
  //   为方便自动评测，需要输出流水线各段保存的PC值，注意是PC不是PC+4，另外ID段寄存器写入信息，Mem段内存写入信息也要输出
  //   周期信号显示控制
  //   计算Sb对应的MemData
  //   rd
endmodule

module \气泡流水线  (
  output RegWrite,
  output MemWrite,
  output [31:0] IF_PC,
  output [31:0] ID_PC,
  output [31:0] EX_PC,
  output [31:0] M_PC,
  output [31:0] WB_PC,
  output [31:0] RDin,
  output [31:0] MDin,
  output [31:0] LedData
);

  wire alu_1_equal, alu_1_out_6, and_1_out, and_2_out, and_3_out, and_4_out, and_5_out, and_6_out, and_7_out,
       and_8_out, and_12_out, B_Jump, BranchTaken, CLK, clock_1_out, clock_2_out, comparator_1_eq,
       comparator_1_lt, comparator_2_eq, d_ff_1_q, DataHazzard, ecall, EX_B_signal, EX_J_signal,
       ex_mem_1_ecall_2, ex_mem_1_jal_2, ex_mem_1_jalr_2, ex_mem_1_memtoreg_2, EX_RegWrite, EX_S_signal, Go,
       halt, id_ex_1_alusrcb_2, id_ex_1_beq_2, id_ex_1_blt_2, id_ex_1_bne_2, id_ex_1_ecall_2, id_ex_1_jalr_2,
       id_ex_1_memtoreg_2, id_ex_1_memwrite_2, id_ex_1_sb_2, id_ex_1_sltiu_2, IR1, IR2, IR3, Ledout,
       MEM_RegWrite, mem_wb_1_jal_2, mem_wb_1_jalr_2, mem_wb_1_memtoreg_2, mips_ram_1_p6, nand_1_out,
       not_1_out, not_2_out, not_4_out, or_1_out, or_2_out, or_3_out, or_4_out, or_9_out, or_10_out,
       or_11_out, or_12_out, \r1r2使用检测_1_r1used , \r1r2使用检测_1_r2used , RST, sb, W1, W2, W3,
       \单周期硬布线控制器_1_alu_src , \单周期硬布线控制器_1_beq , \单周期硬布线控制器_1_blt , \单周期硬布线控制器_1_bne , \单周期硬布线控制器_1_ecall ,
       \单周期硬布线控制器_1_jal , \单周期硬布线控制器_1_jalr , \单周期硬布线控制器_1_memtoreg , \单周期硬布线控制器_1_memwrite ,
       \单周期硬布线控制器_1_regwrite , \单周期硬布线控制器_1_s_type , \单周期硬布线控制器_1_sb , \单周期硬布线控制器_1_sltiu ,
       \单周期硬布线控制器_1_uret , \无条件分支 ;
  wire [1:0] Bit_Sel, EX_Imm_Sel;
  wire [3:0] decoder_1_out0, id_ex_1_aluop_2, RAM_Sel, \单周期硬布线控制器_1_alu_op ;
  wire [4:0] bit_extender_1_out, ID_R1, ID_R2, multiplier_1_out;
  wire [11:0] id_ex_1_imm_b_2, id_ex_1_imm_i_2, id_ex_1_imm_s_2;
  wire [12:0] CNT_num;
  wire [15:0] adder_3_out, \LoadUse次数 , \总周期数 , \插入气泡数 , \无条件分支数 , \条件分支成功数 ;
  wire [19:0] id_ex_1_imm_j_2;
  wire [31:0] adder_2_out, bit_extender_2_out, bit_extender_3_out, bit_extender_4_out, bit_extender_5_out,
       bit_extender_6_out, EX_AluData, EX_IR, EX_JalrData, ex_mem_1_pc_4_2, EX_R1Data, EX_R2Data,
       id_ex_1_pc_4_2, ID_IR, ID_R1Data, if_id_1_pc_4_2, IF_IR, IF_PC_4, MEM_IR, MEM_R1Data,
       mem_wb_1_aludata_2, mem_wb_1_memdata_2, MemData, mips_ram_1_p9, multiplexer_1_out, multiplexer_2_out,
       multiplexer_7_out, multiplexer_8_out, multiplexer_9_out, multiplexer_10_out, not_5_out,
       \regifile_下降沿_1_r2 , shifter_1_out, shifter_2_out, WB_IR, WB_PC_4, WB_R1Data, WB_R2Data;
  wire [31:2] ex_mem_1_aludata_2;

  Button \u_总复位  (.out(RST));
  Button _1 (.out(IR1));
  Button _2 (.out(IR2));
  Button _3 (.out(IR3));
  // Probe on \总周期数 
  // Probe on \总周期数 
  Button \u_继续运行  (.out(Go));
  LED #(.active("true")) led_1 (.in(W1));
  LED #(.active("true")) led_2 (.in(W2));
  LED #(.active("true")) led_3 (.in(W3));
  or or_1 (or_1_out, B_Jump, EX_J_signal);
  Hex_Digit_Display hex_digit_display_1 (.value(LedData[31:28]));  // open: dp
  // Probe on IF_PC[19:0]
  // RiscV_Probe riscv_probe_1: pin names not known; wires that end beside it: IF_IR
  Multiplexer #(.select(1), .width(32), .disabled("Z"), .enable("false")) multiplexer_1 (
    .in0(IF_PC_4), .in1(adder_2_out), .out(multiplexer_1_out), .sel(or_1_out));
  Multiplexer #(.select(1), .width(32), .disabled("Z"), .enable("false")) multiplexer_2 (
    .in0(multiplexer_1_out), .in1(EX_JalrData), .out(multiplexer_2_out), .sel(id_ex_1_jalr_2));
  and and_1 (and_1_out, not_1_out, not_2_out);
  not not_1 (not_1_out, DataHazzard);
  Hex_Digit_Display hex_digit_display_2 (.value(LedData[27:24]));  // open: dp
  Hex_Digit_Display hex_digit_display_3 (.value(LedData[23:20]));  // open: dp
  // Probe on ID_PC[19:0]
  // RiscV_Probe riscv_probe_2: pin names not known; wires that end beside it: ID_IR
  Register #(.width(32), .trigger("rising"), .Select("low")) PC (
    .D(multiplexer_2_out), .en(and_1_out), .Q(IF_PC), .clk(CLK), .clr(RST));
  not not_2 (not_2_out, halt);
  \R1R2使用检测  \r1r2使用检测_1  (
    .OP2(ID_IR[2]), .OP3(ID_IR[3]), .OP4(ID_IR[4]), .OP5(ID_IR[5]), .OP6(ID_IR[6]), .F12(ID_IR[12]),
    .F13(ID_IR[13]), .F14(ID_IR[14]), .F25(ID_IR[25]), .F30(ID_IR[30]), .R1Used(\r1r2使用检测_1_r1used ),
    .R2Used(\r1r2使用检测_1_r2used ));
  Hex_Digit_Display hex_digit_display_4 (.value(LedData[15:12]));  // open: dp
  Hex_Digit_Display hex_digit_display_5 (.value(LedData[19:16]));  // open: dp
  Adder #(.width(32)) adder_1 (.a(IF_PC), .b(32'h4), .out(IF_PC_4));  // open: cin, cout
  Hex_Digit_Display hex_digit_display_6 (.value(LedData[7:4]));  // open: dp
  Hex_Digit_Display hex_digit_display_7 (.value(LedData[11:8]));  // open: dp
  Clock #(.highDuration(1), .lowDuration(1)) clock_1 (.out(clock_1_out));
  // Probe on EX_PC[19:0]
  // RiscV_Probe riscv_probe_3: pin names not known; wires that end beside it: clock_1_out, EX_IR, CLK
  Hex_Digit_Display hex_digit_display_8 (.value(LedData[3:0]));  // open: dp
  ROM #(.addrWidth(10), .dataWidth(32), .Select("high")) rom_1 (.addr(IF_PC[11:2]), .data(IF_IR));
  // Probe on \总周期数 
  // Probe on M_PC[19:0]
  // RiscV_Probe riscv_probe_4: pin names not known; wires that end beside it: MEM_IR
  // RiscV_Probe riscv_probe_5: pin names not known; wires that end beside it: IF_IR
  // Probe on \总周期数 
  // Probe on \无条件分支数 
  // Probe on \条件分支成功数 
  // Probe on \插入气泡数 
  // Probe on \LoadUse次数 
  or or_2 (or_2_out, BranchTaken, RST);
  \数据相关检测  \u_数据相关检测_1  (
    .R1Used(\r1r2使用检测_1_r1used ), .EX_RegWrite(EX_RegWrite), .R2Used(\r1r2使用检测_1_r2used ),
    .WEW_RegWrite(MEM_RegWrite), .DataHazzard(DataHazzard), .ID_R1(ID_R1), .ID_R2(ID_R2),
    .EX_RD(EX_IR[11:7]), .WEW_RD(MEM_IR[11:7]));
  // Probe on IF_PC[11:0]
  // Probe on WB_PC[19:0]
  // RiscV_Probe riscv_probe_6: pin names not known; wires that end beside it: WB_IR
  and and_2 (and_2_out, halt, ~Go);  // AND_Gate
  or or_3 (or_3_out, DataHazzard, and_2_out);
  IF_ID if_id_1 (
    .CLK(CLK), .\RST_高电平有效 (or_2_out), .\en_低电平有效 (or_3_out), .IR(IF_IR), .PC(IF_PC), .PC_4(IF_PC_4),
    .IR_2(ID_IR), .PC_2(ID_PC), .PC_4_2(if_id_1_pc_4_2));
  // Probe on EX_PC[11:0]
  // Probe on ID_PC[11:0]
  // Probe on M_PC[11:0]
  D_Flip_Flop #(.trigger("high"), .Pre_Clr_Positions("LEGACY"), .NegatePresetClear("false"), .enable("true"), .NewFFLayout("false")) d_ff_1 (.Q(d_ff_1_q));  // open: clk, D, Qn, preset, en, reset
  // Probe on 13'hc
  \单周期硬布线控制器  \u_单周期硬布线控制器_1  (
    .Funct({ID_IR[30], ID_IR[25], ID_IR[14:12]}), .OP(ID_IR[6:2]), .ALU_OP(\单周期硬布线控制器_1_alu_op ),
    .MemToReg(\单周期硬布线控制器_1_memtoreg ), .MemWrite(\单周期硬布线控制器_1_memwrite ), .ALU_SRC(\单周期硬布线控制器_1_alu_src ),
    .RegWrite(\单周期硬布线控制器_1_regwrite ), .ecall(\单周期硬布线控制器_1_ecall ), .S_type(\单周期硬布线控制器_1_s_type ),
    .Jalr(\单周期硬布线控制器_1_jalr ), .Beq(\单周期硬布线控制器_1_beq ), .JAL(\单周期硬布线控制器_1_jal ), .Bne(\单周期硬布线控制器_1_bne ),
    .in_3(ID_IR[21]), .uret(\单周期硬布线控制器_1_uret ), .Sltiu(\单周期硬布线控制器_1_sltiu ), .Sb(\单周期硬布线控制器_1_sb ),
    .Blt(\单周期硬布线控制器_1_blt ));
  Multiplexer #(.select(1), .width(5), .disabled("Z"), .enable("false")) multiplexer_3 (
    .in0(ID_IR[19:15]), .in1(5'b10001), .out(ID_R1), .sel(\单周期硬布线控制器_1_ecall ));
  Multiplexer #(.select(1), .width(5), .disabled("Z"), .enable("false")) multiplexer_4 (
    .in0(ID_IR[24:20]), .in1(5'b01010), .out(ID_R2), .sel(\单周期硬布线控制器_1_ecall ));
  assign bit_extender_1_out = {{3{1'b0}}, Bit_Sel};  // Bit_Extender bit_extender_1
  Decoder #(.select(2), .tristate("false"), .disabled("Z"), .enable("false")) decoder_1 (
    .out0(decoder_1_out0[0]), .out1(decoder_1_out0[1]), .out2(decoder_1_out0[2]), .out3(decoder_1_out0[3]),
    .sel(Bit_Sel));
  // Probe on WB_PC[11:0]
  Comparator #(.width(13), .mode("twosComplement")) comparator_1 (
    .a(CNT_num), .b(13'hc), .eq(comparator_1_eq), .lt(comparator_1_lt));  // open: gt
  Clock #(.highDuration(1), .lowDuration(1)) clock_2 (.out(clock_2_out));
  Multiplier #(.width(5)) multiplier_1 (
    .a(bit_extender_1_out), .b(5'b01000), .out(multiplier_1_out));  // open: cin, cout
  Multiplexer #(.select(1), .width(4), .disabled("Z"), .enable("false")) multiplexer_5 (
    .in0(4'b1111), .in1(decoder_1_out0), .out(RAM_Sel), .sel(sb));
  nand nand_1 (nand_1_out, d_ff_1_q, comparator_1_eq);
  Counter #(.width(13), .max('h1fff), .ongoal("stay"), .trigger("rising"), .behavior("old")) counter_1 (
    .count(comparator_1_lt), .Q(CNT_num), .clk(clock_2_out));  // open: load, D, carry, clr, preset
  \Regifile_下降沿  \regifile_下降沿_1  (
    .Din(RDin), .Clk(CLK), .R1(ID_R1Data), .R2(\regifile_下降沿_1_r2 ), .WE(RegWrite), .W_num(WB_IR[11:7]),
    .R1_num(ID_R1), .R2_num(ID_R2));
  Shifter #(.width(32), .shift("ll")) shifter_1 (.in(MDin), .\dist (multiplier_1_out), .out(shifter_1_out));
  assign CLK = nand_1_out ? clock_2_out : 1'bz;  // Controlled_Buffer controlled_buffer_1
  and and_3 (and_3_out, halt, ~Go);  // AND_Gate
  or or_4 (or_4_out, BranchTaken, RST, DataHazzard);
  ID_EX id_ex_1 (
    .CLK(CLK), .\RST_高电平有效 (or_4_out), .\en_低电平有效 (and_3_out), .RegWrite(\单周期硬布线控制器_1_regwrite ), .IR(ID_IR),
    .AluSrcB(\单周期硬布线控制器_1_alu_src ), .AluOP(\单周期硬布线控制器_1_alu_op ), .PC(ID_PC),
    .MemWrite(\单周期硬布线控制器_1_memwrite ), .MemToReg(\单周期硬布线控制器_1_memtoreg ), .PC_4(if_id_1_pc_4_2),
    .Bne(\单周期硬布线控制器_1_bne ), .Beq(\单周期硬布线控制器_1_beq ), .R1(ID_R1Data), .JAL(\单周期硬布线控制器_1_jal ),
    .R2(\regifile_下降沿_1_r2 ), .JALR(\单周期硬布线控制器_1_jalr ), .URET(\单周期硬布线控制器_1_uret ), .Imm_I(ID_IR[31:20]),
    .RegWrite_2(EX_RegWrite), .IR_2(EX_IR), .AluSrcB_2(id_ex_1_alusrcb_2), .AluOP_2(id_ex_1_aluop_2),
    .PC_2(EX_PC), .MemWrite_2(id_ex_1_memwrite_2), .MemToReg_2(id_ex_1_memtoreg_2), .PC_4_2(id_ex_1_pc_4_2),
    .Bne_2(id_ex_1_bne_2), .Beq_2(id_ex_1_beq_2), .R1_2(EX_R1Data), .JAL_2(EX_J_signal), .R2_2(EX_R2Data),
    .JALR_2(id_ex_1_jalr_2), .Imm_I_2(id_ex_1_imm_i_2), .Sltiu(\单周期硬布线控制器_1_sltiu ),
    .Sltiu_2(id_ex_1_sltiu_2), .Sb(\单周期硬布线控制器_1_sb ), .Sb_2(id_ex_1_sb_2), .Blt(\单周期硬布线控制器_1_blt ),
    .Blt_2(id_ex_1_blt_2), .ecall(\单周期硬布线控制器_1_ecall ), .ecall_2(id_ex_1_ecall_2),
    .Imm_S({ID_IR[31:25], ID_IR[11:7]}), .Imm_S_2(id_ex_1_imm_s_2),
    .Imm_B({ID_IR[31], ID_IR[7], ID_IR[30:25], ID_IR[11:8]}), .Imm_B_2(id_ex_1_imm_b_2),
    .Imm_J({ID_IR[31], ID_IR[19:12], ID_IR[20], ID_IR[30:21]}), .Imm_J_2(id_ex_1_imm_j_2),
    .S_Type(\单周期硬布线控制器_1_s_type ), .S_Type_2(EX_S_signal));  // open: URET_2
  Multiplexer #(.select(1), .width(32), .disabled("Z"), .enable("false")) multiplexer_6 (
    .in0(MDin), .in1(shifter_1_out), .out(MemData), .sel(sb));
  Pull_Resistor #(.pull(1)) pull_resistor_1 (.node(CLK));
  or or_5 (\无条件分支 , id_ex_1_jalr_2, EX_J_signal);
  or or_6 (EX_B_signal, id_ex_1_beq_2, id_ex_1_bne_2, id_ex_1_blt_2);
  assign bit_extender_2_out = {{20{id_ex_1_imm_i_2[11]}}, id_ex_1_imm_i_2};  // Bit_Extender bit_extender_2
  assign bit_extender_3_out = {{20{1'b0}}, id_ex_1_imm_i_2};  // Bit_Extender bit_extender_3
  assign bit_extender_4_out = {{20{id_ex_1_imm_s_2[11]}}, id_ex_1_imm_s_2};  // Bit_Extender bit_extender_4
  assign bit_extender_5_out = {{20{id_ex_1_imm_b_2[11]}}, id_ex_1_imm_b_2};  // Bit_Extender bit_extender_5
  assign bit_extender_6_out = {{12{id_ex_1_imm_j_2[19]}}, id_ex_1_imm_j_2};  // Bit_Extender bit_extender_6
  Counter #(.width(16), .max('hffff), .ongoal("wrap"), .trigger("rising"), .behavior("new")) counter_2 (
    .count(\无条件分支 ), .Q(\无条件分支数 ), .clk(CLK), .clr(RST));  // open: load, D, carry, preset, down
  Multiplexer #(.select(1), .width(32), .disabled("Z"), .enable("false")) multiplexer_7 (
    .in0(bit_extender_2_out), .in1(bit_extender_3_out), .out(multiplexer_7_out), .sel(id_ex_1_sltiu_2));
  Multiplexer #(.select(1), .width(32), .disabled("Z"), .enable("false")) multiplexer_8 (
    .in0(EX_R2Data), .in1(multiplexer_9_out), .out(multiplexer_8_out), .sel(id_ex_1_alusrcb_2));
  Multiplexer #(.select(2), .width(32), .disabled("Z"), .enable("false")) multiplexer_9 (
    .in0(multiplexer_7_out), .in1(bit_extender_4_out), .in2(bit_extender_5_out), .in3(bit_extender_6_out),
    .out(multiplexer_9_out), .sel(EX_Imm_Sel));
  ALU alu_1 (
    .X(EX_R1Data), .Y(multiplexer_8_out), .AluOP(id_ex_1_aluop_2), .Equal(alu_1_equal), .Result(EX_AluData),
    .out_6(alu_1_out_6));  // open: Result_2, out_4
  Shifter #(.width(32), .shift("ll")) shifter_2 (.in(multiplexer_9_out), .\dist (5'b00001), .out(shifter_2_out));
  Counter #(.width(16), .max('hffff), .ongoal("wrap"), .trigger("rising"), .behavior("new")) counter_3 (
    .count(B_Jump), .Q(\条件分支成功数 ), .clk(CLK), .clr(RST));  // open: load, D, carry, preset, down
  and and_4 (and_4_out, id_ex_1_beq_2, alu_1_equal);
  and and_5 (and_5_out, id_ex_1_bne_2, ~alu_1_equal);  // AND_Gate
  or or_7 (B_Jump, and_4_out, and_5_out, and_6_out);
  and and_6 (and_6_out, id_ex_1_blt_2, alu_1_out_6);
  Adder #(.width(32)) adder_2 (.a(EX_PC), .b(shifter_2_out), .out(adder_2_out));  // open: cin, cout
  or or_8 (BranchTaken, id_ex_1_jalr_2, B_Jump, EX_J_signal);
  or or_9 (or_9_out, BranchTaken, DataHazzard);
  and and_7 (and_7_out, halt, ~Go);  // AND_Gate
  EX_MEM ex_mem_1 (
    .CLK(CLK), .\RST_高电平有效 (RST), .\en_低电平有效 (and_7_out), .RegWrite(EX_RegWrite),
    .MemWrite(id_ex_1_memwrite_2), .IR(EX_IR), .MemToReg(id_ex_1_memtoreg_2), .JAL(EX_J_signal), .PC(EX_PC),
    .JALR(id_ex_1_jalr_2), .PC_4(id_ex_1_pc_4_2), .ecall(id_ex_1_ecall_2), .R1(EX_R1Data), .Sb(id_ex_1_sb_2),
    .R2(EX_R2Data), .AluData(EX_AluData), .RegWrite_2(MEM_RegWrite), .MemWrite_2(MemWrite), .IR_2(MEM_IR),
    .MemToReg_2(ex_mem_1_memtoreg_2), .JAL_2(ex_mem_1_jal_2), .PC_2(M_PC), .JALR_2(ex_mem_1_jalr_2),
    .PC_4_2(ex_mem_1_pc_4_2), .ecall_2(ex_mem_1_ecall_2), .R1_2(MEM_R1Data), .Sb_2(sb), .R2_2(MDin),
    .AluData_2({ex_mem_1_aludata_2, Bit_Sel}));
  Counter #(.width(16), .max('hffff), .ongoal("wrap"), .trigger("rising"), .behavior("new")) counter_4 (
    .load(BranchTaken), .D(adder_3_out), .count(or_9_out), .Q(\插入气泡数 ), .clk(CLK), .clr(RST));  // open: carry, preset, down
  Adder #(.width(16)) adder_3 (.a(\插入气泡数 ), .b(16'h2), .out(adder_3_out));  // open: cin, cout
  // cs3410_MIPS_RAM mips_ram_1: pin names not known; wires that end beside it: ex_mem_1_aludata_2[21:2], MemData, MemWrite, RAM_Sel, CLK, mips_ram_1_p6, RST, RST, mips_ram_1_p9
  not not_3 (mips_ram_1_p6, MemWrite);
  and and_8 (and_8_out, halt, ~Go);  // AND_Gate
  MEM_WB mem_wb_1 (
    .CLK(CLK), .\RST_高电平有效 (RST), .\en_低电平有效 (and_8_out), .RegWrite(MEM_RegWrite), .IR(MEM_IR),
    .MemToReg(ex_mem_1_memtoreg_2), .JAL(ex_mem_1_jal_2), .PC(M_PC), .JALR(ex_mem_1_jalr_2),
    .PC_4(ex_mem_1_pc_4_2), .ecall(ex_mem_1_ecall_2), .R1(MEM_R1Data), .R2(MDin),
    .AluData({ex_mem_1_aludata_2, Bit_Sel}), .MemData(mips_ram_1_p9), .RegWrite_2(RegWrite), .IR_2(WB_IR),
    .MemToReg_2(mem_wb_1_memtoreg_2), .JAL_2(mem_wb_1_jal_2), .PC_2(WB_PC), .JALR_2(mem_wb_1_jalr_2),
    .PC_4_2(WB_PC_4), .ecall_2(ecall), .R1_2(WB_R1Data), .R2_2(WB_R2Data), .AluData_2(mem_wb_1_aludata_2),
    .MemData_2(mem_wb_1_memdata_2));
  Multiplexer #(.select(1), .width(32), .disabled("Z"), .enable("false")) multiplexer_10 (
    .in0(mem_wb_1_aludata_2), .in1(mem_wb_1_memdata_2), .out(multiplexer_10_out), .sel(mem_wb_1_memtoreg_2));
  or or_10 (or_10_out, mem_wb_1_jalr_2, mem_wb_1_jal_2);
  Multiplexer #(.select(1), .width(32), .disabled("Z"), .enable("false")) multiplexer_11 (
    .in0(multiplexer_10_out), .in1(WB_PC_4), .out(RDin), .sel(or_10_out));
  not not_4 (not_4_out, halt);
  or or_11 (or_11_out, EX_B_signal, EX_J_signal);
  or or_12 (or_12_out, EX_J_signal, EX_S_signal);
  assign not_5_out = ~32'h1;  // NOT_Gate not_5, 32 bits wide
  Comparator #(.width(32), .mode("unsigned")) comparator_2 (
    .a(WB_R1Data), .b(32'h22), .eq(comparator_2_eq));  // open: gt, lt
  Register #(.width(32), .trigger("rising"), .Select("low")) register_1 (
    .D(WB_R2Data), .en(Ledout), .Q(LedData), .clk(CLK), .clr(RST));
  Counter #(.width(16), .max('hffff), .ongoal("stay"), .trigger("rising"), .behavior("old")) counter_5 (
    .count(not_4_out), .Q(\总周期数 ), .clk(CLK));  // open: load, D, carry, clr, preset
  and and_9 (EX_Imm_Sel[1], ~EX_S_signal, or_11_out);  // AND_Gate
  and and_10 (EX_Imm_Sel[0], or_12_out, ~EX_B_signal);  // AND_Gate
  assign EX_JalrData = EX_AluData & not_5_out;  // AND_Gate and_11, 32 bits wide
  and and_12 (and_12_out, ecall, ~comparator_2_eq);  // AND_Gate
  and and_13 (Ledout, comparator_2_eq, ecall);
  D_Flip_Flop #(.trigger("falling"), .Pre_Clr_Positions("ABOVE_BELOW"), .NegatePresetClear("false"), .enable("true"), .NewFFLayout("true")) d_ff_2 (
    .clk(CLK), .D(and_12_out), .Q(halt), .en(ecall), .reset(Go));  // open: Qn, preset

  // Other names for the same wires on the sheet: MEM_PC[31:0] = M_PC; MEM_R2Data[31:0] = MDin

  // Notes on the sheet:
  //   中断源
  //   时空图监测，可删除
  //   中断等待指示
  //   rd
  //   rd
  //   数码管输出
  //   指令存储器
  //   生成DataHazzard信号
  //   contents of rom_1 (hex, n*v repeats v):
  //   100493 100006f 100493 200913 300993 100006f 100493 200913 300993 100006f 100493 200913 300993
  //   100006f 100493 200913 300993 29c000ef 100413 100493 1f49493 900533 2200893 73 24d493 48463 fedff06f
  //   900533 2200893 73 100493 249493 900533 2200893 73 48463 fedff06f 100493 1f49493 900533 2200893 73
  //   4034d493 900533 2200893 73 4044d493 900533 2200893 73 4044d493 900533 2200893 73 4044d493 900533
  //   2200893 73 4044d493 900533 2200893 73 4044d493 900533 2200893 73 4044d493 900533 2200893 73 4044d493
  //   900533 2200893 73 100413 1f41993 41f9d993 433 c00913 300b13 140413 f47413 800293 100313 499993
  //   89e9b3 1300533 2200893 73 406282b3 fe0294e3 140413 f00f93 1f47433 1c41413 800293 100313 49d993
  //   89e9b3 1300533 2200893 73 406282b3 fe0294e3 1c45413 406b0b33 b0463 f95ff06f 2b3 fff2c293 829293
  //   ff2e293 500533 2200893 73 fff00413 493 84a023 140413 448493 84a023 140413 448493 84a023 140413
  //   448493 84a023 140413 448493 84a023 140413 448493 84a023 140413 448493 84a023 140413 448493 84a023
  //   140413 448493 84a023 140413 448493 84a023 140413 448493 84a023 140413 448493 84a023 140413 448493
  //   84a023 140413 448493 84a023 140413 448493 84a023 140413 448493 84a023 140413 448493 140413 433
  //   3c00493 42983 4aa03 149a2b3 28663 134a023 1442023 ffc48493 fe9412e3 800533 2200893 73 440413 3c00493
  //   fc9416e3 a00893 73 413 140413 800533 2200893 73 240413 800533 2200893 73 340413 800533 2200893 73
  //   440413 800533 2200893 73 540413 800533 2200893 73 640413 800533 2200893 73 740413 800533 2200893 73
  //   840413 800533 2200893 2200893 73 8067
  //   指令探针
  //   控制位
  //   JAL
  //   JALR
  //   URET
  //   Sltiu
  //   Sb
  //   rs1
  //   rs2
  //   流水调试日志用
  //   暂停节拍，不能为0
  //   Beq
  //   Bne
  //   MemToReg
  //   MemWrite
  //   AluOP
  //   AluSrcB
  //   RegWrite
  //   Blt
  //   I型指令立即数
  //   S型指令立即数
  //   B型指令立即数
  //   J型指令立即数
  //   戳工具置1进入计数暂停模式，ctrl+k时钟自动运行到对应节拍暂停
  //   ctrl+k关闭时钟连续运行，将控制位置零，进入单步调试模式调试
  //   计算Sb对应的MemData
  //   可计数暂停的时钟源
  //   为方便自动评测，需要输出流水线各段保存的PC值，注意是PC不是PC+4，另外ID段寄存器写入信息，Mem段内存写入信息也要输出
  //   rd
  //   EX阶段 生成立即数选择信号
  //   计算jalr对应的PC
  //   LedData显示控制
  //   周期信号显示控制
  //   生成停机信号halt和LED显示信号Ledout
endmodule

module \重定向流水线  (
  output RegWrite,
  output MemWrite,
  output [31:0] IF_PC,
  output [31:0] ID_PC,
  output [31:0] EX_PC,
  output [31:0] M_PC,
  output [31:0] WB_PC,
  output [31:0] RDin,
  output [31:0] MDin,
  output [31:0] LedData
);

  wire alu_1_equal, alu_1_out_6, and_1_out, and_2_out, and_3_out, and_4_out, and_5_out, and_6_out, and_7_out,
       and_8_out, and_11_out, B_Jump, BranchTaken, CLK, clock_1_out, clock_2_out, comparator_1_eq,
       comparator_1_lt, comparator_2_eq, d_ff_1_q, ecall, EX_B_signal, EX_J_signal, ex_mem_1_ecall_2,
       ex_mem_1_jal_2, ex_mem_1_jalr_2, ex_mem_1_memtoreg_2, EX_MemToReg, EX_RegWrite, EX_S_signal, Go, halt,
       \id_ex_重定向_1_alusrcb_2 , \id_ex_重定向_1_beq_2 , \id_ex_重定向_1_blt_2 , \id_ex_重定向_1_bne_2 ,
       \id_ex_重定向_1_ecall_2 , \id_ex_重定向_1_jalr_2 , \id_ex_重定向_1_memwrite_2 , \id_ex_重定向_1_sb_2 ,
       \id_ex_重定向_1_sltiu_2 , IR1, IR2, IR3, Ledout, LoadUse, MEM_RegWrite, mem_wb_1_jal_2, mem_wb_1_jalr_2,
       mem_wb_1_memtoreg_2, mips_ram_1_p6, nand_1_out, not_1_out, not_2_out, not_4_out, or_1_out, or_2_out,
       or_3_out, or_4_out, or_9_out, or_10_out, or_11_out, or_12_out, \r1r2使用检测_1_r1used ,
       \r1r2使用检测_1_r2used , \r1r2使用检测_2_r1used , \r1r2使用检测_2_r2used , RST, sb, W1, W2, W3,
       \单周期硬布线控制器_1_alu_src , \单周期硬布线控制器_1_beq , \单周期硬布线控制器_1_blt , \单周期硬布线控制器_1_bne , \单周期硬布线控制器_1_ecall ,
       \单周期硬布线控制器_1_jal , \单周期硬布线控制器_1_jalr , \单周期硬布线控制器_1_memtoreg , \单周期硬布线控制器_1_memwrite ,
       \单周期硬布线控制器_1_regwrite , \单周期硬布线控制器_1_s_type , \单周期硬布线控制器_1_sb , \单周期硬布线控制器_1_sltiu ,
       \单周期硬布线控制器_1_uret , \无条件分支 ;
  wire [1:0] Bit_Sel, EX_Imm_Sel, EX_R1_F, EX_R2_F, ID_R1_F, ID_R2_F;
  wire [3:0] decoder_1_out0, \id_ex_重定向_1_aluop_2 , RAM_Sel, \单周期硬布线控制器_1_alu_op ;
  wire [4:0] bit_extender_6_out, ID_R1, ID_R2, multiplier_1_out;
  wire [11:0] \id_ex_重定向_1_imm_b_2 , \id_ex_重定向_1_imm_i_2 , \id_ex_重定向_1_imm_s_2 ;
  wire [12:0] CNT_num;
  wire [15:0] adder_3_out, \LoadUse次数 , \总周期数 , \插入气泡数 , \无条件分支数 , \条件分支成功数 ;
  wire [19:0] \id_ex_重定向_1_imm_j_2 ;
  wire [31:0] adder_2_out, bit_extender_1_out, bit_extender_2_out, bit_extender_3_out, bit_extender_4_out,
       bit_extender_5_out, EX_AluData, EX_IR, ex_mem_1_pc_4_2, EX_R1Data, EX_R2Data, \id_ex_重定向_1_pc_4_2 ,
       ID_IR, ID_R1Data, if_id_1_pc_4_2, IF_IR, IF_PC_4, MEM_IR, MEM_R1Data, mem_wb_1_aludata_2,
       mem_wb_1_memdata_2, MemData, mips_ram_1_p8, multiplexer_1_out, multiplexer_2_out, multiplexer_5_out,
       multiplexer_6_out, multiplexer_7_out, multiplexer_11_out, \regifile_下降沿_1_r2 , RelocationR1Data,
       RelocationR2Data, shifter_1_out, shifter_2_out, WB_IR, WB_PC_4, WB_R1Data, WB_R2Data;
  wire [31:2] MEM_AluData;

  Button \u_总复位  (.out(RST));
  Button _1 (.out(IR1));
  Button _2 (.out(IR2));
  Button _3 (.out(IR3));
  // Probe on \总周期数 
  // Probe on \总周期数 
  Button \u_继续运行  (.out(Go));
  LED #(.active("true")) led_1 (.in(W1));
  LED #(.active("true")) led_2 (.in(W2));
  LED #(.active("true")) led_3 (.in(W3));
  or or_1 (or_1_out, B_Jump, EX_J_signal);
  Hex_Digit_Display hex_digit_display_1 (.value(LedData[31:28]));  // open: dp
  // Probe on IF_PC[19:0]
  // RiscV_Probe riscv_probe_1: pin names not known; wires that end beside it: IF_IR
  Multiplexer #(.select(1), .width(32), .disabled("Z"), .enable("false")) multiplexer_1 (
    .in0(IF_PC_4), .in1(adder_2_out), .out(multiplexer_1_out), .sel(or_1_out));
  Multiplexer #(.select(1), .width(32), .disabled("Z"), .enable("false")) multiplexer_2 (
    .in0(multiplexer_1_out), .in1(EX_AluData), .out(multiplexer_2_out), .sel(\id_ex_重定向_1_jalr_2 ));
  and and_1 (and_1_out, not_1_out, not_2_out);
  not not_1 (not_1_out, LoadUse);
  Hex_Digit_Display hex_digit_display_2 (.value(LedData[23:20]));  // open: dp
  Hex_Digit_Display hex_digit_display_3 (.value(LedData[27:24]));  // open: dp
  // Probe on ID_PC[19:0]
  // RiscV_Probe riscv_probe_2: pin names not known; wires that end beside it: ID_IR
  Register #(.width(32), .trigger("rising"), .Select("low")) PC (
    .D(multiplexer_2_out), .en(and_1_out), .Q(IF_PC), .clk(CLK), .clr(RST));
  not not_2 (not_2_out, halt);
  \R1R2使用检测  \r1r2使用检测_1  (
    .OP2(ID_IR[2]), .OP3(ID_IR[3]), .OP4(ID_IR[4]), .OP5(ID_IR[5]), .OP6(ID_IR[6]), .F12(ID_IR[12]),
    .F13(ID_IR[13]), .F14(ID_IR[14]), .F25(ID_IR[25]), .F30(ID_IR[30]), .R1Used(\r1r2使用检测_1_r1used ),
    .R2Used(\r1r2使用检测_1_r2used ));
  Hex_Digit_Display hex_digit_display_4 (.value(LedData[19:16]));  // open: dp
  Hex_Digit_Display hex_digit_display_5 (.value(LedData[15:12]));  // open: dp
  Adder #(.width(32)) adder_1 (.a(IF_PC), .b(32'h4), .out(IF_PC_4));  // open: cin, cout
  Hex_Digit_Display hex_digit_display_6 (.value(LedData[11:8]));  // open: dp
  Hex_Digit_Display hex_digit_display_7 (.value(LedData[7:4]));  // open: dp
  Clock #(.highDuration(1), .lowDuration(1)) clock_1 (.out(clock_1_out));
  // Probe on EX_PC[19:0]
  // RiscV_Probe riscv_probe_3: pin names not known; wires that end beside it: clock_1_out, EX_IR, CLK
  Hex_Digit_Display hex_digit_display_8 (.value(LedData[3:0]));  // open: dp
  ROM #(.addrWidth(10), .dataWidth(32), .Select("high")) rom_1 (.addr(IF_PC[11:2]), .data(IF_IR));
  // Probe on \总周期数 
  // Probe on M_PC[19:0]
  // RiscV_Probe riscv_probe_4: pin names not known; wires that end beside it: MEM_IR
  // RiscV_Probe riscv_probe_5: pin names not known; wires that end beside it: IF_IR
  \LoadUse信号生成  \loaduse信号生成_1  (
    .R1Used(\r1r2使用检测_1_r1used ), .EX_MemToReg(EX_MemToReg), .ID_R1(ID_R1), .EX_RD(EX_IR[11:7]),
    .ID_R2(ID_R2), .R2Used(\r1r2使用检测_1_r2used ), .LoadUse(LoadUse));
  // Probe on \总周期数 
  // Probe on \无条件分支数 
  // Probe on \条件分支成功数 
  // Probe on \插入气泡数 
  // Probe on \LoadUse次数 
  or or_2 (or_2_out, BranchTaken, RST);
  // Probe on IF_PC[11:0]
  // Probe on WB_PC[19:0]
  // RiscV_Probe riscv_probe_6: pin names not known; wires that end beside it: WB_IR
  and and_2 (and_2_out, halt, ~Go);  // AND_Gate
  or or_3 (or_3_out, LoadUse, and_2_out);
  IF_ID if_id_1 (
    .CLK(CLK), .\RST_高电平有效 (or_2_out), .\en_低电平有效 (or_3_out), .IR(IF_IR), .PC(IF_PC), .PC_4(IF_PC_4),
    .IR_2(ID_IR), .PC_2(ID_PC), .PC_4_2(if_id_1_pc_4_2));
  // Probe on ID_PC[11:0]
  // Probe on EX_PC[11:0]
  // Probe on M_PC[11:0]
  D_Flip_Flop #(.trigger("high"), .Pre_Clr_Positions("LEGACY"), .NegatePresetClear("false"), .enable("true"), .NewFFLayout("false")) d_ff_1 (.Q(d_ff_1_q));  // open: clk, D, Qn, preset, en, reset
  // Probe on 13'hc
  \单周期硬布线控制器  \u_单周期硬布线控制器_1  (
    .Funct({ID_IR[30], ID_IR[25], ID_IR[14:12]}), .OP(ID_IR[6:2]), .ALU_OP(\单周期硬布线控制器_1_alu_op ),
    .MemToReg(\单周期硬布线控制器_1_memtoreg ), .MemWrite(\单周期硬布线控制器_1_memwrite ), .ALU_SRC(\单周期硬布线控制器_1_alu_src ),
    .RegWrite(\单周期硬布线控制器_1_regwrite ), .ecall(\单周期硬布线控制器_1_ecall ), .S_type(\单周期硬布线控制器_1_s_type ),
    .Jalr(\单周期硬布线控制器_1_jalr ), .Beq(\单周期硬布线控制器_1_beq ), .JAL(\单周期硬布线控制器_1_jal ), .Bne(\单周期硬布线控制器_1_bne ),
    .in_3(ID_IR[21]), .uret(\单周期硬布线控制器_1_uret ), .Sltiu(\单周期硬布线控制器_1_sltiu ), .Sb(\单周期硬布线控制器_1_sb ),
    .Blt(\单周期硬布线控制器_1_blt ));
  Multiplexer #(.select(1), .width(5), .disabled("Z"), .enable("false")) multiplexer_3 (
    .in0(ID_IR[19:15]), .in1(5'b10001), .out(ID_R1), .sel(\单周期硬布线控制器_1_ecall ));
  Multiplexer #(.select(1), .width(5), .disabled("Z"), .enable("false")) multiplexer_4 (
    .in0(ID_IR[24:20]), .in1(5'b01010), .out(ID_R2), .sel(\单周期硬布线控制器_1_ecall ));
  // Probe on WB_PC[11:0]
  Comparator #(.width(13), .mode("twosComplement")) comparator_1 (
    .a(CNT_num), .b(13'hc), .eq(comparator_1_eq), .lt(comparator_1_lt));  // open: gt
  Clock #(.highDuration(1), .lowDuration(1)) clock_2 (.out(clock_2_out));
  \R1R2使用检测  \r1r2使用检测_2  (
    .OP2(ID_IR[2]), .OP3(ID_IR[3]), .OP4(ID_IR[4]), .OP5(ID_IR[5]), .OP6(ID_IR[6]), .F12(ID_IR[12]),
    .F13(ID_IR[13]), .F14(ID_IR[14]), .F25(ID_IR[25]), .F30(ID_IR[30]), .R1Used(\r1r2使用检测_2_r1used ),
    .R2Used(\r1r2使用检测_2_r2used ));
  nand nand_1 (nand_1_out, d_ff_1_q, comparator_1_eq);
  Counter #(.width(13), .max('h1fff), .ongoal("stay"), .trigger("rising"), .behavior("old")) counter_1 (
    .count(comparator_1_lt), .Q(CNT_num), .clk(clock_2_out));  // open: load, D, carry, clr, preset
  \Regifile_下降沿  \regifile_下降沿_1  (
    .Din(RDin), .Clk(CLK), .R1(ID_R1Data), .R2(\regifile_下降沿_1_r2 ), .WE(RegWrite), .W_num(WB_IR[11:7]),
    .R1_num(ID_R1), .R2_num(ID_R2));
  assign CLK = nand_1_out ? clock_2_out : 1'bz;  // Controlled_Buffer controlled_buffer_1
  or or_4 (or_4_out, BranchTaken, RST, LoadUse);
  and and_3 (and_3_out, halt, ~Go);  // AND_Gate
  \ID_EX_重定向  \id_ex_重定向_1  (
    .CLK(CLK), .\RST_高电平有效 (or_4_out), .\en_低电平有效 (and_3_out), .RegWrite(\单周期硬布线控制器_1_regwrite ), .IR(ID_IR),
    .AluSrcB(\单周期硬布线控制器_1_alu_src ), .AluOP(\单周期硬布线控制器_1_alu_op ), .PC(ID_PC),
    .MemWrite(\单周期硬布线控制器_1_memwrite ), .PC_4(if_id_1_pc_4_2), .MemToReg(\单周期硬布线控制器_1_memtoreg ),
    .R1(ID_R1Data), .Bne(\单周期硬布线控制器_1_bne ), .R2(\regifile_下降沿_1_r2 ), .Beq(\单周期硬布线控制器_1_beq ),
    .JAL(\单周期硬布线控制器_1_jal ), .Imm_I(ID_IR[31:20]), .Imm_S({ID_IR[31:25], ID_IR[11:7]}),
    .JALR(\单周期硬布线控制器_1_jalr ), .Imm_B({ID_IR[31], ID_IR[7], ID_IR[30:25], ID_IR[11:8]}),
    .URET(\单周期硬布线控制器_1_uret ), .Imm_J({ID_IR[31], ID_IR[19:12], ID_IR[20], ID_IR[30:21]}),
    .ecall(\单周期硬布线控制器_1_ecall ), .Sltiu(\单周期硬布线控制器_1_sltiu ), .Sb(\单周期硬布线控制器_1_sb ), .Blt(\单周期硬布线控制器_1_blt ),
    .S_Type(\单周期硬布线控制器_1_s_type ), .R1_F(ID_R1_F), .R2_F(ID_R2_F), .RegWrite_2(EX_RegWrite), .IR_2(EX_IR),
    .AluSrcB_2(\id_ex_重定向_1_alusrcb_2 ), .AluOP_2(\id_ex_重定向_1_aluop_2 ), .PC_2(EX_PC),
    .MemWrite_2(\id_ex_重定向_1_memwrite_2 ), .PC_4_2(\id_ex_重定向_1_pc_4_2 ), .MemToReg_2(EX_MemToReg),
    .R1_2(EX_R1Data), .Bne_2(\id_ex_重定向_1_bne_2 ), .R2_2(EX_R2Data), .Beq_2(\id_ex_重定向_1_beq_2 ),
    .JAL_2(EX_J_signal), .Imm_I_2(\id_ex_重定向_1_imm_i_2 ), .Imm_S_2(\id_ex_重定向_1_imm_s_2 ),
    .JALR_2(\id_ex_重定向_1_jalr_2 ), .Imm_B_2(\id_ex_重定向_1_imm_b_2 ), .Imm_J_2(\id_ex_重定向_1_imm_j_2 ),
    .ecall_2(\id_ex_重定向_1_ecall_2 ), .Sltiu_2(\id_ex_重定向_1_sltiu_2 ), .Sb_2(\id_ex_重定向_1_sb_2 ),
    .Blt_2(\id_ex_重定向_1_blt_2 ), .S_Type_2(EX_S_signal), .R1_F_2(EX_R1_F), .R2_F_2(EX_R2_F));  // open: URET_2
  Pull_Resistor #(.pull(1)) pull_resistor_1 (.node(CLK));
  or or_5 (\无条件分支 , \id_ex_重定向_1_jalr_2 , EX_J_signal);
  \R1_F_R2_F信号生成  \r1_f_r2_f信号生成_1  (
    .R1Used(\r1r2使用检测_2_r1used ), .ID_R1(ID_R1), .EX_RegWrite(EX_RegWrite), .EX_RD(EX_IR[11:7]),
    .MEM_RegWrite(MEM_RegWrite), .MEM_RD(MEM_IR[11:7]), .R2Used(\r1r2使用检测_2_r2used ), .ID_R2(ID_R2),
    .R1_F(ID_R1_F), .R2_F(ID_R2_F));
  or or_6 (EX_B_signal, \id_ex_重定向_1_beq_2 , \id_ex_重定向_1_bne_2 , \id_ex_重定向_1_blt_2 );
  assign bit_extender_1_out = {{20{\id_ex_重定向_1_imm_i_2 [11]}}, \id_ex_重定向_1_imm_i_2 };  // Bit_Extender bit_extender_1
  assign bit_extender_2_out = {{20{1'b0}}, \id_ex_重定向_1_imm_i_2 };  // Bit_Extender bit_extender_2
  assign bit_extender_3_out = {{20{\id_ex_重定向_1_imm_s_2 [11]}}, \id_ex_重定向_1_imm_s_2 };  // Bit_Extender bit_extender_3
  assign bit_extender_4_out = {{20{\id_ex_重定向_1_imm_b_2 [11]}}, \id_ex_重定向_1_imm_b_2 };  // Bit_Extender bit_extender_4
  assign bit_extender_5_out = {{12{\id_ex_重定向_1_imm_j_2 [19]}}, \id_ex_重定向_1_imm_j_2 };  // Bit_Extender bit_extender_5
  Counter #(.width(16), .max('hffff), .ongoal("wrap"), .trigger("rising"), .behavior("new")) counter_2 (
    .count(\无条件分支 ), .Q(\无条件分支数 ), .clk(CLK), .clr(RST));  // open: load, D, carry, preset, down
  Multiplexer #(.select(1), .width(32), .disabled("Z"), .enable("false")) multiplexer_5 (
    .in0(bit_extender_1_out), .in1(bit_extender_2_out), .out(multiplexer_5_out), .sel(\id_ex_重定向_1_sltiu_2 ));
  Multiplexer #(.select(1), .width(32), .disabled("Z"), .enable("false")) multiplexer_6 (
    .in0(RelocationR2Data), .in1(multiplexer_7_out), .out(multiplexer_6_out), .sel(\id_ex_重定向_1_alusrcb_2 ));
  Multiplexer #(.select(2), .width(32), .disabled("Z"), .enable("false")) multiplexer_7 (
    .in0(multiplexer_5_out), .in1(bit_extender_3_out), .in2(bit_extender_4_out), .in3(bit_extender_5_out),
    .out(multiplexer_7_out), .sel(EX_Imm_Sel));
  ALU alu_1 (
    .X(RelocationR1Data), .Y(multiplexer_6_out), .AluOP(\id_ex_重定向_1_aluop_2 ), .Equal(alu_1_equal),
    .Result(EX_AluData), .out_6(alu_1_out_6));  // open: Result_2, out_4
  Shifter #(.width(32), .shift("ll")) shifter_1 (.in(multiplexer_7_out), .\dist (5'b00001), .out(shifter_1_out));
  Counter #(.width(16), .max('hffff), .ongoal("wrap"), .trigger("rising"), .behavior("new")) counter_3 (
    .count(B_Jump), .Q(\条件分支成功数 ), .clk(CLK), .clr(RST));  // open: load, D, carry, preset, down
  and and_4 (and_4_out, \id_ex_重定向_1_beq_2 , alu_1_equal);
  and and_5 (and_5_out, \id_ex_重定向_1_bne_2 , ~alu_1_equal);  // AND_Gate
  or or_7 (B_Jump, and_4_out, and_5_out, and_6_out);
  and and_6 (and_6_out, \id_ex_重定向_1_blt_2 , alu_1_out_6);
  Adder #(.width(32)) adder_2 (.a(EX_PC), .b(shifter_1_out), .out(adder_2_out));  // open: cin, cout
  or or_8 (BranchTaken, \id_ex_重定向_1_jalr_2 , B_Jump, EX_J_signal);
  Multiplexer #(.select(2), .width(32), .disabled("Z"), .enable("false")) multiplexer_8 (
    .in0(EX_R1Data), .in1(RDin), .in2({MEM_AluData, Bit_Sel}), .out(RelocationR1Data), .sel(EX_R1_F));  // open: in3
  Multiplexer #(.select(2), .width(32), .disabled("Z"), .enable("false")) multiplexer_9 (
    .in0(EX_R2Data), .in1(RDin), .in2({MEM_AluData, Bit_Sel}), .out(RelocationR2Data), .sel(EX_R2_F));  // open: in3
  or or_9 (or_9_out, BranchTaken, LoadUse);
  and and_7 (and_7_out, halt, ~Go);  // AND_Gate
  EX_MEM ex_mem_1 (
    .CLK(CLK), .\RST_高电平有效 (RST), .\en_低电平有效 (and_7_out), .RegWrite(EX_RegWrite),
    .MemWrite(\id_ex_重定向_1_memwrite_2 ), .IR(EX_IR), .MemToReg(EX_MemToReg), .JAL(EX_J_signal), .PC(EX_PC),
    .JALR(\id_ex_重定向_1_jalr_2 ), .PC_4(\id_ex_重定向_1_pc_4_2 ), .ecall(\id_ex_重定向_1_ecall_2 ),
    .R1(RelocationR1Data), .Sb(\id_ex_重定向_1_sb_2 ), .R2(RelocationR2Data), .AluData(EX_AluData),
    .RegWrite_2(MEM_RegWrite), .MemWrite_2(MemWrite), .IR_2(MEM_IR), .MemToReg_2(ex_mem_1_memtoreg_2),
    .JAL_2(ex_mem_1_jal_2), .PC_2(M_PC), .JALR_2(ex_mem_1_jalr_2), .PC_4_2(ex_mem_1_pc_4_2),
    .ecall_2(ex_mem_1_ecall_2), .R1_2(MEM_R1Data), .Sb_2(sb), .R2_2(MDin), .AluData_2({MEM_AluData, Bit_Sel}));
  Counter #(.width(16), .max('hffff), .ongoal("wrap"), .trigger("rising"), .behavior("new")) counter_4 (
    .load(BranchTaken), .D(adder_3_out), .count(or_9_out), .Q(\插入气泡数 ), .clk(CLK), .clr(RST));  // open: carry, preset, down
  Adder #(.width(16)) adder_3 (.a(\插入气泡数 ), .b(16'h2), .out(adder_3_out));  // open: cin, cout
  // cs3410_MIPS_RAM mips_ram_1: pin names not known; wires that end beside it: MEM_AluData[21:2], MemData, MemWrite, RAM_Sel, CLK, mips_ram_1_p6, RST, mips_ram_1_p8
  not not_3 (mips_ram_1_p6, MemWrite);
  Decoder #(.select(2), .tristate("false"), .disabled("Z"), .enable("false")) decoder_1 (
    .out0(decoder_1_out0[0]), .out1(decoder_1_out0[1]), .out2(decoder_1_out0[2]), .out3(decoder_1_out0[3]),
    .sel(Bit_Sel));
  Counter #(.width(16), .max('hffff), .ongoal("wrap"), .trigger("rising"), .behavior("new")) counter_5 (
    .count(LoadUse), .Q(\LoadUse次数 ), .clk(CLK), .clr(RST));  // open: load, D, carry, preset, down
  assign bit_extender_6_out = {{3{1'b0}}, Bit_Sel};  // Bit_Extender bit_extender_6
  Multiplier #(.width(5)) multiplier_1 (
    .a(bit_extender_6_out), .b(5'b01000), .out(multiplier_1_out));  // open: cin, cout
  Multiplexer #(.select(1), .width(4), .disabled("Z"), .enable("false")) multiplexer_10 (
    .in0(4'b1111), .in1(decoder_1_out0), .out(RAM_Sel), .sel(sb));
  and and_8 (and_8_out, halt, ~Go);  // AND_Gate
  MEM_WB mem_wb_1 (
    .CLK(CLK), .\RST_高电平有效 (RST), .\en_低电平有效 (and_8_out), .RegWrite(MEM_RegWrite), .IR(MEM_IR),
    .MemToReg(ex_mem_1_memtoreg_2), .JAL(ex_mem_1_jal_2), .PC(M_PC), .JALR(ex_mem_1_jalr_2),
    .PC_4(ex_mem_1_pc_4_2), .ecall(ex_mem_1_ecall_2), .R1(MEM_R1Data), .R2(MDin),
    .AluData({MEM_AluData, Bit_Sel}), .MemData(mips_ram_1_p8), .RegWrite_2(RegWrite), .IR_2(WB_IR),
    .MemToReg_2(mem_wb_1_memtoreg_2), .JAL_2(mem_wb_1_jal_2), .PC_2(WB_PC), .JALR_2(mem_wb_1_jalr_2),
    .PC_4_2(WB_PC_4), .ecall_2(ecall), .R1_2(WB_R1Data), .R2_2(WB_R2Data), .AluData_2(mem_wb_1_aludata_2),
    .MemData_2(mem_wb_1_memdata_2));
  Shifter #(.width(32), .shift("ll")) shifter_2 (.in(MDin), .\dist (multiplier_1_out), .out(shifter_2_out));
  Multiplexer #(.select(1), .width(32), .disabled("Z"), .enable("false")) multiplexer_11 (
    .in0(mem_wb_1_aludata_2), .in1(mem_wb_1_memdata_2), .out(multiplexer_11_out), .sel(mem_wb_1_memtoreg_2));
  Multiplexer #(.select(1), .width(32), .disabled("Z"), .enable("false")) multiplexer_12 (
    .in0(MDin), .in1(shifter_2_out), .out(MemData), .sel(sb));
  or or_10 (or_10_out, mem_wb_1_jalr_2, mem_wb_1_jal_2);
  Multiplexer #(.select(1), .width(32), .disabled("Z"), .enable("false")) multiplexer_13 (
    .in0(multiplexer_11_out), .in1(WB_PC_4), .out(RDin), .sel(or_10_out));
  not not_4 (not_4_out, halt);
  or or_11 (or_11_out, EX_B_signal, EX_J_signal);
  or or_12 (or_12_out, EX_J_signal, EX_S_signal);
  Comparator #(.width(32), .mode("unsigned")) comparator_2 (
    .a(WB_R1Data), .b(32'h22), .eq(comparator_2_eq));  // open: gt, lt
  Register #(.width(32), .trigger("rising"), .Select("low")) register_1 (
    .D(WB_R2Data), .en(Ledout), .Q(LedData), .clk(CLK), .clr(RST));
  Counter #(.width(16), .max('hffff), .ongoal("stay"), .trigger("rising"), .behavior("old")) counter_6 (
    .count(not_4_out), .Q(\总周期数 ), .clk(CLK));  // open: load, D, carry, clr, preset
  and and_9 (EX_Imm_Sel[1], ~EX_S_signal, or_11_out);  // AND_Gate
  and and_10 (EX_Imm_Sel[0], or_12_out, ~EX_B_signal);  // AND_Gate
  and and_11 (and_11_out, ecall, ~comparator_2_eq);  // AND_Gate
  and and_12 (Ledout, comparator_2_eq, ecall);
  D_Flip_Flop #(.trigger("falling"), .Pre_Clr_Positions("ABOVE_BELOW"), .NegatePresetClear("false"), .enable("true"), .NewFFLayout("true")) d_ff_2 (
    .clk(CLK), .D(and_11_out), .Q(halt), .en(ecall), .reset(Go));  // open: Qn, preset

  // Other names for the same wires on the sheet: MEM_AluData[1:0] = Bit_Sel; MEM_PC[31:0] = M_PC;
  //   MEM_R2Data[31:0] = MDin

  // Notes on the sheet:
  //   中断源
  //   时空图监测，可删除
  //   中断等待指示
  //   rd
  //   数码管输出
  //   指令存储器
  //   生成LoseUse信号
  //   contents of rom_1 (hex, n*v repeats v):
  //   100493 100006f 100493 200913 300993 100006f 100493 200913 300993 100006f 100493 200913 300993
  //   100006f 100493 200913 300993 3a0000ef 100413 100493 1f49493 900533 2200893 73 24d493 48463 fedff06f
  //   900533 2200893 73 100493 249493 900533 2200893 73 48463 fedff06f 100493 1f49493 900533 2200893 73
  //   4034d493 900533 2200893 73 4044d493 900533 2200893 73 4044d493 900533 2200893 73 4044d493 900533
  //   2200893 73 4044d493 900533 2200893 73 4044d493 900533 2200893 73 4044d493 900533 2200893 73 4044d493
  //   900533 2200893 73 100413 1f41993 41f9d993 433 c00913 300b13 140413 f47413 800293 100313 499993
  //   89e9b3 1300533 2200893 73 406282b3 fe0294e3 140413 f00f93 1f47433 1c41413 800293 100313 49d993
  //   89e9b3 1300533 2200893 73 406282b3 fe0294e3 1c45413 406b0b33 b0463 f95ff06f 2b3 fff2c293 829293
  //   ff2e293 500533 2200893 73 fff00413 493 84a023 140413 448493 84a023 140413 448493 84a023 140413
  //   448493 84a023 140413 448493 84a023 140413 448493 84a023 140413 448493 84a023 140413 448493 84a023
  //   140413 448493 84a023 140413 448493 84a023 140413 448493 84a023 140413 448493 84a023 140413 448493
  //   84a023 140413 448493 84a023 140413 448493 84a023 140413 448493 84a023 140413 448493 140413 433
  //   3c00493 42983 4aa03 149a2b3 28663 134a023 1442023 ffc48493 fe9412e3 800533 2200893 73 440413 3c00493
  //   fc9416e3 3200893 73 100293 300313 800493 849493 7648493 1449493 900533 2200893 73 800e13 54d4b3
  //   64d4b3 900533 2200893 73 fffe0e13 fe0e14e3 a00893 73 fff00293 313 1900413 841413 9700493 940533
  //   2200893 73 5484b3 494b313 fe0306e3 a00893 73 313 2000e13 493 100913 930023 900533 2200893 73 12484b3
  //   130313 fffe0e13 fe0e12e3 800e13 313 32483 900533 2200893 73 430313 fffe0e13 fe0e14e3 a00893 73
  //   ff100493 900533 2200893 73 148493 fe04c8e3 a00893 73 a00893 73 413 140413 800533 2200893 73 240413
  //   800533 2200893 73 340413 800533 2200893 73 440413 800533 2200893 73 540413 800533 2200893 73 640413
  //   800533 2200893 73 740413 800533 2200893 73 840413 800533 2200893 2200893 73 8067
  //   指令探针
  //   控制位
  //   JAL
  //   JALR
  //   URET
  //   Sltiu
  //   Sb
  //   rs1
  //   rs2
  //   流水调试日志用
  //   暂停节拍，不能为0
  //   Beq
  //   Bne
  //   MemToReg
  //   MemWrite
  //   AluOP
  //   AluSrcB
  //   RegWrite
  //   Blt
  //   I型指令立即数
  //   S型指令立即数
  //   B型指令立即数
  //   J型指令立即数
  //   戳工具置1进入计数暂停模式，ctrl+k时钟自动运行到对应节拍暂停
  //   ctrl+k关闭时钟连续运行，将控制位置零，进入单步调试模式调试
  //   rd
  //   rd
  //   生成R1_F R2_F信号
  //   可计数暂停的时钟源
  //   为方便自动评测，需要输出流水线各段保存的PC值，注意是PC不是PC+4，另外ID段寄存器写入信息，Mem段内存写入信息也要输出
  //   重定向设置
  //   计算Sb对应的MemData
  //   rd
  //   EX阶段 生成立即数选择信号
  //   LedData显示控制
  //   周期信号显示控制
  //   生成停机信号halt和LED显示信号Ledout
endmodule

module \中断按键参考电路  (
  input  \同步清零信号 ,
  output \与中断屏蔽位与 
);

  wire \_1号中断_out , and_1_out, clock_1_out, d_ff_1_q, or_1_out, or_2_out;

  Clock #(.highDuration(1), .lowDuration(1)) clock_1 (.out(clock_1_out));
  Button \_1号中断  (.out(\_1号中断_out ));
  LED #(.active("true")) \_1号中断等待指示灯  (.in(or_1_out));
  or or_1 (or_1_out, \与中断屏蔽位与 , d_ff_1_q);
  D_Flip_Flop #(.trigger("rising"), .Pre_Clr_Positions("LEGACY"), .NegatePresetClear("false"), .enable("true"), .NewFFLayout("false")) d_ff_1 (
    .clk(\_1号中断_out ), .D(1'b1), .Q(d_ff_1_q), .reset(\与中断屏蔽位与 ));  // open: Qn, preset, en
  or or_2 (or_2_out, d_ff_1_q, \与中断屏蔽位与 );
  and and_1 (and_1_out, or_2_out, ~\同步清零信号 );  // AND_Gate
  D_Flip_Flop #(.trigger("rising"), .Pre_Clr_Positions("LEGACY"), .NegatePresetClear("false"), .enable("true"), .NewFFLayout("false")) IR1 (
    .clk(clock_1_out), .D(and_1_out), .Q(\与中断屏蔽位与 ));  // open: Qn, preset, en, reset

  // Notes on the sheet:
  //   中断信号采样参考电路
  //   Reset 
endmodule
module \单周期_单级中断  (
  input  IR1,
  input  IR2,
  input  IR3,
  output RegWrite,
  output MemWrite,
  output [31:0] PC,
  output [31:0] IR,
  output [31:0] RDin,
  output [31:0] MDin,
  output [31:0] LedData
);

  wire alu_1_equal, alu_1_out_6, and_3_out, and_5_out, and_7_out, and_8_out, and_9_out, B_signal, blt,
       Branch, CLK, clock_2_out, Clr1, Clr2, Clr3, comparator_1_eq, comparator_2_eq, comparator_3_eq,
       comparator_4_eq, comparator_5_eq, comparator_6_eq, comparator_6_lt, d_ff_3_q, decoder_1_out1,
       decoder_1_out2, decoder_1_out3, ecall, Go, halt, IE, INT, IR1_t, IR2_t, IR3_t, IRA, IRB, IRC,
       J_signal, Jalr_signal, Ledout, nand_1_out, not_1_out, not_2_out, not_3_out, or_1_out, or_2_out,
       or_3_out, or_4_out, or_10_out, RST, S_signal, sb, sltiu, URET, W1, W2, W3, \中断信号 ,
       \单周期硬布线控制器_1_alu_src , \单周期硬布线控制器_1_beq , \单周期硬布线控制器_1_bne , \单周期硬布线控制器_1_memtoreg ;
  wire [1:0] Imm_Sel, register_2_q, \中断号 ;
  wire [3:0] decoder_2_out0, RAM_Sel, \单周期硬布线控制器_1_alu_op ;
  wire [4:0] bit_extender_6_out, multiplexer_5_out, multiplexer_6_out, multiplier_1_out;
  wire [12:0] CNT_num;
  wire [15:0] \总周期数 ;
  wire [31:0] adder_2_out, ALU_Res, bit_extender_1_out, bit_extender_2_out, bit_extender_3_out,
       bit_extender_4_out, bit_extender_5_out, Break_PC, INT_Addar, MemData, mips_ram_1_p8,
       multiplexer_1_out, multiplexer_3_out, multiplexer_4_out, multiplexer_7_out, multiplexer_8_out,
       multiplexer_9_out, multiplexer_10_out, PC_4, R1_Data, RET_PC, shifter_1_out, shifter_2_out;

  Clock #(.highDuration(1), .lowDuration(1)) clock_1 ();  // open: out
  Button _1 ();  // open: out
  Button _2 ();  // open: out
  Button _3 ();  // open: out
  Button button_1 (.out(RST));
  Button \u_继续运行  (.out(Go));
  LED #(.active("true")) led_1 (.in(W1));
  LED #(.active("true")) led_2 (.in(W2));
  LED #(.active("true")) led_3 (.in(W3));
  or or_1 (or_1_out, Branch, J_signal);
  Multiplexer #(.select(1), .width(32), .disabled("Z"), .enable("false")) multiplexer_1 (
    .in0(PC_4), .in1(adder_2_out), .out(multiplexer_1_out), .sel(or_1_out));
  Hex_Digit_Display hex_digit_display_1 (.value(LedData[31:28]));  // open: dp
  Multiplexer #(.select(1), .width(32), .disabled("Z"), .enable("false")) multiplexer_2 (
    .in0(multiplexer_1_out), .in1(ALU_Res), .out(Break_PC), .sel(Jalr_signal));
  or or_2 (or_2_out, B_signal, J_signal);
  or or_3 (or_3_out, J_signal, S_signal);
  Hex_Digit_Display hex_digit_display_2 (.value(LedData[23:20]));  // open: dp
  Hex_Digit_Display hex_digit_display_3 (.value(LedData[27:24]));  // open: dp
  Multiplexer #(.select(1), .width(32), .disabled("Z"), .enable("false")) multiplexer_3 (
    .in0(Break_PC), .in1(RET_PC), .out(multiplexer_3_out), .sel(URET));
  Comparator #(.width(16), .mode("twosComplement")) comparator_1 (
    .a(16'h23b), .b(\总周期数 ), .eq(comparator_1_eq));  // open: gt, lt
  or or_4 (or_4_out, comparator_1_eq, comparator_2_eq);
  Comparator #(.width(16), .mode("twosComplement")) comparator_2 (
    .a(\总周期数 ), .b(16'h1), .eq(comparator_2_eq));  // open: gt, lt
  Comparator #(.width(16), .mode("twosComplement")) comparator_3 (
    .a(\总周期数 ), .b(16'h4), .eq(comparator_3_eq));  // open: gt, lt
  Comparator #(.width(16), .mode("twosComplement")) comparator_4 (
    .a(\总周期数 ), .b(16'h7), .eq(comparator_4_eq));  // open: gt, lt
  Hex_Digit_Display hex_digit_display_4 (.value(LedData[15:12]));  // open: dp
  Hex_Digit_Display hex_digit_display_5 (.value(LedData[19:16]));  // open: dp
  Multiplexer #(.select(1), .width(32), .disabled("Z"), .enable("false")) multiplexer_4 (
    .in0(multiplexer_3_out), .in1(INT_Addar), .out(multiplexer_4_out), .sel(INT));
  not not_1 (not_1_out, halt);
  and and_1 (Imm_Sel[1], ~S_signal, or_2_out);  // AND_Gate
  and and_2 (Imm_Sel[0], or_3_out, ~B_signal);  // AND_Gate
  Pull_Resistor #(.pull(0)) pull_resistor_1 (.node(IRA));
  assign IRA = or_4_out ? ~CLK : 1'bz;  // Controlled_Inverter controlled_inverter_1
  Pull_Resistor #(.pull(0)) pull_resistor_2 (.node(IRB));
  assign IRB = comparator_3_eq ? ~CLK : 1'bz;  // Controlled_Inverter controlled_inverter_2
  Pull_Resistor #(.pull(0)) pull_resistor_3 (.node(IRC));
  assign IRC = comparator_4_eq ? ~CLK : 1'bz;  // Controlled_Inverter controlled_inverter_3
  Hex_Digit_Display hex_digit_display_6 (.value(LedData[7:4]));  // open: dp
  Hex_Digit_Display hex_digit_display_7 (.value(LedData[11:8]));  // open: dp
  // Probe on \总周期数 
  Register #(.width(32), .trigger("rising"), .Select("low")) u_PC (
    .D(multiplexer_4_out), .en(not_1_out), .Q(PC), .clk(CLK), .clr(RST));
  Hex_Digit_Display hex_digit_display_8 (.value(LedData[3:0]));  // open: dp
  Adder #(.width(32)) adder_1 (.a(PC), .b(32'h4), .out(PC_4));  // open: cin, cout
  or or_5 (IR1_t, IR1, IRA);
  // RiscV_Probe riscv_probe_1: pin names not known; wires that end beside it: IR
  ROM #(.addrWidth(10), .dataWidth(32), .Select("high")) rom_1 (.addr(PC[11:2]), .data(IR));
  Comparator #(.width(32), .mode("unsigned")) comparator_5 (
    .a(R1_Data), .b(32'h22), .eq(comparator_5_eq));  // open: gt, lt
  or or_6 (IR2_t, IR2, IRB);
  and and_3 (and_3_out, ecall, ~comparator_5_eq);  // AND_Gate
  and and_4 (Ledout, comparator_5_eq, ecall);
  \中断控制器  \u_中断控制器_1  (
    .IRA(IRA), .W1(W1), .Clr1(Clr1), .IRB(IRB), .W2(W2), .Clr2(Clr2), .IRC(IRC), .W3(W3), .Clr3(Clr3),
    .\中断号 (\中断号 ), .\中断请求 (\中断信号 ), .CLK(CLK), .RST(RST));
  \单周期硬布线控制器  \u_单周期硬布线控制器_1  (
    .Funct({IR[30], IR[25], IR[14:12]}), .OP(IR[6:2]), .ALU_OP(\单周期硬布线控制器_1_alu_op ),
    .MemToReg(\单周期硬布线控制器_1_memtoreg ), .MemWrite(MemWrite), .ALU_SRC(\单周期硬布线控制器_1_alu_src ),
    .RegWrite(RegWrite), .ecall(ecall), .S_type(S_signal), .Jalr(Jalr_signal), .Beq(\单周期硬布线控制器_1_beq ),
    .JAL(J_signal), .Bne(\单周期硬布线控制器_1_bne ), .in_3(IR[21]), .uret(URET), .Sltiu(sltiu), .Sb(sb), .Blt(blt));
  Multiplexer #(.select(1), .width(5), .disabled("Z"), .enable("false")) multiplexer_5 (
    .in0(IR[19:15]), .in1(5'b10001), .out(multiplexer_5_out), .sel(ecall));
  Multiplexer #(.select(1), .width(5), .disabled("Z"), .enable("false")) multiplexer_6 (
    .in0(IR[24:20]), .in1(5'b01010), .out(multiplexer_6_out), .sel(ecall));
  D_Flip_Flop #(.trigger("falling"), .Pre_Clr_Positions("ABOVE_BELOW"), .NegatePresetClear("false"), .enable("true"), .NewFFLayout("true")) d_ff_1 (
    .clk(CLK), .D(and_3_out), .Q(halt), .en(ecall), .reset(Go));  // open: Qn, preset
  or or_7 (IR3_t, IR3, IRC);
  assign bit_extender_1_out = {{20{IR[31]}}, IR[31:20]};  // Bit_Extender bit_extender_1
  Multiplexer #(.select(1), .width(32), .disabled("Z"), .enable("false")) multiplexer_7 (
    .in0(bit_extender_1_out), .in1(bit_extender_2_out), .out(multiplexer_7_out), .sel(sltiu));
  assign bit_extender_2_out = {{20{1'b0}}, IR[31:20]};  // Bit_Extender bit_extender_2
  assign bit_extender_3_out = {{20{IR[31]}}, {IR[31:25], IR[11:7]}};  // Bit_Extender bit_extender_3
  assign bit_extender_4_out = {{20{IR[31]}}, {IR[31], IR[7], IR[30:25], IR[11:8]}};  // Bit_Extender bit_extender_4
  assign bit_extender_5_out = {{12{IR[31]}}, {IR[31], IR[19:12], IR[20], IR[30:21]}};  // Bit_Extender bit_extender_5
  or or_8 (B_signal, \单周期硬布线控制器_1_beq , blt, \单周期硬布线控制器_1_bne );
  \Regifile_上升沿  \regifile_上升沿_1  (
    .Din(RDin), .Clk(CLK), .R1(R1_Data), .R2(MDin), .WE(RegWrite), .W_num(IR[11:7]),
    .R1_num(multiplexer_5_out), .R2_num(multiplexer_6_out));
  Multiplexer #(.select(2), .width(32), .disabled("Z"), .enable("false")) multiplexer_8 (
    .in0(multiplexer_7_out), .in1(bit_extender_3_out), .in2(bit_extender_4_out), .in3(bit_extender_5_out),
    .out(multiplexer_8_out), .sel(Imm_Sel));
  and and_5 (and_5_out, ~URET, \中断信号 );  // AND_Gate
  Multiplexer #(.select(1), .width(32), .disabled("Z"), .enable("false")) multiplexer_9 (
    .in0(MDin), .in1(multiplexer_8_out), .out(multiplexer_9_out), .sel(\单周期硬布线控制器_1_alu_src ));
  Register #(.width(32), .trigger("rising"), .Select("low")) register_1 (
    .D(MDin), .en(Ledout), .Q(LedData), .clk(CLK), .clr(RST));
  D_Flip_Flop #(.trigger("rising"), .Pre_Clr_Positions("LEGACY"), .NegatePresetClear("false"), .enable("true"), .NewFFLayout("false")) d_ff_2 (
    .clk(CLK), .D(and_5_out), .Qn(IE));  // open: Q, preset, en, reset
  and and_6 (INT, IE, \中断信号 );
  ALU alu_1 (
    .X(R1_Data), .Y(multiplexer_9_out), .AluOP(\单周期硬布线控制器_1_alu_op ), .Equal(alu_1_equal), .Result(ALU_Res),
    .out_6(alu_1_out_6));  // open: Result_2, out_4
  Shifter #(.width(32), .shift("ll")) shifter_1 (.in(multiplexer_8_out), .\dist (5'b00001), .out(shifter_1_out));
  and and_7 (and_7_out, blt, alu_1_out_6);
  and and_8 (and_8_out, alu_1_equal, \单周期硬布线控制器_1_beq );
  and and_9 (and_9_out, ~alu_1_equal, \单周期硬布线控制器_1_bne );  // AND_Gate
  Adder #(.width(32)) adder_2 (.a(PC), .b(shifter_1_out), .out(adder_2_out));  // open: cin, cout
  or or_9 (Branch, and_7_out, and_8_out, and_9_out);
  not not_2 (not_2_out, halt);
  Register #(.width(2), .trigger("rising"), .Select("low")) register_2 (
    .D(\中断号 ), .en(INT), .Q(register_2_q), .clk(CLK), .clr(RST));
  D_Flip_Flop #(.trigger("high"), .Pre_Clr_Positions("LEGACY"), .NegatePresetClear("false"), .enable("true"), .NewFFLayout("false")) d_ff_3 (.Q(d_ff_3_q));  // open: clk, D, Qn, preset, en, reset
  // Probe on 13'hc
  not not_3 (not_3_out, MemWrite);
  Counter #(.width(16), .max('hffff), .ongoal("stay"), .trigger("rising"), .behavior("old")) counter_1 (
    .count(not_2_out), .Q(\总周期数 ), .clk(CLK));  // open: load, D, carry, clr, preset
  Decoder #(.select(2), .tristate("false"), .disabled("Z"), .enable("false")) decoder_1 (
    .out1(decoder_1_out1), .out2(decoder_1_out2), .out3(decoder_1_out3), .sel(register_2_q));  // open: out0
  Comparator #(.width(13), .mode("twosComplement")) comparator_6 (
    .a(CNT_num), .b(13'hc), .eq(comparator_6_eq), .lt(comparator_6_lt));  // open: gt
  Clock #(.highDuration(1), .lowDuration(1)) clock_2 (.out(clock_2_out));
  // cs3410_MIPS_RAM mips_ram_1: pin names not known; wires that end beside it: ALU_Res[21:2], MemData, MemWrite, RAM_Sel, CLK, not_3_out, RST, mips_ram_1_p8
  and and_10 (Clr1, decoder_1_out1, URET);
  and and_11 (Clr2, decoder_1_out2, URET);
  and and_12 (Clr3, decoder_1_out3, URET);
  Counter #(.width(13), .max('h1fff), .ongoal("stay"), .trigger("rising"), .behavior("old")) counter_2 (
    .count(comparator_6_lt), .Q(CNT_num), .clk(clock_2_out));  // open: load, D, carry, clr, preset
  Multiplexer #(.select(1), .width(32), .disabled("Z"), .enable("false")) multiplexer_10 (
    .in0(ALU_Res), .in1(mips_ram_1_p8), .out(multiplexer_10_out), .sel(\单周期硬布线控制器_1_memtoreg ));
  nand nand_1 (nand_1_out, d_ff_3_q, comparator_6_eq);
  or or_10 (or_10_out, J_signal, Jalr_signal);
  Multiplexer #(.select(1), .width(32), .disabled("Z"), .enable("false")) multiplexer_11 (
    .in0(multiplexer_10_out), .in1(PC_4), .out(RDin), .sel(or_10_out));
  Decoder #(.select(2), .tristate("false"), .disabled("Z"), .enable("false")) decoder_2 (
    .out0(decoder_2_out0[0]), .out1(decoder_2_out0[1]), .out2(decoder_2_out0[2]), .out3(decoder_2_out0[3]),
    .sel(ALU_Res[1:0]));
  assign CLK = nand_1_out ? clock_2_out : 1'bz;  // Controlled_Buffer controlled_buffer_1
  Pull_Resistor #(.pull(1)) pull_resistor_4 (.node(CLK));
  assign bit_extender_6_out = {{3{1'b0}}, ALU_Res[1:0]};  // Bit_Extender bit_extender_6
  Multiplier #(.width(5)) multiplier_1 (
    .a(bit_extender_6_out), .b(5'b01000), .out(multiplier_1_out));  // open: cin, cout
  Multiplexer #(.select(1), .width(4), .disabled("Z"), .enable("false")) multiplexer_12 (
    .in0(4'b1111), .in1(decoder_2_out0), .out(RAM_Sel), .sel(sb));
  Multiplexer #(.select(2), .width(32), .disabled("Z"), .enable("false")) multiplexer_13 (
    .in1(32'h30ac), .in2(32'h3150), .in3(32'h31f4), .out(INT_Addar), .sel(\中断号 ));  // open: in0
  Shifter #(.width(32), .shift("ll")) shifter_2 (.in(MDin), .\dist (multiplier_1_out), .out(shifter_2_out));
  Multiplexer #(.select(1), .width(32), .disabled("Z"), .enable("false")) multiplexer_14 (
    .in0(MDin), .in1(shifter_2_out), .out(MemData), .sel(sb));
  Register #(.width(32), .trigger("falling"), .Select("low")) EPC (
    .D(Break_PC), .en(INT), .Q(RET_PC), .clk(CLK), .clr(RST));

  // Other names for the same wires on the sheet: Bit_Sel[1:0] = ALU_Res[1:0]

  // Notes on the sheet:
  //   中断源
  //   中断等待指示
  //   总复位信号应将除ROM以外所有存储组件全部清零
  //   生成立即数选择信号
  //   单级中断测试信号模拟器
  //   数码管输出
  //   数码管输出应该用寄存器锁存，否则显示数据只能一闪而过
  //   指令存储器
  //   指令探针
  //   指令字
  //   contents of rom_1 (hex, n*v repeats v):
  //   7d000113 100413 1f41993 41f9d993 433 c00913 800b13 140413 f47413 800293 100313 499993 89e9b3 1300533
  //   2200893 73 406282b3 fe0294e3 140413 f00f93 1f47433 1c41413 800293 100313 49d993 89e9b3 1300533
  //   2200893 73 406282b3 fe0294e3 1c45413 406b0b33 b0463 f95ff06f 2b3 fff2c293 1029293 fff2e293 500533
  //   2200893 73 f5dff06f 1112023 410113 a12023 410113 812023 410113 1312023 410113 1412023 410113 1512023
  //   410113 1612023 410113 100b13 300a13 100a93 1600433 441413 14469b3 1300533 2200893 73 fe0416e3
  //   415a0a33 fe0a10e3 ffc10113 12b03 ffc10113 12a83 ffc10113 12a03 ffc10113 12983 ffc10113 12403
  //   ffc10113 12503 ffc10113 12883 200073 1112023 410113 a12023 410113 812023 410113 1312023 410113
  //   1412023 410113 1512023 410113 1612023 410113 200b13 300a13 100a93 1600433 441413 14469b3 1300533
  //   2200893 73 fe0416e3 415a0a33 fe0a10e3 ffc10113 12b03 ffc10113 12a83 ffc10113 12a03 ffc10113 12983
  //   ffc10113 12403 ffc10113 12503 ffc10113 12883 200073 1112023 410113 a12023 410113 812023 410113
  //   1312023 410113 1412023 410113 1512023 410113 1612023 410113 300b13 300a13 100a93 1600433 441413
  //   14469b3 1300533 2200893 73 fe0416e3 415a0a33 fe0a10e3 ffc10113 12b03 ffc10113 12a83 ffc10113 12a03
  //   ffc10113 12983 ffc10113 12403 ffc10113 12503 ffc10113 12883 200073
  //   I型指令立即数
  //   S型指令立即数
  //   B型指令立即数
  //   J型指令立即数
  //   生成停机信号halt和LED显示信号Ledout
  //   中断控制逻辑
  //   JAL
  //   JALR
  //   URET
  //   Sltiu
  //   Sb
  //   rs1
  //   rs2
  //   rd
  //   Beq
  //   Bne
  //   AluOP
  //   AluSrcB
  //   RegWrite
  //   Blt
  //   MemToReg
  //   MemWrite
  //   中断使能信号产生
  //   中断请求信号产生
  //   为方便自动评测，需要输出PC，IR，寄存器堆写如数据RDin
  //   LedData显示控制
  //   RAM写使能MemWrite、RAM写入数据MDin等信号
  //   控制位
  //   暂停节拍，不能为0
  //   数据存储器
  //   周期信号显示控制
  //   中断清零信号产生
  //   戳工具置1进入计数暂停模式，ctrl+k时钟自动运行到对应节拍暂停
  //   ctrl+k关闭时钟连续运行，将控制位置零，进入单步调试模式调试
  //   用这个时钟源需要去掉电路中的其他时钟源
  //   可计数暂停的时钟源
  //   中断入口逻辑
  //   计算Sb对应的MemData
  //   保护现场
endmodule

module \单周期_多级中断  (
  input  IR1,
  input  IR2,
  input  IR3,
  output RegWrite,
  output MemWrite,
  output [31:0] PC,
  output [31:0] IR,
  output [31:0] RDin,
  output [31:0] MDin,
  output [31:0] LedData
);

  wire alu_1_equal, alu_1_out_6, and_5_out, and_7_out, and_8_out, and_9_out, and_10_out, and_14_out,
       and_15_out, and_16_out, and_17_out, and_18_out, and_19_out, and_20_out, and_21_out, and_22_out,
       and_23_out, and_24_out, B_signal, blt, Branch, CLK, clock_2_out, Clr1, Clr2, Clr3, comparator_1_eq,
       comparator_2_eq, comparator_3_eq, comparator_4_eq, comparator_5_eq, comparator_6_eq, comparator_7_eq,
       comparator_8_eq, comparator_10_eq, comparator_11_eq, comparator_11_lt, comparator_12_eq, csrrci,
       csrrsi, d_ff_2_q, d_ff_4_q, decoder_1_out1, decoder_1_out2, decoder_1_out3, decoder_2_out1,
       decoder_2_out2, decoder_2_out3, decoder_4_out1, decoder_4_out2, decoder_4_out3, ecall, EPC1_2_q,
       EPC2_2_q, EPC3_2_q, Go, halt, IE, INT, IR1_t, IR2_t, IR3_t, IRA, IRB, IRC, J_signal, Jalr_signal,
       Ledout, nand_1_out, not_1_out, not_2_out, not_3_out, or_1_out, or_2_out, or_3_out, or_4_out, or_5_out,
       or_11_out, or_12_out, or_13_out, or_14_out, pull_resistor_1_node, pull_resistor_2_node,
       pull_resistor_3_node, RST, S_signal, sb, sltiu, URET, W1, W2, W3, \中断信号 , \单周期硬布线控制器_1_alu_src ,
       \单周期硬布线控制器_1_beq , \单周期硬布线控制器_1_bne , \单周期硬布线控制器_1_memtoreg , \更高优先级 ;
  wire [1:0] Imm_Sel, \中断号 , \当前中断号 ;
  wire [3:0] decoder_3_out0, RAM_Sel, \单周期硬布线控制器_1_alu_op ;
  wire [4:0] bit_extender_6_out, multiplexer_5_out, multiplexer_6_out, multiplier_1_out;
  wire [12:0] CNT_num;
  wire [15:0] \总周期数 ;
  wire [31:0] adder_2_out, ALU_Res, bit_extender_1_out, bit_extender_2_out, bit_extender_3_out,
       bit_extender_4_out, bit_extender_5_out, Break_PC, EPC1_q, EPC2_q, EPC3_q, INT_Addar, MemData,
       mips_ram_1_p8, multiplexer_1_out, multiplexer_3_out, multiplexer_4_out, multiplexer_7_out,
       multiplexer_8_out, multiplexer_9_out, multiplexer_12_out, PC_4, R1_Data, RET_PC, shifter_1_out,
       shifter_2_out;

  Clock #(.highDuration(1), .lowDuration(1)) clock_1 ();  // open: out
  Button _1 (.out(IRA));
  Button _2 (.out(IRB));
  Button _3 (.out(IRC));
  Button button_1 (.out(RST));
  Button \u_继续运行  (.out(Go));
  LED #(.active("true")) led_1 (.in(W1));
  LED #(.active("true")) led_2 (.in(W2));
  LED #(.active("true")) led_3 (.in(W3));
  or or_1 (or_1_out, Branch, J_signal);
  Multiplexer #(.select(1), .width(32), .disabled("Z"), .enable("false")) multiplexer_1 (
    .in0(PC_4), .in1(adder_2_out), .out(multiplexer_1_out), .sel(or_1_out));
  Multiplexer #(.select(1), .width(32), .disabled("Z"), .enable("false")) multiplexer_2 (
    .in0(multiplexer_1_out), .in1(ALU_Res), .out(Break_PC), .sel(Jalr_signal));
  Hex_Digit_Display hex_digit_display_1 (.value(LedData[31:28]));  // open: dp
  or or_2 (or_2_out, B_signal, J_signal);
  or or_3 (or_3_out, J_signal, S_signal);
  Comparator #(.width(16), .mode("twosComplement")) comparator_1 (
    .a(\总周期数 ), .b(16'h7), .eq(comparator_1_eq));  // open: gt, lt
  Comparator #(.width(16), .mode("twosComplement")) comparator_2 (
    .a(\总周期数 ), .b(16'h241), .eq(comparator_2_eq));  // open: gt, lt
  Comparator #(.width(5), .mode("unsigned")) comparator_3 (
    .a(IR[6:2]), .b(5'b11100), .eq(comparator_3_eq));  // open: gt, lt
  Comparator #(.width(3), .mode("unsigned")) comparator_4 (
    .a(3'b110), .b(IR[14:12]), .eq(comparator_4_eq));  // open: gt, lt
  Comparator #(.width(3), .mode("unsigned")) comparator_5 (
    .a(IR[14:12]), .b(3'b111), .eq(comparator_5_eq));  // open: gt, lt
  Hex_Digit_Display hex_digit_display_2 (.value(LedData[27:24]));  // open: dp
  Hex_Digit_Display hex_digit_display_3 (.value(LedData[23:20]));  // open: dp
  Multiplexer #(.select(1), .width(32), .disabled("Z"), .enable("false")) multiplexer_3 (
    .in0(Break_PC), .in1(RET_PC), .out(multiplexer_3_out), .sel(URET));
  and and_1 (Imm_Sel[1], ~S_signal, or_2_out);  // AND_Gate
  and and_2 (Imm_Sel[0], or_3_out, ~B_signal);  // AND_Gate
  Comparator #(.width(16), .mode("twosComplement")) comparator_6 (
    .a(16'h258), .b(\总周期数 ), .eq(comparator_6_eq));  // open: gt, lt
  or or_4 (or_4_out, comparator_6_eq, comparator_7_eq);
  Comparator #(.width(16), .mode("twosComplement")) comparator_7 (
    .a(\总周期数 ), .b(16'h1), .eq(comparator_7_eq));  // open: gt, lt
  Comparator #(.width(16), .mode("twosComplement")) comparator_8 (
    .a(\总周期数 ), .b(16'h4), .eq(comparator_8_eq));  // open: gt, lt
  or or_5 (or_5_out, comparator_1_eq, comparator_2_eq);
  and and_3 (csrrsi, comparator_3_eq, comparator_4_eq);
  and and_4 (csrrci, comparator_3_eq, comparator_5_eq);
  Hex_Digit_Display hex_digit_display_4 (.value(LedData[15:12]));  // open: dp
  Hex_Digit_Display hex_digit_display_5 (.value(LedData[19:16]));  // open: dp
  Multiplexer #(.select(1), .width(32), .disabled("Z"), .enable("false")) multiplexer_4 (
    .in0(multiplexer_3_out), .in1(INT_Addar), .out(multiplexer_4_out), .sel(INT));
  not not_1 (not_1_out, halt);
  Pull_Resistor #(.pull(0)) pull_resistor_1 (.node(pull_resistor_1_node));
  assign pull_resistor_1_node = or_4_out ? ~CLK : 1'bz;  // Controlled_Inverter controlled_inverter_1
  Pull_Resistor #(.pull(0)) pull_resistor_2 (.node(pull_resistor_2_node));
  assign pull_resistor_2_node = comparator_8_eq ? ~CLK : 1'bz;  // Controlled_Inverter controlled_inverter_2
  Pull_Resistor #(.pull(0)) pull_resistor_3 (.node(pull_resistor_3_node));
  assign pull_resistor_3_node = or_5_out ? ~CLK : 1'bz;  // Controlled_Inverter controlled_inverter_3
  Hex_Digit_Display hex_digit_display_6 (.value(LedData[7:4]));  // open: dp
  Hex_Digit_Display hex_digit_display_7 (.value(LedData[11:8]));  // open: dp
  // Probe on \总周期数 
  Register #(.width(32), .trigger("rising"), .Select("low")) u_PC (
    .D(multiplexer_4_out), .en(not_1_out), .Q(PC), .clk(CLK), .clr(RST));
  Hex_Digit_Display hex_digit_display_8 (.value(LedData[3:0]));  // open: dp
  Adder #(.width(32)) adder_1 (.a(PC), .b(32'h4), .out(PC_4));  // open: cin, cout
  // RiscV_Probe riscv_probe_1: pin names not known; wires that end beside it: IR
  ROM #(.addrWidth(10), .dataWidth(32), .Select("high")) rom_1 (.addr(PC[11:2]), .data(IR));
  Comparator #(.width(2), .mode("unsigned")) comparator_9 (.a(\中断号 ), .b(\当前中断号 ), .gt(\更高优先级 ));  // open: eq, lt
  or or_6 (IR1_t, IR1, IRA);
  Comparator #(.width(32), .mode("unsigned")) comparator_10 (
    .a(R1_Data), .b(32'h22), .eq(comparator_10_eq));  // open: gt, lt
  or or_7 (IR2_t, IR2, IRB);
  and and_5 (and_5_out, ecall, ~comparator_10_eq);  // AND_Gate
  and and_6 (Ledout, comparator_10_eq, ecall);
  \中断控制器  \u_中断控制器_1  (
    .IRA(IRA), .W1(W1), .Clr1(Clr1), .IRB(IRB), .W2(W2), .Clr2(Clr2), .IRC(IRC), .W3(W3), .Clr3(Clr3),
    .\中断号 (\中断号 ), .\中断请求 (\中断信号 ), .CLK(CLK), .RST(RST));
  \单周期硬布线控制器  \u_单周期硬布线控制器_1  (
    .Funct({IR[30], IR[25], IR[14:12]}), .OP(IR[6:2]), .ALU_OP(\单周期硬布线控制器_1_alu_op ),
    .MemToReg(\单周期硬布线控制器_1_memtoreg ), .MemWrite(MemWrite), .ALU_SRC(\单周期硬布线控制器_1_alu_src ),
    .RegWrite(RegWrite), .ecall(ecall), .S_type(S_signal), .Jalr(Jalr_signal), .Beq(\单周期硬布线控制器_1_beq ),
    .JAL(J_signal), .Bne(\单周期硬布线控制器_1_bne ), .in_3(IR[21]), .uret(URET), .Sltiu(sltiu), .Sb(sb), .Blt(blt));
  Multiplexer #(.select(1), .width(5), .disabled("Z"), .enable("false")) multiplexer_5 (
    .in0(IR[19:15]), .in1(5'b10001), .out(multiplexer_5_out), .sel(ecall));
  Multiplexer #(.select(1), .width(5), .disabled("Z"), .enable("false")) multiplexer_6 (
    .in0(IR[24:20]), .in1(5'b01010), .out(multiplexer_6_out), .sel(ecall));
  assign bit_extender_1_out = {{20{IR[31]}}, IR[31:20]};  // Bit_Extender bit_extender_1
  assign bit_extender_2_out = {{20{1'b0}}, IR[31:20]};  // Bit_Extender bit_extender_2
  assign bit_extender_3_out = {{20{IR[31]}}, {IR[31:25], IR[11:7]}};  // Bit_Extender bit_extender_3
  assign bit_extender_4_out = {{20{IR[31]}}, {IR[31], IR[7], IR[30:25], IR[11:8]}};  // Bit_Extender bit_extender_4
  assign bit_extender_5_out = {{12{IR[31]}}, {IR[31], IR[19:12], IR[20], IR[30:21]}};  // Bit_Extender bit_extender_5
  D_Flip_Flop #(.trigger("falling"), .Pre_Clr_Positions("ABOVE_BELOW"), .NegatePresetClear("false"), .enable("true"), .NewFFLayout("true")) d_ff_1 (
    .clk(CLK), .D(and_5_out), .Q(halt), .en(ecall), .reset(Go));  // open: Qn, preset
  or or_8 (IR3_t, IR3, IRC);
  or or_9 (B_signal, \单周期硬布线控制器_1_beq , blt, \单周期硬布线控制器_1_bne );
  Multiplexer #(.select(1), .width(32), .disabled("Z"), .enable("false")) multiplexer_7 (
    .in0(bit_extender_1_out), .in1(bit_extender_2_out), .out(multiplexer_7_out), .sel(sltiu));
  and and_7 (and_7_out, \更高优先级 , IE);
  Decoder #(.select(2), .tristate("false"), .disabled("Z"), .enable("false")) decoder_1 (
    .out1(decoder_1_out1), .out2(decoder_1_out2), .out3(decoder_1_out3), .sel(\中断号 ));  // open: out0
  \Regifile_上升沿  \regifile_上升沿_1  (
    .Din(RDin), .Clk(CLK), .R1(R1_Data), .R2(MDin), .WE(RegWrite), .W_num(IR[11:7]),
    .R1_num(multiplexer_5_out), .R2_num(multiplexer_6_out));
  and and_8 (and_8_out, and_7_out, decoder_1_out1);
  and and_9 (and_9_out, decoder_1_out2, and_7_out);
  and and_10 (and_10_out, decoder_1_out3, and_7_out);
  Multiplexer #(.select(2), .width(32), .disabled("Z"), .enable("false")) multiplexer_8 (
    .in0(multiplexer_7_out), .in1(bit_extender_3_out), .in2(bit_extender_4_out), .in3(bit_extender_5_out),
    .out(multiplexer_8_out), .sel(Imm_Sel));
  Decoder #(.select(2), .tristate("false"), .disabled("Z"), .enable("false")) decoder_2 (
    .out1(decoder_2_out1), .out2(decoder_2_out2), .out3(decoder_2_out3), .sel(\当前中断号 ));  // open: out0
  Multiplexer #(.select(1), .width(32), .disabled("Z"), .enable("false")) multiplexer_9 (
    .in0(MDin), .in1(multiplexer_8_out), .out(multiplexer_9_out), .sel(\单周期硬布线控制器_1_alu_src ));
  Register #(.width(32), .trigger("rising"), .Select("low")) register_1 (
    .D(MDin), .en(Ledout), .Q(LedData), .clk(CLK), .clr(RST));
  Register #(.width(32), .trigger("rising"), .Select("low")) EPC1 (
    .D(Break_PC), .en(and_8_out), .Q(EPC1_q), .clk(CLK), .clr(RST));
  ALU alu_1 (
    .X(R1_Data), .Y(multiplexer_9_out), .AluOP(\单周期硬布线控制器_1_alu_op ), .Equal(alu_1_equal), .Result(ALU_Res),
    .out_6(alu_1_out_6));  // open: Result_2, out_4
  Shifter #(.width(32), .shift("ll")) shifter_1 (.in(multiplexer_8_out), .\dist (5'b00001), .out(shifter_1_out));
  and and_11 (Clr1, decoder_2_out1, URET);
  and and_12 (Clr2, decoder_2_out2, URET);
  and and_13 (Clr3, decoder_2_out3, URET);
  Register #(.width(32), .trigger("rising"), .Select("low")) EPC2 (
    .D(Break_PC), .en(and_9_out), .Q(EPC2_q), .clk(CLK), .clr(RST));
  Register #(.width(32), .trigger("rising"), .Select("low")) EPC3 (
    .D(Break_PC), .en(and_10_out), .Q(EPC3_q), .clk(CLK), .clr(RST));
  and and_14 (and_14_out, blt, alu_1_out_6);
  and and_15 (and_15_out, alu_1_equal, \单周期硬布线控制器_1_beq );
  and and_16 (and_16_out, ~alu_1_equal, \单周期硬布线控制器_1_bne );  // AND_Gate
  Adder #(.width(32)) adder_2 (.a(PC), .b(shifter_1_out), .out(adder_2_out));  // open: cin, cout
  or or_10 (Branch, and_14_out, and_15_out, and_16_out);
  not not_2 (not_2_out, halt);
  Multiplexer #(.select(2), .width(32), .disabled("Z"), .enable("false")) multiplexer_10 (
    .in1(EPC1_q), .in2(EPC2_q), .in3(EPC3_q), .out(RET_PC), .sel(\当前中断号 ));  // open: in0
  D_Flip_Flop #(.trigger("high"), .Pre_Clr_Positions("LEGACY"), .NegatePresetClear("false"), .enable("true"), .NewFFLayout("false")) d_ff_2 (.Q(d_ff_2_q));  // open: clk, D, Qn, preset, en, reset
  // Probe on 13'hc
  not not_3 (not_3_out, MemWrite);
  Counter #(.width(16), .max('hffff), .ongoal("stay"), .trigger("rising"), .behavior("old")) counter_1 (
    .count(not_2_out), .Q(\总周期数 ), .clk(CLK));  // open: load, D, carry, clr, preset
  Multiplexer #(.select(2), .width(32), .disabled("Z"), .enable("false")) multiplexer_11 (
    .in1(32'h30ac), .in2(32'h3158), .in3(32'h3204), .out(INT_Addar), .sel(\中断号 ));  // open: in0
  Comparator #(.width(13), .mode("twosComplement")) comparator_11 (
    .a(CNT_num), .b(13'hc), .eq(comparator_11_eq), .lt(comparator_11_lt));  // open: gt
  Clock #(.highDuration(1), .lowDuration(1)) clock_2 (.out(clock_2_out));
  // cs3410_MIPS_RAM mips_ram_1: pin names not known; wires that end beside it: ALU_Res[21:2], MemData, MemWrite, RAM_Sel, CLK, not_3_out, RST, mips_ram_1_p8
  Counter #(.width(13), .max('h1fff), .ongoal("stay"), .trigger("rising"), .behavior("old")) counter_2 (
    .count(comparator_11_lt), .Q(CNT_num), .clk(clock_2_out));  // open: load, D, carry, clr, preset
  Multiplexer #(.select(1), .width(32), .disabled("Z"), .enable("false")) multiplexer_12 (
    .in0(ALU_Res), .in1(mips_ram_1_p8), .out(multiplexer_12_out), .sel(\单周期硬布线控制器_1_memtoreg ));
  nand nand_1 (nand_1_out, d_ff_2_q, comparator_11_eq);
  or or_11 (or_11_out, J_signal, Jalr_signal);
  Multiplexer #(.select(1), .width(32), .disabled("Z"), .enable("false")) multiplexer_13 (
    .in0(multiplexer_12_out), .in1(PC_4), .out(RDin), .sel(or_11_out));
  assign bit_extender_6_out = {{3{1'b0}}, ALU_Res[1:0]};  // Bit_Extender bit_extender_6
  Decoder #(.select(2), .tristate("false"), .disabled("Z"), .enable("false")) decoder_3 (
    .out0(decoder_3_out0[0]), .out1(decoder_3_out0[1]), .out2(decoder_3_out0[2]), .out3(decoder_3_out0[3]),
    .sel(ALU_Res[1:0]));
  or or_12 (or_12_out, URET, \更高优先级 );
  assign CLK = nand_1_out ? clock_2_out : 1'bz;  // Controlled_Buffer controlled_buffer_1
  Pull_Resistor #(.pull(1)) pull_resistor_4 (.node(CLK));
  Multiplier #(.width(5)) multiplier_1 (
    .a(bit_extender_6_out), .b(5'b01000), .out(multiplier_1_out));  // open: cin, cout
  Multiplexer #(.select(1), .width(4), .disabled("Z"), .enable("false")) multiplexer_14 (
    .in0(4'b1111), .in1(decoder_3_out0), .out(RAM_Sel), .sel(sb));
  and and_17 (and_17_out, or_12_out, IE);
  Decoder #(.select(2), .tristate("false"), .disabled("Z"), .enable("false")) decoder_4 (
    .out1(decoder_4_out1), .out2(decoder_4_out2), .out3(decoder_4_out3), .sel(\中断号 ));  // open: out0
  Comparator #(.width(16), .mode("twosComplement")) comparator_12 (
    .a(\总周期数 ), .b({16{1'b0}}), .eq(comparator_12_eq));  // open: gt, lt
  Shifter #(.width(32), .shift("ll")) shifter_2 (.in(MDin), .\dist (multiplier_1_out), .out(shifter_2_out));
  and and_18 (and_18_out, and_17_out, decoder_4_out1);
  and and_19 (and_19_out, and_17_out, decoder_4_out2);
  and and_20 (and_20_out, and_17_out, decoder_4_out3);
  or or_13 (or_13_out, comparator_12_eq, URET);
  and and_21 (and_21_out, \中断信号 , IE, \更高优先级 );
  Multiplexer #(.select(1), .width(32), .disabled("Z"), .enable("false")) multiplexer_15 (
    .in0(MDin), .in1(shifter_2_out), .out(MemData), .sel(sb));
  D_Flip_Flop #(.trigger("rising"), .Pre_Clr_Positions("LEGACY"), .NegatePresetClear("false"), .enable("true"), .NewFFLayout("false")) d_ff_3 (
    .clk(CLK), .D(1'b1), .Q(IE), .preset(or_13_out), .en(csrrsi), .reset(or_14_out));  // open: Qn
  or or_14 (or_14_out, csrrci, d_ff_4_q);
  D_Flip_Flop #(.trigger("rising"), .Pre_Clr_Positions("LEGACY"), .NegatePresetClear("false"), .enable("true"), .NewFFLayout("false")) d_ff_4 (
    .clk(CLK), .D(and_21_out), .Q(d_ff_4_q), .reset(URET));  // open: Qn, preset, en
  Register #(.width(1), .trigger("rising"), .Select("low")) EPC1_2 (
    .D(and_22_out), .en(and_18_out), .Q(EPC1_2_q), .clk(CLK), .clr(RST));
  and and_22 (and_22_out, ~Clr1, 1'b1);  // AND_Gate
  and and_23 (and_23_out, ~Clr2, 1'b1);  // AND_Gate
  Register #(.width(1), .trigger("rising"), .Select("low")) EPC2_2 (
    .D(and_23_out), .en(and_19_out), .Q(EPC2_2_q), .clk(CLK), .clr(RST));
  Register #(.width(1), .trigger("rising"), .Select("low")) EPC3_2 (
    .D(and_24_out), .en(and_20_out), .Q(EPC3_2_q), .clk(CLK), .clr(RST));
  and and_24 (and_24_out, ~Clr3, 1'b1);  // AND_Gate
  and and_25 (INT, ~d_ff_4_q, and_21_out);  // AND_Gate
  Priority_Encoder #(.select(2), .disabled("Z")) priority_encoder_1 (
    .in0(1'b1), .in1(EPC1_2_q), .in2(EPC2_2_q), .in3(EPC3_2_q), .out(\当前中断号 ));  // open: gs, en_out, en_in

  // Other names for the same wires on the sheet: Funct3[2:0] = IR[14:12]; Bit_Sel[1:0] = ALU_Res[1:0];
  //   Opcode[4:0] = IR[6:2]

  // Notes on the sheet:
  //   中断源
  //   中断等待指示
  //   总复位信号应将除ROM以外所有存储组件全部清零
  //   生成立即数选择信号
  //   多级中断测试信号模拟器
  //   生成开关中断信号
  //   数码管输出
  //   开中断
  //   关中断
  //   数码管输出应该用寄存器锁存，否则显示数据只能一闪而过
  //   指令探针
  //   指令存储器
  //   contents of rom_1 (hex, n*v repeats v):
  //   7d000113 100413 1f41993 41f9d993 433 c00913 800b13 140413 f47413 800293 100313 499993 89e9b3 1300533
  //   2200893 73 406282b3 fe0294e3 140413 f00f93 1f47433 1c41413 800293 100313 49d993 89e9b3 1300533
  //   2200893 73 406282b3 fe0294e3 1c45413 406b0b33 b0463 f95ff06f 2b3 fff2c293 1029293 fff2e293 500533
  //   2200893 73 f5dff06f 1112023 410113 a12023 410113 812023 410113 1312023 410113 1412023 410113 1512023
  //   410113 1612023 410113 40e073 100b13 300a13 100a93 1600433 441413 14469b3 1300533 2200893 73 fe0416e3
  //   415a0a33 fe0a10e3 40f073 ffc10113 12b03 ffc10113 12a83 ffc10113 12a03 ffc10113 12983 ffc10113 12403
  //   ffc10113 12503 ffc10113 12883 200073 1112023 410113 a12023 410113 812023 410113 1312023 410113
  //   1412023 410113 1512023 410113 1612023 410113 40e073 200b13 300a13 100a93 1600433 441413 14469b3
  //   1300533 2200893 73 fe0416e3 415a0a33 fe0a10e3 40f073 ffc10113 12b03 ffc10113 12a83 ffc10113 12a03
  //   ffc10113 12983 ffc10113 12403 ffc10113 12503 ffc10113 12883 200073 1112023 410113 a12023 410113
  //   812023 410113 1312023 410113 1412023 410113 1512023 410113 1612023 410113 40e073 300b13 300a13
  //   100a93 1600433 441413 14469b3 1300533 2200893 73 fe0416e3 415a0a33 fe0a10e3 40f073 ffc10113 12b03
  //   ffc10113 12a83 ffc10113 12a03 ffc10113 12983 ffc10113 12403 ffc10113 12503 ffc10113 12883 200073
  //   更高优先级信号产生
  //   指令字
  //   I型指令立即数
  //   S型指令立即数
  //   B型指令立即数
  //   J型指令立即数
  //   生成停机信号halt和LED显示信号Ledout
  //   中断控制逻辑
  //   JAL
  //   JALR
  //   URET
  //   Sltiu
  //   Sb
  //   rs1
  //   rs2
  //   rd
  //   Beq
  //   Bne
  //   MemToReg
  //   MemWrite
  //   AluOP
  //   AluSrcB
  //   RegWrite
  //   Blt
  //   中断清零信号产生
  //   为方便自动评测，需要输出PC，IR，寄存器堆写如数据RDin
  //   LedData显示控制
  //   保护现场
  //   RAM写使能MemWrite、RAM写入数据MDin等信号
  //   控制位
  //   暂停节拍，不能为0
  //   数据存储器
  //   周期信号显示控制
  //   中断入口逻辑
  //   戳工具置1进入计数暂停模式，ctrl+k时钟自动运行到对应节拍暂停
  //   ctrl+k关闭时钟连续运行，将控制位置零，进入单步调试模式调试
  //   用这个时钟源需要去掉电路中的其他时钟源
  //   可计数暂停的时钟源
  //   计算Sb对应的MemData
  //   中断使能信号产生
  //   当前中断号产生
endmodule

module \重定向流水线_单级中断  (
  output RegWrite,
  output MemWrite,
  output [31:0] IF_PC,
  output [31:0] ID_PC,
  output [31:0] EX_PC,
  output [31:0] M_PC,
  output [31:0] WB_PC,
  output [31:0] RDin,
  output [31:0] MDin,
  output [31:0] LedData
);

  wire alu_1_equal, alu_1_out_6, and_1_out, and_3_out, and_5_out, and_9_out, and_10_out, and_11_out,
       and_12_out, and_13_out, and_14_out, and_17_out, B_Jump, BranchTaken, CLK, clock_1_out, clock_2_out,
       Clr1, Clr2, Clr3, comparator_1_eq, comparator_2_eq, comparator_3_eq, comparator_3_lt, comparator_4_eq,
       d_ff_2_q, decoder_1_out1, decoder_1_out2, decoder_1_out3, ecall, EX_B_signal, EX_J_signal,
       ex_mem_1_ecall_2, ex_mem_1_jal_2, ex_mem_1_jalr_2, ex_mem_1_memtoreg_2, EX_MemToReg, EX_RegWrite,
       EX_S_signal, EX_URET, Go, halt, \id_ex_重定向_1_alusrcb_2 , \id_ex_重定向_1_beq_2 , \id_ex_重定向_1_blt_2 ,
       \id_ex_重定向_1_bne_2 , \id_ex_重定向_1_ecall_2 , \id_ex_重定向_1_jalr_2 , \id_ex_重定向_1_memwrite_2 ,
       \id_ex_重定向_1_sb_2 , \id_ex_重定向_1_sltiu_2 , IE, IF_URET, INT, IRA, IRB, IRC, Ledout, LoadUse,
       MEM_RegWrite, mem_wb_1_jal_2, mem_wb_1_jalr_2, mem_wb_1_memtoreg_2, mips_ram_1_p6, nand_1_out,
       not_1_out, not_2_out, not_4_out, or_1_out, or_2_out, or_3_out, or_4_out, or_7_out, or_10_out,
       or_12_out, or_13_out, or_14_out, or_15_out, \r1r2使用检测_1_r1used , \r1r2使用检测_1_r2used ,
       \r1r2使用检测_2_r1used , \r1r2使用检测_2_r2used , register_2_q, register_3_q, register_4_q, register_7_q, RST,
       sb, W1, W2, W3, \中断信号 , \单周期硬布线控制器_1_alu_src , \单周期硬布线控制器_1_beq , \单周期硬布线控制器_1_blt ,
       \单周期硬布线控制器_1_bne , \单周期硬布线控制器_1_ecall , \单周期硬布线控制器_1_jal , \单周期硬布线控制器_1_jalr , \单周期硬布线控制器_1_memtoreg ,
       \单周期硬布线控制器_1_memwrite , \单周期硬布线控制器_1_regwrite , \单周期硬布线控制器_1_s_type , \单周期硬布线控制器_1_sb ,
       \单周期硬布线控制器_1_sltiu , \单周期硬布线控制器_1_uret , \无条件分支 ;
  wire [1:0] Bit_Sel, EX_Imm_Sel, EX_R1_F, EX_R2_F, ID_R1_F, ID_R2_F, register_1_q, \中断号 ;
  wire [2:0] Funct3, register_5_q;
  wire [3:0] decoder_2_out0, \id_ex_重定向_1_aluop_2 , RAM_Sel, \单周期硬布线控制器_1_alu_op ;
  wire [4:0] bit_extender_6_out, ID_R1, ID_R2, multiplier_1_out;
  wire [11:0] \id_ex_重定向_1_imm_b_2 , \id_ex_重定向_1_imm_i_2 , \id_ex_重定向_1_imm_s_2 ;
  wire [12:0] CNT_num;
  wire [15:0] adder_3_out, \LoadUse次数 , \总周期数 , \插入气泡数 , \无条件分支数 , \条件分支成功数 ;
  wire [19:0] \id_ex_重定向_1_imm_j_2 ;
  wire [31:0] adder_2_out, bit_extender_1_out, bit_extender_2_out, bit_extender_3_out, bit_extender_4_out,
       bit_extender_5_out, Break_PC, EX_AluData, EX_IR, ex_mem_1_pc_4_2, EX_R1Data, EX_R2Data,
       \id_ex_重定向_1_pc_4_2 , ID_IR, ID_R1Data, if_id_1_pc_4_2, IF_IR, IF_PC_4, INT_Addar, MEM_IR, MEM_R1Data,
       mem_wb_1_aludata_2, mem_wb_1_memdata_2, MemData, mips_ram_1_p8, multiplexer_1_out, multiplexer_2_out,
       multiplexer_3_out, multiplexer_4_out, multiplexer_8_out, multiplexer_9_out, multiplexer_10_out,
       multiplexer_16_out, \regifile_下降沿_1_r2 , RelocationR1Data, RelocationR2Data, RET_PC, shifter_1_out,
       shifter_2_out, WB_IR, WB_PC_4, WB_R1Data, WB_R2Data;
  wire [31:2] MEM_AluData;

  Button \u_总复位  (.out(RST));
  Button _1 (.out(IRA));
  Button _2 (.out(IRB));
  Button _3 (.out(IRC));
  // Probe on \总周期数 
  // Probe on \总周期数 
  Button \u_继续运行  (.out(Go));
  LED #(.active("true")) led_1 (.in(W1));
  LED #(.active("true")) led_2 (.in(W2));
  LED #(.active("true")) led_3 (.in(W3));
  or or_1 (or_1_out, B_Jump, EX_J_signal);
  Hex_Digit_Display hex_digit_display_1 (.value(LedData[31:28]));  // open: dp
  // Probe on IF_PC[19:0]
  // RiscV_Probe riscv_probe_1: pin names not known; wires that end beside it: {IF_IR[31:15], Funct3, IF_IR[11:0]}
  Multiplexer #(.select(1), .width(32), .disabled("Z"), .enable("false")) multiplexer_1 (
    .in0(IF_PC_4), .in1(adder_2_out), .out(multiplexer_1_out), .sel(or_1_out));
  Multiplexer #(.select(1), .width(32), .disabled("Z"), .enable("false")) multiplexer_2 (
    .in0(multiplexer_1_out), .in1(EX_AluData), .out(multiplexer_2_out), .sel(\id_ex_重定向_1_jalr_2 ));
  Hex_Digit_Display hex_digit_display_2 (.value(LedData[27:24]));  // open: dp
  Hex_Digit_Display hex_digit_display_3 (.value(LedData[23:20]));  // open: dp
  // Probe on ID_PC[19:0]
  // RiscV_Probe riscv_probe_2: pin names not known; wires that end beside it: ID_IR
  Multiplexer #(.select(1), .width(32), .disabled("Z"), .enable("false")) multiplexer_3 (
    .in0(multiplexer_2_out), .in1(INT_Addar), .out(multiplexer_3_out), .sel(INT));
  \R1R2使用检测  \r1r2使用检测_1  (
    .OP2(ID_IR[2]), .OP3(ID_IR[3]), .OP4(ID_IR[4]), .OP5(ID_IR[5]), .OP6(ID_IR[6]), .F12(ID_IR[12]),
    .F13(ID_IR[13]), .F14(ID_IR[14]), .F25(ID_IR[25]), .F30(ID_IR[30]), .R1Used(\r1r2使用检测_1_r1used ),
    .R2Used(\r1r2使用检测_1_r2used ));
  Hex_Digit_Display hex_digit_display_4 (.value(LedData[19:16]));  // open: dp
  Hex_Digit_Display hex_digit_display_5 (.value(LedData[15:12]));  // open: dp
  Multiplexer #(.select(1), .width(32), .disabled("Z"), .enable("false")) multiplexer_4 (
    .in0(multiplexer_3_out), .in1(RET_PC), .out(multiplexer_4_out), .sel(IF_URET));
  and and_1 (and_1_out, not_1_out, not_2_out);
  not not_1 (not_1_out, LoadUse);
  not not_2 (not_2_out, halt);
  \中断控制器  \u_中断控制器_1  (
    .IRA(IRA), .W1(W1), .Clr1(Clr1), .IRB(IRB), .W2(W2), .Clr2(Clr2), .IRC(IRC), .W3(W3), .Clr3(Clr3),
    .\中断号 (\中断号 ), .\中断请求 (\中断信号 ), .CLK(CLK), .RST(RST));
  Hex_Digit_Display hex_digit_display_6 (.value(LedData[11:8]));  // open: dp
  Hex_Digit_Display hex_digit_display_7 (.value(LedData[7:4]));  // open: dp
  Clock #(.highDuration(1), .lowDuration(1)) clock_1 (.out(clock_1_out));
  // Probe on EX_PC[19:0]
  // RiscV_Probe riscv_probe_3: pin names not known; wires that end beside it: clock_1_out, EX_IR, CLK
  Register #(.width(32), .trigger("rising"), .Select("low")) PC (
    .D(multiplexer_4_out), .en(and_1_out), .Q(IF_PC), .clk(CLK), .clr(RST));
  Hex_Digit_Display hex_digit_display_8 (.value(LedData[3:0]));  // open: dp
  Adder #(.width(32)) adder_1 (.a(IF_PC), .b(32'h4), .out(IF_PC_4));  // open: cin, cout
  Comparator #(.width(5), .mode("twosComplement")) comparator_1 (
    .a(IF_IR[6:2]), .b(5'b11100), .eq(comparator_1_eq));  // open: gt, lt
  Comparator #(.width(3), .mode("twosComplement")) comparator_2 (
    .a(Funct3), .b(3'b000), .eq(comparator_2_eq));  // open: gt, lt
  // Probe on \总周期数 
  // Probe on M_PC[19:0]
  // RiscV_Probe riscv_probe_4: pin names not known; wires that end beside it: MEM_IR
  and and_2 (IF_URET, comparator_1_eq, IF_IR[21], comparator_2_eq);
  \LoadUse信号生成  \loaduse信号生成_1  (
    .R1Used(\r1r2使用检测_1_r1used ), .EX_MemToReg(EX_MemToReg), .ID_R1(ID_R1), .EX_RD(EX_IR[11:7]),
    .ID_R2(ID_R2), .R2Used(\r1r2使用检测_1_r2used ), .LoadUse(LoadUse));
  // Probe on \总周期数 
  // Probe on \无条件分支数 
  // Probe on \条件分支成功数 
  // Probe on \插入气泡数 
  // Probe on \LoadUse次数 
  // RiscV_Probe riscv_probe_5: pin names not known; wires that end beside it: {IF_IR[31:15], Funct3, IF_IR[11:0]}
  ROM #(.addrWidth(10), .dataWidth(32), .Select("high")) rom_1 (
    .addr(IF_PC[11:2]), .data({IF_IR[31:15], Funct3, IF_IR[11:0]}));
  // Probe on IF_PC[11:0]
  // Probe on WB_PC[19:0]
  // RiscV_Probe riscv_probe_6: pin names not known; wires that end beside it: WB_IR
  and and_3 (and_3_out, ~EX_URET, \中断信号 );  // AND_Gate
  and and_4 (INT, IE, \中断信号 );
  // Probe on ID_PC[11:0]
  // Probe on EX_PC[11:0]
  or or_2 (or_2_out, BranchTaken, INT, RST);
  or or_3 (or_3_out, LoadUse, and_5_out);
  D_Flip_Flop #(.trigger("rising"), .Pre_Clr_Positions("LEGACY"), .NegatePresetClear("false"), .enable("true"), .NewFFLayout("false")) d_ff_1 (
    .clk(CLK), .D(and_3_out), .Qn(IE));  // open: Q, preset, en, reset
  // Probe on M_PC[11:0]
  D_Flip_Flop #(.trigger("high"), .Pre_Clr_Positions("LEGACY"), .NegatePresetClear("false"), .enable("true"), .NewFFLayout("false")) d_ff_2 (.Q(d_ff_2_q));  // open: clk, D, Qn, preset, en, reset
  // Probe on 13'hc
  and and_5 (and_5_out, halt, ~Go);  // AND_Gate
  IF_ID if_id_1 (
    .CLK(CLK), .\RST_高电平有效 (or_2_out), .\en_低电平有效 (or_3_out), .IR({IF_IR[31:15], Funct3, IF_IR[11:0]}),
    .PC(IF_PC), .PC_4(IF_PC_4), .IR_2(ID_IR), .PC_2(ID_PC), .PC_4_2(if_id_1_pc_4_2));
  // Probe on WB_PC[11:0]
  Comparator #(.width(13), .mode("twosComplement")) comparator_3 (
    .a(CNT_num), .b(13'hc), .eq(comparator_3_eq), .lt(comparator_3_lt));  // open: gt
  Clock #(.highDuration(1), .lowDuration(1)) clock_2 (.out(clock_2_out));
  \R1R2使用检测  \r1r2使用检测_2  (
    .OP2(ID_IR[2]), .OP3(ID_IR[3]), .OP4(ID_IR[4]), .OP5(ID_IR[5]), .OP6(ID_IR[6]), .F12(ID_IR[12]),
    .F13(ID_IR[13]), .F14(ID_IR[14]), .F25(ID_IR[25]), .F30(ID_IR[30]), .R1Used(\r1r2使用检测_2_r1used ),
    .R2Used(\r1r2使用检测_2_r2used ));
  Register #(.width(2), .trigger("rising"), .Select("low")) register_1 (
    .D(\中断号 ), .en(INT), .Q(register_1_q), .clk(CLK), .clr(RST));
  nand nand_1 (nand_1_out, d_ff_2_q, comparator_3_eq);
  Counter #(.width(13), .max('h1fff), .ongoal("stay"), .trigger("rising"), .behavior("old")) counter_1 (
    .count(comparator_3_lt), .Q(CNT_num), .clk(clock_2_out));  // open: load, D, carry, clr, preset
  \单周期硬布线控制器  \u_单周期硬布线控制器_1  (
    .Funct({ID_IR[30], ID_IR[25], ID_IR[14:12]}), .OP(ID_IR[6:2]), .ALU_OP(\单周期硬布线控制器_1_alu_op ),
    .MemToReg(\单周期硬布线控制器_1_memtoreg ), .MemWrite(\单周期硬布线控制器_1_memwrite ), .ALU_SRC(\单周期硬布线控制器_1_alu_src ),
    .RegWrite(\单周期硬布线控制器_1_regwrite ), .ecall(\单周期硬布线控制器_1_ecall ), .S_type(\单周期硬布线控制器_1_s_type ),
    .Jalr(\单周期硬布线控制器_1_jalr ), .Beq(\单周期硬布线控制器_1_beq ), .JAL(\单周期硬布线控制器_1_jal ), .Bne(\单周期硬布线控制器_1_bne ),
    .in_3(ID_IR[21]), .uret(\单周期硬布线控制器_1_uret ), .Sltiu(\单周期硬布线控制器_1_sltiu ), .Sb(\单周期硬布线控制器_1_sb ),
    .Blt(\单周期硬布线控制器_1_blt ));
  Multiplexer #(.select(1), .width(5), .disabled("Z"), .enable("false")) multiplexer_5 (
    .in0(ID_IR[19:15]), .in1(5'b10001), .out(ID_R1), .sel(\单周期硬布线控制器_1_ecall ));
  Multiplexer #(.select(1), .width(5), .disabled("Z"), .enable("false")) multiplexer_6 (
    .in0(ID_IR[24:20]), .in1(5'b01010), .out(ID_R2), .sel(\单周期硬布线控制器_1_ecall ));
  Decoder #(.select(2), .tristate("false"), .disabled("Z"), .enable("false")) decoder_1 (
    .out1(decoder_1_out1), .out2(decoder_1_out2), .out3(decoder_1_out3), .sel(register_1_q));  // open: out0
  assign CLK = nand_1_out ? clock_2_out : 1'bz;  // Controlled_Buffer controlled_buffer_1
  and and_6 (Clr1, decoder_1_out1, IF_URET);
  and and_7 (Clr2, decoder_1_out2, IF_URET);
  and and_8 (Clr3, decoder_1_out3, IF_URET);
  Pull_Resistor #(.pull(1)) pull_resistor_1 (.node(CLK));
  \Regifile_下降沿  \regifile_下降沿_1  (
    .Din(RDin), .Clk(CLK), .R1(ID_R1Data), .R2(\regifile_下降沿_1_r2 ), .WE(RegWrite), .W_num(WB_IR[11:7]),
    .R1_num(ID_R1), .R2_num(ID_R2));
  \R1_F_R2_F信号生成  \r1_f_r2_f信号生成_1  (
    .R1Used(\r1r2使用检测_2_r1used ), .ID_R1(ID_R1), .EX_RegWrite(EX_RegWrite), .EX_RD(EX_IR[11:7]),
    .MEM_RegWrite(MEM_RegWrite), .MEM_RD(MEM_IR[11:7]), .R2Used(\r1r2使用检测_2_r2used ), .ID_R2(ID_R2),
    .R1_F(ID_R1_F), .R2_F(ID_R2_F));
  or or_4 (or_4_out, BranchTaken, RST, LoadUse, INT);
  and and_9 (and_9_out, halt, ~Go);  // AND_Gate
  \ID_EX_重定向  \id_ex_重定向_1  (
    .CLK(CLK), .\RST_高电平有效 (or_4_out), .\en_低电平有效 (and_9_out), .RegWrite(\单周期硬布线控制器_1_regwrite ), .IR(ID_IR),
    .AluSrcB(\单周期硬布线控制器_1_alu_src ), .AluOP(\单周期硬布线控制器_1_alu_op ), .PC(ID_PC),
    .MemWrite(\单周期硬布线控制器_1_memwrite ), .PC_4(if_id_1_pc_4_2), .MemToReg(\单周期硬布线控制器_1_memtoreg ),
    .R1(ID_R1Data), .Bne(\单周期硬布线控制器_1_bne ), .R2(\regifile_下降沿_1_r2 ), .Beq(\单周期硬布线控制器_1_beq ),
    .JAL(\单周期硬布线控制器_1_jal ), .Imm_I(ID_IR[31:20]), .Imm_S({ID_IR[31:25], ID_IR[11:7]}),
    .JALR(\单周期硬布线控制器_1_jalr ), .Imm_B({ID_IR[31], ID_IR[7], ID_IR[30:25], ID_IR[11:8]}),
    .URET(\单周期硬布线控制器_1_uret ), .Imm_J({ID_IR[31], ID_IR[19:12], ID_IR[20], ID_IR[30:21]}),
    .ecall(\单周期硬布线控制器_1_ecall ), .Sltiu(\单周期硬布线控制器_1_sltiu ), .Sb(\单周期硬布线控制器_1_sb ), .Blt(\单周期硬布线控制器_1_blt ),
    .S_Type(\单周期硬布线控制器_1_s_type ), .R1_F(ID_R1_F), .R2_F(ID_R2_F), .RegWrite_2(EX_RegWrite), .IR_2(EX_IR),
    .AluSrcB_2(\id_ex_重定向_1_alusrcb_2 ), .AluOP_2(\id_ex_重定向_1_aluop_2 ), .PC_2(EX_PC),
    .MemWrite_2(\id_ex_重定向_1_memwrite_2 ), .PC_4_2(\id_ex_重定向_1_pc_4_2 ), .MemToReg_2(EX_MemToReg),
    .R1_2(EX_R1Data), .Bne_2(\id_ex_重定向_1_bne_2 ), .R2_2(EX_R2Data), .Beq_2(\id_ex_重定向_1_beq_2 ),
    .JAL_2(EX_J_signal), .Imm_I_2(\id_ex_重定向_1_imm_i_2 ), .Imm_S_2(\id_ex_重定向_1_imm_s_2 ),
    .JALR_2(\id_ex_重定向_1_jalr_2 ), .Imm_B_2(\id_ex_重定向_1_imm_b_2 ), .URET_2(EX_URET),
    .Imm_J_2(\id_ex_重定向_1_imm_j_2 ), .ecall_2(\id_ex_重定向_1_ecall_2 ), .Sltiu_2(\id_ex_重定向_1_sltiu_2 ),
    .Sb_2(\id_ex_重定向_1_sb_2 ), .Blt_2(\id_ex_重定向_1_blt_2 ), .S_Type_2(EX_S_signal), .R1_F_2(EX_R1_F),
    .R2_F_2(EX_R2_F));
  Counter #(.width(16), .max('hffff), .ongoal("wrap"), .trigger("rising"), .behavior("new")) counter_2 (
    .count(\无条件分支 ), .Q(\无条件分支数 ), .clk(CLK), .clr(RST));  // open: load, D, carry, preset, down
  or or_5 (\无条件分支 , \id_ex_重定向_1_jalr_2 , EX_J_signal);
  or or_6 (EX_B_signal, \id_ex_重定向_1_beq_2 , \id_ex_重定向_1_bne_2 , \id_ex_重定向_1_blt_2 );
  assign bit_extender_1_out = {{20{\id_ex_重定向_1_imm_i_2 [11]}}, \id_ex_重定向_1_imm_i_2 };  // Bit_Extender bit_extender_1
  assign bit_extender_2_out = {{20{1'b0}}, \id_ex_重定向_1_imm_i_2 };  // Bit_Extender bit_extender_2
  assign bit_extender_3_out = {{20{\id_ex_重定向_1_imm_s_2 [11]}}, \id_ex_重定向_1_imm_s_2 };  // Bit_Extender bit_extender_3
  assign bit_extender_4_out = {{20{\id_ex_重定向_1_imm_b_2 [11]}}, \id_ex_重定向_1_imm_b_2 };  // Bit_Extender bit_extender_4
  assign bit_extender_5_out = {{12{\id_ex_重定向_1_imm_j_2 [19]}}, \id_ex_重定向_1_imm_j_2 };  // Bit_Extender bit_extender_5
  Multiplexer #(.select(2), .width(32), .disabled("Z"), .enable("false")) multiplexer_7 (
    .in1(32'h30ac), .in2(32'h3150), .in3(32'h31f4), .out(INT_Addar), .sel(\中断号 ));  // open: in0
  Multiplexer #(.select(1), .width(32), .disabled("Z"), .enable("false")) multiplexer_8 (
    .in0(bit_extender_1_out), .in1(bit_extender_2_out), .out(multiplexer_8_out), .sel(\id_ex_重定向_1_sltiu_2 ));
  Multiplexer #(.select(2), .width(32), .disabled("Z"), .enable("false")) multiplexer_9 (
    .in0(multiplexer_8_out), .in1(bit_extender_3_out), .in2(bit_extender_4_out), .in3(bit_extender_5_out),
    .out(multiplexer_9_out), .sel(EX_Imm_Sel));
  Counter #(.width(16), .max('hffff), .ongoal("wrap"), .trigger("rising"), .behavior("new")) counter_3 (
    .count(B_Jump), .Q(\条件分支成功数 ), .clk(CLK), .clr(RST));  // open: load, D, carry, preset, down
  Multiplexer #(.select(1), .width(32), .disabled("Z"), .enable("false")) multiplexer_10 (
    .in0(RelocationR2Data), .in1(multiplexer_9_out), .out(multiplexer_10_out), .sel(\id_ex_重定向_1_alusrcb_2 ));
  Shifter #(.width(32), .shift("ll")) shifter_1 (.in(multiplexer_9_out), .\dist (5'b00001), .out(shifter_1_out));
  ALU alu_1 (
    .X(RelocationR1Data), .Y(multiplexer_10_out), .AluOP(\id_ex_重定向_1_aluop_2 ), .Equal(alu_1_equal),
    .Result(EX_AluData), .out_6(alu_1_out_6));  // open: Result_2, out_4
  Adder #(.width(32)) adder_2 (.a(EX_PC), .b(shifter_1_out), .out(adder_2_out));  // open: cin, cout
  Multiplexer #(.select(2), .width(32), .disabled("Z"), .enable("false")) multiplexer_11 (
    .in0(EX_R1Data), .in1(RDin), .in2({MEM_AluData, Bit_Sel}), .out(RelocationR1Data), .sel(EX_R1_F));  // open: in3
  Multiplexer #(.select(2), .width(32), .disabled("Z"), .enable("false")) multiplexer_12 (
    .in0(EX_R2Data), .in1(RDin), .in2({MEM_AluData, Bit_Sel}), .out(RelocationR2Data), .sel(EX_R2_F));  // open: in3
  or or_7 (or_7_out, BranchTaken, LoadUse);
  and and_10 (and_10_out, \id_ex_重定向_1_beq_2 , alu_1_equal);
  or or_8 (B_Jump, and_10_out, and_11_out, and_12_out);
  and and_11 (and_11_out, \id_ex_重定向_1_bne_2 , ~alu_1_equal);  // AND_Gate
  and and_12 (and_12_out, \id_ex_重定向_1_blt_2 , alu_1_out_6);
  Register #(.width(1), .trigger("rising"), .Select("low")) register_2 (
    .D(BranchTaken), .Q(register_2_q), .clk(CLK), .clr(RST));  // open: en
  Register #(.width(1), .trigger("rising"), .Select("low")) register_3 (
    .D(LoadUse), .Q(register_3_q), .clk(CLK), .clr(RST));  // open: en
  Register #(.width(1), .trigger("rising"), .Select("low")) register_4 (
    .D(EX_URET), .Q(register_4_q), .clk(CLK), .clr(RST));  // open: en
  Counter #(.width(16), .max('hffff), .ongoal("wrap"), .trigger("rising"), .behavior("new")) counter_4 (
    .load(BranchTaken), .D(adder_3_out), .count(or_7_out), .Q(\插入气泡数 ), .clk(CLK), .clr(RST));  // open: carry, preset, down
  or or_9 (BranchTaken, \id_ex_重定向_1_jalr_2 , B_Jump, EX_J_signal);
  or or_10 (or_10_out, INT, RST);
  Register #(.width(1), .trigger("rising"), .Select("low")) register_5 (
    .D(register_2_q), .Q(register_5_q[0]), .clk(CLK), .clr(RST));  // open: en
  Register #(.width(1), .trigger("rising"), .Select("low")) register_6 (
    .D(register_5_q[0]), .Q(register_5_q[1]), .clk(CLK), .clr(RST));  // open: en
  Register #(.width(1), .trigger("rising"), .Select("low")) register_7 (
    .D(register_3_q), .Q(register_7_q), .clk(CLK), .clr(RST));  // open: en
  Adder #(.width(16)) adder_3 (.a(\插入气泡数 ), .b(16'h2), .out(adder_3_out));  // open: cin, cout
  and and_13 (and_13_out, halt, ~Go);  // AND_Gate
  EX_MEM ex_mem_1 (
    .CLK(CLK), .\RST_高电平有效 (or_10_out), .\en_低电平有效 (and_13_out), .RegWrite(EX_RegWrite),
    .MemWrite(\id_ex_重定向_1_memwrite_2 ), .IR(EX_IR), .MemToReg(EX_MemToReg), .JAL(EX_J_signal), .PC(EX_PC),
    .JALR(\id_ex_重定向_1_jalr_2 ), .PC_4(\id_ex_重定向_1_pc_4_2 ), .ecall(\id_ex_重定向_1_ecall_2 ),
    .R1(RelocationR1Data), .Sb(\id_ex_重定向_1_sb_2 ), .R2(RelocationR2Data), .AluData(EX_AluData),
    .RegWrite_2(MEM_RegWrite), .MemWrite_2(MemWrite), .IR_2(MEM_IR), .MemToReg_2(ex_mem_1_memtoreg_2),
    .JAL_2(ex_mem_1_jal_2), .PC_2(M_PC), .JALR_2(ex_mem_1_jalr_2), .PC_4_2(ex_mem_1_pc_4_2),
    .ecall_2(ex_mem_1_ecall_2), .R1_2(MEM_R1Data), .Sb_2(sb), .R2_2(MDin), .AluData_2({MEM_AluData, Bit_Sel}));
  or or_11 (register_5_q[2], register_7_q, register_4_q);
  Decoder #(.select(2), .tristate("false"), .disabled("Z"), .enable("false")) decoder_2 (
    .out0(decoder_2_out0[0]), .out1(decoder_2_out0[1]), .out2(decoder_2_out0[2]), .out3(decoder_2_out0[3]),
    .sel(Bit_Sel));
  Counter #(.width(16), .max('hffff), .ongoal("wrap"), .trigger("rising"), .behavior("new")) counter_5 (
    .count(LoadUse), .Q(\LoadUse次数 ), .clk(CLK), .clr(RST));  // open: load, D, carry, preset, down
  assign bit_extender_6_out = {{3{1'b0}}, Bit_Sel};  // Bit_Extender bit_extender_6
  Multiplier #(.width(5)) multiplier_1 (
    .a(bit_extender_6_out), .b(5'b01000), .out(multiplier_1_out));  // open: cin, cout
  Multiplexer #(.select(1), .width(4), .disabled("Z"), .enable("false")) multiplexer_13 (
    .in0(4'b1111), .in1(decoder_2_out0), .out(RAM_Sel), .sel(sb));
  Multiplexer #(.select(3), .width(32), .disabled("Z"), .enable("false")) multiplexer_14 (
    .in0(M_PC), .in1(ID_PC), .in2(EX_PC), .in4(EX_PC), .out(Break_PC), .sel(register_5_q));  // open: in3, in5, in6, in7
  // cs3410_MIPS_RAM mips_ram_1: pin names not known; wires that end beside it: MEM_AluData[21:2], MemData, MemWrite, RAM_Sel, CLK, mips_ram_1_p6, RST, mips_ram_1_p8
  not not_3 (mips_ram_1_p6, MemWrite);
  Shifter #(.width(32), .shift("ll")) shifter_2 (.in(MDin), .\dist (multiplier_1_out), .out(shifter_2_out));
  or or_12 (or_12_out, INT, RST);
  and and_14 (and_14_out, halt, ~Go);  // AND_Gate
  Multiplexer #(.select(1), .width(32), .disabled("Z"), .enable("false")) multiplexer_15 (
    .in0(MDin), .in1(shifter_2_out), .out(MemData), .sel(sb));
  MEM_WB mem_wb_1 (
    .CLK(CLK), .\RST_高电平有效 (or_12_out), .\en_低电平有效 (and_14_out), .RegWrite(MEM_RegWrite), .IR(MEM_IR),
    .MemToReg(ex_mem_1_memtoreg_2), .JAL(ex_mem_1_jal_2), .PC(M_PC), .JALR(ex_mem_1_jalr_2),
    .PC_4(ex_mem_1_pc_4_2), .ecall(ex_mem_1_ecall_2), .R1(MEM_R1Data), .R2(MDin),
    .AluData({MEM_AluData, Bit_Sel}), .MemData(mips_ram_1_p8), .RegWrite_2(RegWrite), .IR_2(WB_IR),
    .MemToReg_2(mem_wb_1_memtoreg_2), .JAL_2(mem_wb_1_jal_2), .PC_2(WB_PC), .JALR_2(mem_wb_1_jalr_2),
    .PC_4_2(WB_PC_4), .ecall_2(ecall), .R1_2(WB_R1Data), .R2_2(WB_R2Data), .AluData_2(mem_wb_1_aludata_2),
    .MemData_2(mem_wb_1_memdata_2));
  Multiplexer #(.select(1), .width(32), .disabled("Z"), .enable("false")) multiplexer_16 (
    .in0(mem_wb_1_aludata_2), .in1(mem_wb_1_memdata_2), .out(multiplexer_16_out), .sel(mem_wb_1_memtoreg_2));
  Register #(.width(32), .trigger("falling"), .Select("low")) EPC (
    .D(Break_PC), .en(INT), .Q(RET_PC), .clk(CLK), .clr(RST));
  or or_13 (or_13_out, mem_wb_1_jalr_2, mem_wb_1_jal_2);
  Multiplexer #(.select(1), .width(32), .disabled("Z"), .enable("false")) multiplexer_17 (
    .in0(multiplexer_16_out), .in1(WB_PC_4), .out(RDin), .sel(or_13_out));
  not not_4 (not_4_out, halt);
  Counter #(.width(16), .max('hffff), .ongoal("stay"), .trigger("rising"), .behavior("old")) counter_6 (
    .count(not_4_out), .Q(\总周期数 ), .clk(CLK));  // open: load, D, carry, clr, preset
  or or_14 (or_14_out, EX_B_signal, EX_J_signal);
  or or_15 (or_15_out, EX_J_signal, EX_S_signal);
  Comparator #(.width(32), .mode("unsigned")) comparator_4 (
    .a(WB_R1Data), .b(32'h22), .eq(comparator_4_eq));  // open: gt, lt
  Register #(.width(32), .trigger("rising"), .Select("low")) register_8 (
    .D(WB_R2Data), .en(Ledout), .Q(LedData), .clk(CLK), .clr(RST));
  and and_15 (EX_Imm_Sel[1], ~EX_S_signal, or_14_out);  // AND_Gate
  and and_16 (EX_Imm_Sel[0], or_15_out, ~EX_B_signal);  // AND_Gate
  and and_17 (and_17_out, ecall, ~comparator_4_eq);  // AND_Gate
  and and_18 (Ledout, comparator_4_eq, ecall);
  D_Flip_Flop #(.trigger("falling"), .Pre_Clr_Positions("ABOVE_BELOW"), .NegatePresetClear("false"), .enable("true"), .NewFFLayout("true")) d_ff_3 (
    .clk(CLK), .D(and_17_out), .Q(halt), .en(ecall), .reset(Go));  // open: Qn, preset

  // Other names for the same wires on the sheet: Opcode[4:0] = IF_IR[6:2]; IF_IR[14:12] = Funct3;
  //   MEM_AluData[1:0] = Bit_Sel; MEM_PC[31:0] = M_PC; MEM_R2Data[31:0] = MDin

  // Notes on the sheet:
  //   中断源
  //   时空图监测，可删除
  //   中断等待指示
  //   rd
  //   数码管输出
  //   中断控制逻辑
  //   生成LoseUse信号
  //   指令存储器
  //   指令探针
  //   contents of rom_1 (hex, n*v repeats v):
  //   7d000113 100413 1f41993 41f9d993 433 c00913 800b13 140413 f47413 800293 100313 499993 89e9b3 1300533
  //   2200893 73 406282b3 fe0294e3 140413 f00f93 1f47433 1c41413 800293 100313 49d993 89e9b3 1300533
  //   2200893 73 406282b3 fe0294e3 1c45413 406b0b33 b0463 f95ff06f 2b3 fff2c293 1029293 fff2e293 500533
  //   2200893 73 f5dff06f 1112023 410113 a12023 410113 812023 410113 1312023 410113 1412023 410113 1512023
  //   410113 1612023 410113 100b13 300a13 100a93 1600433 441413 14469b3 1300533 2200893 73 fe0416e3
  //   415a0a33 fe0a10e3 ffc10113 12b03 ffc10113 12a83 ffc10113 12a03 ffc10113 12983 ffc10113 12403
  //   ffc10113 12503 ffc10113 12883 200073 1112023 410113 a12023 410113 812023 410113 1312023 410113
  //   1412023 410113 1512023 410113 1612023 410113 200b13 300a13 100a93 1600433 441413 14469b3 1300533
  //   2200893 73 fe0416e3 415a0a33 fe0a10e3 ffc10113 12b03 ffc10113 12a83 ffc10113 12a03 ffc10113 12983
  //   ffc10113 12403 ffc10113 12503 ffc10113 12883 200073 1112023 410113 a12023 410113 812023 410113
  //   1312023 410113 1412023 410113 1512023 410113 1612023 410113 300b13 300a13 100a93 1600433 441413
  //   14469b3 1300533 2200893 73 fe0416e3 415a0a33 fe0a10e3 ffc10113 12b03 ffc10113 12a83 ffc10113 12a03
  //   ffc10113 12983 ffc10113 12403 ffc10113 12503 ffc10113 12883 200073
  //   中断使能信号产生
  //   中断请求信号产生
  //   控制位
  //   流水调试日志用
  //   暂停节拍，不能为0
  //   rs1
  //   rs2
  //   戳工具置1进入计数暂停模式，ctrl+k时钟自动运行到对应节拍暂停
  //   ctrl+k关闭时钟连续运行，将控制位置零，进入单步调试模式调试
  //   JAL
  //   JALR
  //   URET
  //   Sltiu
  //   Sb
  //   rd
  //   rd
  //   Beq
  //   Bne
  //   MemToReg
  //   MemWrite
  //   AluOP
  //   AluSrcB
  //   RegWrite
  //   Blt
  //   I型指令立即数
  //   S型指令立即数
  //   B型指令立即数
  //   J型指令立即数
  //   生成R1_F R2_F信号
  //   中断清零信号产生
  //   可计数暂停的时钟源
  //   为方便自动评测，需要输出流水线各段保存的PC值，注意是PC不是PC+4，另外ID段寄存器写入信息，Mem段内存写入信息也要输出
  //   中断入口逻辑
  //   重定向设置
  //   ID.PC
  //   EX.PC
  //   EX.PC
  //   EX.PC
  //   保护现场
  //   计算Sb对应的MemData
  //   rd
  //   LedData显示控制
  //   周期信号显示控制
  //   EX阶段 生成立即数选择信号
  //   生成停机信号halt和LED显示信号Ledout
endmodule

module \重定向流水线_动态分支预测  (
  output RegWrite,
  output MemWrite,
  output [31:0] IF_PC,
  output [31:0] ID_PC,
  output [31:0] EX_PC,
  output [31:0] M_PC,
  output [31:0] WB_PC,
  output [31:0] RDin,
  output [31:0] MDin,
  output [31:0] LedData
);

  wire alu_1_equal, alu_1_out_6, and_1_out, and_2_out, and_3_out, and_4_out, and_5_out, and_6_out, and_7_out,
       and_8_out, and_11_out, B_Jump, BranchTaken, btb_1_predictjump, CLK, clock_1_out, clock_2_out,
       comparator_1_eq, comparator_1_lt, comparator_2_eq, comparator_3_eq, d_ff_1_q, ecall, EX_B_signal,
       EX_Branch, EX_J_signal, EX_Jalr, ex_mem_1_ecall_2, ex_mem_1_jal_2, ex_mem_1_jalr_2,
       ex_mem_1_memtoreg_2, EX_MemToReg, EX_PredictJump, EX_RegWrite, EX_S_signal, Go, halt,
       \id_ex_动态分支预测_1_alusrcb_2 , \id_ex_动态分支预测_1_beq_2 , \id_ex_动态分支预测_1_blt_2 , \id_ex_动态分支预测_1_bne_2 ,
       \id_ex_动态分支预测_1_ecall_2 , \id_ex_动态分支预测_1_memwrite_2 , \id_ex_动态分支预测_1_sb_2 ,
       \id_ex_动态分支预测_1_sltiu_2 , \if_id_动态分支预测_1_predictjump_2 , IR1, IR2, IR3, Ledout, LoadUse,
       MEM_RegWrite, mem_wb_1_jal_2, mem_wb_1_jalr_2, mem_wb_1_memtoreg_2, mips_ram_1_p6, nand_1_out,
       not_1_out, not_2_out, not_5_out, or_1_out, or_4_out, or_5_out, or_6_out, or_11_out, or_12_out,
       or_13_out, or_14_out, PredictError, \r1r2使用检测_1_r1used , \r1r2使用检测_1_r2used , \r1r2使用检测_2_r1used ,
       \r1r2使用检测_2_r2used , RST, sb, W1, W2, W3, \单周期硬布线控制器_1_alu_src , \单周期硬布线控制器_1_beq , \单周期硬布线控制器_1_blt ,
       \单周期硬布线控制器_1_bne , \单周期硬布线控制器_1_ecall , \单周期硬布线控制器_1_jal , \单周期硬布线控制器_1_jalr , \单周期硬布线控制器_1_memtoreg ,
       \单周期硬布线控制器_1_memwrite , \单周期硬布线控制器_1_regwrite , \单周期硬布线控制器_1_s_type , \单周期硬布线控制器_1_sb ,
       \单周期硬布线控制器_1_sltiu , \单周期硬布线控制器_1_uret , \无条件分支 ;
  wire [0:0] or_3_out;
  wire [1:0] Bit_Sel, EX_Imm_Sel, EX_R1_F, EX_R2_F, ID_R1_F, ID_R2_F;
  wire [3:0] decoder_1_out0, \id_ex_动态分支预测_1_aluop_2 , RAM_Sel, \单周期硬布线控制器_1_alu_op ;
  wire [4:0] bit_extender_6_out, ID_R1, ID_R2, multiplier_1_out;
  wire [11:0] \id_ex_动态分支预测_1_imm_b_2 , \id_ex_动态分支预测_1_imm_i_2 , \id_ex_动态分支预测_1_imm_s_2 ;
  wire [12:0] CNT_num;
  wire [15:0] adder_3_out, \LoadUse次数 , \总周期数 , \插入气泡数 , \无条件分支数 , \条件分支成功数 ;
  wire [19:0] \id_ex_动态分支预测_1_imm_j_2 ;
  wire [31:0] bit_extender_1_out, bit_extender_2_out, bit_extender_3_out, bit_extender_4_out,
       bit_extender_5_out, btb_1_jumpaddr, EX_AluData, EX_B_JAddr, EX_BranchAddr, EX_IR, ex_mem_1_pc_4_2,
       EX_PC_4, EX_R1Data, EX_R2Data, ID_IR, ID_R1Data, \if_id_动态分支预测_1_pc_4_2 , IF_IR, IF_PC_4, MEM_IR,
       MEM_R1Data, mem_wb_1_aludata_2, mem_wb_1_memdata_2, MemData, mips_ram_1_p8, multiplexer_1_out,
       multiplexer_2_out, multiplexer_3_out, multiplexer_4_out, multiplexer_8_out, multiplexer_9_out,
       multiplexer_10_out, multiplexer_14_out, \regifile_下降沿_1_r2 , RelocationR1Data, RelocationR2Data,
       shifter_1_out, shifter_2_out, undriven, WB_IR, WB_PC_4, WB_R1Data, WB_R2Data;
  wire [31:2] MEM_AluData;

  Button \u_总复位  (.out(RST));
  Button _1 (.out(IR1));
  Button _2 (.out(IR2));
  Button _3 (.out(IR3));
  // Probe on \总周期数 
  // Probe on \总周期数 
  Button \u_继续运行  (.out(Go));
  LED #(.active("true")) led_1 (.in(W1));
  LED #(.active("true")) led_2 (.in(W2));
  LED #(.active("true")) led_3 (.in(W3));
  or or_1 (or_1_out, B_Jump, EX_J_signal);
  Multiplexer #(.select(1), .width(32), .disabled("Z"), .enable("false")) multiplexer_1 (
    .in0(EX_PC_4), .in1(EX_B_JAddr), .out(multiplexer_1_out), .sel(or_1_out));
  Hex_Digit_Display hex_digit_display_1 (.value(LedData[31:28]));  // open: dp
  // Probe on IF_PC[19:0]
  // RiscV_Probe riscv_probe_1: pin names not known; wires that end beside it: IF_IR
  Multiplexer #(.select(1), .width(32), .disabled("Z"), .enable("false")) multiplexer_2 (
    .in0(multiplexer_4_out), .in1(multiplexer_3_out), .out(multiplexer_2_out), .sel(PredictError));
  Multiplexer #(.select(1), .width(32), .disabled("Z"), .enable("false")) multiplexer_3 (
    .in0(multiplexer_1_out), .in1(EX_AluData), .out(multiplexer_3_out), .sel(EX_Jalr));
  not not_1 (not_1_out, LoadUse);
  Hex_Digit_Display hex_digit_display_2 (.value(LedData[23:20]));  // open: dp
  Hex_Digit_Display hex_digit_display_3 (.value(LedData[27:24]));  // open: dp
  // Probe on ID_PC[19:0]
  // RiscV_Probe riscv_probe_2: pin names not known; wires that end beside it: ID_IR
  Register #(.width(32), .trigger("rising"), .Select("low")) PC (
    .D(multiplexer_2_out), .en(and_1_out), .Q(IF_PC), .clk(CLK), .clr(RST));
  and and_1 (and_1_out, not_1_out, not_2_out);
  not not_2 (not_2_out, halt);
  \R1R2使用检测  \r1r2使用检测_1  (
    .OP2(ID_IR[2]), .OP3(ID_IR[3]), .OP4(ID_IR[4]), .OP5(ID_IR[5]), .OP6(ID_IR[6]), .F12(ID_IR[12]),
    .F13(ID_IR[13]), .F14(ID_IR[14]), .F25(ID_IR[25]), .F30(ID_IR[30]), .R1Used(\r1r2使用检测_1_r1used ),
    .R2Used(\r1r2使用检测_1_r2used ));
  or or_2 (EX_Branch, EX_Jalr, EX_J_signal, EX_B_signal);
  Hex_Digit_Display hex_digit_display_4 (.value(LedData[15:12]));  // open: dp
  Hex_Digit_Display hex_digit_display_5 (.value(LedData[19:16]));  // open: dp
  Adder #(.width(32)) adder_1 (.a(IF_PC), .b(32'h4), .out(IF_PC_4));  // open: cin, cout
  Hex_Digit_Display hex_digit_display_6 (.value(LedData[7:4]));  // open: dp
  Hex_Digit_Display hex_digit_display_7 (.value(LedData[11:8]));  // open: dp
  Clock #(.highDuration(1), .lowDuration(1)) clock_1 (.out(clock_1_out));
  // Probe on EX_PC[19:0]
  // RiscV_Probe riscv_probe_3: pin names not known; wires that end beside it: clock_1_out, EX_IR, CLK
  Multiplexer #(.select(1), .width(32), .disabled("Z"), .enable("false")) multiplexer_4 (
    .in0(IF_PC_4), .in1(btb_1_jumpaddr), .out(multiplexer_4_out), .sel(btb_1_predictjump));
  Hex_Digit_Display hex_digit_display_8 (.value(LedData[3:0]));  // open: dp
  ROM #(.addrWidth(10), .dataWidth(32), .Select("high")) rom_1 (.addr(IF_PC[11:2]), .data(IF_IR));
  BTB btb_1 (
    .PC(IF_PC), .EX_PC(EX_PC), .EX_BranchAddr(EX_BranchAddr), .EX_Branch(EX_Branch),
    .EX_BranchTaken(BranchTaken), .CLK(CLK), .PredictJump(btb_1_predictjump), .JumpAddr(btb_1_jumpaddr),
    .\initial (2'b00));
  // Probe on \总周期数 
  // Probe on M_PC[19:0]
  // RiscV_Probe riscv_probe_4: pin names not known; wires that end beside it: MEM_IR
  // RiscV_Probe riscv_probe_5: pin names not known; wires that end beside it: IF_IR
  \LoadUse信号生成  \loaduse信号生成_1  (
    .R1Used(\r1r2使用检测_1_r1used ), .EX_MemToReg(EX_MemToReg), .ID_R1(ID_R1), .EX_RD(EX_IR[11:7]),
    .ID_R2(ID_R2), .R2Used(\r1r2使用检测_1_r2used ), .LoadUse(LoadUse));
  or or_3 (or_3_out[0], EX_J_signal, EX_B_signal);
  // Probe on \总周期数 
  // Probe on \无条件分支数 
  // Probe on \条件分支成功数 
  // Probe on \插入气泡数 
  // Probe on \LoadUse次数 
  or or_4 (or_4_out, PredictError, RST);
  Multiplexer #(.select(2), .width(32), .disabled("Z"), .enable("false")) multiplexer_5 (
    .in0(IF_PC), .in1(EX_B_JAddr), .in2(EX_AluData), .in3(undriven), .out(EX_BranchAddr),
    .sel({EX_Jalr, or_3_out[0]}));
  // Probe on IF_PC[11:0]
  // Probe on WB_PC[19:0]
  // RiscV_Probe riscv_probe_6: pin names not known; wires that end beside it: WB_IR
  and and_2 (and_2_out, halt, ~Go);  // AND_Gate
  or or_5 (or_5_out, LoadUse, and_2_out);
  \IF_ID_动态分支预测  \if_id_动态分支预测_1  (
    .CLK(CLK), .\RST_高电平有效 (or_4_out), .\en_低电平有效 (or_5_out), .IR(IF_IR), .PC(IF_PC), .PC_4(IF_PC_4),
    .PredictJump(btb_1_predictjump), .IR_2(ID_IR), .PC_2(ID_PC), .PC_4_2(\if_id_动态分支预测_1_pc_4_2 ),
    .PredictJump_2(\if_id_动态分支预测_1_predictjump_2 ));
  // Probe on EX_PC[11:0]
  // Probe on ID_PC[11:0]
  // Probe on M_PC[11:0]
  D_Flip_Flop #(.trigger("high"), .Pre_Clr_Positions("LEGACY"), .NegatePresetClear("false"), .enable("true"), .NewFFLayout("false")) d_ff_1 (.Q(d_ff_1_q));  // open: clk, D, Qn, preset, en, reset
  // Probe on 13'hc
  \单周期硬布线控制器  \u_单周期硬布线控制器_1  (
    .Funct({ID_IR[30], ID_IR[25], ID_IR[14:12]}), .OP(ID_IR[6:2]), .ALU_OP(\单周期硬布线控制器_1_alu_op ),
    .MemToReg(\单周期硬布线控制器_1_memtoreg ), .MemWrite(\单周期硬布线控制器_1_memwrite ), .ALU_SRC(\单周期硬布线控制器_1_alu_src ),
    .RegWrite(\单周期硬布线控制器_1_regwrite ), .ecall(\单周期硬布线控制器_1_ecall ), .S_type(\单周期硬布线控制器_1_s_type ),
    .Jalr(\单周期硬布线控制器_1_jalr ), .Beq(\单周期硬布线控制器_1_beq ), .JAL(\单周期硬布线控制器_1_jal ), .Bne(\单周期硬布线控制器_1_bne ),
    .in_3(ID_IR[21]), .uret(\单周期硬布线控制器_1_uret ), .Sltiu(\单周期硬布线控制器_1_sltiu ), .Sb(\单周期硬布线控制器_1_sb ),
    .Blt(\单周期硬布线控制器_1_blt ));
  Multiplexer #(.select(1), .width(5), .disabled("Z"), .enable("false")) multiplexer_6 (
    .in0(ID_IR[19:15]), .in1(5'b10001), .out(ID_R1), .sel(\单周期硬布线控制器_1_ecall ));
  Multiplexer #(.select(1), .width(5), .disabled("Z"), .enable("false")) multiplexer_7 (
    .in0(ID_IR[24:20]), .in1(5'b01010), .out(ID_R2), .sel(\单周期硬布线控制器_1_ecall ));
  // Probe on WB_PC[11:0]
  Comparator #(.width(13), .mode("twosComplement")) comparator_1 (
    .a(CNT_num), .b(13'hc), .eq(comparator_1_eq), .lt(comparator_1_lt));  // open: gt
  Clock #(.highDuration(1), .lowDuration(1)) clock_2 (.out(clock_2_out));
  \R1R2使用检测  \r1r2使用检测_2  (
    .OP2(ID_IR[2]), .OP3(ID_IR[3]), .OP4(ID_IR[4]), .OP5(ID_IR[5]), .OP6(ID_IR[6]), .F12(ID_IR[12]),
    .F13(ID_IR[13]), .F14(ID_IR[14]), .F25(ID_IR[25]), .F30(ID_IR[30]), .R1Used(\r1r2使用检测_2_r1used ),
    .R2Used(\r1r2使用检测_2_r2used ));
  nand nand_1 (nand_1_out, d_ff_1_q, comparator_1_eq);
  Counter #(.width(13), .max('h1fff), .ongoal("stay"), .trigger("rising"), .behavior("old")) counter_1 (
    .count(comparator_1_lt), .Q(CNT_num), .clk(clock_2_out));  // open: load, D, carry, clr, preset
  \Regifile_下降沿  \regifile_下降沿_1  (
    .Din(RDin), .Clk(CLK), .R1(ID_R1Data), .R2(\regifile_下降沿_1_r2 ), .WE(RegWrite), .W_num(WB_IR[11:7]),
    .R1_num(ID_R1), .R2_num(ID_R2));
  assign CLK = nand_1_out ? clock_2_out : 1'bz;  // Controlled_Buffer controlled_buffer_1
  and and_3 (and_3_out, halt, ~Go);  // AND_Gate
  or or_6 (or_6_out, PredictError, RST, LoadUse);
  \ID_EX_动态分支预测  \id_ex_动态分支预测_1  (
    .CLK(CLK), .\RST_高电平有效 (or_6_out), .\en_低电平有效 (and_3_out), .RegWrite(\单周期硬布线控制器_1_regwrite ), .IR(ID_IR),
    .AluSrcB(\单周期硬布线控制器_1_alu_src ), .AluOP(\单周期硬布线控制器_1_alu_op ), .PC(ID_PC),
    .MemWrite(\单周期硬布线控制器_1_memwrite ), .PC_4(\if_id_动态分支预测_1_pc_4_2 ), .MemToReg(\单周期硬布线控制器_1_memtoreg ),
    .R1(ID_R1Data), .Bne(\单周期硬布线控制器_1_bne ), .R2(\regifile_下降沿_1_r2 ), .Beq(\单周期硬布线控制器_1_beq ),
    .JAL(\单周期硬布线控制器_1_jal ), .Imm_I(ID_IR[31:20]), .Imm_S({ID_IR[31:25], ID_IR[11:7]}),
    .JALR(\单周期硬布线控制器_1_jalr ), .Imm_B({ID_IR[31], ID_IR[7], ID_IR[30:25], ID_IR[11:8]}),
    .URET(\单周期硬布线控制器_1_uret ), .Imm_J({ID_IR[31], ID_IR[19:12], ID_IR[20], ID_IR[30:21]}),
    .ecall(\单周期硬布线控制器_1_ecall ), .Sltiu(\单周期硬布线控制器_1_sltiu ), .Sb(\单周期硬布线控制器_1_sb ), .Blt(\单周期硬布线控制器_1_blt ),
    .S_Type(\单周期硬布线控制器_1_s_type ), .R1_F(ID_R1_F), .R2_F(ID_R2_F),
    .PredictJump(\if_id_动态分支预测_1_predictjump_2 ), .RegWrite_2(EX_RegWrite), .IR_2(EX_IR),
    .AluSrcB_2(\id_ex_动态分支预测_1_alusrcb_2 ), .AluOP_2(\id_ex_动态分支预测_1_aluop_2 ), .PC_2(EX_PC),
    .MemWrite_2(\id_ex_动态分支预测_1_memwrite_2 ), .PC_4_2(EX_PC_4), .MemToReg_2(EX_MemToReg), .R1_2(EX_R1Data),
    .Bne_2(\id_ex_动态分支预测_1_bne_2 ), .R2_2(EX_R2Data), .Beq_2(\id_ex_动态分支预测_1_beq_2 ), .JAL_2(EX_J_signal),
    .Imm_I_2(\id_ex_动态分支预测_1_imm_i_2 ), .Imm_S_2(\id_ex_动态分支预测_1_imm_s_2 ), .JALR_2(EX_Jalr),
    .Imm_B_2(\id_ex_动态分支预测_1_imm_b_2 ), .Imm_J_2(\id_ex_动态分支预测_1_imm_j_2 ),
    .ecall_2(\id_ex_动态分支预测_1_ecall_2 ), .Sltiu_2(\id_ex_动态分支预测_1_sltiu_2 ), .Sb_2(\id_ex_动态分支预测_1_sb_2 ),
    .Blt_2(\id_ex_动态分支预测_1_blt_2 ), .S_Type_2(EX_S_signal), .R1_F_2(EX_R1_F), .R2_F_2(EX_R2_F),
    .PredictJump_2(EX_PredictJump));  // open: URET_2
  Pull_Resistor #(.pull(1)) pull_resistor_1 (.node(CLK));
  \R1_F_R2_F信号生成  \r1_f_r2_f信号生成_1  (
    .R1Used(\r1r2使用检测_2_r1used ), .ID_R1(ID_R1), .EX_RegWrite(EX_RegWrite), .EX_RD(EX_IR[11:7]),
    .MEM_RegWrite(MEM_RegWrite), .MEM_RD(MEM_IR[11:7]), .R2Used(\r1r2使用检测_2_r2used ), .ID_R2(ID_R2),
    .R1_F(ID_R1_F), .R2_F(ID_R2_F));
  or or_7 (\无条件分支 , EX_Jalr, EX_J_signal);
  or or_8 (EX_B_signal, \id_ex_动态分支预测_1_beq_2 , \id_ex_动态分支预测_1_bne_2 , \id_ex_动态分支预测_1_blt_2 );
  assign bit_extender_1_out = {{20{\id_ex_动态分支预测_1_imm_i_2 [11]}}, \id_ex_动态分支预测_1_imm_i_2 };  // Bit_Extender bit_extender_1
  assign bit_extender_2_out = {{20{1'b0}}, \id_ex_动态分支预测_1_imm_i_2 };  // Bit_Extender bit_extender_2
  assign bit_extender_3_out = {{20{\id_ex_动态分支预测_1_imm_s_2 [11]}}, \id_ex_动态分支预测_1_imm_s_2 };  // Bit_Extender bit_extender_3
  assign bit_extender_4_out = {{20{\id_ex_动态分支预测_1_imm_b_2 [11]}}, \id_ex_动态分支预测_1_imm_b_2 };  // Bit_Extender bit_extender_4
  assign bit_extender_5_out = {{12{\id_ex_动态分支预测_1_imm_j_2 [19]}}, \id_ex_动态分支预测_1_imm_j_2 };  // Bit_Extender bit_extender_5
  Multiplexer #(.select(1), .width(32), .disabled("Z"), .enable("false")) multiplexer_8 (
    .in0(bit_extender_1_out), .in1(bit_extender_2_out), .out(multiplexer_8_out),
    .sel(\id_ex_动态分支预测_1_sltiu_2 ));
  Counter #(.width(16), .max('hffff), .ongoal("wrap"), .trigger("rising"), .behavior("new")) counter_2 (
    .count(\无条件分支 ), .Q(\无条件分支数 ), .clk(CLK), .clr(RST));  // open: load, D, carry, preset, down
  Multiplexer #(.select(1), .width(32), .disabled("Z"), .enable("false")) multiplexer_9 (
    .in0(RelocationR2Data), .in1(multiplexer_10_out), .out(multiplexer_9_out),
    .sel(\id_ex_动态分支预测_1_alusrcb_2 ));
  Multiplexer #(.select(2), .width(32), .disabled("Z"), .enable("false")) multiplexer_10 (
    .in0(multiplexer_8_out), .in1(bit_extender_3_out), .in2(bit_extender_4_out), .in3(bit_extender_5_out),
    .out(multiplexer_10_out), .sel(EX_Imm_Sel));
  ALU alu_1 (
    .X(RelocationR1Data), .Y(multiplexer_9_out), .AluOP(\id_ex_动态分支预测_1_aluop_2 ), .Equal(alu_1_equal),
    .Result(EX_AluData), .out_6(alu_1_out_6));  // open: Result_2, out_4
  Shifter #(.width(32), .shift("ll")) shifter_1 (.in(multiplexer_10_out), .\dist (5'b00001), .out(shifter_1_out));
  and and_4 (and_4_out, \id_ex_动态分支预测_1_beq_2 , alu_1_equal);
  and and_5 (and_5_out, \id_ex_动态分支预测_1_bne_2 , ~alu_1_equal);  // AND_Gate
  or or_9 (B_Jump, and_4_out, and_5_out, and_6_out);
  and and_6 (and_6_out, \id_ex_动态分支预测_1_blt_2 , alu_1_out_6);
  Adder #(.width(32)) adder_2 (.a(EX_PC), .b(shifter_1_out), .out(EX_B_JAddr));  // open: cin, cout
  Counter #(.width(16), .max('hffff), .ongoal("wrap"), .trigger("rising"), .behavior("new")) counter_3 (
    .count(B_Jump), .Q(\条件分支成功数 ), .clk(CLK), .clr(RST));  // open: load, D, carry, preset, down
  or or_10 (BranchTaken, EX_Jalr, B_Jump, EX_J_signal);
  Multiplexer #(.select(2), .width(32), .disabled("Z"), .enable("false")) multiplexer_11 (
    .in0(EX_R1Data), .in1(RDin), .in2({MEM_AluData, Bit_Sel}), .out(RelocationR1Data), .sel(EX_R1_F));  // open: in3
  Multiplexer #(.select(2), .width(32), .disabled("Z"), .enable("false")) multiplexer_12 (
    .in0(EX_R2Data), .in1(RDin), .in2({MEM_AluData, Bit_Sel}), .out(RelocationR2Data), .sel(EX_R2_F));  // open: in3
  and and_7 (and_7_out, halt, ~Go);  // AND_Gate
  EX_MEM ex_mem_1 (
    .CLK(CLK), .\RST_高电平有效 (RST), .\en_低电平有效 (and_7_out), .RegWrite(EX_RegWrite),
    .MemWrite(\id_ex_动态分支预测_1_memwrite_2 ), .IR(EX_IR), .MemToReg(EX_MemToReg), .JAL(EX_J_signal),
    .PC(EX_PC), .JALR(EX_Jalr), .PC_4(EX_PC_4), .ecall(\id_ex_动态分支预测_1_ecall_2 ), .R1(RelocationR1Data),
    .Sb(\id_ex_动态分支预测_1_sb_2 ), .R2(RelocationR2Data), .AluData(EX_AluData), .RegWrite_2(MEM_RegWrite),
    .MemWrite_2(MemWrite), .IR_2(MEM_IR), .MemToReg_2(ex_mem_1_memtoreg_2), .JAL_2(ex_mem_1_jal_2),
    .PC_2(M_PC), .JALR_2(ex_mem_1_jalr_2), .PC_4_2(ex_mem_1_pc_4_2), .ecall_2(ex_mem_1_ecall_2),
    .R1_2(MEM_R1Data), .Sb_2(sb), .R2_2(MDin), .AluData_2({MEM_AluData, Bit_Sel}));
  Comparator #(.width(1), .mode("twosComplement")) comparator_2 (
    .a(EX_PredictJump), .b(BranchTaken), .eq(comparator_2_eq));  // open: gt, lt
  or or_11 (or_11_out, PredictError, LoadUse);
  Counter #(.width(16), .max('hffff), .ongoal("wrap"), .trigger("rising"), .behavior("new")) counter_4 (
    .load(PredictError), .D(adder_3_out), .count(or_11_out), .Q(\插入气泡数 ), .clk(CLK), .clr(RST));  // open: carry, preset, down
  not not_3 (PredictError, comparator_2_eq);
  Adder #(.width(16)) adder_3 (.a(\插入气泡数 ), .b(16'h2), .out(adder_3_out));  // open: cin, cout
  // cs3410_MIPS_RAM mips_ram_1: pin names not known; wires that end beside it: MEM_AluData[21:2], MemData, MemWrite, RAM_Sel, CLK, mips_ram_1_p6, RST, mips_ram_1_p8
  not not_4 (mips_ram_1_p6, MemWrite);
  Decoder #(.select(2), .tristate("false"), .disabled("Z"), .enable("false")) decoder_1 (
    .out0(decoder_1_out0[0]), .out1(decoder_1_out0[1]), .out2(decoder_1_out0[2]), .out3(decoder_1_out0[3]),
    .sel(Bit_Sel));
  assign bit_extender_6_out = {{3{1'b0}}, Bit_Sel};  // Bit_Extender bit_extender_6
  Multiplier #(.width(5)) multiplier_1 (
    .a(bit_extender_6_out), .b(5'b01000), .out(multiplier_1_out));  // open: cin, cout
  Multiplexer #(.select(1), .width(4), .disabled("Z"), .enable("false")) multiplexer_13 (
    .in0(4'b1111), .in1(decoder_1_out0), .out(RAM_Sel), .sel(sb));
  Counter #(.width(16), .max('hffff), .ongoal("wrap"), .trigger("rising"), .behavior("new")) counter_5 (
    .count(LoadUse), .Q(\LoadUse次数 ), .clk(CLK), .clr(RST));  // open: load, D, carry, preset, down
  and and_8 (and_8_out, halt, ~Go);  // AND_Gate
  MEM_WB mem_wb_1 (
    .CLK(CLK), .\RST_高电平有效 (RST), .\en_低电平有效 (and_8_out), .RegWrite(MEM_RegWrite), .IR(MEM_IR),
    .MemToReg(ex_mem_1_memtoreg_2), .JAL(ex_mem_1_jal_2), .PC(M_PC), .JALR(ex_mem_1_jalr_2),
    .PC_4(ex_mem_1_pc_4_2), .ecall(ex_mem_1_ecall_2), .R1(MEM_R1Data), .R2(MDin),
    .AluData({MEM_AluData, Bit_Sel}), .MemData(mips_ram_1_p8), .RegWrite_2(RegWrite), .IR_2(WB_IR),
    .MemToReg_2(mem_wb_1_memtoreg_2), .JAL_2(mem_wb_1_jal_2), .PC_2(WB_PC), .JALR_2(mem_wb_1_jalr_2),
    .PC_4_2(WB_PC_4), .ecall_2(ecall), .R1_2(WB_R1Data), .R2_2(WB_R2Data), .AluData_2(mem_wb_1_aludata_2),
    .MemData_2(mem_wb_1_memdata_2));
  Shifter #(.width(32), .shift("ll")) shifter_2 (.in(MDin), .\dist (multiplier_1_out), .out(shifter_2_out));
  Multiplexer #(.select(1), .width(32), .disabled("Z"), .enable("false")) multiplexer_14 (
    .in0(mem_wb_1_aludata_2), .in1(mem_wb_1_memdata_2), .out(multiplexer_14_out), .sel(mem_wb_1_memtoreg_2));
  Multiplexer #(.select(1), .width(32), .disabled("Z"), .enable("false")) multiplexer_15 (
    .in0(MDin), .in1(shifter_2_out), .out(MemData), .sel(sb));
  or or_12 (or_12_out, mem_wb_1_jalr_2, mem_wb_1_jal_2);
  Multiplexer #(.select(1), .width(32), .disabled("Z"), .enable("false")) multiplexer_16 (
    .in0(multiplexer_14_out), .in1(WB_PC_4), .out(RDin), .sel(or_12_out));
  not not_5 (not_5_out, halt);
  or or_13 (or_13_out, EX_B_signal, EX_J_signal);
  or or_14 (or_14_out, EX_J_signal, EX_S_signal);
  Comparator #(.width(32), .mode("unsigned")) comparator_3 (
    .a(WB_R1Data), .b(32'h22), .eq(comparator_3_eq));  // open: gt, lt
  Register #(.width(32), .trigger("rising"), .Select("low")) register_1 (
    .D(WB_R2Data), .en(Ledout), .Q(LedData), .clk(CLK), .clr(RST));
  Counter #(.width(16), .max('hffff), .ongoal("stay"), .trigger("rising"), .behavior("old")) counter_6 (
    .count(not_5_out), .Q(\总周期数 ), .clk(CLK));  // open: load, D, carry, clr, preset
  and and_9 (EX_Imm_Sel[1], ~EX_S_signal, or_13_out);  // AND_Gate
  and and_10 (EX_Imm_Sel[0], or_14_out, ~EX_B_signal);  // AND_Gate
  and and_11 (and_11_out, ecall, ~comparator_3_eq);  // AND_Gate
  and and_12 (Ledout, comparator_3_eq, ecall);
  D_Flip_Flop #(.trigger("falling"), .Pre_Clr_Positions("ABOVE_BELOW"), .NegatePresetClear("false"), .enable("true"), .NewFFLayout("true")) d_ff_2 (
    .clk(CLK), .D(and_11_out), .Q(halt), .en(ecall), .reset(Go));  // open: Qn, preset

  // Other names for the same wires on the sheet: MEM_AluData[1:0] = Bit_Sel; MEM_PC[31:0] = M_PC;
  //   MEM_R2Data[31:0] = MDin

  // Notes on the sheet:
  //   中断源
  //   时空图监测，可删除
  //   中断等待指示
  //   rd
  //   生成EX.Branch信号
  //   数码管输出
  //   生成LoseUse信号
  //   指令存储器
  //   contents of rom_1 (hex, n*v repeats v):
  //   100493 100006f 100493 200913 300993 100006f 100493 200913 300993 100006f 100493 200913 300993
  //   100006f 100493 200913 300993 3a0000ef 100413 100493 1f49493 900533 2200893 73 24d493 48463 fedff06f
  //   900533 2200893 73 100493 249493 900533 2200893 73 48463 fedff06f 100493 1f49493 900533 2200893 73
  //   4034d493 900533 2200893 73 4044d493 900533 2200893 73 4044d493 900533 2200893 73 4044d493 900533
  //   2200893 73 4044d493 900533 2200893 73 4044d493 900533 2200893 73 4044d493 900533 2200893 73 4044d493
  //   900533 2200893 73 100413 1f41993 41f9d993 433 c00913 300b13 140413 f47413 800293 100313 499993
  //   89e9b3 1300533 2200893 73 406282b3 fe0294e3 140413 f00f93 1f47433 1c41413 800293 100313 49d993
  //   89e9b3 1300533 2200893 73 406282b3 fe0294e3 1c45413 406b0b33 b0463 f95ff06f 2b3 fff2c293 829293
  //   ff2e293 500533 2200893 73 fff00413 493 84a023 140413 448493 84a023 140413 448493 84a023 140413
  //   448493 84a023 140413 448493 84a023 140413 448493 84a023 140413 448493 84a023 140413 448493 84a023
  //   140413 448493 84a023 140413 448493 84a023 140413 448493 84a023 140413 448493 84a023 140413 448493
  //   84a023 140413 448493 84a023 140413 448493 84a023 140413 448493 84a023 140413 448493 140413 433
  //   3c00493 42983 4aa03 149a2b3 28663 134a023 1442023 ffc48493 fe9412e3 800533 2200893 73 440413 3c00493
  //   fc9416e3 3200893 73 100293 300313 800493 849493 7648493 1449493 900533 2200893 73 800e13 54d4b3
  //   64d4b3 900533 2200893 73 fffe0e13 fe0e14e3 a00893 73 fff00293 313 1900413 841413 9700493 940533
  //   2200893 73 5484b3 494b313 fe0306e3 a00893 73 313 2000e13 493 100913 930023 900533 2200893 73 12484b3
  //   130313 fffe0e13 fe0e12e3 800e13 313 32483 900533 2200893 73 430313 fffe0e13 fe0e14e3 a00893 73
  //   ff100493 900533 2200893 73 148493 fe04c8e3 a00893 73 a00893 73 413 140413 800533 2200893 73 240413
  //   800533 2200893 73 340413 800533 2200893 73 440413 800533 2200893 73 540413 800533 2200893 73 640413
  //   800533 2200893 73 740413 800533 2200893 73 840413 800533 2200893 2200893 73 8067
  //   指令探针
  //   生成EX.BranchAddr信号
  //   控制位
  //   JAL
  //   JALR
  //   URET
  //   Sltiu
  //   Sb
  //   rs1
  //   rs2
  //   流水调试日志用
  //   暂停节拍，不能为0
  //   Beq
  //   Bne
  //   MemToReg
  //   MemWrite
  //   AluOP
  //   AluSrcB
  //   RegWrite
  //   Blt
  //   I型指令立即数
  //   S型指令立即数
  //   B型指令立即数
  //   J型指令立即数
  //   戳工具置1进入计数暂停模式，ctrl+k时钟自动运行到对应节拍暂停
  //   ctrl+k关闭时钟连续运行，将控制位置零，进入单步调试模式调试
  //   rd
  //   rd
  //   生成R1_F R2_F信号
  //   可计数暂停的时钟源
  //   为方便自动评测，需要输出流水线各段保存的PC值，注意是PC不是PC+4，另外ID段寄存器写入信息，Mem段内存写入信息也要输出
  //   重定向设置
  //   计算Sb对应的MemData
  //   rd
  //   EX阶段 生成立即数选择信号
  //   LedData显示控制
  //   周期信号显示控制
  //   生成停机信号halt和LED显示信号Ledout
endmodule

module \封装正确性测试  (
);

  wire IR1, IR2, IR3, MemW, RegW;
  wire [31:0] EX_PC, ID_PC, IF_PC, IR, LED, MDin, MDinr, MEM_PC, PC, RDin, RDinr, WB_PC;

  \单周期RISC_V  \u_单周期risc_v_1  (
    .IR1(IR1), .IR2(IR2), .IR3(IR3), .RegWrite(RegW), .MemWrite(MemW), .PC(PC), .IR(IR), .RDin(RDin),
    .MDin(MDin), .LedData(LED));
  \气泡流水线  \u_气泡流水线_1  (
    .RegWrite(RegW), .MemWrite(MemW), .IF_PC(IF_PC), .ID_PC(ID_PC), .EX_PC(EX_PC), .M_PC(MEM_PC),
    .WB_PC(WB_PC), .RDin(RDinr), .MDin(MDinr), .LedData(LED));
  \单周期_单级中断  \u_单周期_单级中断_1  (
    .IR1(IR1), .IR2(IR2), .IR3(IR3), .RegWrite(RegW), .MemWrite(MemW), .PC(PC), .IR(IR), .RDin(RDin),
    .MDin(MDin), .LedData(LED));
  \理想流水线  \u_理想流水线_1  (
    .RegWrite(RegW), .MemWrite(MemW), .IF_PC(IF_PC), .ID_PC(ID_PC), .EX_PC(EX_PC), .M_PC(MEM_PC),
    .WB_PC(WB_PC), .RDin(RDinr), .MDin(MDinr), .LedData(LED));
  \重定向流水线  \u_重定向流水线_1  (
    .RegWrite(RegW), .MemWrite(MemW), .IF_PC(IF_PC), .ID_PC(ID_PC), .EX_PC(EX_PC), .M_PC(MEM_PC),
    .WB_PC(WB_PC), .RDin(RDinr), .MDin(MDinr), .LedData(LED));
  \单周期_多级中断  \u_单周期_多级中断_1  (
    .IR1(IR1), .IR2(IR2), .IR3(IR3), .RegWrite(RegW), .MemWrite(MemW), .PC(PC), .IR(IR), .RDin(RDin),
    .MDin(MDin), .LedData(LED));

  // Notes on the sheet:
  //   单周期封装测试
  //   气泡流水封装测试
  //   单周期+单级中断封装测试
  //   请检查上面封装有无位宽不匹配，引脚标签是否和连接的标签相对应，否则无法在educoder平台上正确测试
  //   理想流水封装测试
  //   重定向流水封装测试
  //   单周期+多级中断封装测试
endmodule

module MIPS_RAM (
  input  [11:0] \字节地址 ,
  input  [31:0] Din,
  input  CLK,
  input  WE,
  input  [1:0] Mode,
  output [31:0] DataOut
);

  wire and_1_out, and_2_out, and_3_out, and_4_out, and_5_out, and_6_out, demultiplexer_1_out0,
       demultiplexer_1_out1, demultiplexer_1_out2, demultiplexer_1_out3, w0, w1, w2, w3, \半字访问 , \字节访问 ,
       \字访问 ;
  wire [7:0] Din0, Din1, Din2, Din3, multiplexer_1_out, \计数器_q ;
  wire [15:0] multiplexer_2_out;
  wire [31:0] bit_extender_1_out, bit_extender_2_out, ram_4_data;

  Decoder #(.select(2), .tristate("false"), .disabled("Z"), .enable("false")) decoder_1 (
    .out0(\字访问 ), .out1(\字节访问 ), .out2(\半字访问 ), .sel(Mode));  // open: out3
  and and_1 (and_1_out, WE, w3);
  RAM #(.addrWidth(10), .dataWidth(8), .bus("separate"), .Select("high")) ram_1 (
    .addr(\字节地址 [11:2]), .din(Din3), .data(ram_4_data[31:24]), .str(and_1_out), .clk(CLK));  // open: sel, ld, clr
  Demultiplexer #(.select(2), .width(1), .tristate("false"), .disabled("Z"), .enable("false")) demultiplexer_1 (
    .out0(demultiplexer_1_out0), .out1(demultiplexer_1_out1), .out2(demultiplexer_1_out2),
    .out3(demultiplexer_1_out3), .in(\字节访问 ), .sel(\字节地址 [1:0]));
  and and_2 (and_2_out, \半字访问 , \字节地址 [1]);
  and and_3 (and_3_out, \半字访问 , ~\字节地址 [1]);  // AND_Gate
  and and_4 (and_4_out, WE, w2);
  // Probe on DataOut
  RAM #(.addrWidth(10), .dataWidth(8), .bus("separate"), .Select("high")) ram_2 (
    .addr(\字节地址 [11:2]), .din(Din2), .data(ram_4_data[23:16]), .str(and_4_out), .clk(CLK));  // open: sel, ld, clr
  or or_1 (w3, \字访问 , demultiplexer_1_out3, and_2_out);
  or or_2 (w2, \字访问 , demultiplexer_1_out2, and_2_out);
  or or_3 (w1, \字访问 , demultiplexer_1_out1, and_3_out);
  or or_4 (w0, \字访问 , demultiplexer_1_out0, and_3_out);
  and and_5 (and_5_out, WE, w1);
  Counter #(.width(8), .max('hff), .ongoal("wrap"), .trigger("rising"), .behavior("old")) \u_计数器  (
    .Q(\计数器_q ), .clk(CLK));  // open: load, D, count, carry, clr, preset
  RAM #(.addrWidth(10), .dataWidth(8), .bus("separate"), .Select("high")) ram_3 (
    .addr(\字节地址 [11:2]), .din(Din1), .data(ram_4_data[15:8]), .str(and_5_out), .clk(CLK));  // open: sel, ld, clr
  // Probe on \计数器_q 
  Multiplexer #(.select(2), .width(8), .disabled("Z"), .enable("false")) multiplexer_1 (
    .in0(ram_4_data[7:0]), .in1(ram_4_data[15:8]), .in2(ram_4_data[23:16]), .in3(ram_4_data[31:24]),
    .out(multiplexer_1_out), .sel(\字节地址 [1:0]));
  Multiplexer #(.select(1), .width(16), .disabled("Z"), .enable("false")) multiplexer_2 (
    .in0(ram_4_data[15:0]), .in1(ram_4_data[31:16]), .out(multiplexer_2_out), .sel(\字节地址 [1]));
  and and_6 (and_6_out, WE, w0);
  assign bit_extender_1_out = {{24{1'b0}}, multiplexer_1_out};  // Bit_Extender bit_extender_1
  assign bit_extender_2_out = {{16{1'b0}}, multiplexer_2_out};  // Bit_Extender bit_extender_2
  RAM #(.addrWidth(10), .dataWidth(8), .bus("separate"), .Select("high")) ram_4 (
    .addr(\字节地址 [11:2]), .din(Din0), .data(ram_4_data[7:0]), .str(and_6_out), .clk(CLK));  // open: sel, ld, clr
  Multiplexer #(.select(2), .width(32), .disabled("Z"), .enable("false")) multiplexer_3 (
    .in0(ram_4_data), .in1(bit_extender_1_out), .in2(bit_extender_2_out), .in3({32{1'b0}}), .out(DataOut),
    .sel(Mode));
  Multiplexer #(.select(2), .width(8), .disabled("Z"), .enable("false")) multiplexer_4 (
    .in0(Din[7:0]), .in1(Din[7:0]), .in2(Din[7:0]), .out(Din0), .sel(Mode));  // open: in3
  Multiplexer #(.select(2), .width(8), .disabled("Z"), .enable("false")) multiplexer_5 (
    .in0(Din[15:8]), .in1(Din[7:0]), .in2(Din[15:8]), .out(Din1), .sel(Mode));  // open: in3
  Multiplexer #(.select(2), .width(8), .disabled("Z"), .enable("false")) multiplexer_6 (
    .in0(Din[23:16]), .in1(Din[7:0]), .in2(Din[7:0]), .out(Din2), .sel(Mode));  // open: in3
  Multiplexer #(.select(2), .width(8), .disabled("Z"), .enable("false")) multiplexer_7 (
    .in0(Din[31:24]), .in1(Din[7:0]), .in2(Din[15:8]), .out(Din3), .sel(Mode));  // open: in3

  // Other names for the same wires on the sheet: Dout[31:0] = DataOut

  // Notes on the sheet:
  //   输入引脚区
  //   请勿增改引脚，请勿修改子电路封装
  //   电路功能：利用下图中给定的RAM器件实现既既可以按照字节，也可以按照半字，也可以按照32位字访问的MIPS存储器
  //   输出引脚区
  //   请在下方利用上方输入输出引脚的隧道信号构建电路，ctrl+d复制选择部件
  //   为方便测试，注意Dout应一直输出数据，所有数据位不得悬空，所有RAM芯片ld控制端悬空即可
endmodule

module IF_ID (
  input  CLK,
  input  \RST_高电平有效 ,
  input  \en_低电平有效 ,
  input  [31:0] IR,
  input  [31:0] PC,
  input  [31:0] PC_4,
  output [31:0] IR_2,
  output [31:0] PC_2,
  output [31:0] PC_4_2
);

  wire not_1_out;
  wire [31:0] multiplexer_1_out, multiplexer_2_out, multiplexer_3_out;

  not not_1 (not_1_out, \en_低电平有效 );
  Multiplexer #(.select(1), .width(32), .disabled("Z"), .enable("false")) multiplexer_1 (
    .in0(IR), .in1({32{1'b0}}), .out(multiplexer_1_out), .sel(\RST_高电平有效 ));
  Multiplexer #(.select(1), .width(32), .disabled("Z"), .enable("false")) multiplexer_2 (
    .in0(PC), .in1({32{1'b0}}), .out(multiplexer_2_out), .sel(\RST_高电平有效 ));
  Multiplexer #(.select(1), .width(32), .disabled("Z"), .enable("false")) multiplexer_3 (
    .in0(PC_4), .in1({32{1'b0}}), .out(multiplexer_3_out), .sel(\RST_高电平有效 ));
  Register #(.width(32), .trigger("rising"), .Select("low")) register_1 (
    .D(multiplexer_1_out), .en(not_1_out), .Q(IR_2), .clk(CLK));  // open: clr
  Register #(.width(32), .trigger("rising"), .Select("low")) register_2 (
    .D(multiplexer_2_out), .en(not_1_out), .Q(PC_2), .clk(CLK));  // open: clr
  Register #(.width(32), .trigger("rising"), .Select("low")) register_3 (
    .D(multiplexer_3_out), .en(not_1_out), .Q(PC_4_2), .clk(CLK));  // open: clr
  Pull_Resistor #(.pull(0)) pull_resistor_1 (.node(\RST_高电平有效 ));
  Pull_Resistor #(.pull(0)) pull_resistor_2 (.node(not_1_out));
endmodule

module \IF_ID_动态分支预测  (
  input  CLK,
  input  \RST_高电平有效 ,
  input  \en_低电平有效 ,
  input  [31:0] IR,
  input  [31:0] PC,
  input  [31:0] PC_4,
  input  PredictJump,
  output [31:0] IR_2,
  output [31:0] PC_2,
  output [31:0] PC_4_2,
  output PredictJump_2
);

  wire multiplexer_4_out, not_1_out;
  wire [31:0] multiplexer_1_out, multiplexer_2_out, multiplexer_3_out;

  not not_1 (not_1_out, \en_低电平有效 );
  Multiplexer #(.select(1), .width(32), .disabled("Z"), .enable("false")) multiplexer_1 (
    .in0(IR), .in1({32{1'b0}}), .out(multiplexer_1_out), .sel(\RST_高电平有效 ));
  Multiplexer #(.select(1), .width(32), .disabled("Z"), .enable("false")) multiplexer_2 (
    .in0(PC), .in1({32{1'b0}}), .out(multiplexer_2_out), .sel(\RST_高电平有效 ));
  Multiplexer #(.select(1), .width(32), .disabled("Z"), .enable("false")) multiplexer_3 (
    .in0(PC_4), .in1({32{1'b0}}), .out(multiplexer_3_out), .sel(\RST_高电平有效 ));
  Multiplexer #(.select(1), .width(1), .disabled("Z"), .enable("false")) multiplexer_4 (
    .in0(PredictJump), .in1(1'b0), .out(multiplexer_4_out), .sel(\RST_高电平有效 ));
  Register #(.width(32), .trigger("rising"), .Select("low")) register_1 (
    .D(multiplexer_1_out), .en(not_1_out), .Q(IR_2), .clk(CLK));  // open: clr
  Register #(.width(32), .trigger("rising"), .Select("low")) register_2 (
    .D(multiplexer_2_out), .en(not_1_out), .Q(PC_2), .clk(CLK));  // open: clr
  Register #(.width(32), .trigger("rising"), .Select("low")) register_3 (
    .D(multiplexer_3_out), .en(not_1_out), .Q(PC_4_2), .clk(CLK));  // open: clr
  Register #(.width(1), .trigger("rising"), .Select("low")) register_4 (
    .D(multiplexer_4_out), .en(not_1_out), .Q(PredictJump_2), .clk(CLK));  // open: clr
  Pull_Resistor #(.pull(0)) pull_resistor_1 (.node(\RST_高电平有效 ));
  Pull_Resistor #(.pull(0)) pull_resistor_2 (.node(not_1_out));
endmodule

module ID_EX (
  input  CLK,
  input  \RST_高电平有效 ,
  input  \en_低电平有效 ,
  input  RegWrite,
  input  [31:0] IR,
  input  AluSrcB,
  input  [3:0] AluOP,
  input  [31:0] PC,
  input  MemWrite,
  input  [31:0] PC_4,
  input  MemToReg,
  input  [31:0] R1,
  input  Bne,
  input  [31:0] R2,
  input  Beq,
  input  JAL,
  input  [11:0] Imm_I,
  input  [11:0] Imm_S,
  input  JALR,
  input  [11:0] Imm_B,
  input  URET,
  input  [19:0] Imm_J,
  input  ecall,
  input  Sltiu,
  input  Sb,
  input  Blt,
  input  S_Type,
  output RegWrite_2,
  output [31:0] IR_2,
  output AluSrcB_2,
  output [3:0] AluOP_2,
  output [31:0] PC_2,
  output MemWrite_2,
  output [31:0] PC_4_2,
  output MemToReg_2,
  output [31:0] R1_2,
  output Bne_2,
  output [31:0] R2_2,
  output Beq_2,
  output JAL_2,
  output [11:0] Imm_I_2,
  output [11:0] Imm_S_2,
  output JALR_2,
  output [11:0] Imm_B_2,
  output URET_2,
  output [19:0] Imm_J_2,
  output ecall_2,
  output Sltiu_2,
  output Sb_2,
  output Blt_2,
  output S_Type_2
);

  wire multiplexer_1_out, multiplexer_2_out, multiplexer_4_out, multiplexer_5_out, multiplexer_6_out,
       multiplexer_7_out, multiplexer_8_out, multiplexer_9_out, multiplexer_10_out, multiplexer_11_out,
       multiplexer_12_out, multiplexer_13_out, multiplexer_14_out, multiplexer_15_out, not_1_out;
  wire [3:0] multiplexer_3_out;
  wire [11:0] multiplexer_21_out, multiplexer_22_out, multiplexer_23_out;
  wire [19:0] multiplexer_24_out;
  wire [31:0] multiplexer_16_out, multiplexer_17_out, multiplexer_18_out, multiplexer_19_out,
       multiplexer_20_out;

  not not_1 (not_1_out, \en_低电平有效 );
  Multiplexer #(.select(1), .width(1), .disabled("Z"), .enable("false")) multiplexer_1 (
    .in0(RegWrite), .in1(1'b0), .out(multiplexer_1_out), .sel(\RST_高电平有效 ));
  Multiplexer #(.select(1), .width(1), .disabled("Z"), .enable("false")) multiplexer_2 (
    .in0(AluSrcB), .in1(1'b0), .out(multiplexer_2_out), .sel(\RST_高电平有效 ));
  Multiplexer #(.select(1), .width(4), .disabled("Z"), .enable("false")) multiplexer_3 (
    .in0(AluOP), .in1(4'b0000), .out(multiplexer_3_out), .sel(\RST_高电平有效 ));
  Multiplexer #(.select(1), .width(1), .disabled("Z"), .enable("false")) multiplexer_4 (
    .in0(MemWrite), .in1(1'b0), .out(multiplexer_4_out), .sel(\RST_高电平有效 ));
  Multiplexer #(.select(1), .width(1), .disabled("Z"), .enable("false")) multiplexer_5 (
    .in0(MemToReg), .in1(1'b0), .out(multiplexer_5_out), .sel(\RST_高电平有效 ));
  Multiplexer #(.select(1), .width(1), .disabled("Z"), .enable("false")) multiplexer_6 (
    .in0(Bne), .in1(1'b0), .out(multiplexer_6_out), .sel(\RST_高电平有效 ));
  Multiplexer #(.select(1), .width(1), .disabled("Z"), .enable("false")) multiplexer_7 (
    .in0(Beq), .in1(1'b0), .out(multiplexer_7_out), .sel(\RST_高电平有效 ));
  Multiplexer #(.select(1), .width(1), .disabled("Z"), .enable("false")) multiplexer_8 (
    .in0(JAL), .in1(1'b0), .out(multiplexer_8_out), .sel(\RST_高电平有效 ));
  Multiplexer #(.select(1), .width(1), .disabled("Z"), .enable("false")) multiplexer_9 (
    .in0(JALR), .in1(1'b0), .out(multiplexer_9_out), .sel(\RST_高电平有效 ));
  Multiplexer #(.select(1), .width(1), .disabled("Z"), .enable("false")) multiplexer_10 (
    .in0(URET), .in1(1'b0), .out(multiplexer_10_out), .sel(\RST_高电平有效 ));
  Multiplexer #(.select(1), .width(1), .disabled("Z"), .enable("false")) multiplexer_11 (
    .in0(ecall), .in1(1'b0), .out(multiplexer_11_out), .sel(\RST_高电平有效 ));
  Multiplexer #(.select(1), .width(1), .disabled("Z"), .enable("false")) multiplexer_12 (
    .in0(Sltiu), .in1(1'b0), .out(multiplexer_12_out), .sel(\RST_高电平有效 ));
  Multiplexer #(.select(1), .width(1), .disabled("Z"), .enable("false")) multiplexer_13 (
    .in0(Sb), .in1(1'b0), .out(multiplexer_13_out), .sel(\RST_高电平有效 ));
  Multiplexer #(.select(1), .width(1), .disabled("Z"), .enable("false")) multiplexer_14 (
    .in0(Blt), .in1(1'b0), .out(multiplexer_14_out), .sel(\RST_高电平有效 ));
  Multiplexer #(.select(1), .width(1), .disabled("Z"), .enable("false")) multiplexer_15 (
    .in0(S_Type), .in1(1'b0), .out(multiplexer_15_out), .sel(\RST_高电平有效 ));
  Register #(.width(1), .trigger("rising"), .Select("low")) register_1 (
    .D(multiplexer_1_out), .en(not_1_out), .Q(RegWrite_2), .clk(CLK));  // open: clr
  Register #(.width(1), .trigger("rising"), .Select("low")) register_2 (
    .D(multiplexer_2_out), .en(not_1_out), .Q(AluSrcB_2), .clk(CLK));  // open: clr
  Register #(.width(4), .trigger("rising"), .Select("low")) register_3 (
    .D(multiplexer_3_out), .Q(AluOP_2), .clk(CLK));  // open: en, clr
  Register #(.width(1), .trigger("rising"), .Select("low")) register_4 (
    .D(multiplexer_4_out), .en(not_1_out), .Q(MemWrite_2), .clk(CLK));  // open: clr
  Register #(.width(1), .trigger("rising"), .Select("low")) register_5 (
    .D(multiplexer_5_out), .en(not_1_out), .Q(MemToReg_2), .clk(CLK));  // open: clr
  Register #(.width(1), .trigger("rising"), .Select("low")) register_6 (
    .D(multiplexer_6_out), .en(not_1_out), .Q(Bne_2), .clk(CLK));  // open: clr
  Register #(.width(1), .trigger("rising"), .Select("low")) register_7 (
    .D(multiplexer_7_out), .en(not_1_out), .Q(Beq_2), .clk(CLK));  // open: clr
  Register #(.width(1), .trigger("rising"), .Select("low")) register_8 (
    .D(multiplexer_8_out), .en(not_1_out), .Q(JAL_2), .clk(CLK));  // open: clr
  Register #(.width(1), .trigger("rising"), .Select("low")) register_9 (
    .D(multiplexer_9_out), .en(not_1_out), .Q(JALR_2), .clk(CLK));  // open: clr
  Register #(.width(1), .trigger("rising"), .Select("low")) register_10 (
    .D(multiplexer_10_out), .en(not_1_out), .Q(URET_2), .clk(CLK));  // open: clr
  Register #(.width(1), .trigger("rising"), .Select("low")) register_11 (
    .D(multiplexer_11_out), .en(not_1_out), .Q(ecall_2), .clk(CLK));  // open: clr
  Register #(.width(1), .trigger("rising"), .Select("low")) register_12 (
    .D(multiplexer_12_out), .en(not_1_out), .Q(Sltiu_2), .clk(CLK));  // open: clr
  Register #(.width(1), .trigger("rising"), .Select("low")) register_13 (
    .D(multiplexer_13_out), .en(not_1_out), .Q(Sb_2), .clk(CLK));  // open: clr
  Register #(.width(1), .trigger("rising"), .Select("low")) register_14 (
    .D(multiplexer_14_out), .en(not_1_out), .Q(Blt_2), .clk(CLK));  // open: clr
  Register #(.width(1), .trigger("rising"), .Select("low")) register_15 (
    .D(multiplexer_15_out), .en(not_1_out), .Q(S_Type_2), .clk(CLK));  // open: clr
  Pull_Resistor #(.pull(0)) pull_resistor_1 (.node(\RST_高电平有效 ));
  Pull_Resistor #(.pull(0)) pull_resistor_2 (.node(not_1_out));
  Multiplexer #(.select(1), .width(32), .disabled("Z"), .enable("false")) multiplexer_16 (
    .in0(IR), .in1({32{1'b0}}), .out(multiplexer_16_out), .sel(\RST_高电平有效 ));
  Multiplexer #(.select(1), .width(32), .disabled("Z"), .enable("false")) multiplexer_17 (
    .in0(PC), .in1({32{1'b0}}), .out(multiplexer_17_out), .sel(\RST_高电平有效 ));
  Multiplexer #(.select(1), .width(32), .disabled("Z"), .enable("false")) multiplexer_18 (
    .in0(PC_4), .in1({32{1'b0}}), .out(multiplexer_18_out), .sel(\RST_高电平有效 ));
  Multiplexer #(.select(1), .width(32), .disabled("Z"), .enable("false")) multiplexer_19 (
    .in0(R1), .in1({32{1'b0}}), .out(multiplexer_19_out), .sel(\RST_高电平有效 ));
  Multiplexer #(.select(1), .width(32), .disabled("Z"), .enable("false")) multiplexer_20 (
    .in0(R2), .in1({32{1'b0}}), .out(multiplexer_20_out), .sel(\RST_高电平有效 ));
  Multiplexer #(.select(1), .width(12), .disabled("Z"), .enable("false")) multiplexer_21 (
    .in0(Imm_I), .in1({12{1'b0}}), .out(multiplexer_21_out), .sel(\RST_高电平有效 ));
  Multiplexer #(.select(1), .width(12), .disabled("Z"), .enable("false")) multiplexer_22 (
    .in0(Imm_S), .in1({12{1'b0}}), .out(multiplexer_22_out), .sel(\RST_高电平有效 ));
  Multiplexer #(.select(1), .width(12), .disabled("Z"), .enable("false")) multiplexer_23 (
    .in0(Imm_B), .in1({12{1'b0}}), .out(multiplexer_23_out), .sel(\RST_高电平有效 ));
  Multiplexer #(.select(1), .width(20), .disabled("Z"), .enable("false")) multiplexer_24 (
    .in0(Imm_J), .in1({20{1'b0}}), .out(multiplexer_24_out), .sel(\RST_高电平有效 ));
  Register #(.width(32), .trigger("rising"), .Select("low")) register_16 (
    .D(multiplexer_16_out), .en(not_1_out), .Q(IR_2), .clk(CLK));  // open: clr
  Register #(.width(32), .trigger("rising"), .Select("low")) register_17 (
    .D(multiplexer_17_out), .en(not_1_out), .Q(PC_2), .clk(CLK));  // open: clr
  Register #(.width(32), .trigger("rising"), .Select("low")) register_18 (
    .D(multiplexer_18_out), .en(not_1_out), .Q(PC_4_2), .clk(CLK));  // open: clr
  Register #(.width(32), .trigger("rising"), .Select("low")) register_19 (
    .D(multiplexer_19_out), .en(not_1_out), .Q(R1_2), .clk(CLK));  // open: clr
  Register #(.width(32), .trigger("rising"), .Select("low")) register_20 (
    .D(multiplexer_20_out), .en(not_1_out), .Q(R2_2), .clk(CLK));  // open: clr
  Register #(.width(12), .trigger("rising"), .Select("low")) register_21 (
    .D(multiplexer_21_out), .en(not_1_out), .Q(Imm_I_2), .clk(CLK));  // open: clr
  Register #(.width(12), .trigger("rising"), .Select("low")) register_22 (
    .D(multiplexer_22_out), .en(not_1_out), .Q(Imm_S_2), .clk(CLK));  // open: clr
  Register #(.width(12), .trigger("rising"), .Select("low")) register_23 (
    .D(multiplexer_23_out), .en(not_1_out), .Q(Imm_B_2), .clk(CLK));  // open: clr
  Register #(.width(20), .trigger("rising"), .Select("low")) register_24 (
    .D(multiplexer_24_out), .en(not_1_out), .Q(Imm_J_2), .clk(CLK));  // open: clr
endmodule
module \ID_EX_重定向  (
  input  CLK,
  input  \RST_高电平有效 ,
  input  \en_低电平有效 ,
  input  RegWrite,
  input  [31:0] IR,
  input  AluSrcB,
  input  [3:0] AluOP,
  input  [31:0] PC,
  input  MemWrite,
  input  [31:0] PC_4,
  input  MemToReg,
  input  [31:0] R1,
  input  Bne,
  input  [31:0] R2,
  input  Beq,
  input  JAL,
  input  [11:0] Imm_I,
  input  [11:0] Imm_S,
  input  JALR,
  input  [11:0] Imm_B,
  input  URET,
  input  [19:0] Imm_J,
  input  ecall,
  input  Sltiu,
  input  Sb,
  input  Blt,
  input  S_Type,
  input  [1:0] R1_F,
  input  [1:0] R2_F,
  output RegWrite_2,
  output [31:0] IR_2,
  output AluSrcB_2,
  output [3:0] AluOP_2,
  output [31:0] PC_2,
  output MemWrite_2,
  output [31:0] PC_4_2,
  output MemToReg_2,
  output [31:0] R1_2,
  output Bne_2,
  output [31:0] R2_2,
  output Beq_2,
  output JAL_2,
  output [11:0] Imm_I_2,
  output [11:0] Imm_S_2,
  output JALR_2,
  output [11:0] Imm_B_2,
  output URET_2,
  output [19:0] Imm_J_2,
  output ecall_2,
  output Sltiu_2,
  output Sb_2,
  output Blt_2,
  output S_Type_2,
  output [1:0] R1_F_2,
  output [1:0] R2_F_2
);

  wire multiplexer_1_out, multiplexer_2_out, multiplexer_4_out, multiplexer_5_out, multiplexer_6_out,
       multiplexer_7_out, multiplexer_8_out, multiplexer_9_out, multiplexer_10_out, multiplexer_11_out,
       multiplexer_12_out, multiplexer_13_out, multiplexer_14_out, multiplexer_15_out, not_1_out;
  wire [1:0] multiplexer_16_out, multiplexer_17_out;
  wire [3:0] multiplexer_3_out;
  wire [11:0] multiplexer_23_out, multiplexer_24_out, multiplexer_25_out;
  wire [19:0] multiplexer_26_out;
  wire [31:0] multiplexer_18_out, multiplexer_19_out, multiplexer_20_out, multiplexer_21_out,
       multiplexer_22_out;

  not not_1 (not_1_out, \en_低电平有效 );
  Multiplexer #(.select(1), .width(1), .disabled("Z"), .enable("false")) multiplexer_1 (
    .in0(RegWrite), .in1(1'b0), .out(multiplexer_1_out), .sel(\RST_高电平有效 ));
  Multiplexer #(.select(1), .width(1), .disabled("Z"), .enable("false")) multiplexer_2 (
    .in0(AluSrcB), .in1(1'b0), .out(multiplexer_2_out), .sel(\RST_高电平有效 ));
  Multiplexer #(.select(1), .width(4), .disabled("Z"), .enable("false")) multiplexer_3 (
    .in0(AluOP), .in1(4'b0000), .out(multiplexer_3_out), .sel(\RST_高电平有效 ));
  Multiplexer #(.select(1), .width(1), .disabled("Z"), .enable("false")) multiplexer_4 (
    .in0(MemWrite), .in1(1'b0), .out(multiplexer_4_out), .sel(\RST_高电平有效 ));
  Multiplexer #(.select(1), .width(1), .disabled("Z"), .enable("false")) multiplexer_5 (
    .in0(MemToReg), .in1(1'b0), .out(multiplexer_5_out), .sel(\RST_高电平有效 ));
  Multiplexer #(.select(1), .width(1), .disabled("Z"), .enable("false")) multiplexer_6 (
    .in0(Bne), .in1(1'b0), .out(multiplexer_6_out), .sel(\RST_高电平有效 ));
  Multiplexer #(.select(1), .width(1), .disabled("Z"), .enable("false")) multiplexer_7 (
    .in0(Beq), .in1(1'b0), .out(multiplexer_7_out), .sel(\RST_高电平有效 ));
  Multiplexer #(.select(1), .width(1), .disabled("Z"), .enable("false")) multiplexer_8 (
    .in0(JAL), .in1(1'b0), .out(multiplexer_8_out), .sel(\RST_高电平有效 ));
  Multiplexer #(.select(1), .width(1), .disabled("Z"), .enable("false")) multiplexer_9 (
    .in0(JALR), .in1(1'b0), .out(multiplexer_9_out), .sel(\RST_高电平有效 ));
  Multiplexer #(.select(1), .width(1), .disabled("Z"), .enable("false")) multiplexer_10 (
    .in0(URET), .in1(1'b0), .out(multiplexer_10_out), .sel(\RST_高电平有效 ));
  Multiplexer #(.select(1), .width(1), .disabled("Z"), .enable("false")) multiplexer_11 (
    .in0(ecall), .in1(1'b0), .out(multiplexer_11_out), .sel(\RST_高电平有效 ));
  Multiplexer #(.select(1), .width(1), .disabled("Z"), .enable("false")) multiplexer_12 (
    .in0(Sltiu), .in1(1'b0), .out(multiplexer_12_out), .sel(\RST_高电平有效 ));
  Multiplexer #(.select(1), .width(1), .disabled("Z"), .enable("false")) multiplexer_13 (
    .in0(Sb), .in1(1'b0), .out(multiplexer_13_out), .sel(\RST_高电平有效 ));
  Multiplexer #(.select(1), .width(1), .disabled("Z"), .enable("false")) multiplexer_14 (
    .in0(Blt), .in1(1'b0), .out(multiplexer_14_out), .sel(\RST_高电平有效 ));
  Multiplexer #(.select(1), .width(1), .disabled("Z"), .enable("false")) multiplexer_15 (
    .in0(S_Type), .in1(1'b0), .out(multiplexer_15_out), .sel(\RST_高电平有效 ));
  Multiplexer #(.select(1), .width(2), .disabled("Z"), .enable("false")) multiplexer_16 (
    .in0(R1_F), .in1(2'b00), .out(multiplexer_16_out), .sel(\RST_高电平有效 ));
  Multiplexer #(.select(1), .width(2), .disabled("Z"), .enable("false")) multiplexer_17 (
    .in0(R2_F), .in1(2'b00), .out(multiplexer_17_out), .sel(\RST_高电平有效 ));
  Register #(.width(1), .trigger("rising"), .Select("low")) register_1 (
    .D(multiplexer_1_out), .en(not_1_out), .Q(RegWrite_2), .clk(CLK));  // open: clr
  Register #(.width(1), .trigger("rising"), .Select("low")) register_2 (
    .D(multiplexer_2_out), .en(not_1_out), .Q(AluSrcB_2), .clk(CLK));  // open: clr
  Register #(.width(4), .trigger("rising"), .Select("low")) register_3 (
    .D(multiplexer_3_out), .Q(AluOP_2), .clk(CLK));  // open: en, clr
  Register #(.width(1), .trigger("rising"), .Select("low")) register_4 (
    .D(multiplexer_4_out), .en(not_1_out), .Q(MemWrite_2), .clk(CLK));  // open: clr
  Register #(.width(1), .trigger("rising"), .Select("low")) register_5 (
    .D(multiplexer_5_out), .en(not_1_out), .Q(MemToReg_2), .clk(CLK));  // open: clr
  Register #(.width(1), .trigger("rising"), .Select("low")) register_6 (
    .D(multiplexer_6_out), .en(not_1_out), .Q(Bne_2), .clk(CLK));  // open: clr
  Register #(.width(1), .trigger("rising"), .Select("low")) register_7 (
    .D(multiplexer_7_out), .en(not_1_out), .Q(Beq_2), .clk(CLK));  // open: clr
  Register #(.width(1), .trigger("rising"), .Select("low")) register_8 (
    .D(multiplexer_8_out), .en(not_1_out), .Q(JAL_2), .clk(CLK));  // open: clr
  Register #(.width(1), .trigger("rising"), .Select("low")) register_9 (
    .D(multiplexer_9_out), .en(not_1_out), .Q(JALR_2), .clk(CLK));  // open: clr
  Register #(.width(1), .trigger("rising"), .Select("low")) register_10 (
    .D(multiplexer_10_out), .en(not_1_out), .Q(URET_2), .clk(CLK));  // open: clr
  Register #(.width(1), .trigger("rising"), .Select("low")) register_11 (
    .D(multiplexer_11_out), .en(not_1_out), .Q(ecall_2), .clk(CLK));  // open: clr
  Register #(.width(1), .trigger("rising"), .Select("low")) register_12 (
    .D(multiplexer_12_out), .en(not_1_out), .Q(Sltiu_2), .clk(CLK));  // open: clr
  Register #(.width(1), .trigger("rising"), .Select("low")) register_13 (
    .D(multiplexer_13_out), .en(not_1_out), .Q(Sb_2), .clk(CLK));  // open: clr
  Register #(.width(1), .trigger("rising"), .Select("low")) register_14 (
    .D(multiplexer_14_out), .en(not_1_out), .Q(Blt_2), .clk(CLK));  // open: clr
  Register #(.width(1), .trigger("rising"), .Select("low")) register_15 (
    .D(multiplexer_15_out), .en(not_1_out), .Q(S_Type_2), .clk(CLK));  // open: clr
  Register #(.width(2), .trigger("rising"), .Select("low")) register_16 (
    .D(multiplexer_16_out), .en(not_1_out), .Q(R1_F_2), .clk(CLK));  // open: clr
  Register #(.width(2), .trigger("rising"), .Select("low")) register_17 (
    .D(multiplexer_17_out), .en(not_1_out), .Q(R2_F_2), .clk(CLK));  // open: clr
  Pull_Resistor #(.pull(0)) pull_resistor_1 (.node(\RST_高电平有效 ));
  Pull_Resistor #(.pull(0)) pull_resistor_2 (.node(not_1_out));
  Multiplexer #(.select(1), .width(32), .disabled("Z"), .enable("false")) multiplexer_18 (
    .in0(IR), .in1({32{1'b0}}), .out(multiplexer_18_out), .sel(\RST_高电平有效 ));
  Multiplexer #(.select(1), .width(32), .disabled("Z"), .enable("false")) multiplexer_19 (
    .in0(PC), .in1({32{1'b0}}), .out(multiplexer_19_out), .sel(\RST_高电平有效 ));
  Multiplexer #(.select(1), .width(32), .disabled("Z"), .enable("false")) multiplexer_20 (
    .in0(PC_4), .in1({32{1'b0}}), .out(multiplexer_20_out), .sel(\RST_高电平有效 ));
  Multiplexer #(.select(1), .width(32), .disabled("Z"), .enable("false")) multiplexer_21 (
    .in0(R1), .in1({32{1'b0}}), .out(multiplexer_21_out), .sel(\RST_高电平有效 ));
  Multiplexer #(.select(1), .width(32), .disabled("Z"), .enable("false")) multiplexer_22 (
    .in0(R2), .in1({32{1'b0}}), .out(multiplexer_22_out), .sel(\RST_高电平有效 ));
  Multiplexer #(.select(1), .width(12), .disabled("Z"), .enable("false")) multiplexer_23 (
    .in0(Imm_I), .in1({12{1'b0}}), .out(multiplexer_23_out), .sel(\RST_高电平有效 ));
  Multiplexer #(.select(1), .width(12), .disabled("Z"), .enable("false")) multiplexer_24 (
    .in0(Imm_S), .in1({12{1'b0}}), .out(multiplexer_24_out), .sel(\RST_高电平有效 ));
  Multiplexer #(.select(1), .width(12), .disabled("Z"), .enable("false")) multiplexer_25 (
    .in0(Imm_B), .in1({12{1'b0}}), .out(multiplexer_25_out), .sel(\RST_高电平有效 ));
  Multiplexer #(.select(1), .width(20), .disabled("Z"), .enable("false")) multiplexer_26 (
    .in0(Imm_J), .in1({20{1'b0}}), .out(multiplexer_26_out), .sel(\RST_高电平有效 ));
  Register #(.width(32), .trigger("rising"), .Select("low")) register_18 (
    .D(multiplexer_18_out), .en(not_1_out), .Q(IR_2), .clk(CLK));  // open: clr
  Register #(.width(32), .trigger("rising"), .Select("low")) register_19 (
    .D(multiplexer_19_out), .en(not_1_out), .Q(PC_2), .clk(CLK));  // open: clr
  Register #(.width(32), .trigger("rising"), .Select("low")) register_20 (
    .D(multiplexer_20_out), .en(not_1_out), .Q(PC_4_2), .clk(CLK));  // open: clr
  Register #(.width(32), .trigger("rising"), .Select("low")) register_21 (
    .D(multiplexer_21_out), .en(not_1_out), .Q(R1_2), .clk(CLK));  // open: clr
  Register #(.width(32), .trigger("rising"), .Select("low")) register_22 (
    .D(multiplexer_22_out), .en(not_1_out), .Q(R2_2), .clk(CLK));  // open: clr
  Register #(.width(12), .trigger("rising"), .Select("low")) register_23 (
    .D(multiplexer_23_out), .en(not_1_out), .Q(Imm_I_2), .clk(CLK));  // open: clr
  Register #(.width(12), .trigger("rising"), .Select("low")) register_24 (
    .D(multiplexer_24_out), .en(not_1_out), .Q(Imm_S_2), .clk(CLK));  // open: clr
  Register #(.width(12), .trigger("rising"), .Select("low")) register_25 (
    .D(multiplexer_25_out), .en(not_1_out), .Q(Imm_B_2), .clk(CLK));  // open: clr
  Register #(.width(20), .trigger("rising"), .Select("low")) register_26 (
    .D(multiplexer_26_out), .en(not_1_out), .Q(Imm_J_2), .clk(CLK));  // open: clr
endmodule

module \ID_EX_动态分支预测  (
  input  CLK,
  input  \RST_高电平有效 ,
  input  \en_低电平有效 ,
  input  RegWrite,
  input  [31:0] IR,
  input  AluSrcB,
  input  [3:0] AluOP,
  input  [31:0] PC,
  input  MemWrite,
  input  [31:0] PC_4,
  input  MemToReg,
  input  [31:0] R1,
  input  Bne,
  input  [31:0] R2,
  input  Beq,
  input  JAL,
  input  [11:0] Imm_I,
  input  [11:0] Imm_S,
  input  JALR,
  input  [11:0] Imm_B,
  input  URET,
  input  [19:0] Imm_J,
  input  ecall,
  input  Sltiu,
  input  Sb,
  input  Blt,
  input  S_Type,
  input  [1:0] R1_F,
  input  [1:0] R2_F,
  input  PredictJump,
  output RegWrite_2,
  output [31:0] IR_2,
  output AluSrcB_2,
  output [3:0] AluOP_2,
  output [31:0] PC_2,
  output MemWrite_2,
  output [31:0] PC_4_2,
  output MemToReg_2,
  output [31:0] R1_2,
  output Bne_2,
  output [31:0] R2_2,
  output Beq_2,
  output JAL_2,
  output [11:0] Imm_I_2,
  output [11:0] Imm_S_2,
  output JALR_2,
  output [11:0] Imm_B_2,
  output URET_2,
  output [19:0] Imm_J_2,
  output ecall_2,
  output Sltiu_2,
  output Sb_2,
  output Blt_2,
  output S_Type_2,
  output [1:0] R1_F_2,
  output [1:0] R2_F_2,
  output PredictJump_2
);

  wire multiplexer_1_out, multiplexer_2_out, multiplexer_4_out, multiplexer_5_out, multiplexer_6_out,
       multiplexer_7_out, multiplexer_8_out, multiplexer_9_out, multiplexer_10_out, multiplexer_11_out,
       multiplexer_12_out, multiplexer_13_out, multiplexer_14_out, multiplexer_15_out, multiplexer_18_out,
       not_1_out;
  wire [1:0] multiplexer_16_out, multiplexer_17_out;
  wire [3:0] multiplexer_3_out;
  wire [11:0] multiplexer_24_out, multiplexer_25_out, multiplexer_26_out;
  wire [19:0] multiplexer_27_out;
  wire [31:0] multiplexer_19_out, multiplexer_20_out, multiplexer_21_out, multiplexer_22_out,
       multiplexer_23_out;

  not not_1 (not_1_out, \en_低电平有效 );
  Multiplexer #(.select(1), .width(1), .disabled("Z"), .enable("false")) multiplexer_1 (
    .in0(RegWrite), .in1(1'b0), .out(multiplexer_1_out), .sel(\RST_高电平有效 ));
  Multiplexer #(.select(1), .width(1), .disabled("Z"), .enable("false")) multiplexer_2 (
    .in0(AluSrcB), .in1(1'b0), .out(multiplexer_2_out), .sel(\RST_高电平有效 ));
  Multiplexer #(.select(1), .width(4), .disabled("Z"), .enable("false")) multiplexer_3 (
    .in0(AluOP), .in1(4'b0000), .out(multiplexer_3_out), .sel(\RST_高电平有效 ));
  Multiplexer #(.select(1), .width(1), .disabled("Z"), .enable("false")) multiplexer_4 (
    .in0(MemWrite), .in1(1'b0), .out(multiplexer_4_out), .sel(\RST_高电平有效 ));
  Multiplexer #(.select(1), .width(1), .disabled("Z"), .enable("false")) multiplexer_5 (
    .in0(MemToReg), .in1(1'b0), .out(multiplexer_5_out), .sel(\RST_高电平有效 ));
  Multiplexer #(.select(1), .width(1), .disabled("Z"), .enable("false")) multiplexer_6 (
    .in0(Bne), .in1(1'b0), .out(multiplexer_6_out), .sel(\RST_高电平有效 ));
  Multiplexer #(.select(1), .width(1), .disabled("Z"), .enable("false")) multiplexer_7 (
    .in0(Beq), .in1(1'b0), .out(multiplexer_7_out), .sel(\RST_高电平有效 ));
  Multiplexer #(.select(1), .width(1), .disabled("Z"), .enable("false")) multiplexer_8 (
    .in0(JAL), .in1(1'b0), .out(multiplexer_8_out), .sel(\RST_高电平有效 ));
  Multiplexer #(.select(1), .width(1), .disabled("Z"), .enable("false")) multiplexer_9 (
    .in0(JALR), .in1(1'b0), .out(multiplexer_9_out), .sel(\RST_高电平有效 ));
  Multiplexer #(.select(1), .width(1), .disabled("Z"), .enable("false")) multiplexer_10 (
    .in0(URET), .in1(1'b0), .out(multiplexer_10_out), .sel(\RST_高电平有效 ));
  Multiplexer #(.select(1), .width(1), .disabled("Z"), .enable("false")) multiplexer_11 (
    .in0(ecall), .in1(1'b0), .out(multiplexer_11_out), .sel(\RST_高电平有效 ));
  Multiplexer #(.select(1), .width(1), .disabled("Z"), .enable("false")) multiplexer_12 (
    .in0(Sltiu), .in1(1'b0), .out(multiplexer_12_out), .sel(\RST_高电平有效 ));
  Multiplexer #(.select(1), .width(1), .disabled("Z"), .enable("false")) multiplexer_13 (
    .in0(Sb), .in1(1'b0), .out(multiplexer_13_out), .sel(\RST_高电平有效 ));
  Multiplexer #(.select(1), .width(1), .disabled("Z"), .enable("false")) multiplexer_14 (
    .in0(Blt), .in1(1'b0), .out(multiplexer_14_out), .sel(\RST_高电平有效 ));
  Multiplexer #(.select(1), .width(1), .disabled("Z"), .enable("false")) multiplexer_15 (
    .in0(S_Type), .in1(1'b0), .out(multiplexer_15_out), .sel(\RST_高电平有效 ));
  Multiplexer #(.select(1), .width(2), .disabled("Z"), .enable("false")) multiplexer_16 (
    .in0(R1_F), .in1(2'b00), .out(multiplexer_16_out), .sel(\RST_高电平有效 ));
  Multiplexer #(.select(1), .width(2), .disabled("Z"), .enable("false")) multiplexer_17 (
    .in0(R2_F), .in1(2'b00), .out(multiplexer_17_out), .sel(\RST_高电平有效 ));
  Multiplexer #(.select(1), .width(1), .disabled("Z"), .enable("false")) multiplexer_18 (
    .in0(PredictJump), .in1(1'b0), .out(multiplexer_18_out), .sel(\RST_高电平有效 ));
  Register #(.width(1), .trigger("rising"), .Select("low")) register_1 (
    .D(multiplexer_1_out), .en(not_1_out), .Q(RegWrite_2), .clk(CLK));  // open: clr
  Register #(.width(1), .trigger("rising"), .Select("low")) register_2 (
    .D(multiplexer_2_out), .en(not_1_out), .Q(AluSrcB_2), .clk(CLK));  // open: clr
  Register #(.width(4), .trigger("rising"), .Select("low")) register_3 (
    .D(multiplexer_3_out), .Q(AluOP_2), .clk(CLK));  // open: en, clr
  Register #(.width(1), .trigger("rising"), .Select("low")) register_4 (
    .D(multiplexer_4_out), .en(not_1_out), .Q(MemWrite_2), .clk(CLK));  // open: clr
  Register #(.width(1), .trigger("rising"), .Select("low")) register_5 (
    .D(multiplexer_5_out), .en(not_1_out), .Q(MemToReg_2), .clk(CLK));  // open: clr
  Register #(.width(1), .trigger("rising"), .Select("low")) register_6 (
    .D(multiplexer_6_out), .en(not_1_out), .Q(Bne_2), .clk(CLK));  // open: clr
  Register #(.width(1), .trigger("rising"), .Select("low")) register_7 (
    .D(multiplexer_7_out), .en(not_1_out), .Q(Beq_2), .clk(CLK));  // open: clr
  Register #(.width(1), .trigger("rising"), .Select("low")) register_8 (
    .D(multiplexer_8_out), .en(not_1_out), .Q(JAL_2), .clk(CLK));  // open: clr
  Register #(.width(1), .trigger("rising"), .Select("low")) register_9 (
    .D(multiplexer_9_out), .en(not_1_out), .Q(JALR_2), .clk(CLK));  // open: clr
  Register #(.width(1), .trigger("rising"), .Select("low")) register_10 (
    .D(multiplexer_10_out), .en(not_1_out), .Q(URET_2), .clk(CLK));  // open: clr
  Register #(.width(1), .trigger("rising"), .Select("low")) register_11 (
    .D(multiplexer_11_out), .en(not_1_out), .Q(ecall_2), .clk(CLK));  // open: clr
  Register #(.width(1), .trigger("rising"), .Select("low")) register_12 (
    .D(multiplexer_12_out), .en(not_1_out), .Q(Sltiu_2), .clk(CLK));  // open: clr
  Register #(.width(1), .trigger("rising"), .Select("low")) register_13 (
    .D(multiplexer_13_out), .en(not_1_out), .Q(Sb_2), .clk(CLK));  // open: clr
  Register #(.width(1), .trigger("rising"), .Select("low")) register_14 (
    .D(multiplexer_14_out), .en(not_1_out), .Q(Blt_2), .clk(CLK));  // open: clr
  Register #(.width(1), .trigger("rising"), .Select("low")) register_15 (
    .D(multiplexer_15_out), .en(not_1_out), .Q(S_Type_2), .clk(CLK));  // open: clr
  Register #(.width(2), .trigger("rising"), .Select("low")) register_16 (
    .D(multiplexer_16_out), .en(not_1_out), .Q(R1_F_2), .clk(CLK));  // open: clr
  Register #(.width(2), .trigger("rising"), .Select("low")) register_17 (
    .D(multiplexer_17_out), .en(not_1_out), .Q(R2_F_2), .clk(CLK));  // open: clr
  Register #(.width(1), .trigger("rising"), .Select("low")) register_18 (
    .D(multiplexer_18_out), .en(not_1_out), .Q(PredictJump_2), .clk(CLK));  // open: clr
  Pull_Resistor #(.pull(0)) pull_resistor_1 (.node(\RST_高电平有效 ));
  Pull_Resistor #(.pull(0)) pull_resistor_2 (.node(not_1_out));
  Multiplexer #(.select(1), .width(32), .disabled("Z"), .enable("false")) multiplexer_19 (
    .in0(IR), .in1({32{1'b0}}), .out(multiplexer_19_out), .sel(\RST_高电平有效 ));
  Multiplexer #(.select(1), .width(32), .disabled("Z"), .enable("false")) multiplexer_20 (
    .in0(PC), .in1({32{1'b0}}), .out(multiplexer_20_out), .sel(\RST_高电平有效 ));
  Multiplexer #(.select(1), .width(32), .disabled("Z"), .enable("false")) multiplexer_21 (
    .in0(PC_4), .in1({32{1'b0}}), .out(multiplexer_21_out), .sel(\RST_高电平有效 ));
  Multiplexer #(.select(1), .width(32), .disabled("Z"), .enable("false")) multiplexer_22 (
    .in0(R1), .in1({32{1'b0}}), .out(multiplexer_22_out), .sel(\RST_高电平有效 ));
  Multiplexer #(.select(1), .width(32), .disabled("Z"), .enable("false")) multiplexer_23 (
    .in0(R2), .in1({32{1'b0}}), .out(multiplexer_23_out), .sel(\RST_高电平有效 ));
  Multiplexer #(.select(1), .width(12), .disabled("Z"), .enable("false")) multiplexer_24 (
    .in0(Imm_I), .in1({12{1'b0}}), .out(multiplexer_24_out), .sel(\RST_高电平有效 ));
  Multiplexer #(.select(1), .width(12), .disabled("Z"), .enable("false")) multiplexer_25 (
    .in0(Imm_S), .in1({12{1'b0}}), .out(multiplexer_25_out), .sel(\RST_高电平有效 ));
  Multiplexer #(.select(1), .width(12), .disabled("Z"), .enable("false")) multiplexer_26 (
    .in0(Imm_B), .in1({12{1'b0}}), .out(multiplexer_26_out), .sel(\RST_高电平有效 ));
  Multiplexer #(.select(1), .width(20), .disabled("Z"), .enable("false")) multiplexer_27 (
    .in0(Imm_J), .in1({20{1'b0}}), .out(multiplexer_27_out), .sel(\RST_高电平有效 ));
  Register #(.width(32), .trigger("rising"), .Select("low")) register_19 (
    .D(multiplexer_19_out), .en(not_1_out), .Q(IR_2), .clk(CLK));  // open: clr
  Register #(.width(32), .trigger("rising"), .Select("low")) register_20 (
    .D(multiplexer_20_out), .en(not_1_out), .Q(PC_2), .clk(CLK));  // open: clr
  Register #(.width(32), .trigger("rising"), .Select("low")) register_21 (
    .D(multiplexer_21_out), .en(not_1_out), .Q(PC_4_2), .clk(CLK));  // open: clr
  Register #(.width(32), .trigger("rising"), .Select("low")) register_22 (
    .D(multiplexer_22_out), .en(not_1_out), .Q(R1_2), .clk(CLK));  // open: clr
  Register #(.width(32), .trigger("rising"), .Select("low")) register_23 (
    .D(multiplexer_23_out), .en(not_1_out), .Q(R2_2), .clk(CLK));  // open: clr
  Register #(.width(12), .trigger("rising"), .Select("low")) register_24 (
    .D(multiplexer_24_out), .en(not_1_out), .Q(Imm_I_2), .clk(CLK));  // open: clr
  Register #(.width(12), .trigger("rising"), .Select("low")) register_25 (
    .D(multiplexer_25_out), .en(not_1_out), .Q(Imm_S_2), .clk(CLK));  // open: clr
  Register #(.width(12), .trigger("rising"), .Select("low")) register_26 (
    .D(multiplexer_26_out), .en(not_1_out), .Q(Imm_B_2), .clk(CLK));  // open: clr
  Register #(.width(20), .trigger("rising"), .Select("low")) register_27 (
    .D(multiplexer_27_out), .en(not_1_out), .Q(Imm_J_2), .clk(CLK));  // open: clr
endmodule

module EX_MEM (
  input  CLK,
  input  \RST_高电平有效 ,
  input  \en_低电平有效 ,
  input  RegWrite,
  input  MemWrite,
  input  [31:0] IR,
  input  MemToReg,
  input  JAL,
  input  [31:0] PC,
  input  JALR,
  input  [31:0] PC_4,
  input  ecall,
  input  [31:0] R1,
  input  Sb,
  input  [31:0] R2,
  input  [31:0] AluData,
  output RegWrite_2,
  output MemWrite_2,
  output [31:0] IR_2,
  output MemToReg_2,
  output JAL_2,
  output [31:0] PC_2,
  output JALR_2,
  output [31:0] PC_4_2,
  output ecall_2,
  output [31:0] R1_2,
  output Sb_2,
  output [31:0] R2_2,
  output [31:0] AluData_2
);

  wire multiplexer_1_out, multiplexer_2_out, multiplexer_3_out, multiplexer_4_out, multiplexer_5_out,
       multiplexer_6_out, multiplexer_7_out, not_1_out;
  wire [31:0] multiplexer_8_out, multiplexer_9_out, multiplexer_10_out, multiplexer_11_out,
       multiplexer_12_out, multiplexer_13_out;

  not not_1 (not_1_out, \en_低电平有效 );
  Multiplexer #(.select(1), .width(1), .disabled("Z"), .enable("false")) multiplexer_1 (
    .in0(RegWrite), .in1(1'b0), .out(multiplexer_1_out), .sel(\RST_高电平有效 ));
  Multiplexer #(.select(1), .width(1), .disabled("Z"), .enable("false")) multiplexer_2 (
    .in0(MemWrite), .in1(1'b0), .out(multiplexer_2_out), .sel(\RST_高电平有效 ));
  Multiplexer #(.select(1), .width(1), .disabled("Z"), .enable("false")) multiplexer_3 (
    .in0(MemToReg), .in1(1'b0), .out(multiplexer_3_out), .sel(\RST_高电平有效 ));
  Multiplexer #(.select(1), .width(1), .disabled("Z"), .enable("false")) multiplexer_4 (
    .in0(JAL), .in1(1'b0), .out(multiplexer_4_out), .sel(\RST_高电平有效 ));
  Multiplexer #(.select(1), .width(1), .disabled("Z"), .enable("false")) multiplexer_5 (
    .in0(JALR), .in1(1'b0), .out(multiplexer_5_out), .sel(\RST_高电平有效 ));
  Multiplexer #(.select(1), .width(1), .disabled("Z"), .enable("false")) multiplexer_6 (
    .in0(ecall), .in1(1'b0), .out(multiplexer_6_out), .sel(\RST_高电平有效 ));
  Multiplexer #(.select(1), .width(1), .disabled("Z"), .enable("false")) multiplexer_7 (
    .in0(Sb), .in1(1'b0), .out(multiplexer_7_out), .sel(\RST_高电平有效 ));
  Register #(.width(1), .trigger("rising"), .Select("low")) register_1 (
    .D(multiplexer_1_out), .en(not_1_out), .Q(RegWrite_2), .clk(CLK));  // open: clr
  Register #(.width(1), .trigger("rising"), .Select("low")) register_2 (
    .D(multiplexer_2_out), .en(not_1_out), .Q(MemWrite_2), .clk(CLK));  // open: clr
  Register #(.width(1), .trigger("rising"), .Select("low")) register_3 (
    .D(multiplexer_3_out), .en(not_1_out), .Q(MemToReg_2), .clk(CLK));  // open: clr
  Register #(.width(1), .trigger("rising"), .Select("low")) register_4 (
    .D(multiplexer_4_out), .en(not_1_out), .Q(JAL_2), .clk(CLK));  // open: clr
  Register #(.width(1), .trigger("rising"), .Select("low")) register_5 (
    .D(multiplexer_5_out), .en(not_1_out), .Q(JALR_2), .clk(CLK));  // open: clr
  Register #(.width(1), .trigger("rising"), .Select("low")) register_6 (
    .D(multiplexer_6_out), .en(not_1_out), .Q(ecall_2), .clk(CLK));  // open: clr
  Register #(.width(1), .trigger("rising"), .Select("low")) register_7 (
    .D(multiplexer_7_out), .en(not_1_out), .Q(Sb_2), .clk(CLK));  // open: clr
  Pull_Resistor #(.pull(0)) pull_resistor_1 (.node(\RST_高电平有效 ));
  Pull_Resistor #(.pull(0)) pull_resistor_2 (.node(not_1_out));
  Multiplexer #(.select(1), .width(32), .disabled("Z"), .enable("false")) multiplexer_8 (
    .in0(IR), .in1({32{1'b0}}), .out(multiplexer_8_out), .sel(\RST_高电平有效 ));
  Multiplexer #(.select(1), .width(32), .disabled("Z"), .enable("false")) multiplexer_9 (
    .in0(PC), .in1({32{1'b0}}), .out(multiplexer_9_out), .sel(\RST_高电平有效 ));
  Multiplexer #(.select(1), .width(32), .disabled("Z"), .enable("false")) multiplexer_10 (
    .in0(PC_4), .in1({32{1'b0}}), .out(multiplexer_10_out), .sel(\RST_高电平有效 ));
  Multiplexer #(.select(1), .width(32), .disabled("Z"), .enable("false")) multiplexer_11 (
    .in0(R1), .in1({32{1'b0}}), .out(multiplexer_11_out), .sel(\RST_高电平有效 ));
  Multiplexer #(.select(1), .width(32), .disabled("Z"), .enable("false")) multiplexer_12 (
    .in0(R2), .in1({32{1'b0}}), .out(multiplexer_12_out), .sel(\RST_高电平有效 ));
  Multiplexer #(.select(1), .width(32), .disabled("Z"), .enable("false")) multiplexer_13 (
    .in0(AluData), .in1({32{1'b0}}), .out(multiplexer_13_out), .sel(\RST_高电平有效 ));
  Register #(.width(32), .trigger("rising"), .Select("low")) register_8 (
    .D(multiplexer_8_out), .en(not_1_out), .Q(IR_2), .clk(CLK));  // open: clr
  Register #(.width(32), .trigger("rising"), .Select("low")) register_9 (
    .D(multiplexer_9_out), .en(not_1_out), .Q(PC_2), .clk(CLK));  // open: clr
  Register #(.width(32), .trigger("rising"), .Select("low")) register_10 (
    .D(multiplexer_10_out), .en(not_1_out), .Q(PC_4_2), .clk(CLK));  // open: clr
  Register #(.width(32), .trigger("rising"), .Select("low")) register_11 (
    .D(multiplexer_11_out), .en(not_1_out), .Q(R1_2), .clk(CLK));  // open: clr
  Register #(.width(32), .trigger("rising"), .Select("low")) register_12 (
    .D(multiplexer_12_out), .en(not_1_out), .Q(R2_2), .clk(CLK));  // open: clr
  Register #(.width(32), .trigger("rising"), .Select("low")) register_13 (
    .D(multiplexer_13_out), .en(not_1_out), .Q(AluData_2), .clk(CLK));  // open: clr
endmodule

module MEM_WB (
  input  CLK,
  input  \RST_高电平有效 ,
  input  \en_低电平有效 ,
  input  RegWrite,
  input  [31:0] IR,
  input  MemToReg,
  input  JAL,
  input  [31:0] PC,
  input  JALR,
  input  [31:0] PC_4,
  input  ecall,
  input  [31:0] R1,
  input  [31:0] R2,
  input  [31:0] AluData,
  input  [31:0] MemData,
  output RegWrite_2,
  output [31:0] IR_2,
  output MemToReg_2,
  output JAL_2,
  output [31:0] PC_2,
  output JALR_2,
  output [31:0] PC_4_2,
  output ecall_2,
  output [31:0] R1_2,
  output [31:0] R2_2,
  output [31:0] AluData_2,
  output [31:0] MemData_2
);

  wire multiplexer_1_out, multiplexer_2_out, multiplexer_3_out, multiplexer_4_out, multiplexer_5_out,
       not_1_out;
  wire [31:0] multiplexer_6_out, multiplexer_7_out, multiplexer_8_out, multiplexer_9_out, multiplexer_10_out,
       multiplexer_11_out, multiplexer_12_out;

  not not_1 (not_1_out, \en_低电平有效 );
  Multiplexer #(.select(1), .width(1), .disabled("Z"), .enable("false")) multiplexer_1 (
    .in0(RegWrite), .in1(1'b0), .out(multiplexer_1_out), .sel(\RST_高电平有效 ));
  Multiplexer #(.select(1), .width(1), .disabled("Z"), .enable("false")) multiplexer_2 (
    .in0(MemToReg), .in1(1'b0), .out(multiplexer_2_out), .sel(\RST_高电平有效 ));
  Multiplexer #(.select(1), .width(1), .disabled("Z"), .enable("false")) multiplexer_3 (
    .in0(JAL), .in1(1'b0), .out(multiplexer_3_out), .sel(\RST_高电平有效 ));
  Multiplexer #(.select(1), .width(1), .disabled("Z"), .enable("false")) multiplexer_4 (
    .in0(JALR), .in1(1'b0), .out(multiplexer_4_out), .sel(\RST_高电平有效 ));
  Multiplexer #(.select(1), .width(1), .disabled("Z"), .enable("false")) multiplexer_5 (
    .in0(ecall), .in1(1'b0), .out(multiplexer_5_out), .sel(\RST_高电平有效 ));
  Register #(.width(1), .trigger("rising"), .Select("low")) register_1 (
    .D(multiplexer_1_out), .en(not_1_out), .Q(RegWrite_2), .clk(CLK));  // open: clr
  Register #(.width(1), .trigger("rising"), .Select("low")) register_2 (
    .D(multiplexer_2_out), .en(not_1_out), .Q(MemToReg_2), .clk(CLK));  // open: clr
  Register #(.width(1), .trigger("rising"), .Select("low")) register_3 (
    .D(multiplexer_3_out), .en(not_1_out), .Q(JAL_2), .clk(CLK));  // open: clr
  Register #(.width(1), .trigger("rising"), .Select("low")) register_4 (
    .D(multiplexer_4_out), .en(not_1_out), .Q(JALR_2), .clk(CLK));  // open: clr
  Register #(.width(1), .trigger("rising"), .Select("low")) register_5 (
    .D(multiplexer_5_out), .en(not_1_out), .Q(ecall_2), .clk(CLK));  // open: clr
  Pull_Resistor #(.pull(0)) pull_resistor_1 (.node(\RST_高电平有效 ));
  Pull_Resistor #(.pull(0)) pull_resistor_2 (.node(not_1_out));
  Multiplexer #(.select(1), .width(32), .disabled("Z"), .enable("false")) multiplexer_6 (
    .in0(IR), .in1({32{1'b0}}), .out(multiplexer_6_out), .sel(\RST_高电平有效 ));
  Multiplexer #(.select(1), .width(32), .disabled("Z"), .enable("false")) multiplexer_7 (
    .in0(PC), .in1({32{1'b0}}), .out(multiplexer_7_out), .sel(\RST_高电平有效 ));
  Multiplexer #(.select(1), .width(32), .disabled("Z"), .enable("false")) multiplexer_8 (
    .in0(PC_4), .in1({32{1'b0}}), .out(multiplexer_8_out), .sel(\RST_高电平有效 ));
  Multiplexer #(.select(1), .width(32), .disabled("Z"), .enable("false")) multiplexer_9 (
    .in0(R1), .in1({32{1'b0}}), .out(multiplexer_9_out), .sel(\RST_高电平有效 ));
  Multiplexer #(.select(1), .width(32), .disabled("Z"), .enable("false")) multiplexer_10 (
    .in0(R2), .in1({32{1'b0}}), .out(multiplexer_10_out), .sel(\RST_高电平有效 ));
  Multiplexer #(.select(1), .width(32), .disabled("Z"), .enable("false")) multiplexer_11 (
    .in0(AluData), .in1({32{1'b0}}), .out(multiplexer_11_out), .sel(\RST_高电平有效 ));
  Multiplexer #(.select(1), .width(32), .disabled("Z"), .enable("false")) multiplexer_12 (
    .in0(MemData), .in1({32{1'b0}}), .out(multiplexer_12_out), .sel(\RST_高电平有效 ));
  Register #(.width(32), .trigger("rising"), .Select("low")) register_6 (
    .D(multiplexer_6_out), .en(not_1_out), .Q(IR_2), .clk(CLK));  // open: clr
  Register #(.width(32), .trigger("rising"), .Select("low")) register_7 (
    .D(multiplexer_7_out), .en(not_1_out), .Q(PC_2), .clk(CLK));  // open: clr
  Register #(.width(32), .trigger("rising"), .Select("low")) register_8 (
    .D(multiplexer_8_out), .en(not_1_out), .Q(PC_4_2), .clk(CLK));  // open: clr
  Register #(.width(32), .trigger("rising"), .Select("low")) register_9 (
    .D(multiplexer_9_out), .en(not_1_out), .Q(R1_2), .clk(CLK));  // open: clr
  Register #(.width(32), .trigger("rising"), .Select("low")) register_10 (
    .D(multiplexer_10_out), .en(not_1_out), .Q(R2_2), .clk(CLK));  // open: clr
  Register #(.width(32), .trigger("rising"), .Select("low")) register_11 (
    .D(multiplexer_11_out), .en(not_1_out), .Q(AluData_2), .clk(CLK));  // open: clr
  Register #(.width(32), .trigger("rising"), .Select("low")) register_12 (
    .D(multiplexer_12_out), .en(not_1_out), .Q(MemData_2), .clk(CLK));  // open: clr
endmodule

module \数据相关检测  (
  input  R1Used,
  input  EX_RegWrite,
  input  [4:0] ID_R1,
  input  [4:0] ID_R2,
  input  R2Used,
  input  WEW_RegWrite,
  input  [4:0] EX_RD,
  input  [4:0] WEW_RD,
  output DataHazzard
);

  wire and_1_out, and_2_out, and_3_out, and_4_out, comparator_1_eq, comparator_2_eq, comparator_3_eq,
       comparator_4_eq, comparator_5_eq, comparator_6_eq;

  Comparator #(.width(5), .mode("twosComplement")) comparator_1 (
    .a(ID_R1), .b(EX_RD), .eq(comparator_1_eq));  // open: gt, lt
  Comparator #(.width(5), .mode("twosComplement")) comparator_2 (
    .a(ID_R1), .b({5{1'b0}}), .eq(comparator_2_eq));  // open: gt, lt
  Comparator #(.width(5), .mode("twosComplement")) comparator_3 (
    .a(ID_R2), .b(EX_RD), .eq(comparator_3_eq));  // open: gt, lt
  Comparator #(.width(5), .mode("twosComplement")) comparator_4 (
    .a(ID_R2), .b({5{1'b0}}), .eq(comparator_4_eq));  // open: gt, lt
  Comparator #(.width(5), .mode("twosComplement")) comparator_5 (
    .a(ID_R1), .b(WEW_RD), .eq(comparator_5_eq));  // open: gt, lt
  Comparator #(.width(5), .mode("twosComplement")) comparator_6 (
    .a(ID_R2), .b(WEW_RD), .eq(comparator_6_eq));  // open: gt, lt
  and and_1 (and_1_out, R1Used, EX_RegWrite, comparator_1_eq, ~comparator_2_eq);  // AND_Gate
  and and_2 (and_2_out, R2Used, EX_RegWrite, comparator_3_eq, ~comparator_4_eq);  // AND_Gate
  and and_3 (and_3_out, R1Used, WEW_RegWrite, comparator_5_eq, ~comparator_2_eq);  // AND_Gate
  and and_4 (and_4_out, R2Used, WEW_RegWrite, comparator_6_eq, ~comparator_4_eq);  // AND_Gate
  or or_1 (DataHazzard, and_1_out, and_2_out, and_3_out, and_4_out);

  // Notes on the sheet:
  //   ID.R1
  //   ID.R2
  //   EX.RD
endmodule

module \R1R2使用检测  (
  input  OP2,
  input  OP3,
  input  OP4,
  input  OP5,
  input  OP6,
  input  F12,
  input  F13,
  input  F14,
  input  F25,
  input  F30,
  output R1Used,
  output R2Used
);

  wire and_1_out, and_2_out, and_3_out, and_4_out, and_5_out, and_6_out, and_7_out, and_8_out, and_9_out,
       and_10_out, and_11_out, and_12_out, and_13_out, and_14_out, and_15_out, and_16_out, and_17_out,
       and_18_out, and_19_out, and_20_out, and_21_out, and_22_out, and_23_out, and_24_out, and_25_out,
       and_26_out, and_27_out, and_28_out, and_29_out, and_30_out, and_31_out, and_32_out, and_33_out,
       and_34_out, and_35_out, and_36_out, and_37_out, not_1_out, not_2_out, not_3_out, not_4_out, not_5_out,
       not_6_out, not_7_out, not_8_out, not_9_out, not_10_out, not_11_out, not_12_out, not_13_out,
       not_14_out, not_15_out, not_16_out, not_17_out, not_18_out, not_19_out, not_20_out, not_21_out,
       not_22_out, not_23_out, not_24_out, not_25_out, not_26_out, not_27_out, not_28_out, not_29_out,
       not_30_out, not_31_out, not_32_out, not_33_out, not_34_out, not_35_out, not_36_out, not_37_out,
       not_38_out, not_39_out, not_40_out, not_41_out, not_42_out, not_43_out, not_44_out, not_45_out,
       not_46_out, not_47_out, not_48_out, not_49_out, not_50_out, not_51_out, not_52_out, not_53_out,
       not_54_out, not_55_out, not_56_out, not_57_out, not_58_out, not_59_out, not_60_out, not_61_out,
       not_62_out, not_63_out, not_64_out, not_65_out, not_66_out, not_67_out, not_68_out, not_69_out,
       not_70_out, not_71_out, not_72_out, not_73_out, not_74_out, not_75_out, not_76_out, not_77_out,
       not_78_out, not_79_out, not_80_out, not_81_out, not_82_out, not_83_out, not_84_out, not_85_out,
       not_86_out, not_87_out, not_88_out, not_89_out, not_90_out, not_91_out, not_92_out, not_93_out,
       not_94_out, not_95_out, not_96_out, not_97_out, not_98_out, not_99_out, not_100_out, not_101_out,
       not_102_out, not_103_out, not_104_out, not_105_out, not_106_out, not_107_out, not_108_out,
       not_109_out, not_110_out, not_111_out, not_112_out, not_113_out, not_114_out, not_115_out,
       not_116_out, not_117_out, not_118_out, not_119_out, not_120_out, not_121_out, not_122_out,
       not_123_out, not_124_out, not_125_out, not_126_out, not_127_out, not_128_out, not_129_out,
       not_130_out, not_131_out, not_132_out, not_133_out, not_134_out, not_135_out, not_136_out,
       not_137_out, not_138_out, not_139_out, not_140_out, not_141_out, not_142_out, not_143_out,
       not_144_out, not_145_out, not_146_out, not_147_out, not_148_out, not_149_out, not_150_out,
       not_151_out, not_152_out, not_153_out, not_154_out, not_155_out, not_156_out, not_157_out,
       not_158_out, not_159_out, not_160_out, not_161_out, not_162_out, not_163_out, not_164_out,
       not_165_out, not_166_out, not_167_out, not_168_out, not_169_out, not_170_out, not_171_out,
       not_172_out, not_173_out, not_174_out, not_175_out, not_176_out, not_177_out, not_178_out,
       not_179_out, not_180_out, not_181_out, not_182_out, not_183_out, not_184_out, not_185_out,
       not_186_out, not_187_out, not_188_out, not_189_out, not_190_out, not_191_out, not_192_out,
       not_193_out, not_194_out, not_195_out, not_196_out, not_197_out, not_198_out, not_199_out,
       not_200_out, not_201_out, not_202_out, not_203_out, not_204_out, not_205_out, not_206_out,
       not_207_out, not_208_out, not_209_out, not_210_out, not_211_out, not_212_out, not_213_out,
       not_214_out, not_215_out, not_216_out, not_217_out, not_218_out, not_219_out, not_220_out, not_221_out;

  not not_1 (not_1_out, F30);
  not not_2 (not_2_out, F25);
  not not_3 (not_3_out, F14);
  not not_4 (not_4_out, F13);
  not not_5 (not_5_out, F12);
  not not_6 (not_6_out, OP6);
  not not_7 (not_7_out, OP3);
  not not_8 (not_8_out, OP2);
  not not_9 (not_9_out, F25);
  not not_10 (not_10_out, F14);
  not not_11 (not_11_out, F13);
  not not_12 (not_12_out, F12);
  not not_13 (not_13_out, OP6);
  not not_14 (not_14_out, OP3);
  not not_15 (not_15_out, OP2);
  not not_16 (not_16_out, F30);
  not not_17 (not_17_out, F25);
  not not_18 (not_18_out, OP6);
  not not_19 (not_19_out, OP3);
  not not_20 (not_20_out, OP2);
  not not_21 (not_21_out, F30);
  not not_22 (not_22_out, F25);
  not not_23 (not_23_out, F12);
  not not_24 (not_24_out, OP6);
  not not_25 (not_25_out, OP3);
  not not_26 (not_26_out, OP2);
  not not_27 (not_27_out, F30);
  not not_28 (not_28_out, F25);
  not not_29 (not_29_out, F14);
  not not_30 (not_30_out, F12);
  not not_31 (not_31_out, OP6);
  not not_32 (not_32_out, OP3);
  not not_33 (not_33_out, OP2);
  not not_34 (not_34_out, F30);
  not not_35 (not_35_out, F25);
  not not_36 (not_36_out, F14);
  not not_37 (not_37_out, OP6);
  not not_38 (not_38_out, OP3);
  not not_39 (not_39_out, OP2);
  not not_40 (not_40_out, F14);
  not not_41 (not_41_out, F13);
  not not_42 (not_42_out, F12);
  not not_43 (not_43_out, OP6);
  not not_44 (not_44_out, OP5);
  not not_45 (not_45_out, OP3);
  not not_46 (not_46_out, OP2);
  not not_47 (not_47_out, OP6);
  not not_48 (not_48_out, OP5);
  not not_49 (not_49_out, OP3);
  not not_50 (not_50_out, OP2);
  not not_51 (not_51_out, F12);
  not not_52 (not_52_out, OP6);
  not not_53 (not_53_out, OP5);
  not not_54 (not_54_out, OP3);
  not not_55 (not_55_out, OP2);
  not not_56 (not_56_out, F13);
  not not_57 (not_57_out, F12);
  not not_58 (not_58_out, OP6);
  not not_59 (not_59_out, OP5);
  not not_60 (not_60_out, OP3);
  not not_61 (not_61_out, OP2);
  not not_62 (not_62_out, F14);
  not not_63 (not_63_out, F12);
  not not_64 (not_64_out, OP6);
  not not_65 (not_65_out, OP5);
  not not_66 (not_66_out, OP3);
  not not_67 (not_67_out, OP2);
  not not_68 (not_68_out, F30);
  not not_69 (not_69_out, F25);
  not not_70 (not_70_out, F14);
  not not_71 (not_71_out, F13);
  not not_72 (not_72_out, OP6);
  not not_73 (not_73_out, OP5);
  not not_74 (not_74_out, OP3);
  not not_75 (not_75_out, OP2);
  not not_76 (not_76_out, F30);
  not not_77 (not_77_out, F25);
  not not_78 (not_78_out, F13);
  not not_79 (not_79_out, OP6);
  not not_80 (not_80_out, OP5);
  not not_81 (not_81_out, OP3);
  not not_82 (not_82_out, OP2);
  not not_83 (not_83_out, F25);
  not not_84 (not_84_out, F13);
  not not_85 (not_85_out, OP6);
  not not_86 (not_86_out, OP5);
  not not_87 (not_87_out, OP3);
  not not_88 (not_88_out, OP2);
  not not_89 (not_89_out, F14);
  not not_90 (not_90_out, F12);
  not not_91 (not_91_out, OP6);
  not not_92 (not_92_out, OP5);
  not not_93 (not_93_out, OP4);
  not not_94 (not_94_out, OP3);
  not not_95 (not_95_out, OP2);
  not not_96 (not_96_out, F14);
  not not_97 (not_97_out, F12);
  not not_98 (not_98_out, OP6);
  not not_99 (not_99_out, OP4);
  not not_100 (not_100_out, OP3);
  not not_101 (not_101_out, OP2);
  not not_102 (not_102_out, F14);
  not not_103 (not_103_out, F13);
  not not_104 (not_104_out, F12);
  not not_105 (not_105_out, OP3);
  not not_106 (not_106_out, OP2);
  not not_107 (not_107_out, F14);
  not not_108 (not_108_out, F13);
  not not_109 (not_109_out, F12);
  not not_110 (not_110_out, OP4);
  not not_111 (not_111_out, OP3);
  not not_112 (not_112_out, OP2);
  not not_113 (not_113_out, F14);
  not not_114 (not_114_out, F13);
  not not_115 (not_115_out, OP4);
  not not_116 (not_116_out, OP3);
  not not_117 (not_117_out, OP2);
  not not_118 (not_118_out, OP4);
  not not_119 (not_119_out, OP3);
  not not_120 (not_120_out, F30);
  not not_121 (not_121_out, F25);
  not not_122 (not_122_out, F13);
  not not_123 (not_123_out, OP6);
  not not_124 (not_124_out, OP3);
  not not_125 (not_125_out, OP2);
  not not_126 (not_126_out, F14);
  not not_127 (not_127_out, OP6);
  not not_128 (not_128_out, OP5);
  not not_129 (not_129_out, OP3);
  not not_130 (not_130_out, OP2);
  not not_131 (not_131_out, F14);
  not not_132 (not_132_out, F13);
  not not_133 (not_133_out, F12);
  not not_134 (not_134_out, OP6);
  not not_135 (not_135_out, OP4);
  not not_136 (not_136_out, OP3);
  not not_137 (not_137_out, OP2);
  not not_138 (not_138_out, F13);
  not not_139 (not_139_out, F12);
  not not_140 (not_140_out, OP4);
  not not_141 (not_141_out, OP3);
  not not_142 (not_142_out, OP2);
  not not_143 (not_143_out, F30);
  not not_144 (not_144_out, F25);
  not not_145 (not_145_out, F14);
  not not_146 (not_146_out, F13);
  not not_147 (not_147_out, F12);
  not not_148 (not_148_out, OP6);
  not not_149 (not_149_out, OP3);
  not not_150 (not_150_out, OP2);
  not not_151 (not_151_out, F25);
  not not_152 (not_152_out, F14);
  not not_153 (not_153_out, F13);
  not not_154 (not_154_out, F12);
  not not_155 (not_155_out, OP6);
  not not_156 (not_156_out, OP3);
  not not_157 (not_157_out, OP2);
  not not_158 (not_158_out, F30);
  not not_159 (not_159_out, F25);
  not not_160 (not_160_out, OP6);
  not not_161 (not_161_out, OP3);
  not not_162 (not_162_out, OP2);
  not not_163 (not_163_out, F30);
  not not_164 (not_164_out, F25);
  not not_165 (not_165_out, F12);
  not not_166 (not_166_out, OP6);
  not not_167 (not_167_out, OP3);
  not not_168 (not_168_out, OP2);
  not not_169 (not_169_out, F30);
  not not_170 (not_170_out, F25);
  not not_171 (not_171_out, F14);
  not not_172 (not_172_out, F12);
  not not_173 (not_173_out, OP6);
  not not_174 (not_174_out, OP3);
  not not_175 (not_175_out, OP2);
  not not_176 (not_176_out, F30);
  not not_177 (not_177_out, F25);
  not not_178 (not_178_out, F14);
  not not_179 (not_179_out, OP6);
  not not_180 (not_180_out, OP3);
  not not_181 (not_181_out, OP2);
  not not_182 (not_182_out, F14);
  not not_183 (not_183_out, F12);
  not not_184 (not_184_out, OP6);
  not not_185 (not_185_out, OP4);
  not not_186 (not_186_out, OP3);
  not not_187 (not_187_out, OP2);
  not not_188 (not_188_out, F14);
  not not_189 (not_189_out, F13);
  not not_190 (not_190_out, F12);
  not not_191 (not_191_out, OP3);
  not not_192 (not_192_out, OP2);
  not not_193 (not_193_out, F14);
  not not_194 (not_194_out, F13);
  not not_195 (not_195_out, F12);
  not not_196 (not_196_out, OP4);
  not not_197 (not_197_out, OP3);
  not not_198 (not_198_out, OP2);
  not not_199 (not_199_out, F14);
  not not_200 (not_200_out, F13);
  not not_201 (not_201_out, OP4);
  not not_202 (not_202_out, OP3);
  not not_203 (not_203_out, OP2);
  not not_204 (not_204_out, F30);
  not not_205 (not_205_out, F25);
  not not_206 (not_206_out, F13);
  not not_207 (not_207_out, OP6);
  not not_208 (not_208_out, OP3);
  not not_209 (not_209_out, OP2);
  not not_210 (not_210_out, F14);
  not not_211 (not_211_out, F13);
  not not_212 (not_212_out, F12);
  not not_213 (not_213_out, OP6);
  not not_214 (not_214_out, OP4);
  not not_215 (not_215_out, OP3);
  not not_216 (not_216_out, OP2);
  not not_217 (not_217_out, F13);
  not not_218 (not_218_out, F12);
  not not_219 (not_219_out, OP4);
  not not_220 (not_220_out, OP3);
  not not_221 (not_221_out, OP2);
  and and_1 (and_1_out, not_1_out, not_2_out, not_3_out, not_4_out, not_5_out, not_6_out, OP5, OP4, not_7_out, not_8_out);
  and and_2 (and_2_out, F30, not_9_out, not_10_out, not_11_out, not_12_out, not_13_out, OP5, OP4, not_14_out, not_15_out);
  and and_3 (and_3_out, not_16_out, not_17_out, F14, F13, F12, not_18_out, OP5, OP4, not_19_out, not_20_out);
  and and_4 (and_4_out, not_21_out, not_22_out, F14, F13, not_23_out, not_24_out, OP5, OP4, not_25_out, not_26_out);
  and and_5 (and_5_out, not_27_out, not_28_out, not_29_out, F13, not_30_out, not_31_out, OP5, OP4, not_32_out, not_33_out);
  and and_6 (and_6_out, not_34_out, not_35_out, not_36_out, F13, F12, not_37_out, OP5, OP4, not_38_out, not_39_out);
  and and_7 (and_7_out, not_40_out, not_41_out, not_42_out, not_43_out, not_44_out, OP4, not_45_out, not_46_out);
  and and_8 (and_8_out, F14, F13, F12, not_47_out, not_48_out, OP4, not_49_out, not_50_out);
  and and_9 (and_9_out, F14, F13, not_51_out, not_52_out, not_53_out, OP4, not_54_out, not_55_out);
  and and_10 (and_10_out, F14, not_56_out, not_57_out, not_58_out, not_59_out, OP4, not_60_out, not_61_out);
  and and_11 (and_11_out, not_62_out, F13, not_63_out, not_64_out, not_65_out, OP4, not_66_out, not_67_out);
  and and_12 (and_12_out, not_68_out, not_69_out, not_70_out, not_71_out, F12, not_72_out, not_73_out, OP4, not_74_out, not_75_out);
  and and_13 (and_13_out, not_76_out, not_77_out, F14, not_78_out, F12, not_79_out, not_80_out, OP4, not_81_out, not_82_out);
  and and_14 (and_14_out, F30, not_83_out, F14, not_84_out, F12, not_85_out, not_86_out, OP4, not_87_out, not_88_out);
  and and_15 (and_15_out, not_89_out, F13, not_90_out, not_91_out, not_92_out, not_93_out, not_94_out, not_95_out);
  and and_16 (and_16_out, not_96_out, F13, not_97_out, not_98_out, OP5, not_99_out, not_100_out, not_101_out);
  and and_17 (and_17_out, not_102_out, not_103_out, not_104_out, OP6, OP5, OP4, not_105_out, not_106_out);
  and and_18 (and_18_out, not_107_out, not_108_out, not_109_out, OP6, OP5, not_110_out, not_111_out, not_112_out);
  and and_19 (and_19_out, not_113_out, not_114_out, F12, OP6, OP5, not_115_out, not_116_out, not_117_out);
  and and_20 (and_20_out, OP6, OP5, not_118_out, not_119_out, OP2);
  and and_21 (and_21_out, not_120_out, not_121_out, F14, not_122_out, F12, not_123_out, OP5, OP4, not_124_out, not_125_out);
  and and_22 (and_22_out, not_126_out, F13, F12, not_127_out, not_128_out, OP4, not_129_out, not_130_out);
  and and_23 (and_23_out, not_131_out, not_132_out, not_133_out, not_134_out, OP5, not_135_out, not_136_out, not_137_out);
  and and_24 (and_24_out, F14, not_138_out, not_139_out, OP6, OP5, not_140_out, not_141_out, not_142_out);
  and and_25 (and_25_out, not_143_out, not_144_out, not_145_out, not_146_out, not_147_out, not_148_out, OP5, OP4, not_149_out, not_150_out);
  and and_26 (and_26_out, F30, not_151_out, not_152_out, not_153_out, not_154_out, not_155_out, OP5, OP4, not_156_out, not_157_out);
  and and_27 (and_27_out, not_158_out, not_159_out, F14, F13, F12, not_160_out, OP5, OP4, not_161_out, not_162_out);
  and and_28 (and_28_out, not_163_out, not_164_out, F14, F13, not_165_out, not_166_out, OP5, OP4, not_167_out, not_168_out);
  and and_29 (and_29_out, not_169_out, not_170_out, not_171_out, F13, not_172_out, not_173_out, OP5, OP4, not_174_out, not_175_out);
  and and_30 (and_30_out, not_176_out, not_177_out, not_178_out, F13, F12, not_179_out, OP5, OP4, not_180_out, not_181_out);
  and and_31 (and_31_out, not_182_out, F13, not_183_out, not_184_out, OP5, not_185_out, not_186_out, not_187_out);
  and and_32 (and_32_out, not_188_out, not_189_out, not_190_out, OP6, OP5, OP4, not_191_out, not_192_out);
  and and_33 (and_33_out, not_193_out, not_194_out, not_195_out, OP6, OP5, not_196_out, not_197_out, not_198_out);
  and and_34 (and_34_out, not_199_out, not_200_out, F12, OP6, OP5, not_201_out, not_202_out, not_203_out);
  and and_35 (and_35_out, not_204_out, not_205_out, F14, not_206_out, F12, not_207_out, OP5, OP4, not_208_out, not_209_out);
  and and_36 (and_36_out, not_210_out, not_211_out, not_212_out, not_213_out, OP5, not_214_out, not_215_out, not_216_out);
  and and_37 (and_37_out, F14, not_217_out, not_218_out, OP6, OP5, not_219_out, not_220_out, not_221_out);
  or or_1 (R2Used, and_25_out, and_26_out, and_27_out, and_28_out, and_29_out, and_30_out, and_31_out, and_32_out, and_33_out, and_34_out, and_35_out, and_36_out, and_37_out);
  or or_2 (R1Used, and_1_out, and_2_out, and_3_out, and_4_out, and_5_out, and_6_out, and_7_out, and_8_out, and_9_out, and_10_out, and_11_out, and_12_out, and_13_out, and_14_out, and_15_out, and_16_out, and_17_out, and_18_out, and_19_out, and_20_out, and_21_out, and_22_out, and_23_out, and_24_out);
endmodule

module \LoadUse信号生成  (
  input  R1Used,
  input  EX_MemToReg,
  input  [4:0] ID_R1,
  input  [4:0] EX_RD,
  input  [4:0] ID_R2,
  input  R2Used,
  output LoadUse
);

  wire and_1_out, and_2_out, comparator_1_eq, comparator_2_eq, comparator_3_eq, comparator_4_eq;

  Comparator #(.width(5), .mode("twosComplement")) comparator_1 (
    .a(ID_R1), .b({5{1'b0}}), .eq(comparator_1_eq));  // open: gt, lt
  Comparator #(.width(5), .mode("twosComplement")) comparator_2 (
    .a(ID_R1), .b(EX_RD), .eq(comparator_2_eq));  // open: gt, lt
  Comparator #(.width(5), .mode("twosComplement")) comparator_3 (
    .a(EX_RD), .b(ID_R2), .eq(comparator_3_eq));  // open: gt, lt
  Comparator #(.width(5), .mode("twosComplement")) comparator_4 (
    .a({5{1'b0}}), .b(ID_R2), .eq(comparator_4_eq));  // open: gt, lt
  and and_1 (and_1_out, R1Used, EX_MemToReg, comparator_2_eq, ~comparator_1_eq);  // AND_Gate
  and and_2 (and_2_out, ~comparator_4_eq, comparator_3_eq, EX_MemToReg, R2Used);  // AND_Gate
  or or_1 (LoadUse, and_1_out, and_2_out);
endmodule

module \R1_F_R2_F信号生成  (
  input  R1Used,
  input  [4:0] ID_R1,
  input  EX_RegWrite,
  input  [4:0] EX_RD,
  input  MEM_RegWrite,
  input  [4:0] MEM_RD,
  input  R2Used,
  input  [4:0] ID_R2,
  output [1:0] R1_F,
  output [1:0] R2_F
);

  wire comparator_1_eq, comparator_2_eq, comparator_3_eq, comparator_4_eq, comparator_5_eq, comparator_6_eq,
       not_1_out, not_2_out;
  wire [1:0] and_1_out, and_3_out;

  Comparator #(.width(5), .mode("twosComplement")) comparator_1 (
    .a(ID_R1), .b({5{1'b0}}), .eq(comparator_1_eq));  // open: gt, lt
  not not_1 (not_1_out, comparator_1_eq);
  Comparator #(.width(5), .mode("twosComplement")) comparator_2 (
    .a(ID_R1), .b(EX_RD), .eq(comparator_2_eq));  // open: gt, lt
  Comparator #(.width(5), .mode("twosComplement")) comparator_3 (
    .a(ID_R1), .b(MEM_RD), .eq(comparator_3_eq));  // open: gt, lt
  not not_2 (not_2_out, comparator_4_eq);
  Comparator #(.width(5), .mode("twosComplement")) comparator_4 (
    .a(ID_R2), .b({5{1'b0}}), .eq(comparator_4_eq));  // open: gt, lt
  Comparator #(.width(5), .mode("twosComplement")) comparator_5 (
    .a(ID_R2), .b(EX_RD), .eq(comparator_5_eq));  // open: gt, lt
  Comparator #(.width(5), .mode("twosComplement")) comparator_6 (
    .a(ID_R2), .b(MEM_RD), .eq(comparator_6_eq));  // open: gt, lt
  and and_1 (and_1_out[0], R1Used, not_1_out, EX_RegWrite, comparator_2_eq);
  and and_2 (and_1_out[1], not_1_out, R1Used, MEM_RegWrite, comparator_3_eq);
  and and_3 (and_3_out[0], R2Used, not_2_out, EX_RegWrite, comparator_5_eq);
  and and_4 (and_3_out[1], not_2_out, R2Used, MEM_RegWrite, comparator_6_eq);
  Multiplexer #(.select(2), .width(2), .disabled("Z"), .enable("false")) multiplexer_1 (
    .in0(2'b00), .in1(2'b10), .in2(2'b01), .in3(2'b10), .out(R1_F), .sel(and_1_out));
  Multiplexer #(.select(2), .width(2), .disabled("Z"), .enable("false")) multiplexer_2 (
    .in0(2'b00), .in1(2'b10), .in2(2'b01), .in3(2'b10), .out(R2_F), .sel(and_3_out));
endmodule

module \中断控制器  (
  input  IRA,
  input  Clr1,
  input  IRB,
  input  Clr2,
  input  IRC,
  input  Clr3,
  input  CLK,
  input  RST,
  output [1:0] \中断号 ,
  output \中断请求 ,
  output W1,
  output W2,
  output W3
);

  wire and_1_out, and_2_out, and_3_out, not_1_out, not_2_out, not_3_out, or_4_out, or_5_out, or_6_out,
       or_7_out, or_8_out, or_9_out, register_1_q, register_2_q, register_3_q, register_4_q, register_5_q,
       register_6_q;

  or or_1 (W1, register_4_q, register_1_q);
  or or_2 (W2, register_5_q, register_2_q);
  or or_3 (W3, register_6_q, register_3_q);
  Register #(.width(1), .trigger("rising"), .Select("low")) register_1 (
    .D(1'b1), .Q(register_1_q), .clk(IRA), .clr(or_4_out));  // open: en
  or or_4 (or_4_out, register_4_q, RST);
  Register #(.width(1), .trigger("rising"), .Select("low")) register_2 (
    .D(1'b1), .Q(register_2_q), .clk(IRB), .clr(or_5_out));  // open: en
  or or_5 (or_5_out, register_5_q, RST);
  Register #(.width(1), .trigger("rising"), .Select("low")) register_3 (
    .D(1'b1), .Q(register_3_q), .clk(IRC), .clr(or_6_out));  // open: en
  or or_6 (or_6_out, register_6_q, RST);
  or or_7 (or_7_out, register_1_q, register_4_q);
  or or_8 (or_8_out, register_2_q, register_5_q);
  or or_9 (or_9_out, register_3_q, register_6_q);
  and and_1 (and_1_out, or_7_out, not_1_out);
  not not_1 (not_1_out, Clr1);
  and and_2 (and_2_out, or_8_out, not_2_out);
  not not_2 (not_2_out, Clr2);
  and and_3 (and_3_out, or_9_out, not_3_out);
  not not_3 (not_3_out, Clr3);
  Register #(.width(1), .trigger("rising"), .Select("low")) register_4 (
    .D(and_1_out), .Q(register_4_q), .clk(CLK), .clr(RST));  // open: en
  Register #(.width(1), .trigger("rising"), .Select("low")) register_5 (
    .D(and_2_out), .Q(register_5_q), .clk(CLK), .clr(RST));  // open: en
  Register #(.width(1), .trigger("rising"), .Select("low")) register_6 (
    .D(and_3_out), .Q(register_6_q), .clk(CLK), .clr(RST));  // open: en
  Priority_Encoder #(.select(2), .disabled("Z")) priority_encoder_1 (
    .in0(1'b1), .in1(register_4_q), .in2(register_5_q), .in3(register_6_q), .out(\中断号 ));  // open: gs, en_out, en_in
  or or_10 (\中断请求 , register_4_q, register_5_q, register_6_q);
endmodule

module BTB (
  input  [31:0] PC,
  input  [31:0] EX_PC,
  input  [31:0] EX_BranchAddr,
  input  EX_Branch,
  input  EX_BranchTaken,
  input  CLK,
  input  [1:0] \initial ,
  output PredictJump,
  output [31:0] JumpAddr
);

  wire and_1_out, and_2_out, and_3_out, and_4_out, and_5_out, and_6_out, and_7_out, and_8_out, Clr0, Clr1,
       Clr2, Clr3, Clr4, Clr5, Clr6, Clr7, comparator_1_eq, comparator_2_eq, comparator_3_eq,
       comparator_4_eq, comparator_5_eq, comparator_6_eq, comparator_7_eq, comparator_8_eq, comparator_9_eq,
       comparator_10_eq, comparator_11_eq, comparator_12_eq, comparator_13_eq, comparator_14_eq,
       comparator_15_eq, comparator_16_eq, d_ff_1_qn, d_ff_2_qn, d_ff_3_qn, d_ff_4_qn, d_ff_5_qn, d_ff_6_qn,
       d_ff_7_qn, d_ff_8_qn, decoder_1_out0, decoder_1_out1, decoder_1_out2, decoder_1_out3, decoder_1_out4,
       decoder_1_out5, decoder_1_out6, decoder_1_out7, decoder_2_out0, decoder_2_out1, decoder_2_out2,
       decoder_2_out3, decoder_2_out4, decoder_2_out5, decoder_2_out6, decoder_2_out7, EX_Hit, EX_Miss, Full,
       L0, L1, L2, L3, L4, L5, L6, L7, M0, M1, M2, M3, M4, M5, M6, M7, not_1_out, not_2_out, not_3_out,
       not_4_out, not_5_out, not_6_out, not_7_out, not_8_out, or_1_out, or_2_out, or_3_out, or_4_out,
       or_5_out, or_6_out, or_7_out, or_8_out, or_10_out, or_11_out, or_12_out, or_13_out, or_14_out,
       or_15_out, or_16_out, or_17_out, priority_encoder_1_gs, v0, v1, v2, v3, v4, v5, v6, v7, Write0,
       Write1, Write2, Write3, Write4, Write5, Write6, Write7;
  wire [0:0] controlled_buffer_9_out, controlled_buffer_10_out, controlled_buffer_11_out,
       controlled_buffer_12_out, controlled_buffer_13_out, controlled_buffer_14_out,
       controlled_buffer_15_out, controlled_buffer_16_out;
  wire [1:0] fsm_1_next_state, fsm_2_next_state, fsm_3_next_state, fsm_4_next_state, fsm_5_next_state,
       fsm_6_next_state, fsm_7_next_state, fsm_8_next_state, Predict0, Predict1, Predict2, Predict3,
       Predict4, Predict5, Predict6, Predict7, \分支预测历史位_2_q , \分支预测历史位_3_q , \分支预测历史位_4_q , \分支预测历史位_5_q ,
       \分支预测历史位_6_q , \分支预测历史位_7_q , \分支预测历史位_8_q , \分支预测历史位_q ;
  wire [2:0] max_1_max_num, max_2_max_num, max_3_max_num, max_4_max_num, max_5_max_num, max_6_max_num,
       max_7_max_num, priority_encoder_1_out;
  wire [15:0] C0, C1, C2, C3, C4, C5, C6, C7, max_1_max, max_2_max, max_3_max, max_4_max, max_5_max,
       max_6_max;
  wire [31:0] Tag0, Tag1, Tag2, Tag3, Tag4, Tag5, Tag6, Tag7, \分支目标地址_2_q , \分支目标地址_3_q , \分支目标地址_4_q ,
       \分支目标地址_5_q , \分支目标地址_6_q , \分支目标地址_7_q , \分支目标地址_8_q , \分支目标地址_q ;

  Register #(.width(1), .trigger("rising"), .Select("low")) Valid (
    .D(1'b1), .en(Write0), .Q(v0), .clk(CLK));  // open: clr
  Register #(.width(1), .trigger("rising"), .Select("low")) Valid_2 (
    .D(1'b1), .en(Write1), .Q(v1), .clk(CLK));  // open: clr
  Register #(.width(1), .trigger("rising"), .Select("low")) Valid_3 (
    .D(1'b1), .en(Write2), .Q(v2), .clk(CLK));  // open: clr
  Register #(.width(1), .trigger("rising"), .Select("low")) Valid_4 (
    .D(1'b1), .en(Write3), .Q(v3), .clk(CLK));  // open: clr
  Register #(.width(1), .trigger("rising"), .Select("low")) Valid_5 (
    .D(1'b1), .en(Write4), .Q(v4), .clk(CLK));  // open: clr
  Register #(.width(1), .trigger("rising"), .Select("low")) Valid_6 (
    .D(1'b1), .en(Write5), .Q(v5), .clk(CLK));  // open: clr
  Register #(.width(1), .trigger("rising"), .Select("low")) Valid_7 (
    .D(1'b1), .en(Write6), .Q(v6), .clk(CLK));  // open: clr
  Register #(.width(1), .trigger("rising"), .Select("low")) Valid_8 (
    .D(1'b1), .en(Write7), .Q(v7), .clk(CLK));  // open: clr
  Register #(.width(32), .trigger("rising"), .Select("low")) \u_分支指令地址  (
    .D(EX_PC), .en(Write0), .Q(Tag0), .clk(CLK));  // open: clr
  Register #(.width(32), .trigger("rising"), .Select("low")) \u_分支指令地址_2  (
    .D(EX_PC), .en(Write1), .Q(Tag1), .clk(CLK));  // open: clr
  Register #(.width(32), .trigger("rising"), .Select("low")) \u_分支指令地址_3  (
    .D(EX_PC), .en(Write2), .Q(Tag2), .clk(CLK));  // open: clr
  Register #(.width(32), .trigger("rising"), .Select("low")) \u_分支指令地址_4  (
    .D(EX_PC), .en(Write3), .Q(Tag3), .clk(CLK));  // open: clr
  Register #(.width(32), .trigger("rising"), .Select("low")) \u_分支指令地址_5  (
    .D(EX_PC), .en(Write4), .Q(Tag4), .clk(CLK));  // open: clr
  Register #(.width(32), .trigger("rising"), .Select("low")) \u_分支指令地址_6  (
    .D(EX_PC), .en(Write5), .Q(Tag5), .clk(CLK));  // open: clr
  Register #(.width(32), .trigger("rising"), .Select("low")) \u_分支指令地址_7  (
    .D(EX_PC), .en(Write6), .Q(Tag6), .clk(CLK));  // open: clr
  Register #(.width(32), .trigger("rising"), .Select("low")) \u_分支指令地址_8  (
    .D(EX_PC), .en(Write7), .Q(Tag7), .clk(CLK));  // open: clr
  Register #(.width(32), .trigger("rising"), .Select("low")) \u_分支目标地址  (
    .D(EX_BranchAddr), .en(Write0), .Q(\分支目标地址_q ), .clk(CLK));  // open: clr
  assign JumpAddr = L0 ? \分支目标地址_q  : 32'bz;  // Controlled_Buffer controlled_buffer_1
  assign JumpAddr = L1 ? \分支目标地址_2_q  : 32'bz;  // Controlled_Buffer controlled_buffer_2
  Register #(.width(32), .trigger("rising"), .Select("low")) \u_分支目标地址_2  (
    .D(EX_BranchAddr), .en(Write1), .Q(\分支目标地址_2_q ), .clk(CLK));  // open: clr
  assign JumpAddr = L2 ? \分支目标地址_3_q  : 32'bz;  // Controlled_Buffer controlled_buffer_3
  Register #(.width(32), .trigger("rising"), .Select("low")) \u_分支目标地址_3  (
    .D(EX_BranchAddr), .en(Write2), .Q(\分支目标地址_3_q ), .clk(CLK));  // open: clr
  assign JumpAddr = L3 ? \分支目标地址_4_q  : 32'bz;  // Controlled_Buffer controlled_buffer_4
  Register #(.width(32), .trigger("rising"), .Select("low")) \u_分支目标地址_4  (
    .D(EX_BranchAddr), .en(Write3), .Q(\分支目标地址_4_q ), .clk(CLK));  // open: clr
  assign JumpAddr = L4 ? \分支目标地址_5_q  : 32'bz;  // Controlled_Buffer controlled_buffer_5
  Register #(.width(32), .trigger("rising"), .Select("low")) \u_分支目标地址_5  (
    .D(EX_BranchAddr), .en(Write4), .Q(\分支目标地址_5_q ), .clk(CLK));  // open: clr
  Register #(.width(32), .trigger("rising"), .Select("low")) \u_分支目标地址_6  (
    .D(EX_BranchAddr), .en(Write5), .Q(\分支目标地址_6_q ), .clk(CLK));  // open: clr
  assign JumpAddr = L5 ? \分支目标地址_6_q  : 32'bz;  // Controlled_Buffer controlled_buffer_6
  assign JumpAddr = L6 ? \分支目标地址_7_q  : 32'bz;  // Controlled_Buffer controlled_buffer_7
  Register #(.width(32), .trigger("rising"), .Select("low")) \u_分支目标地址_7  (
    .D(EX_BranchAddr), .en(Write6), .Q(\分支目标地址_7_q ), .clk(CLK));  // open: clr
  assign JumpAddr = L7 ? \分支目标地址_8_q  : 32'bz;  // Controlled_Buffer controlled_buffer_8
  Register #(.width(32), .trigger("rising"), .Select("low")) \u_分支目标地址_8  (
    .D(EX_BranchAddr), .en(Write7), .Q(\分支目标地址_8_q ), .clk(CLK));  // open: clr
  FSM fsm_1 (.Now_State(Predict0), .Jump(EX_BranchTaken), .Next_State(fsm_1_next_state));
  and and_1 (and_1_out, EX_Branch, M0);
  FSM fsm_2 (.Now_State(Predict1), .Jump(EX_BranchTaken), .Next_State(fsm_2_next_state));
  and and_2 (and_2_out, EX_Branch, M1);
  FSM fsm_3 (.Now_State(Predict2), .Jump(EX_BranchTaken), .Next_State(fsm_3_next_state));
  and and_3 (and_3_out, EX_Branch, M2);
  FSM fsm_4 (.Now_State(Predict3), .Jump(EX_BranchTaken), .Next_State(fsm_4_next_state));
  and and_4 (and_4_out, EX_Branch, M3);
  FSM fsm_5 (.Now_State(Predict4), .Jump(EX_BranchTaken), .Next_State(fsm_5_next_state));
  and and_5 (and_5_out, EX_Branch, M4);
  FSM fsm_6 (.Now_State(Predict5), .Jump(EX_BranchTaken), .Next_State(fsm_6_next_state));
  and and_6 (and_6_out, EX_Branch, M5);
  FSM fsm_7 (.Now_State(Predict6), .Jump(EX_BranchTaken), .Next_State(fsm_7_next_state));
  and and_7 (and_7_out, EX_Branch, M6);
  FSM fsm_8 (.Now_State(Predict7), .Jump(EX_BranchTaken), .Next_State(fsm_8_next_state));
  and and_8 (and_8_out, EX_Branch, M7);
  Register #(.width(2), .trigger("rising"), .Select("low")) \u_分支预测历史位  (
    .D(fsm_1_next_state), .en(and_1_out), .Q(\分支预测历史位_q ), .clk(CLK));  // open: clr
  Register #(.width(2), .trigger("rising"), .Select("low")) \u_分支预测历史位_2  (
    .D(fsm_2_next_state), .en(and_2_out), .Q(\分支预测历史位_2_q ), .clk(CLK));  // open: clr
  Register #(.width(2), .trigger("rising"), .Select("low")) \u_分支预测历史位_3  (
    .D(fsm_3_next_state), .en(and_3_out), .Q(\分支预测历史位_3_q ), .clk(CLK));  // open: clr
  Register #(.width(2), .trigger("rising"), .Select("low")) \u_分支预测历史位_4  (
    .D(fsm_4_next_state), .en(and_4_out), .Q(\分支预测历史位_4_q ), .clk(CLK));  // open: clr
  Register #(.width(2), .trigger("rising"), .Select("low")) \u_分支预测历史位_5  (
    .D(fsm_5_next_state), .en(and_5_out), .Q(\分支预测历史位_5_q ), .clk(CLK));  // open: clr
  Register #(.width(2), .trigger("rising"), .Select("low")) \u_分支预测历史位_6  (
    .D(fsm_6_next_state), .en(and_6_out), .Q(\分支预测历史位_6_q ), .clk(CLK));  // open: clr
  Register #(.width(2), .trigger("rising"), .Select("low")) \u_分支预测历史位_7  (
    .D(fsm_7_next_state), .en(and_7_out), .Q(\分支预测历史位_7_q ), .clk(CLK));  // open: clr
  Register #(.width(2), .trigger("rising"), .Select("low")) \u_分支预测历史位_8  (
    .D(fsm_8_next_state), .en(and_8_out), .Q(\分支预测历史位_8_q ), .clk(CLK));  // open: clr
  D_Flip_Flop #(.trigger("falling"), .Pre_Clr_Positions("LEGACY"), .NegatePresetClear("false"), .enable("true"), .NewFFLayout("false")) d_ff_1 (
    .clk(and_1_out), .D(1'b1), .Qn(d_ff_1_qn));  // open: Q, preset, en, reset
  Multiplexer #(.select(1), .width(2), .disabled("Z"), .enable("false")) multiplexer_1 (
    .in0(\分支预测历史位_q ), .in1(\initial ), .out(Predict0), .sel(d_ff_1_qn));
  D_Flip_Flop #(.trigger("falling"), .Pre_Clr_Positions("LEGACY"), .NegatePresetClear("false"), .enable("true"), .NewFFLayout("false")) d_ff_2 (
    .clk(and_2_out), .D(1'b1), .Qn(d_ff_2_qn));  // open: Q, preset, en, reset
  Multiplexer #(.select(1), .width(2), .disabled("Z"), .enable("false")) multiplexer_2 (
    .in0(\分支预测历史位_2_q ), .in1(\initial ), .out(Predict1), .sel(d_ff_2_qn));
  D_Flip_Flop #(.trigger("falling"), .Pre_Clr_Positions("LEGACY"), .NegatePresetClear("false"), .enable("true"), .NewFFLayout("false")) d_ff_3 (
    .clk(and_3_out), .D(1'b1), .Qn(d_ff_3_qn));  // open: Q, preset, en, reset
  Multiplexer #(.select(1), .width(2), .disabled("Z"), .enable("false")) multiplexer_3 (
    .in0(\分支预测历史位_3_q ), .in1(\initial ), .out(Predict2), .sel(d_ff_3_qn));
  D_Flip_Flop #(.trigger("falling"), .Pre_Clr_Positions("LEGACY"), .NegatePresetClear("false"), .enable("true"), .NewFFLayout("false")) d_ff_4 (
    .clk(and_4_out), .D(1'b1), .Qn(d_ff_4_qn));  // open: Q, preset, en, reset
  Multiplexer #(.select(1), .width(2), .disabled("Z"), .enable("false")) multiplexer_4 (
    .in0(\分支预测历史位_4_q ), .in1(\initial ), .out(Predict3), .sel(d_ff_4_qn));
  D_Flip_Flop #(.trigger("falling"), .Pre_Clr_Positions("LEGACY"), .NegatePresetClear("false"), .enable("true"), .NewFFLayout("false")) d_ff_5 (
    .clk(and_5_out), .D(1'b1), .Qn(d_ff_5_qn));  // open: Q, preset, en, reset
  Multiplexer #(.select(1), .width(2), .disabled("Z"), .enable("false")) multiplexer_5 (
    .in0(\分支预测历史位_5_q ), .in1(\initial ), .out(Predict4), .sel(d_ff_5_qn));
  D_Flip_Flop #(.trigger("falling"), .Pre_Clr_Positions("LEGACY"), .NegatePresetClear("false"), .enable("true"), .NewFFLayout("false")) d_ff_6 (
    .clk(and_6_out), .D(1'b1), .Qn(d_ff_6_qn));  // open: Q, preset, en, reset
  Multiplexer #(.select(1), .width(2), .disabled("Z"), .enable("false")) multiplexer_6 (
    .in0(\分支预测历史位_6_q ), .in1(\initial ), .out(Predict5), .sel(d_ff_6_qn));
  D_Flip_Flop #(.trigger("falling"), .Pre_Clr_Positions("LEGACY"), .NegatePresetClear("false"), .enable("true"), .NewFFLayout("false")) d_ff_7 (
    .clk(and_7_out), .D(1'b1), .Qn(d_ff_7_qn));  // open: Q, preset, en, reset
  Multiplexer #(.select(1), .width(2), .disabled("Z"), .enable("false")) multiplexer_7 (
    .in0(\分支预测历史位_7_q ), .in1(\initial ), .out(Predict6), .sel(d_ff_7_qn));
  D_Flip_Flop #(.trigger("falling"), .Pre_Clr_Positions("LEGACY"), .NegatePresetClear("false"), .enable("true"), .NewFFLayout("false")) d_ff_8 (
    .clk(and_8_out), .D(1'b1), .Qn(d_ff_8_qn));  // open: Q, preset, en, reset
  Multiplexer #(.select(1), .width(2), .disabled("Z"), .enable("false")) multiplexer_8 (
    .in0(\分支预测历史位_8_q ), .in1(\initial ), .out(Predict7), .sel(d_ff_8_qn));
  Counter #(.width(16), .max('hffff), .ongoal("wrap"), .trigger("rising"), .behavior("old")) \u_淘汰计数  (
    .Q(C0), .clk(CLK), .clr(Clr0));  // open: load, D, count, carry, preset
  Counter #(.width(16), .max('hffff), .ongoal("wrap"), .trigger("rising"), .behavior("old")) \u_淘汰计数_2  (
    .Q(C1), .clk(CLK), .clr(Clr1));  // open: load, D, count, carry, preset
  Counter #(.width(16), .max('hffff), .ongoal("wrap"), .trigger("rising"), .behavior("old")) \u_淘汰计数_3  (
    .Q(C2), .clk(CLK), .clr(Clr2));  // open: load, D, count, carry, preset
  Counter #(.width(16), .max('hffff), .ongoal("wrap"), .trigger("rising"), .behavior("old")) \u_淘汰计数_4  (
    .Q(C3), .clk(CLK), .clr(Clr3));  // open: load, D, count, carry, preset
  Counter #(.width(16), .max('hffff), .ongoal("wrap"), .trigger("rising"), .behavior("old")) \u_淘汰计数_5  (
    .Q(C4), .clk(CLK), .clr(Clr4));  // open: load, D, count, carry, preset
  Counter #(.width(16), .max('hffff), .ongoal("wrap"), .trigger("rising"), .behavior("old")) \u_淘汰计数_6  (
    .Q(C5), .clk(CLK), .clr(Clr5));  // open: load, D, count, carry, preset
  Counter #(.width(16), .max('hffff), .ongoal("wrap"), .trigger("rising"), .behavior("old")) \u_淘汰计数_7  (
    .Q(C6), .clk(CLK), .clr(Clr6));  // open: load, D, count, carry, preset
  Counter #(.width(16), .max('hffff), .ongoal("wrap"), .trigger("rising"), .behavior("old")) \u_淘汰计数_8  (
    .Q(C7), .clk(CLK), .clr(Clr7));  // open: load, D, count, carry, preset
  not not_1 (not_1_out, v0);
  not not_2 (not_2_out, v1);
  not not_3 (not_3_out, v2);
  not not_4 (not_4_out, v3);
  not not_5 (not_5_out, v4);
  not not_6 (not_6_out, v5);
  not not_7 (not_7_out, v6);
  not not_8 (not_8_out, v7);
  Comparator #(.width(32), .mode("twosComplement")) comparator_1 (
    .a(PC), .b(Tag0), .eq(comparator_1_eq));  // open: gt, lt
  Comparator #(.width(32), .mode("twosComplement")) comparator_2 (
    .a(PC), .b(Tag1), .eq(comparator_2_eq));  // open: gt, lt
  Comparator #(.width(32), .mode("twosComplement")) comparator_3 (
    .a(PC), .b(Tag2), .eq(comparator_3_eq));  // open: gt, lt
  Comparator #(.width(32), .mode("twosComplement")) comparator_4 (
    .a(PC), .b(Tag3), .eq(comparator_4_eq));  // open: gt, lt
  Comparator #(.width(32), .mode("twosComplement")) comparator_5 (
    .a(PC), .b(Tag4), .eq(comparator_5_eq));  // open: gt, lt
  Comparator #(.width(32), .mode("twosComplement")) comparator_6 (
    .a(PC), .b(Tag5), .eq(comparator_6_eq));  // open: gt, lt
  Comparator #(.width(32), .mode("twosComplement")) comparator_7 (
    .a(PC), .b(Tag6), .eq(comparator_7_eq));  // open: gt, lt
  Comparator #(.width(32), .mode("twosComplement")) comparator_8 (
    .a(PC), .b(Tag7), .eq(comparator_8_eq));  // open: gt, lt
  MAX max_1 (.Y(C1), .X(C0), .Y_num(3'b001), .X_num(3'b000), .MAX(max_1_max), .Max_num(max_1_max_num));
  MAX max_2 (
    .Y(max_3_max), .X(max_1_max), .Y_num(max_3_max_num), .X_num(max_1_max_num), .MAX(max_2_max),
    .Max_num(max_2_max_num));
  MAX max_3 (.Y(C3), .X(C2), .Y_num(3'b011), .X_num(3'b010), .MAX(max_3_max), .Max_num(max_3_max_num));
  MAX max_4 (.Y(C5), .X(C4), .Y_num(3'b101), .X_num(3'b100), .MAX(max_4_max), .Max_num(max_4_max_num));
  MAX max_5 (
    .Y(max_6_max), .X(max_4_max), .Y_num(max_6_max_num), .X_num(max_4_max_num), .MAX(max_5_max),
    .Max_num(max_5_max_num));
  MAX max_6 (.Y(C7), .X(C6), .Y_num(3'b111), .X_num(3'b110), .MAX(max_6_max), .Max_num(max_6_max_num));
  and and_9 (L0, comparator_1_eq, v0);
  and and_10 (L1, comparator_2_eq, v1);
  and and_11 (L2, comparator_3_eq, v2);
  and and_12 (L3, comparator_4_eq, v3);
  and and_13 (L4, comparator_5_eq, v4);
  and and_14 (L5, comparator_6_eq, v5);
  and and_15 (L6, comparator_7_eq, v6);
  and and_16 (L7, comparator_8_eq, v7);
  Priority_Encoder #(.select(3), .disabled("Z")) priority_encoder_1 (
    .in0(not_1_out), .in1(not_2_out), .in2(not_3_out), .in3(not_4_out), .in4(not_5_out), .in5(not_6_out),
    .in6(not_7_out), .in7(not_8_out), .out(priority_encoder_1_out), .gs(priority_encoder_1_gs), .en_out(Full));  // open: en_in
  MAX max_7 (
    .Y(max_5_max), .X(max_2_max), .Y_num(max_5_max_num), .X_num(max_2_max_num), .Max_num(max_7_max_num));  // open: MAX
  Decoder #(.select(3), .tristate("false"), .disabled(0), .enable("true")) decoder_1 (
    .out0(decoder_1_out0), .out1(decoder_1_out1), .out2(decoder_1_out2), .out3(decoder_1_out3),
    .out4(decoder_1_out4), .out5(decoder_1_out5), .out6(decoder_1_out6), .out7(decoder_1_out7),
    .sel(priority_encoder_1_out), .en(priority_encoder_1_gs));
  Decoder #(.select(3), .tristate("false"), .disabled(0), .enable("true")) decoder_2 (
    .out0(decoder_2_out0), .out1(decoder_2_out1), .out2(decoder_2_out2), .out3(decoder_2_out3),
    .out4(decoder_2_out4), .out5(decoder_2_out5), .out6(decoder_2_out6), .out7(decoder_2_out7),
    .sel(max_7_max_num), .en(Full));
  Comparator #(.width(32), .mode("twosComplement")) comparator_9 (
    .a(EX_PC), .b(Tag0), .eq(comparator_9_eq));  // open: gt, lt
  Comparator #(.width(32), .mode("twosComplement")) comparator_10 (
    .a(EX_PC), .b(Tag1), .eq(comparator_10_eq));  // open: gt, lt
  Comparator #(.width(32), .mode("twosComplement")) comparator_11 (
    .a(EX_PC), .b(Tag2), .eq(comparator_11_eq));  // open: gt, lt
  Comparator #(.width(32), .mode("twosComplement")) comparator_12 (
    .a(EX_PC), .b(Tag3), .eq(comparator_12_eq));  // open: gt, lt
  Comparator #(.width(32), .mode("twosComplement")) comparator_13 (
    .a(EX_PC), .b(Tag4), .eq(comparator_13_eq));  // open: gt, lt
  Comparator #(.width(32), .mode("twosComplement")) comparator_14 (
    .a(EX_PC), .b(Tag5), .eq(comparator_14_eq));  // open: gt, lt
  Comparator #(.width(32), .mode("twosComplement")) comparator_15 (
    .a(EX_PC), .b(Tag6), .eq(comparator_15_eq));  // open: gt, lt
  Comparator #(.width(32), .mode("twosComplement")) comparator_16 (
    .a(EX_PC), .b(Tag7), .eq(comparator_16_eq));  // open: gt, lt
  and and_17 (M0, comparator_9_eq, v0);
  and and_18 (M1, comparator_10_eq, v1);
  and and_19 (M2, comparator_11_eq, v2);
  and and_20 (M3, comparator_12_eq, v3);
  and and_21 (M4, comparator_13_eq, v4);
  and and_22 (M5, comparator_14_eq, v5);
  and and_23 (M6, comparator_15_eq, v6);
  and and_24 (M7, comparator_16_eq, v7);
  or or_1 (or_1_out, decoder_1_out0, decoder_2_out0);
  or or_2 (or_2_out, decoder_1_out1, decoder_2_out1);
  or or_3 (or_3_out, decoder_1_out2, decoder_2_out2);
  or or_4 (or_4_out, decoder_1_out3, decoder_2_out3);
  or or_5 (or_5_out, decoder_1_out4, decoder_2_out4);
  or or_6 (or_6_out, decoder_1_out5, decoder_2_out5);
  or or_7 (or_7_out, decoder_1_out6, decoder_2_out6);
  or or_8 (or_8_out, decoder_1_out7, decoder_2_out7);
  and and_25 (Write0, EX_Miss, or_1_out, EX_Branch);
  and and_26 (Write1, EX_Miss, or_2_out, EX_Branch);
  and and_27 (Write2, EX_Miss, or_3_out, EX_Branch);
  and and_28 (Write3, EX_Miss, or_4_out, EX_Branch);
  and and_29 (Write4, EX_Miss, or_5_out, EX_Branch);
  and and_30 (Write5, EX_Miss, or_6_out, EX_Branch);
  and and_31 (Write6, EX_Miss, or_7_out, EX_Branch);
  and and_32 (Write7, EX_Miss, or_8_out, EX_Branch);
  or or_9 (EX_Hit, M0, M1, M2, M3, M4, M5, M6, M7);
  not not_9 (EX_Miss, EX_Hit);
  assign {PredictJump, controlled_buffer_9_out[0]} = L0 ? Predict0 : 2'bz;  // Controlled_Buffer controlled_buffer_9
  assign {PredictJump, controlled_buffer_10_out[0]} = L1 ? Predict1 : 2'bz;  // Controlled_Buffer controlled_buffer_10
  assign {PredictJump, controlled_buffer_11_out[0]} = L2 ? Predict2 : 2'bz;  // Controlled_Buffer controlled_buffer_11
  assign {PredictJump, controlled_buffer_12_out[0]} = L3 ? Predict3 : 2'bz;  // Controlled_Buffer controlled_buffer_12
  assign {PredictJump, controlled_buffer_13_out[0]} = L4 ? Predict4 : 2'bz;  // Controlled_Buffer controlled_buffer_13
  assign {PredictJump, controlled_buffer_14_out[0]} = L5 ? Predict5 : 2'bz;  // Controlled_Buffer controlled_buffer_14
  assign {PredictJump, controlled_buffer_15_out[0]} = L6 ? Predict6 : 2'bz;  // Controlled_Buffer controlled_buffer_15
  assign {PredictJump, controlled_buffer_16_out[0]} = L7 ? Predict7 : 2'bz;  // Controlled_Buffer controlled_buffer_16
  or or_10 (or_10_out, L0, Write0);
  or or_11 (or_11_out, L1, Write1);
  or or_12 (or_12_out, L2, Write2);
  or or_13 (or_13_out, L3, Write3);
  Pull_Resistor #(.pull(0)) pull_resistor_1 (.node(PredictJump));
  D_Flip_Flop #(.trigger("rising"), .Pre_Clr_Positions("ABOVE_BELOW"), .NegatePresetClear("false"), .enable("false"), .NewFFLayout("true")) d_ff_9 (
    .clk(CLK), .D(or_10_out), .Q(Clr0));  // open: Qn, preset, reset
  D_Flip_Flop #(.trigger("rising"), .Pre_Clr_Positions("ABOVE_BELOW"), .NegatePresetClear("false"), .enable("false"), .NewFFLayout("true")) d_ff_10 (
    .clk(CLK), .D(or_11_out), .Q(Clr1));  // open: Qn, preset, reset
  D_Flip_Flop #(.trigger("rising"), .Pre_Clr_Positions("ABOVE_BELOW"), .NegatePresetClear("false"), .enable("false"), .NewFFLayout("true")) d_ff_11 (
    .clk(CLK), .D(or_12_out), .Q(Clr2));  // open: Qn, preset, reset
  D_Flip_Flop #(.trigger("rising"), .Pre_Clr_Positions("ABOVE_BELOW"), .NegatePresetClear("false"), .enable("false"), .NewFFLayout("true")) d_ff_12 (
    .clk(CLK), .D(or_13_out), .Q(Clr3));  // open: Qn, preset, reset
  or or_14 (or_14_out, L4, Write4);
  or or_15 (or_15_out, L5, Write5);
  or or_16 (or_16_out, L6, Write6);
  or or_17 (or_17_out, L7, Write7);
  D_Flip_Flop #(.trigger("rising"), .Pre_Clr_Positions("ABOVE_BELOW"), .NegatePresetClear("false"), .enable("false"), .NewFFLayout("true")) d_ff_13 (
    .clk(CLK), .D(or_14_out), .Q(Clr4));  // open: Qn, preset, reset
  D_Flip_Flop #(.trigger("rising"), .Pre_Clr_Positions("ABOVE_BELOW"), .NegatePresetClear("false"), .enable("false"), .NewFFLayout("true")) d_ff_14 (
    .clk(CLK), .D(or_15_out), .Q(Clr5));  // open: Qn, preset, reset
  D_Flip_Flop #(.trigger("rising"), .Pre_Clr_Positions("ABOVE_BELOW"), .NegatePresetClear("false"), .enable("false"), .NewFFLayout("true")) d_ff_15 (
    .clk(CLK), .D(or_16_out), .Q(Clr6));  // open: Qn, preset, reset
  D_Flip_Flop #(.trigger("rising"), .Pre_Clr_Positions("ABOVE_BELOW"), .NegatePresetClear("false"), .enable("false"), .NewFFLayout("true")) d_ff_16 (
    .clk(CLK), .D(or_17_out), .Q(Clr7));  // open: Qn, preset, reset

  // Other names for the same wires on the sheet: Tag[31:0] = EX_PC

  // Notes on the sheet:
  //   生成命中信号
  //   生成写入信号
  //   生成清零信号
endmodule

module FSM (
  input  [1:0] Now_State,
  input  Jump,
  output [1:0] Next_State
);

  wire and_1_out, and_2_out, and_3_out, and_4_out, not_1_out, not_2_out, not_3_out, not_4_out, not_5_out;

  not not_1 (not_1_out, Now_State[0]);
  not not_2 (not_2_out, Now_State[1]);
  not not_3 (not_3_out, Now_State[0]);
  not not_4 (not_4_out, Now_State[0]);
  not not_5 (not_5_out, Jump);
  and and_1 (and_1_out, Now_State[0], Jump);
  and and_2 (and_2_out, Now_State[1], not_1_out);
  and and_3 (and_3_out, not_2_out, not_3_out, Jump);
  and and_4 (and_4_out, Now_State[1], not_4_out, not_5_out);
  or or_1 (Next_State[1], and_1_out, and_2_out);
  or or_2 (Next_State[0], and_3_out, and_4_out);
endmodule

module MAX (
  input  [15:0] Y,
  input  [15:0] X,
  input  [2:0] Y_num,
  input  [2:0] X_num,
  output [15:0] MAX,
  output [2:0] Max_num
);

  wire comparator_1_eq, comparator_1_gt, or_1_out;

  Multiplexer #(.select(1), .width(16), .disabled("Z"), .enable("false")) multiplexer_1 (
    .in0(Y), .in1(X), .out(MAX), .sel(or_1_out));
  Comparator #(.width(16), .mode("unsigned")) comparator_1 (
    .a(X), .b(Y), .gt(comparator_1_gt), .eq(comparator_1_eq));  // open: lt
  or or_1 (or_1_out, comparator_1_gt, comparator_1_eq);
  Multiplexer #(.select(1), .width(3), .disabled("Z"), .enable("false")) multiplexer_2 (
    .in0(Y_num), .in1(X_num), .out(Max_num), .sel(or_1_out));

  // Notes on the sheet:
  //   输出两个输入中的较大值，并输出较大值的3位编号
endmodule
module \团队任务  (
  input  IR1,
  input  IR2,
  input  IR3,
  output RegWrite,
  output MemWrite,
  output [31:0] PC,
  output [31:0] IR,
  output [31:0] RDin,
  output [31:0] MDin,
  output [31:0] LedData
);

  wire alu_1_equal, alu_1_out_6, and_3_out, and_6_out, and_8_out, and_9_out, and_10_out, B_signal, blt,
       Branch, CLK, clock_2_out, Clr_DOWN, Clr_LEFT, Clr_RIGHT, Clr_UP, comparator_5_eq, comparator_5_lt,
       comparator_6_eq, comparator_7_eq, d_ff_1_q, decoder_2_out0, decoder_2_out1, decoder_2_out2,
       decoder_2_out3, DOWN, ecall, Go, halt, IE, INT, IR1_t, IR2_t, IR3_t, IRA, IRB, IRC, J_signal,
       Jalr_signal, LEFT, Lost, nand_1_out, nor_1_out, not_1_out, or_4_out, or_5_out, or_6_out, or_7_out,
       or_8_out, or_11_out, or_12_out, random, RIGHT, RST, S_signal, sb, sltiu, UP, update, URET, W1, W2, W3,
       W4, Win, \中断信号 , \单周期硬布线控制器_1_alu_src , \单周期硬布线控制器_1_beq , \单周期硬布线控制器_1_bne , \单周期硬布线控制器_1_memtoreg ;
  wire [1:0] Imm_Sel, register_9_q, \中断号 ;
  wire [3:0] decoder_1_out0, multiplexer_4_out, RAM_Sel, random_Adr, \单周期硬布线控制器_1_alu_op ;
  wire [4:0] bit_extender_6_out, multiplexer_7_out, multiplexer_8_out, multiplier_1_out;
  wire [6:0] keyboard_1_data;
  wire [9:0] bit_extender_7_out, multiplexer_15_out;
  wire [12:0] CNT_num;
  wire [15:0] \总周期数 ;
  wire [31:0] adder_2_out, ALU_Res, bit_extender_1_out, bit_extender_2_out, bit_extender_3_out,
       bit_extender_4_out, bit_extender_5_out, Break_PC, Data0, Data1, Data2, Data3, Data4, Data5, Data6,
       Data7, Data8, Data9, Data10, Data11, Data12, Data13, Data14, Data15, INT_Addar, Led0, Led1, Led2,
       Led3, Led4, Led5, Led6, Led7, Led8, Led9, Led10, Led11, Led12, Led13, Led14, Led15, \led译码器_1_col0 ,
       \led译码器_1_col1 , \led译码器_1_col2 , \led译码器_1_col3 , \led译码器_1_col4 , \led译码器_1_col5 , \led译码器_1_col6 ,
       \led译码器_1_col7 , \led译码器_1_col8 , \led译码器_1_col9 , \led译码器_1_col10 , \led译码器_1_col11 ,
       \led译码器_1_col12 , \led译码器_1_col13 , \led译码器_1_col14 , \led译码器_1_col15 , \led译码器_1_col16 ,
       \led译码器_1_col17 , \led译码器_1_col18 , \led译码器_1_col19 , \led译码器_1_col20 , \led译码器_1_col21 ,
       \led译码器_1_col22 , \led译码器_1_col23 , \led译码器_1_col24 , \led译码器_1_col25 , \led译码器_1_col26 ,
       \led译码器_1_col27 , \led译码器_1_col28 , \led译码器_1_col29 , \led译码器_1_col30 , \led译码器_1_col31 ,
       \led译码器_2_col0 , \led译码器_2_col1 , \led译码器_2_col2 , \led译码器_2_col3 , \led译码器_2_col4 , \led译码器_2_col5 ,
       \led译码器_2_col6 , \led译码器_2_col7 , \led译码器_2_col8 , \led译码器_2_col9 , \led译码器_2_col10 ,
       \led译码器_2_col11 , \led译码器_2_col12 , \led译码器_2_col13 , \led译码器_2_col14 , \led译码器_2_col15 ,
       \led译码器_2_col16 , \led译码器_2_col17 , \led译码器_2_col18 , \led译码器_2_col19 , \led译码器_2_col20 ,
       \led译码器_2_col21 , \led译码器_2_col22 , \led译码器_2_col23 , \led译码器_2_col24 , \led译码器_2_col25 ,
       \led译码器_2_col26 , \led译码器_2_col27 , \led译码器_2_col28 , \led译码器_2_col29 , \led译码器_2_col30 ,
       \led译码器_2_col31 , \led译码器_3_col0 , \led译码器_3_col1 , \led译码器_3_col2 , \led译码器_3_col3 , \led译码器_3_col4 ,
       \led译码器_3_col5 , \led译码器_3_col6 , \led译码器_3_col7 , \led译码器_3_col8 , \led译码器_3_col9 , \led译码器_3_col10 ,
       \led译码器_3_col11 , \led译码器_3_col12 , \led译码器_3_col13 , \led译码器_3_col14 , \led译码器_3_col15 ,
       \led译码器_3_col16 , \led译码器_3_col17 , \led译码器_3_col18 , \led译码器_3_col19 , \led译码器_3_col20 ,
       \led译码器_3_col21 , \led译码器_3_col22 , \led译码器_3_col23 , \led译码器_3_col24 , \led译码器_3_col25 ,
       \led译码器_3_col26 , \led译码器_3_col27 , \led译码器_3_col28 , \led译码器_3_col29 , \led译码器_3_col30 ,
       \led译码器_3_col31 , \led译码器_4_col0 , \led译码器_4_col1 , \led译码器_4_col2 , \led译码器_4_col3 , \led译码器_4_col4 ,
       \led译码器_4_col5 , \led译码器_4_col6 , \led译码器_4_col7 , \led译码器_4_col8 , \led译码器_4_col9 , \led译码器_4_col10 ,
       \led译码器_4_col11 , \led译码器_4_col12 , \led译码器_4_col13 , \led译码器_4_col14 , \led译码器_4_col15 ,
       \led译码器_4_col16 , \led译码器_4_col17 , \led译码器_4_col18 , \led译码器_4_col19 , \led译码器_4_col20 ,
       \led译码器_4_col21 , \led译码器_4_col22 , \led译码器_4_col23 , \led译码器_4_col24 , \led译码器_4_col25 ,
       \led译码器_4_col26 , \led译码器_4_col27 , \led译码器_4_col28 , \led译码器_4_col29 , \led译码器_4_col30 ,
       \led译码器_4_col31 , \led译码器_5_col0 , \led译码器_5_col1 , \led译码器_5_col2 , \led译码器_5_col3 , \led译码器_5_col4 ,
       \led译码器_5_col5 , \led译码器_5_col6 , \led译码器_5_col7 , \led译码器_5_col8 , \led译码器_5_col9 , \led译码器_5_col10 ,
       \led译码器_5_col11 , \led译码器_5_col12 , \led译码器_5_col13 , \led译码器_5_col14 , \led译码器_5_col15 ,
       \led译码器_5_col16 , \led译码器_5_col17 , \led译码器_5_col18 , \led译码器_5_col19 , \led译码器_5_col20 ,
       \led译码器_5_col21 , \led译码器_5_col22 , \led译码器_5_col23 , \led译码器_5_col24 , \led译码器_5_col25 ,
       \led译码器_5_col26 , \led译码器_5_col27 , \led译码器_5_col28 , \led译码器_5_col29 , \led译码器_5_col30 ,
       \led译码器_5_col31 , \led译码器_6_col0 , \led译码器_6_col1 , \led译码器_6_col2 , \led译码器_6_col3 , \led译码器_6_col4 ,
       \led译码器_6_col5 , \led译码器_6_col6 , \led译码器_6_col7 , \led译码器_6_col8 , \led译码器_6_col9 , \led译码器_6_col10 ,
       \led译码器_6_col11 , \led译码器_6_col12 , \led译码器_6_col13 , \led译码器_6_col14 , \led译码器_6_col15 ,
       \led译码器_6_col16 , \led译码器_6_col17 , \led译码器_6_col18 , \led译码器_6_col19 , \led译码器_6_col20 ,
       \led译码器_6_col21 , \led译码器_6_col22 , \led译码器_6_col23 , \led译码器_6_col24 , \led译码器_6_col25 ,
       \led译码器_6_col26 , \led译码器_6_col27 , \led译码器_6_col28 , \led译码器_6_col29 , \led译码器_6_col30 ,
       \led译码器_6_col31 , \led译码器_7_col0 , \led译码器_7_col1 , \led译码器_7_col2 , \led译码器_7_col3 , \led译码器_7_col4 ,
       \led译码器_7_col5 , \led译码器_7_col6 , \led译码器_7_col7 , \led译码器_7_col8 , \led译码器_7_col9 , \led译码器_7_col10 ,
       \led译码器_7_col11 , \led译码器_7_col12 , \led译码器_7_col13 , \led译码器_7_col14 , \led译码器_7_col15 ,
       \led译码器_7_col16 , \led译码器_7_col17 , \led译码器_7_col18 , \led译码器_7_col19 , \led译码器_7_col20 ,
       \led译码器_7_col21 , \led译码器_7_col22 , \led译码器_7_col23 , \led译码器_7_col24 , \led译码器_7_col25 ,
       \led译码器_7_col26 , \led译码器_7_col27 , \led译码器_7_col28 , \led译码器_7_col29 , \led译码器_7_col30 ,
       \led译码器_7_col31 , \led译码器_8_col0 , \led译码器_8_col1 , \led译码器_8_col2 , \led译码器_8_col3 , \led译码器_8_col4 ,
       \led译码器_8_col5 , \led译码器_8_col6 , \led译码器_8_col7 , \led译码器_8_col8 , \led译码器_8_col9 , \led译码器_8_col10 ,
       \led译码器_8_col11 , \led译码器_8_col12 , \led译码器_8_col13 , \led译码器_8_col14 , \led译码器_8_col15 ,
       \led译码器_8_col16 , \led译码器_8_col17 , \led译码器_8_col18 , \led译码器_8_col19 , \led译码器_8_col20 ,
       \led译码器_8_col21 , \led译码器_8_col22 , \led译码器_8_col23 , \led译码器_8_col24 , \led译码器_8_col25 ,
       \led译码器_8_col26 , \led译码器_8_col27 , \led译码器_8_col28 , \led译码器_8_col29 , \led译码器_8_col30 ,
       \led译码器_8_col31 , \led译码器_9_col0 , \led译码器_9_col1 , \led译码器_9_col2 , \led译码器_9_col3 , \led译码器_9_col4 ,
       \led译码器_9_col5 , \led译码器_9_col6 , \led译码器_9_col7 , \led译码器_9_col8 , \led译码器_9_col9 , \led译码器_9_col10 ,
       \led译码器_9_col11 , \led译码器_9_col12 , \led译码器_9_col13 , \led译码器_9_col14 , \led译码器_9_col15 ,
       \led译码器_9_col16 , \led译码器_9_col17 , \led译码器_9_col18 , \led译码器_9_col19 , \led译码器_9_col20 ,
       \led译码器_9_col21 , \led译码器_9_col22 , \led译码器_9_col23 , \led译码器_9_col24 , \led译码器_9_col25 ,
       \led译码器_9_col26 , \led译码器_9_col27 , \led译码器_9_col28 , \led译码器_9_col29 , \led译码器_9_col30 ,
       \led译码器_9_col31 , \led译码器_10_col0 , \led译码器_10_col1 , \led译码器_10_col2 , \led译码器_10_col3 ,
       \led译码器_10_col4 , \led译码器_10_col5 , \led译码器_10_col6 , \led译码器_10_col7 , \led译码器_10_col8 ,
       \led译码器_10_col9 , \led译码器_10_col10 , \led译码器_10_col11 , \led译码器_10_col12 , \led译码器_10_col13 ,
       \led译码器_10_col14 , \led译码器_10_col15 , \led译码器_10_col16 , \led译码器_10_col17 , \led译码器_10_col18 ,
       \led译码器_10_col19 , \led译码器_10_col20 , \led译码器_10_col21 , \led译码器_10_col22 , \led译码器_10_col23 ,
       \led译码器_10_col24 , \led译码器_10_col25 , \led译码器_10_col26 , \led译码器_10_col27 , \led译码器_10_col28 ,
       \led译码器_10_col29 , \led译码器_10_col30 , \led译码器_10_col31 , \led译码器_11_col0 , \led译码器_11_col1 ,
       \led译码器_11_col2 , \led译码器_11_col3 , \led译码器_11_col4 , \led译码器_11_col5 , \led译码器_11_col6 ,
       \led译码器_11_col7 , \led译码器_11_col8 , \led译码器_11_col9 , \led译码器_11_col10 , \led译码器_11_col11 ,
       \led译码器_11_col12 , \led译码器_11_col13 , \led译码器_11_col14 , \led译码器_11_col15 , \led译码器_11_col16 ,
       \led译码器_11_col17 , \led译码器_11_col18 , \led译码器_11_col19 , \led译码器_11_col20 , \led译码器_11_col21 ,
       \led译码器_11_col22 , \led译码器_11_col23 , \led译码器_11_col24 , \led译码器_11_col25 , \led译码器_11_col26 ,
       \led译码器_11_col27 , \led译码器_11_col28 , \led译码器_11_col29 , \led译码器_11_col30 , \led译码器_11_col31 ,
       \led译码器_12_col0 , \led译码器_12_col1 , \led译码器_12_col2 , \led译码器_12_col3 , \led译码器_12_col4 ,
       \led译码器_12_col5 , \led译码器_12_col6 , \led译码器_12_col7 , \led译码器_12_col8 , \led译码器_12_col9 ,
       \led译码器_12_col10 , \led译码器_12_col11 , \led译码器_12_col12 , \led译码器_12_col13 , \led译码器_12_col14 ,
       \led译码器_12_col15 , \led译码器_12_col16 , \led译码器_12_col17 , \led译码器_12_col18 , \led译码器_12_col19 ,
       \led译码器_12_col20 , \led译码器_12_col21 , \led译码器_12_col22 , \led译码器_12_col23 , \led译码器_12_col24 ,
       \led译码器_12_col25 , \led译码器_12_col26 , \led译码器_12_col27 , \led译码器_12_col28 , \led译码器_12_col29 ,
       \led译码器_12_col30 , \led译码器_12_col31 , \led译码器_13_col0 , \led译码器_13_col1 , \led译码器_13_col2 ,
       \led译码器_13_col3 , \led译码器_13_col4 , \led译码器_13_col5 , \led译码器_13_col6 , \led译码器_13_col7 ,
       \led译码器_13_col8 , \led译码器_13_col9 , \led译码器_13_col10 , \led译码器_13_col11 , \led译码器_13_col12 ,
       \led译码器_13_col13 , \led译码器_13_col14 , \led译码器_13_col15 , \led译码器_13_col16 , \led译码器_13_col17 ,
       \led译码器_13_col18 , \led译码器_13_col19 , \led译码器_13_col20 , \led译码器_13_col21 , \led译码器_13_col22 ,
       \led译码器_13_col23 , \led译码器_13_col24 , \led译码器_13_col25 , \led译码器_13_col26 , \led译码器_13_col27 ,
       \led译码器_13_col28 , \led译码器_13_col29 , \led译码器_13_col30 , \led译码器_13_col31 , \led译码器_14_col0 ,
       \led译码器_14_col1 , \led译码器_14_col2 , \led译码器_14_col3 , \led译码器_14_col4 , \led译码器_14_col5 ,
       \led译码器_14_col6 , \led译码器_14_col7 , \led译码器_14_col8 , \led译码器_14_col9 , \led译码器_14_col10 ,
       \led译码器_14_col11 , \led译码器_14_col12 , \led译码器_14_col13 , \led译码器_14_col14 , \led译码器_14_col15 ,
       \led译码器_14_col16 , \led译码器_14_col17 , \led译码器_14_col18 , \led译码器_14_col19 , \led译码器_14_col20 ,
       \led译码器_14_col21 , \led译码器_14_col22 , \led译码器_14_col23 , \led译码器_14_col24 , \led译码器_14_col25 ,
       \led译码器_14_col26 , \led译码器_14_col27 , \led译码器_14_col28 , \led译码器_14_col29 , \led译码器_14_col30 ,
       \led译码器_14_col31 , \led译码器_15_col0 , \led译码器_15_col1 , \led译码器_15_col2 , \led译码器_15_col3 ,
       \led译码器_15_col4 , \led译码器_15_col5 , \led译码器_15_col6 , \led译码器_15_col7 , \led译码器_15_col8 ,
       \led译码器_15_col9 , \led译码器_15_col10 , \led译码器_15_col11 , \led译码器_15_col12 , \led译码器_15_col13 ,
       \led译码器_15_col14 , \led译码器_15_col15 , \led译码器_15_col16 , \led译码器_15_col17 , \led译码器_15_col18 ,
       \led译码器_15_col19 , \led译码器_15_col20 , \led译码器_15_col21 , \led译码器_15_col22 , \led译码器_15_col23 ,
       \led译码器_15_col24 , \led译码器_15_col25 , \led译码器_15_col26 , \led译码器_15_col27 , \led译码器_15_col28 ,
       \led译码器_15_col29 , \led译码器_15_col30 , \led译码器_15_col31 , \led译码器_16_col0 , \led译码器_16_col1 ,
       \led译码器_16_col2 , \led译码器_16_col3 , \led译码器_16_col4 , \led译码器_16_col5 , \led译码器_16_col6 ,
       \led译码器_16_col7 , \led译码器_16_col8 , \led译码器_16_col9 , \led译码器_16_col10 , \led译码器_16_col11 ,
       \led译码器_16_col12 , \led译码器_16_col13 , \led译码器_16_col14 , \led译码器_16_col15 , \led译码器_16_col16 ,
       \led译码器_16_col17 , \led译码器_16_col18 , \led译码器_16_col19 , \led译码器_16_col20 , \led译码器_16_col21 ,
       \led译码器_16_col22 , \led译码器_16_col23 , \led译码器_16_col24 , \led译码器_16_col25 , \led译码器_16_col26 ,
       \led译码器_16_col27 , \led译码器_16_col28 , \led译码器_16_col29 , \led译码器_16_col30 , \led译码器_16_col31 ,
       MemData, mips_ram_1_p7, multiplexer_1_out, multiplexer_3_out, multiplexer_5_out, multiplexer_6_out,
       multiplexer_9_out, multiplexer_10_out, multiplexer_11_out, multiplexer_13_out, multiplexer_17_out,
       PC_4, R1_Data, random_Num, RET_PC, shifter_1_out, shifter_2_out;

  Clock #(.highDuration(1), .lowDuration(1)) clock_1 ();  // open: out
  Button _1 (.out(IRA));
  Button _2 (.out(IRB));
  Button _3 (.out(IRC));
  Button button_1 (.out(RST));
  Button \u_继续运行  (.out(Go));
  LED #(.active("true")) led_1 (.in(W1));
  LED #(.active("true")) led_2 (.in(W2));
  LED #(.active("true")) led_3 (.in(W3));
  DotMatrix #(.inputtype("column"), .matrixcols(32), .matrixrows(32), .persist(0), .dotshape("square")) dotmatrix_1 (
    .col0(\led译码器_1_col0 ), .col1(\led译码器_1_col1 ), .col2(\led译码器_1_col2 ), .col3(\led译码器_1_col3 ),
    .col4(\led译码器_1_col4 ), .col5(\led译码器_1_col5 ), .col6(\led译码器_1_col6 ), .col7(\led译码器_1_col7 ),
    .col8(\led译码器_1_col8 ), .col9(\led译码器_1_col9 ), .col10(\led译码器_1_col10 ), .col11(\led译码器_1_col11 ),
    .col12(\led译码器_1_col12 ), .col13(\led译码器_1_col13 ), .col14(\led译码器_1_col14 ), .col15(\led译码器_1_col15 ),
    .col16(\led译码器_1_col16 ), .col17(\led译码器_1_col17 ), .col18(\led译码器_1_col18 ), .col19(\led译码器_1_col19 ),
    .col20(\led译码器_1_col20 ), .col21(\led译码器_1_col21 ), .col22(\led译码器_1_col22 ), .col23(\led译码器_1_col23 ),
    .col24(\led译码器_1_col24 ), .col25(\led译码器_1_col25 ), .col26(\led译码器_1_col26 ), .col27(\led译码器_1_col27 ),
    .col28(\led译码器_1_col28 ), .col29(\led译码器_1_col29 ), .col30(\led译码器_1_col30 ), .col31(\led译码器_1_col31 ));
  DotMatrix #(.inputtype("column"), .matrixcols(32), .matrixrows(32), .persist(0), .dotshape("square")) dotmatrix_2 (
    .col0(\led译码器_2_col0 ), .col1(\led译码器_2_col1 ), .col2(\led译码器_2_col2 ), .col3(\led译码器_2_col3 ),
    .col4(\led译码器_2_col4 ), .col5(\led译码器_2_col5 ), .col6(\led译码器_2_col6 ), .col7(\led译码器_2_col7 ),
    .col8(\led译码器_2_col8 ), .col9(\led译码器_2_col9 ), .col10(\led译码器_2_col10 ), .col11(\led译码器_2_col11 ),
    .col12(\led译码器_2_col12 ), .col13(\led译码器_2_col13 ), .col14(\led译码器_2_col14 ), .col15(\led译码器_2_col15 ),
    .col16(\led译码器_2_col16 ), .col17(\led译码器_2_col17 ), .col18(\led译码器_2_col18 ), .col19(\led译码器_2_col19 ),
    .col20(\led译码器_2_col20 ), .col21(\led译码器_2_col21 ), .col22(\led译码器_2_col22 ), .col23(\led译码器_2_col23 ),
    .col24(\led译码器_2_col24 ), .col25(\led译码器_2_col25 ), .col26(\led译码器_2_col26 ), .col27(\led译码器_2_col27 ),
    .col28(\led译码器_2_col28 ), .col29(\led译码器_2_col29 ), .col30(\led译码器_2_col30 ), .col31(\led译码器_2_col31 ));
  DotMatrix #(.inputtype("column"), .matrixcols(32), .matrixrows(32), .persist(0), .dotshape("square")) dotmatrix_3 (
    .col0(\led译码器_3_col0 ), .col1(\led译码器_3_col1 ), .col2(\led译码器_3_col2 ), .col3(\led译码器_3_col3 ),
    .col4(\led译码器_3_col4 ), .col5(\led译码器_3_col5 ), .col6(\led译码器_3_col6 ), .col7(\led译码器_3_col7 ),
    .col8(\led译码器_3_col8 ), .col9(\led译码器_3_col9 ), .col10(\led译码器_3_col10 ), .col11(\led译码器_3_col11 ),
    .col12(\led译码器_3_col12 ), .col13(\led译码器_3_col13 ), .col14(\led译码器_3_col14 ), .col15(\led译码器_3_col15 ),
    .col16(\led译码器_3_col16 ), .col17(\led译码器_3_col17 ), .col18(\led译码器_3_col18 ), .col19(\led译码器_3_col19 ),
    .col20(\led译码器_3_col20 ), .col21(\led译码器_3_col21 ), .col22(\led译码器_3_col22 ), .col23(\led译码器_3_col23 ),
    .col24(\led译码器_3_col24 ), .col25(\led译码器_3_col25 ), .col26(\led译码器_3_col26 ), .col27(\led译码器_3_col27 ),
    .col28(\led译码器_3_col28 ), .col29(\led译码器_3_col29 ), .col30(\led译码器_3_col30 ), .col31(\led译码器_3_col31 ));
  DotMatrix #(.inputtype("column"), .matrixcols(32), .matrixrows(32), .persist(0), .dotshape("square")) dotmatrix_4 (
    .col0(\led译码器_4_col0 ), .col1(\led译码器_4_col1 ), .col2(\led译码器_4_col2 ), .col3(\led译码器_4_col3 ),
    .col4(\led译码器_4_col4 ), .col5(\led译码器_4_col5 ), .col6(\led译码器_4_col6 ), .col7(\led译码器_4_col7 ),
    .col8(\led译码器_4_col8 ), .col9(\led译码器_4_col9 ), .col10(\led译码器_4_col10 ), .col11(\led译码器_4_col11 ),
    .col12(\led译码器_4_col12 ), .col13(\led译码器_4_col13 ), .col14(\led译码器_4_col14 ), .col15(\led译码器_4_col15 ),
    .col16(\led译码器_4_col16 ), .col17(\led译码器_4_col17 ), .col18(\led译码器_4_col18 ), .col19(\led译码器_4_col19 ),
    .col20(\led译码器_4_col20 ), .col21(\led译码器_4_col21 ), .col22(\led译码器_4_col22 ), .col23(\led译码器_4_col23 ),
    .col24(\led译码器_4_col24 ), .col25(\led译码器_4_col25 ), .col26(\led译码器_4_col26 ), .col27(\led译码器_4_col27 ),
    .col28(\led译码器_4_col28 ), .col29(\led译码器_4_col29 ), .col30(\led译码器_4_col30 ), .col31(\led译码器_4_col31 ));
  Hex_Digit_Display hex_digit_display_1 (.value(LedData[31:28]));  // open: dp
  \LED译码器  \led译码器_1  (
    .Num(Led0), .col8(\led译码器_1_col8 ), .col16(\led译码器_1_col16 ), .col24(\led译码器_1_col24 ),
    .col0(\led译码器_1_col0 ), .col9(\led译码器_1_col9 ), .col17(\led译码器_1_col17 ), .col25(\led译码器_1_col25 ),
    .col1(\led译码器_1_col1 ), .col10(\led译码器_1_col10 ), .col18(\led译码器_1_col18 ), .col26(\led译码器_1_col26 ),
    .col2(\led译码器_1_col2 ), .col11(\led译码器_1_col11 ), .col19(\led译码器_1_col19 ), .col27(\led译码器_1_col27 ),
    .col3(\led译码器_1_col3 ), .col12(\led译码器_1_col12 ), .col20(\led译码器_1_col20 ), .col28(\led译码器_1_col28 ),
    .col4(\led译码器_1_col4 ), .col13(\led译码器_1_col13 ), .col21(\led译码器_1_col21 ), .col29(\led译码器_1_col29 ),
    .col5(\led译码器_1_col5 ), .col14(\led译码器_1_col14 ), .col22(\led译码器_1_col22 ), .col30(\led译码器_1_col30 ),
    .col6(\led译码器_1_col6 ), .col15(\led译码器_1_col15 ), .col23(\led译码器_1_col23 ), .col31(\led译码器_1_col31 ),
    .col7(\led译码器_1_col7 ));
  \LED译码器  \led译码器_2  (
    .Num(Led4), .col8(\led译码器_2_col8 ), .col16(\led译码器_2_col16 ), .col24(\led译码器_2_col24 ),
    .col0(\led译码器_2_col0 ), .col9(\led译码器_2_col9 ), .col17(\led译码器_2_col17 ), .col25(\led译码器_2_col25 ),
    .col1(\led译码器_2_col1 ), .col10(\led译码器_2_col10 ), .col18(\led译码器_2_col18 ), .col26(\led译码器_2_col26 ),
    .col2(\led译码器_2_col2 ), .col11(\led译码器_2_col11 ), .col19(\led译码器_2_col19 ), .col27(\led译码器_2_col27 ),
    .col3(\led译码器_2_col3 ), .col12(\led译码器_2_col12 ), .col20(\led译码器_2_col20 ), .col28(\led译码器_2_col28 ),
    .col4(\led译码器_2_col4 ), .col13(\led译码器_2_col13 ), .col21(\led译码器_2_col21 ), .col29(\led译码器_2_col29 ),
    .col5(\led译码器_2_col5 ), .col14(\led译码器_2_col14 ), .col22(\led译码器_2_col22 ), .col30(\led译码器_2_col30 ),
    .col6(\led译码器_2_col6 ), .col15(\led译码器_2_col15 ), .col23(\led译码器_2_col23 ), .col31(\led译码器_2_col31 ),
    .col7(\led译码器_2_col7 ));
  \LED译码器  \led译码器_3  (
    .Num(Led8), .col8(\led译码器_3_col8 ), .col16(\led译码器_3_col16 ), .col24(\led译码器_3_col24 ),
    .col0(\led译码器_3_col0 ), .col9(\led译码器_3_col9 ), .col17(\led译码器_3_col17 ), .col25(\led译码器_3_col25 ),
    .col1(\led译码器_3_col1 ), .col10(\led译码器_3_col10 ), .col18(\led译码器_3_col18 ), .col26(\led译码器_3_col26 ),
    .col2(\led译码器_3_col2 ), .col11(\led译码器_3_col11 ), .col19(\led译码器_3_col19 ), .col27(\led译码器_3_col27 ),
    .col3(\led译码器_3_col3 ), .col12(\led译码器_3_col12 ), .col20(\led译码器_3_col20 ), .col28(\led译码器_3_col28 ),
    .col4(\led译码器_3_col4 ), .col13(\led译码器_3_col13 ), .col21(\led译码器_3_col21 ), .col29(\led译码器_3_col29 ),
    .col5(\led译码器_3_col5 ), .col14(\led译码器_3_col14 ), .col22(\led译码器_3_col22 ), .col30(\led译码器_3_col30 ),
    .col6(\led译码器_3_col6 ), .col15(\led译码器_3_col15 ), .col23(\led译码器_3_col23 ), .col31(\led译码器_3_col31 ),
    .col7(\led译码器_3_col7 ));
  \LED译码器  \led译码器_4  (
    .Num(Led12), .col8(\led译码器_4_col8 ), .col16(\led译码器_4_col16 ), .col24(\led译码器_4_col24 ),
    .col0(\led译码器_4_col0 ), .col9(\led译码器_4_col9 ), .col17(\led译码器_4_col17 ), .col25(\led译码器_4_col25 ),
    .col1(\led译码器_4_col1 ), .col10(\led译码器_4_col10 ), .col18(\led译码器_4_col18 ), .col26(\led译码器_4_col26 ),
    .col2(\led译码器_4_col2 ), .col11(\led译码器_4_col11 ), .col19(\led译码器_4_col19 ), .col27(\led译码器_4_col27 ),
    .col3(\led译码器_4_col3 ), .col12(\led译码器_4_col12 ), .col20(\led译码器_4_col20 ), .col28(\led译码器_4_col28 ),
    .col4(\led译码器_4_col4 ), .col13(\led译码器_4_col13 ), .col21(\led译码器_4_col21 ), .col29(\led译码器_4_col29 ),
    .col5(\led译码器_4_col5 ), .col14(\led译码器_4_col14 ), .col22(\led译码器_4_col22 ), .col30(\led译码器_4_col30 ),
    .col6(\led译码器_4_col6 ), .col15(\led译码器_4_col15 ), .col23(\led译码器_4_col23 ), .col31(\led译码器_4_col31 ),
    .col7(\led译码器_4_col7 ));
  Hex_Digit_Display hex_digit_display_2 (.value(LedData[27:24]));  // open: dp
  Hex_Digit_Display hex_digit_display_3 (.value(LedData[23:20]));  // open: dp
  Hex_Digit_Display hex_digit_display_4 (.value(LedData[15:12]));  // open: dp
  Hex_Digit_Display hex_digit_display_5 (.value(LedData[19:16]));  // open: dp
  Keyboard #(.Char_bit_width(7), .buflen(32), .trigger("rising")) keyboard_1 (
    .clk(CLK), .re(1'b1), .data(keyboard_1_data));  // open: clr, avail
  Hex_Digit_Display hex_digit_display_6 (.value(LedData[7:4]));  // open: dp
  Hex_Digit_Display hex_digit_display_7 (.value(LedData[11:8]));  // open: dp
  // Probe on \总周期数 
  Hex_Digit_Display hex_digit_display_8 (.value(LedData[3:0]));  // open: dp
  DotMatrix #(.inputtype("column"), .matrixcols(32), .matrixrows(32), .persist(0), .dotshape("square")) dotmatrix_5 (
    .col0(\led译码器_5_col0 ), .col1(\led译码器_5_col1 ), .col2(\led译码器_5_col2 ), .col3(\led译码器_5_col3 ),
    .col4(\led译码器_5_col4 ), .col5(\led译码器_5_col5 ), .col6(\led译码器_5_col6 ), .col7(\led译码器_5_col7 ),
    .col8(\led译码器_5_col8 ), .col9(\led译码器_5_col9 ), .col10(\led译码器_5_col10 ), .col11(\led译码器_5_col11 ),
    .col12(\led译码器_5_col12 ), .col13(\led译码器_5_col13 ), .col14(\led译码器_5_col14 ), .col15(\led译码器_5_col15 ),
    .col16(\led译码器_5_col16 ), .col17(\led译码器_5_col17 ), .col18(\led译码器_5_col18 ), .col19(\led译码器_5_col19 ),
    .col20(\led译码器_5_col20 ), .col21(\led译码器_5_col21 ), .col22(\led译码器_5_col22 ), .col23(\led译码器_5_col23 ),
    .col24(\led译码器_5_col24 ), .col25(\led译码器_5_col25 ), .col26(\led译码器_5_col26 ), .col27(\led译码器_5_col27 ),
    .col28(\led译码器_5_col28 ), .col29(\led译码器_5_col29 ), .col30(\led译码器_5_col30 ), .col31(\led译码器_5_col31 ));
  DotMatrix #(.inputtype("column"), .matrixcols(32), .matrixrows(32), .persist(0), .dotshape("square")) dotmatrix_6 (
    .col0(\led译码器_6_col0 ), .col1(\led译码器_6_col1 ), .col2(\led译码器_6_col2 ), .col3(\led译码器_6_col3 ),
    .col4(\led译码器_6_col4 ), .col5(\led译码器_6_col5 ), .col6(\led译码器_6_col6 ), .col7(\led译码器_6_col7 ),
    .col8(\led译码器_6_col8 ), .col9(\led译码器_6_col9 ), .col10(\led译码器_6_col10 ), .col11(\led译码器_6_col11 ),
    .col12(\led译码器_6_col12 ), .col13(\led译码器_6_col13 ), .col14(\led译码器_6_col14 ), .col15(\led译码器_6_col15 ),
    .col16(\led译码器_6_col16 ), .col17(\led译码器_6_col17 ), .col18(\led译码器_6_col18 ), .col19(\led译码器_6_col19 ),
    .col20(\led译码器_6_col20 ), .col21(\led译码器_6_col21 ), .col22(\led译码器_6_col22 ), .col23(\led译码器_6_col23 ),
    .col24(\led译码器_6_col24 ), .col25(\led译码器_6_col25 ), .col26(\led译码器_6_col26 ), .col27(\led译码器_6_col27 ),
    .col28(\led译码器_6_col28 ), .col29(\led译码器_6_col29 ), .col30(\led译码器_6_col30 ), .col31(\led译码器_6_col31 ));
  DotMatrix #(.inputtype("column"), .matrixcols(32), .matrixrows(32), .persist(0), .dotshape("square")) dotmatrix_7 (
    .col0(\led译码器_7_col0 ), .col1(\led译码器_7_col1 ), .col2(\led译码器_7_col2 ), .col3(\led译码器_7_col3 ),
    .col4(\led译码器_7_col4 ), .col5(\led译码器_7_col5 ), .col6(\led译码器_7_col6 ), .col7(\led译码器_7_col7 ),
    .col8(\led译码器_7_col8 ), .col9(\led译码器_7_col9 ), .col10(\led译码器_7_col10 ), .col11(\led译码器_7_col11 ),
    .col12(\led译码器_7_col12 ), .col13(\led译码器_7_col13 ), .col14(\led译码器_7_col14 ), .col15(\led译码器_7_col15 ),
    .col16(\led译码器_7_col16 ), .col17(\led译码器_7_col17 ), .col18(\led译码器_7_col18 ), .col19(\led译码器_7_col19 ),
    .col20(\led译码器_7_col20 ), .col21(\led译码器_7_col21 ), .col22(\led译码器_7_col22 ), .col23(\led译码器_7_col23 ),
    .col24(\led译码器_7_col24 ), .col25(\led译码器_7_col25 ), .col26(\led译码器_7_col26 ), .col27(\led译码器_7_col27 ),
    .col28(\led译码器_7_col28 ), .col29(\led译码器_7_col29 ), .col30(\led译码器_7_col30 ), .col31(\led译码器_7_col31 ));
  DotMatrix #(.inputtype("column"), .matrixcols(32), .matrixrows(32), .persist(0), .dotshape("square")) dotmatrix_8 (
    .col0(\led译码器_8_col0 ), .col1(\led译码器_8_col1 ), .col2(\led译码器_8_col2 ), .col3(\led译码器_8_col3 ),
    .col4(\led译码器_8_col4 ), .col5(\led译码器_8_col5 ), .col6(\led译码器_8_col6 ), .col7(\led译码器_8_col7 ),
    .col8(\led译码器_8_col8 ), .col9(\led译码器_8_col9 ), .col10(\led译码器_8_col10 ), .col11(\led译码器_8_col11 ),
    .col12(\led译码器_8_col12 ), .col13(\led译码器_8_col13 ), .col14(\led译码器_8_col14 ), .col15(\led译码器_8_col15 ),
    .col16(\led译码器_8_col16 ), .col17(\led译码器_8_col17 ), .col18(\led译码器_8_col18 ), .col19(\led译码器_8_col19 ),
    .col20(\led译码器_8_col20 ), .col21(\led译码器_8_col21 ), .col22(\led译码器_8_col22 ), .col23(\led译码器_8_col23 ),
    .col24(\led译码器_8_col24 ), .col25(\led译码器_8_col25 ), .col26(\led译码器_8_col26 ), .col27(\led译码器_8_col27 ),
    .col28(\led译码器_8_col28 ), .col29(\led译码器_8_col29 ), .col30(\led译码器_8_col30 ), .col31(\led译码器_8_col31 ));
  \LED译码器  \led译码器_5  (
    .Num(Led1), .col8(\led译码器_5_col8 ), .col16(\led译码器_5_col16 ), .col24(\led译码器_5_col24 ),
    .col0(\led译码器_5_col0 ), .col9(\led译码器_5_col9 ), .col17(\led译码器_5_col17 ), .col25(\led译码器_5_col25 ),
    .col1(\led译码器_5_col1 ), .col10(\led译码器_5_col10 ), .col18(\led译码器_5_col18 ), .col26(\led译码器_5_col26 ),
    .col2(\led译码器_5_col2 ), .col11(\led译码器_5_col11 ), .col19(\led译码器_5_col19 ), .col27(\led译码器_5_col27 ),
    .col3(\led译码器_5_col3 ), .col12(\led译码器_5_col12 ), .col20(\led译码器_5_col20 ), .col28(\led译码器_5_col28 ),
    .col4(\led译码器_5_col4 ), .col13(\led译码器_5_col13 ), .col21(\led译码器_5_col21 ), .col29(\led译码器_5_col29 ),
    .col5(\led译码器_5_col5 ), .col14(\led译码器_5_col14 ), .col22(\led译码器_5_col22 ), .col30(\led译码器_5_col30 ),
    .col6(\led译码器_5_col6 ), .col15(\led译码器_5_col15 ), .col23(\led译码器_5_col23 ), .col31(\led译码器_5_col31 ),
    .col7(\led译码器_5_col7 ));
  \LED译码器  \led译码器_6  (
    .Num(Led5), .col8(\led译码器_6_col8 ), .col16(\led译码器_6_col16 ), .col24(\led译码器_6_col24 ),
    .col0(\led译码器_6_col0 ), .col9(\led译码器_6_col9 ), .col17(\led译码器_6_col17 ), .col25(\led译码器_6_col25 ),
    .col1(\led译码器_6_col1 ), .col10(\led译码器_6_col10 ), .col18(\led译码器_6_col18 ), .col26(\led译码器_6_col26 ),
    .col2(\led译码器_6_col2 ), .col11(\led译码器_6_col11 ), .col19(\led译码器_6_col19 ), .col27(\led译码器_6_col27 ),
    .col3(\led译码器_6_col3 ), .col12(\led译码器_6_col12 ), .col20(\led译码器_6_col20 ), .col28(\led译码器_6_col28 ),
    .col4(\led译码器_6_col4 ), .col13(\led译码器_6_col13 ), .col21(\led译码器_6_col21 ), .col29(\led译码器_6_col29 ),
    .col5(\led译码器_6_col5 ), .col14(\led译码器_6_col14 ), .col22(\led译码器_6_col22 ), .col30(\led译码器_6_col30 ),
    .col6(\led译码器_6_col6 ), .col15(\led译码器_6_col15 ), .col23(\led译码器_6_col23 ), .col31(\led译码器_6_col31 ),
    .col7(\led译码器_6_col7 ));
  \LED译码器  \led译码器_7  (
    .Num(Led9), .col8(\led译码器_7_col8 ), .col16(\led译码器_7_col16 ), .col24(\led译码器_7_col24 ),
    .col0(\led译码器_7_col0 ), .col9(\led译码器_7_col9 ), .col17(\led译码器_7_col17 ), .col25(\led译码器_7_col25 ),
    .col1(\led译码器_7_col1 ), .col10(\led译码器_7_col10 ), .col18(\led译码器_7_col18 ), .col26(\led译码器_7_col26 ),
    .col2(\led译码器_7_col2 ), .col11(\led译码器_7_col11 ), .col19(\led译码器_7_col19 ), .col27(\led译码器_7_col27 ),
    .col3(\led译码器_7_col3 ), .col12(\led译码器_7_col12 ), .col20(\led译码器_7_col20 ), .col28(\led译码器_7_col28 ),
    .col4(\led译码器_7_col4 ), .col13(\led译码器_7_col13 ), .col21(\led译码器_7_col21 ), .col29(\led译码器_7_col29 ),
    .col5(\led译码器_7_col5 ), .col14(\led译码器_7_col14 ), .col22(\led译码器_7_col22 ), .col30(\led译码器_7_col30 ),
    .col6(\led译码器_7_col6 ), .col15(\led译码器_7_col15 ), .col23(\led译码器_7_col23 ), .col31(\led译码器_7_col31 ),
    .col7(\led译码器_7_col7 ));
  \LED译码器  \led译码器_8  (
    .Num(Led13), .col8(\led译码器_8_col8 ), .col16(\led译码器_8_col16 ), .col24(\led译码器_8_col24 ),
    .col0(\led译码器_8_col0 ), .col9(\led译码器_8_col9 ), .col17(\led译码器_8_col17 ), .col25(\led译码器_8_col25 ),
    .col1(\led译码器_8_col1 ), .col10(\led译码器_8_col10 ), .col18(\led译码器_8_col18 ), .col26(\led译码器_8_col26 ),
    .col2(\led译码器_8_col2 ), .col11(\led译码器_8_col11 ), .col19(\led译码器_8_col19 ), .col27(\led译码器_8_col27 ),
    .col3(\led译码器_8_col3 ), .col12(\led译码器_8_col12 ), .col20(\led译码器_8_col20 ), .col28(\led译码器_8_col28 ),
    .col4(\led译码器_8_col4 ), .col13(\led译码器_8_col13 ), .col21(\led译码器_8_col21 ), .col29(\led译码器_8_col29 ),
    .col5(\led译码器_8_col5 ), .col14(\led译码器_8_col14 ), .col22(\led译码器_8_col22 ), .col30(\led译码器_8_col30 ),
    .col6(\led译码器_8_col6 ), .col15(\led译码器_8_col15 ), .col23(\led译码器_8_col23 ), .col31(\led译码器_8_col31 ),
    .col7(\led译码器_8_col7 ));
  or or_1 (IR1_t, IR1, IRA);
  Comparator #(.width(7), .mode("twosComplement")) comparator_1 (
    .a(keyboard_1_data), .b(7'b1110111), .eq(UP));  // open: gt, lt
  or or_2 (IR2_t, IR2, IRB);
  Comparator #(.width(7), .mode("twosComplement")) comparator_2 (
    .a(keyboard_1_data), .b(7'b1110011), .eq(DOWN));  // open: gt, lt
  or or_3 (IR3_t, IR3, IRC);
  DotMatrix #(.inputtype("column"), .matrixcols(32), .matrixrows(32), .persist(0), .dotshape("square")) dotmatrix_9 (
    .col0(\led译码器_9_col0 ), .col1(\led译码器_9_col1 ), .col2(\led译码器_9_col2 ), .col3(\led译码器_9_col3 ),
    .col4(\led译码器_9_col4 ), .col5(\led译码器_9_col5 ), .col6(\led译码器_9_col6 ), .col7(\led译码器_9_col7 ),
    .col8(\led译码器_9_col8 ), .col9(\led译码器_9_col9 ), .col10(\led译码器_9_col10 ), .col11(\led译码器_9_col11 ),
    .col12(\led译码器_9_col12 ), .col13(\led译码器_9_col13 ), .col14(\led译码器_9_col14 ), .col15(\led译码器_9_col15 ),
    .col16(\led译码器_9_col16 ), .col17(\led译码器_9_col17 ), .col18(\led译码器_9_col18 ), .col19(\led译码器_9_col19 ),
    .col20(\led译码器_9_col20 ), .col21(\led译码器_9_col21 ), .col22(\led译码器_9_col22 ), .col23(\led译码器_9_col23 ),
    .col24(\led译码器_9_col24 ), .col25(\led译码器_9_col25 ), .col26(\led译码器_9_col26 ), .col27(\led译码器_9_col27 ),
    .col28(\led译码器_9_col28 ), .col29(\led译码器_9_col29 ), .col30(\led译码器_9_col30 ), .col31(\led译码器_9_col31 ));
  DotMatrix #(.inputtype("column"), .matrixcols(32), .matrixrows(32), .persist(0), .dotshape("square")) dotmatrix_10 (
    .col0(\led译码器_10_col0 ), .col1(\led译码器_10_col1 ), .col2(\led译码器_10_col2 ), .col3(\led译码器_10_col3 ),
    .col4(\led译码器_10_col4 ), .col5(\led译码器_10_col5 ), .col6(\led译码器_10_col6 ), .col7(\led译码器_10_col7 ),
    .col8(\led译码器_10_col8 ), .col9(\led译码器_10_col9 ), .col10(\led译码器_10_col10 ), .col11(\led译码器_10_col11 ),
    .col12(\led译码器_10_col12 ), .col13(\led译码器_10_col13 ), .col14(\led译码器_10_col14 ),
    .col15(\led译码器_10_col15 ), .col16(\led译码器_10_col16 ), .col17(\led译码器_10_col17 ),
    .col18(\led译码器_10_col18 ), .col19(\led译码器_10_col19 ), .col20(\led译码器_10_col20 ),
    .col21(\led译码器_10_col21 ), .col22(\led译码器_10_col22 ), .col23(\led译码器_10_col23 ),
    .col24(\led译码器_10_col24 ), .col25(\led译码器_10_col25 ), .col26(\led译码器_10_col26 ),
    .col27(\led译码器_10_col27 ), .col28(\led译码器_10_col28 ), .col29(\led译码器_10_col29 ),
    .col30(\led译码器_10_col30 ), .col31(\led译码器_10_col31 ));
  DotMatrix #(.inputtype("column"), .matrixcols(32), .matrixrows(32), .persist(0), .dotshape("square")) dotmatrix_11 (
    .col0(\led译码器_11_col0 ), .col1(\led译码器_11_col1 ), .col2(\led译码器_11_col2 ), .col3(\led译码器_11_col3 ),
    .col4(\led译码器_11_col4 ), .col5(\led译码器_11_col5 ), .col6(\led译码器_11_col6 ), .col7(\led译码器_11_col7 ),
    .col8(\led译码器_11_col8 ), .col9(\led译码器_11_col9 ), .col10(\led译码器_11_col10 ), .col11(\led译码器_11_col11 ),
    .col12(\led译码器_11_col12 ), .col13(\led译码器_11_col13 ), .col14(\led译码器_11_col14 ),
    .col15(\led译码器_11_col15 ), .col16(\led译码器_11_col16 ), .col17(\led译码器_11_col17 ),
    .col18(\led译码器_11_col18 ), .col19(\led译码器_11_col19 ), .col20(\led译码器_11_col20 ),
    .col21(\led译码器_11_col21 ), .col22(\led译码器_11_col22 ), .col23(\led译码器_11_col23 ),
    .col24(\led译码器_11_col24 ), .col25(\led译码器_11_col25 ), .col26(\led译码器_11_col26 ),
    .col27(\led译码器_11_col27 ), .col28(\led译码器_11_col28 ), .col29(\led译码器_11_col29 ),
    .col30(\led译码器_11_col30 ), .col31(\led译码器_11_col31 ));
  DotMatrix #(.inputtype("column"), .matrixcols(32), .matrixrows(32), .persist(0), .dotshape("square")) dotmatrix_12 (
    .col0(\led译码器_12_col0 ), .col1(\led译码器_12_col1 ), .col2(\led译码器_12_col2 ), .col3(\led译码器_12_col3 ),
    .col4(\led译码器_12_col4 ), .col5(\led译码器_12_col5 ), .col6(\led译码器_12_col6 ), .col7(\led译码器_12_col7 ),
    .col8(\led译码器_12_col8 ), .col9(\led译码器_12_col9 ), .col10(\led译码器_12_col10 ), .col11(\led译码器_12_col11 ),
    .col12(\led译码器_12_col12 ), .col13(\led译码器_12_col13 ), .col14(\led译码器_12_col14 ),
    .col15(\led译码器_12_col15 ), .col16(\led译码器_12_col16 ), .col17(\led译码器_12_col17 ),
    .col18(\led译码器_12_col18 ), .col19(\led译码器_12_col19 ), .col20(\led译码器_12_col20 ),
    .col21(\led译码器_12_col21 ), .col22(\led译码器_12_col22 ), .col23(\led译码器_12_col23 ),
    .col24(\led译码器_12_col24 ), .col25(\led译码器_12_col25 ), .col26(\led译码器_12_col26 ),
    .col27(\led译码器_12_col27 ), .col28(\led译码器_12_col28 ), .col29(\led译码器_12_col29 ),
    .col30(\led译码器_12_col30 ), .col31(\led译码器_12_col31 ));
  \LED译码器  \led译码器_9  (
    .Num(Led2), .col8(\led译码器_9_col8 ), .col16(\led译码器_9_col16 ), .col24(\led译码器_9_col24 ),
    .col0(\led译码器_9_col0 ), .col9(\led译码器_9_col9 ), .col17(\led译码器_9_col17 ), .col25(\led译码器_9_col25 ),
    .col1(\led译码器_9_col1 ), .col10(\led译码器_9_col10 ), .col18(\led译码器_9_col18 ), .col26(\led译码器_9_col26 ),
    .col2(\led译码器_9_col2 ), .col11(\led译码器_9_col11 ), .col19(\led译码器_9_col19 ), .col27(\led译码器_9_col27 ),
    .col3(\led译码器_9_col3 ), .col12(\led译码器_9_col12 ), .col20(\led译码器_9_col20 ), .col28(\led译码器_9_col28 ),
    .col4(\led译码器_9_col4 ), .col13(\led译码器_9_col13 ), .col21(\led译码器_9_col21 ), .col29(\led译码器_9_col29 ),
    .col5(\led译码器_9_col5 ), .col14(\led译码器_9_col14 ), .col22(\led译码器_9_col22 ), .col30(\led译码器_9_col30 ),
    .col6(\led译码器_9_col6 ), .col15(\led译码器_9_col15 ), .col23(\led译码器_9_col23 ), .col31(\led译码器_9_col31 ),
    .col7(\led译码器_9_col7 ));
  \LED译码器  \led译码器_10  (
    .Num(Led6), .col8(\led译码器_10_col8 ), .col16(\led译码器_10_col16 ), .col24(\led译码器_10_col24 ),
    .col0(\led译码器_10_col0 ), .col9(\led译码器_10_col9 ), .col17(\led译码器_10_col17 ), .col25(\led译码器_10_col25 ),
    .col1(\led译码器_10_col1 ), .col10(\led译码器_10_col10 ), .col18(\led译码器_10_col18 ), .col26(\led译码器_10_col26 ),
    .col2(\led译码器_10_col2 ), .col11(\led译码器_10_col11 ), .col19(\led译码器_10_col19 ), .col27(\led译码器_10_col27 ),
    .col3(\led译码器_10_col3 ), .col12(\led译码器_10_col12 ), .col20(\led译码器_10_col20 ), .col28(\led译码器_10_col28 ),
    .col4(\led译码器_10_col4 ), .col13(\led译码器_10_col13 ), .col21(\led译码器_10_col21 ), .col29(\led译码器_10_col29 ),
    .col5(\led译码器_10_col5 ), .col14(\led译码器_10_col14 ), .col22(\led译码器_10_col22 ), .col30(\led译码器_10_col30 ),
    .col6(\led译码器_10_col6 ), .col15(\led译码器_10_col15 ), .col23(\led译码器_10_col23 ), .col31(\led译码器_10_col31 ),
    .col7(\led译码器_10_col7 ));
  \LED译码器  \led译码器_11  (
    .Num(Led10), .col8(\led译码器_11_col8 ), .col16(\led译码器_11_col16 ), .col24(\led译码器_11_col24 ),
    .col0(\led译码器_11_col0 ), .col9(\led译码器_11_col9 ), .col17(\led译码器_11_col17 ), .col25(\led译码器_11_col25 ),
    .col1(\led译码器_11_col1 ), .col10(\led译码器_11_col10 ), .col18(\led译码器_11_col18 ), .col26(\led译码器_11_col26 ),
    .col2(\led译码器_11_col2 ), .col11(\led译码器_11_col11 ), .col19(\led译码器_11_col19 ), .col27(\led译码器_11_col27 ),
    .col3(\led译码器_11_col3 ), .col12(\led译码器_11_col12 ), .col20(\led译码器_11_col20 ), .col28(\led译码器_11_col28 ),
    .col4(\led译码器_11_col4 ), .col13(\led译码器_11_col13 ), .col21(\led译码器_11_col21 ), .col29(\led译码器_11_col29 ),
    .col5(\led译码器_11_col5 ), .col14(\led译码器_11_col14 ), .col22(\led译码器_11_col22 ), .col30(\led译码器_11_col30 ),
    .col6(\led译码器_11_col6 ), .col15(\led译码器_11_col15 ), .col23(\led译码器_11_col23 ), .col31(\led译码器_11_col31 ),
    .col7(\led译码器_11_col7 ));
  \LED译码器  \led译码器_12  (
    .Num(Led14), .col8(\led译码器_12_col8 ), .col16(\led译码器_12_col16 ), .col24(\led译码器_12_col24 ),
    .col0(\led译码器_12_col0 ), .col9(\led译码器_12_col9 ), .col17(\led译码器_12_col17 ), .col25(\led译码器_12_col25 ),
    .col1(\led译码器_12_col1 ), .col10(\led译码器_12_col10 ), .col18(\led译码器_12_col18 ), .col26(\led译码器_12_col26 ),
    .col2(\led译码器_12_col2 ), .col11(\led译码器_12_col11 ), .col19(\led译码器_12_col19 ), .col27(\led译码器_12_col27 ),
    .col3(\led译码器_12_col3 ), .col12(\led译码器_12_col12 ), .col20(\led译码器_12_col20 ), .col28(\led译码器_12_col28 ),
    .col4(\led译码器_12_col4 ), .col13(\led译码器_12_col13 ), .col21(\led译码器_12_col21 ), .col29(\led译码器_12_col29 ),
    .col5(\led译码器_12_col5 ), .col14(\led译码器_12_col14 ), .col22(\led译码器_12_col22 ), .col30(\led译码器_12_col30 ),
    .col6(\led译码器_12_col6 ), .col15(\led译码器_12_col15 ), .col23(\led译码器_12_col23 ), .col31(\led译码器_12_col31 ),
    .col7(\led译码器_12_col7 ));
  Comparator #(.width(7), .mode("twosComplement")) comparator_3 (
    .a(keyboard_1_data), .b(7'b1100001), .eq(LEFT));  // open: gt, lt
  DotMatrix #(.inputtype("column"), .matrixcols(32), .matrixrows(32), .persist(0), .dotshape("square")) dotmatrix_13 (
    .col0(\led译码器_13_col0 ), .col1(\led译码器_13_col1 ), .col2(\led译码器_13_col2 ), .col3(\led译码器_13_col3 ),
    .col4(\led译码器_13_col4 ), .col5(\led译码器_13_col5 ), .col6(\led译码器_13_col6 ), .col7(\led译码器_13_col7 ),
    .col8(\led译码器_13_col8 ), .col9(\led译码器_13_col9 ), .col10(\led译码器_13_col10 ), .col11(\led译码器_13_col11 ),
    .col12(\led译码器_13_col12 ), .col13(\led译码器_13_col13 ), .col14(\led译码器_13_col14 ),
    .col15(\led译码器_13_col15 ), .col16(\led译码器_13_col16 ), .col17(\led译码器_13_col17 ),
    .col18(\led译码器_13_col18 ), .col19(\led译码器_13_col19 ), .col20(\led译码器_13_col20 ),
    .col21(\led译码器_13_col21 ), .col22(\led译码器_13_col22 ), .col23(\led译码器_13_col23 ),
    .col24(\led译码器_13_col24 ), .col25(\led译码器_13_col25 ), .col26(\led译码器_13_col26 ),
    .col27(\led译码器_13_col27 ), .col28(\led译码器_13_col28 ), .col29(\led译码器_13_col29 ),
    .col30(\led译码器_13_col30 ), .col31(\led译码器_13_col31 ));
  DotMatrix #(.inputtype("column"), .matrixcols(32), .matrixrows(32), .persist(0), .dotshape("square")) dotmatrix_14 (
    .col0(\led译码器_14_col0 ), .col1(\led译码器_14_col1 ), .col2(\led译码器_14_col2 ), .col3(\led译码器_14_col3 ),
    .col4(\led译码器_14_col4 ), .col5(\led译码器_14_col5 ), .col6(\led译码器_14_col6 ), .col7(\led译码器_14_col7 ),
    .col8(\led译码器_14_col8 ), .col9(\led译码器_14_col9 ), .col10(\led译码器_14_col10 ), .col11(\led译码器_14_col11 ),
    .col12(\led译码器_14_col12 ), .col13(\led译码器_14_col13 ), .col14(\led译码器_14_col14 ),
    .col15(\led译码器_14_col15 ), .col16(\led译码器_14_col16 ), .col17(\led译码器_14_col17 ),
    .col18(\led译码器_14_col18 ), .col19(\led译码器_14_col19 ), .col20(\led译码器_14_col20 ),
    .col21(\led译码器_14_col21 ), .col22(\led译码器_14_col22 ), .col23(\led译码器_14_col23 ),
    .col24(\led译码器_14_col24 ), .col25(\led译码器_14_col25 ), .col26(\led译码器_14_col26 ),
    .col27(\led译码器_14_col27 ), .col28(\led译码器_14_col28 ), .col29(\led译码器_14_col29 ),
    .col30(\led译码器_14_col30 ), .col31(\led译码器_14_col31 ));
  DotMatrix #(.inputtype("column"), .matrixcols(32), .matrixrows(32), .persist(0), .dotshape("square")) dotmatrix_15 (
    .col0(\led译码器_15_col0 ), .col1(\led译码器_15_col1 ), .col2(\led译码器_15_col2 ), .col3(\led译码器_15_col3 ),
    .col4(\led译码器_15_col4 ), .col5(\led译码器_15_col5 ), .col6(\led译码器_15_col6 ), .col7(\led译码器_15_col7 ),
    .col8(\led译码器_15_col8 ), .col9(\led译码器_15_col9 ), .col10(\led译码器_15_col10 ), .col11(\led译码器_15_col11 ),
    .col12(\led译码器_15_col12 ), .col13(\led译码器_15_col13 ), .col14(\led译码器_15_col14 ),
    .col15(\led译码器_15_col15 ), .col16(\led译码器_15_col16 ), .col17(\led译码器_15_col17 ),
    .col18(\led译码器_15_col18 ), .col19(\led译码器_15_col19 ), .col20(\led译码器_15_col20 ),
    .col21(\led译码器_15_col21 ), .col22(\led译码器_15_col22 ), .col23(\led译码器_15_col23 ),
    .col24(\led译码器_15_col24 ), .col25(\led译码器_15_col25 ), .col26(\led译码器_15_col26 ),
    .col27(\led译码器_15_col27 ), .col28(\led译码器_15_col28 ), .col29(\led译码器_15_col29 ),
    .col30(\led译码器_15_col30 ), .col31(\led译码器_15_col31 ));
  DotMatrix #(.inputtype("column"), .matrixcols(32), .matrixrows(32), .persist(0), .dotshape("square")) dotmatrix_16 (
    .col0(\led译码器_16_col0 ), .col1(\led译码器_16_col1 ), .col2(\led译码器_16_col2 ), .col3(\led译码器_16_col3 ),
    .col4(\led译码器_16_col4 ), .col5(\led译码器_16_col5 ), .col6(\led译码器_16_col6 ), .col7(\led译码器_16_col7 ),
    .col8(\led译码器_16_col8 ), .col9(\led译码器_16_col9 ), .col10(\led译码器_16_col10 ), .col11(\led译码器_16_col11 ),
    .col12(\led译码器_16_col12 ), .col13(\led译码器_16_col13 ), .col14(\led译码器_16_col14 ),
    .col15(\led译码器_16_col15 ), .col16(\led译码器_16_col16 ), .col17(\led译码器_16_col17 ),
    .col18(\led译码器_16_col18 ), .col19(\led译码器_16_col19 ), .col20(\led译码器_16_col20 ),
    .col21(\led译码器_16_col21 ), .col22(\led译码器_16_col22 ), .col23(\led译码器_16_col23 ),
    .col24(\led译码器_16_col24 ), .col25(\led译码器_16_col25 ), .col26(\led译码器_16_col26 ),
    .col27(\led译码器_16_col27 ), .col28(\led译码器_16_col28 ), .col29(\led译码器_16_col29 ),
    .col30(\led译码器_16_col30 ), .col31(\led译码器_16_col31 ));
  Comparator #(.width(7), .mode("twosComplement")) comparator_4 (
    .a(keyboard_1_data), .b(7'b1100100), .eq(RIGHT));  // open: gt, lt
  \LED译码器  \led译码器_13  (
    .Num(Led3), .col8(\led译码器_13_col8 ), .col16(\led译码器_13_col16 ), .col24(\led译码器_13_col24 ),
    .col0(\led译码器_13_col0 ), .col9(\led译码器_13_col9 ), .col17(\led译码器_13_col17 ), .col25(\led译码器_13_col25 ),
    .col1(\led译码器_13_col1 ), .col10(\led译码器_13_col10 ), .col18(\led译码器_13_col18 ), .col26(\led译码器_13_col26 ),
    .col2(\led译码器_13_col2 ), .col11(\led译码器_13_col11 ), .col19(\led译码器_13_col19 ), .col27(\led译码器_13_col27 ),
    .col3(\led译码器_13_col3 ), .col12(\led译码器_13_col12 ), .col20(\led译码器_13_col20 ), .col28(\led译码器_13_col28 ),
    .col4(\led译码器_13_col4 ), .col13(\led译码器_13_col13 ), .col21(\led译码器_13_col21 ), .col29(\led译码器_13_col29 ),
    .col5(\led译码器_13_col5 ), .col14(\led译码器_13_col14 ), .col22(\led译码器_13_col22 ), .col30(\led译码器_13_col30 ),
    .col6(\led译码器_13_col6 ), .col15(\led译码器_13_col15 ), .col23(\led译码器_13_col23 ), .col31(\led译码器_13_col31 ),
    .col7(\led译码器_13_col7 ));
  \LED译码器  \led译码器_14  (
    .Num(Led7), .col8(\led译码器_14_col8 ), .col16(\led译码器_14_col16 ), .col24(\led译码器_14_col24 ),
    .col0(\led译码器_14_col0 ), .col9(\led译码器_14_col9 ), .col17(\led译码器_14_col17 ), .col25(\led译码器_14_col25 ),
    .col1(\led译码器_14_col1 ), .col10(\led译码器_14_col10 ), .col18(\led译码器_14_col18 ), .col26(\led译码器_14_col26 ),
    .col2(\led译码器_14_col2 ), .col11(\led译码器_14_col11 ), .col19(\led译码器_14_col19 ), .col27(\led译码器_14_col27 ),
    .col3(\led译码器_14_col3 ), .col12(\led译码器_14_col12 ), .col20(\led译码器_14_col20 ), .col28(\led译码器_14_col28 ),
    .col4(\led译码器_14_col4 ), .col13(\led译码器_14_col13 ), .col21(\led译码器_14_col21 ), .col29(\led译码器_14_col29 ),
    .col5(\led译码器_14_col5 ), .col14(\led译码器_14_col14 ), .col22(\led译码器_14_col22 ), .col30(\led译码器_14_col30 ),
    .col6(\led译码器_14_col6 ), .col15(\led译码器_14_col15 ), .col23(\led译码器_14_col23 ), .col31(\led译码器_14_col31 ),
    .col7(\led译码器_14_col7 ));
  \LED译码器  \led译码器_15  (
    .Num(Led11), .col8(\led译码器_15_col8 ), .col16(\led译码器_15_col16 ), .col24(\led译码器_15_col24 ),
    .col0(\led译码器_15_col0 ), .col9(\led译码器_15_col9 ), .col17(\led译码器_15_col17 ), .col25(\led译码器_15_col25 ),
    .col1(\led译码器_15_col1 ), .col10(\led译码器_15_col10 ), .col18(\led译码器_15_col18 ), .col26(\led译码器_15_col26 ),
    .col2(\led译码器_15_col2 ), .col11(\led译码器_15_col11 ), .col19(\led译码器_15_col19 ), .col27(\led译码器_15_col27 ),
    .col3(\led译码器_15_col3 ), .col12(\led译码器_15_col12 ), .col20(\led译码器_15_col20 ), .col28(\led译码器_15_col28 ),
    .col4(\led译码器_15_col4 ), .col13(\led译码器_15_col13 ), .col21(\led译码器_15_col21 ), .col29(\led译码器_15_col29 ),
    .col5(\led译码器_15_col5 ), .col14(\led译码器_15_col14 ), .col22(\led译码器_15_col22 ), .col30(\led译码器_15_col30 ),
    .col6(\led译码器_15_col6 ), .col15(\led译码器_15_col15 ), .col23(\led译码器_15_col23 ), .col31(\led译码器_15_col31 ),
    .col7(\led译码器_15_col7 ));
  \LED译码器  \led译码器_16  (
    .Num(Led15), .col8(\led译码器_16_col8 ), .col16(\led译码器_16_col16 ), .col24(\led译码器_16_col24 ),
    .col0(\led译码器_16_col0 ), .col9(\led译码器_16_col9 ), .col17(\led译码器_16_col17 ), .col25(\led译码器_16_col25 ),
    .col1(\led译码器_16_col1 ), .col10(\led译码器_16_col10 ), .col18(\led译码器_16_col18 ), .col26(\led译码器_16_col26 ),
    .col2(\led译码器_16_col2 ), .col11(\led译码器_16_col11 ), .col19(\led译码器_16_col19 ), .col27(\led译码器_16_col27 ),
    .col3(\led译码器_16_col3 ), .col12(\led译码器_16_col12 ), .col20(\led译码器_16_col20 ), .col28(\led译码器_16_col28 ),
    .col4(\led译码器_16_col4 ), .col13(\led译码器_16_col13 ), .col21(\led译码器_16_col21 ), .col29(\led译码器_16_col29 ),
    .col5(\led译码器_16_col5 ), .col14(\led译码器_16_col14 ), .col22(\led译码器_16_col22 ), .col30(\led译码器_16_col30 ),
    .col6(\led译码器_16_col6 ), .col15(\led译码器_16_col15 ), .col23(\led译码器_16_col23 ), .col31(\led译码器_16_col31 ),
    .col7(\led译码器_16_col7 ));
  LED #(.active("true")) led_4 (.in(or_4_out));
  or or_4 (or_4_out, W1, W2, W3, W4);
  D_Flip_Flop #(.trigger("high"), .Pre_Clr_Positions("LEGACY"), .NegatePresetClear("false"), .enable("true"), .NewFFLayout("false")) d_ff_1 (.Q(d_ff_1_q));  // open: clk, D, Qn, preset, en, reset
  // Probe on 13'hc
  Comparator #(.width(13), .mode("twosComplement")) comparator_5 (
    .a(CNT_num), .b(13'hc), .eq(comparator_5_eq), .lt(comparator_5_lt));  // open: gt
  Clock #(.highDuration(1), .lowDuration(1)) clock_2 (.out(clock_2_out));
  Counter #(.width(13), .max('h1fff), .ongoal("stay"), .trigger("rising"), .behavior("old")) counter_1 (
    .count(comparator_5_lt), .Q(CNT_num), .clk(clock_2_out));  // open: load, D, carry, clr, preset
  nand nand_1 (nand_1_out, d_ff_1_q, comparator_5_eq);
  assign CLK = nand_1_out ? clock_2_out : 1'bz;  // Controlled_Buffer controlled_buffer_1
  Pull_Resistor #(.pull(1)) pull_resistor_1 (.node(CLK));
  LED #(.active("true")) led_5 (.in(Win));
  LED #(.active("true")) led_6 (.in(Lost));
  or or_5 (or_5_out, Branch, J_signal);
  Multiplexer #(.select(1), .width(32), .disabled("Z"), .enable("false")) multiplexer_1 (
    .in0(PC_4), .in1(adder_2_out), .out(multiplexer_1_out), .sel(or_5_out));
  Multiplexer #(.select(1), .width(32), .disabled("Z"), .enable("false")) multiplexer_2 (
    .in0(multiplexer_1_out), .in1(ALU_Res), .out(Break_PC), .sel(Jalr_signal));
  Multiplexer #(.select(1), .width(32), .disabled("Z"), .enable("false")) multiplexer_3 (
    .in0(MemData), .in1(random_Num), .out(multiplexer_3_out), .sel(random));
  Multiplexer #(.select(1), .width(4), .disabled("Z"), .enable("false")) multiplexer_4 (
    .in0(ALU_Res[5:2]), .in1(random_Adr), .out(multiplexer_4_out), .sel(random));
  or or_6 (or_6_out, MemWrite, random);
  Multiplexer #(.select(1), .width(32), .disabled("Z"), .enable("false")) multiplexer_5 (
    .in0(Break_PC), .in1(RET_PC), .out(multiplexer_5_out), .sel(URET));
  or or_7 (or_7_out, B_signal, J_signal);
  or or_8 (or_8_out, J_signal, S_signal);
  Multiplexer #(.select(1), .width(32), .disabled("Z"), .enable("false")) multiplexer_6 (
    .in0(multiplexer_5_out), .in1(INT_Addar), .out(multiplexer_6_out), .sel(INT));
  not not_1 (not_1_out, halt);
  and and_1 (Imm_Sel[1], ~S_signal, or_7_out);  // AND_Gate
  and and_2 (Imm_Sel[0], or_8_out, ~B_signal);  // AND_Gate
  \_16格数据存储  \u_16格数据存储_1  (
    .CLK(CLK), .Din(multiplexer_3_out), .MenWrite(or_6_out), .Byte_Adr(multiplexer_4_out), .Data0(Data0),
    .Data1(Data1), .Data2(Data2), .Data3(Data3), .Data4(Data4), .Data5(Data5), .Data6(Data6), .Data7(Data7),
    .Data10(Data10), .Data11(Data11), .Data12(Data12), .Data13(Data13), .Data14(Data14), .Data15(Data15),
    .RST(RST), .Data8(Data8), .Data9(Data9));
  Register #(.width(32), .trigger("rising"), .Select("low")) u_PC (
    .D(multiplexer_6_out), .en(not_1_out), .Q(PC), .clk(CLK), .clr(RST));
  \按键中断控制器  \u_按键中断控制器_1  (
    .UP(UP), .Clr_UP(Clr_UP), .DOWN(DOWN), .Clr_DOWN(Clr_DOWN), .LEFT(LEFT), .Clr_LEFT(Clr_LEFT),
    .RIGHT(RIGHT), .Clr_RIGHT(Clr_RIGHT), .\中断号 (\中断号 ), .\中断请求 (\中断信号 ), .CLK(CLK), .RST(RST), .UP_2(W1),
    .DOWN_2(W2), .LEFT_2(W3), .RIGHT_2(W4));
  Adder #(.width(32)) adder_1 (.a(PC), .b(32'h4), .out(PC_4));  // open: cin, cout
  // RiscV_Probe riscv_probe_1: pin names not known; wires that end beside it: IR
  ROM #(.addrWidth(10), .dataWidth(32), .Select("high")) rom_1 (.addr(PC[11:2]), .data(IR));
  Comparator #(.width(32), .mode("unsigned")) comparator_6 (
    .a(R1_Data), .b(32'h22), .eq(comparator_6_eq));  // open: gt, lt
  Comparator #(.width(32), .mode("unsigned")) comparator_7 (
    .a(R1_Data), .b(32'h2c), .eq(comparator_7_eq));  // open: gt, lt
  and and_3 (and_3_out, ecall, nor_1_out);
  nor nor_1 (nor_1_out, comparator_6_eq, comparator_7_eq);
  and and_4 (random, comparator_6_eq, ecall);
  and and_5 (update, comparator_7_eq, ecall);
  \单周期硬布线控制器  \u_单周期硬布线控制器_1  (
    .Funct({IR[30], IR[25], IR[14:12]}), .OP(IR[6:2]), .ALU_OP(\单周期硬布线控制器_1_alu_op ),
    .MemToReg(\单周期硬布线控制器_1_memtoreg ), .MemWrite(MemWrite), .ALU_SRC(\单周期硬布线控制器_1_alu_src ),
    .RegWrite(RegWrite), .ecall(ecall), .S_type(S_signal), .Jalr(Jalr_signal), .Beq(\单周期硬布线控制器_1_beq ),
    .JAL(J_signal), .Bne(\单周期硬布线控制器_1_bne ), .in_3(IR[21]), .uret(URET), .Sltiu(sltiu), .Sb(sb), .Blt(blt));
  Multiplexer #(.select(1), .width(5), .disabled("Z"), .enable("false")) multiplexer_7 (
    .in0(IR[19:15]), .in1(5'b10001), .out(multiplexer_7_out), .sel(ecall));
  Multiplexer #(.select(1), .width(5), .disabled("Z"), .enable("false")) multiplexer_8 (
    .in0(IR[24:20]), .in1(5'b01010), .out(multiplexer_8_out), .sel(ecall));
  and and_6 (and_6_out, ~URET, \中断信号 );  // AND_Gate
  and and_7 (INT, IE, \中断信号 );
  Register #(.width(32), .trigger("rising"), .Select("low")) register_1 (
    .D(Data0), .en(update), .Q(Led0), .clk(CLK), .clr(RST));
  Register #(.width(32), .trigger("rising"), .Select("low")) register_2 (
    .D(Data4), .en(update), .Q(Led4), .clk(CLK), .clr(RST));
  Register #(.width(32), .trigger("rising"), .Select("low")) register_3 (
    .D(Data8), .en(update), .Q(Led8), .clk(CLK), .clr(RST));
  Register #(.width(32), .trigger("rising"), .Select("low")) register_4 (
    .D(Data12), .en(update), .Q(Led12), .clk(CLK), .clr(RST));
  assign bit_extender_1_out = {{20{IR[31]}}, IR[31:20]};  // Bit_Extender bit_extender_1
  assign bit_extender_2_out = {{20{1'b0}}, IR[31:20]};  // Bit_Extender bit_extender_2
  assign bit_extender_3_out = {{20{IR[31]}}, {IR[31:25], IR[11:7]}};  // Bit_Extender bit_extender_3
  assign bit_extender_4_out = {{20{IR[31]}}, {IR[31], IR[7], IR[30:25], IR[11:8]}};  // Bit_Extender bit_extender_4
  assign bit_extender_5_out = {{12{IR[31]}}, {IR[31], IR[19:12], IR[20], IR[30:21]}};  // Bit_Extender bit_extender_5
  D_Flip_Flop #(.trigger("falling"), .Pre_Clr_Positions("ABOVE_BELOW"), .NegatePresetClear("false"), .enable("true"), .NewFFLayout("true")) d_ff_2 (
    .clk(CLK), .D(and_3_out), .Q(halt), .en(ecall), .reset(Go));  // open: Qn, preset
  D_Flip_Flop #(.trigger("rising"), .Pre_Clr_Positions("LEGACY"), .NegatePresetClear("false"), .enable("true"), .NewFFLayout("false")) d_ff_3 (
    .clk(CLK), .D(and_6_out), .Qn(IE));  // open: Q, preset, en, reset
  or or_9 (B_signal, \单周期硬布线控制器_1_beq , blt, \单周期硬布线控制器_1_bne );
  Multiplexer #(.select(1), .width(32), .disabled("Z"), .enable("false")) multiplexer_9 (
    .in0(bit_extender_1_out), .in1(bit_extender_2_out), .out(multiplexer_9_out), .sel(sltiu));
  Register #(.width(32), .trigger("rising"), .Select("low")) register_5 (
    .D(Data1), .en(update), .Q(Led1), .clk(CLK), .clr(RST));
  Register #(.width(32), .trigger("rising"), .Select("low")) register_6 (
    .D(Data5), .en(update), .Q(Led5), .clk(CLK), .clr(RST));
  Register #(.width(32), .trigger("rising"), .Select("low")) register_7 (
    .D(Data9), .en(update), .Q(Led9), .clk(CLK), .clr(RST));
  Register #(.width(32), .trigger("rising"), .Select("low")) register_8 (
    .D(Data13), .en(update), .Q(Led13), .clk(CLK), .clr(RST));
  \Regifile_上升沿  \regifile_上升沿_1  (
    .Din(RDin), .Clk(CLK), .R1(R1_Data), .R2(MDin), .WE(RegWrite), .W_num(IR[11:7]),
    .R1_num(multiplexer_7_out), .R2_num(multiplexer_8_out));
  Multiplexer #(.select(2), .width(32), .disabled("Z"), .enable("false")) multiplexer_10 (
    .in0(multiplexer_9_out), .in1(bit_extender_3_out), .in2(bit_extender_4_out), .in3(bit_extender_5_out),
    .out(multiplexer_10_out), .sel(Imm_Sel));
  assign bit_extender_6_out = {{3{1'b0}}, ALU_Res[1:0]};  // Bit_Extender bit_extender_6
  Decoder #(.select(2), .tristate("false"), .disabled("Z"), .enable("false")) decoder_1 (
    .out0(decoder_1_out0[0]), .out1(decoder_1_out0[1]), .out2(decoder_1_out0[2]), .out3(decoder_1_out0[3]),
    .sel(ALU_Res[1:0]));
  Multiplexer #(.select(1), .width(32), .disabled("Z"), .enable("false")) multiplexer_11 (
    .in0(MDin), .in1(multiplexer_10_out), .out(multiplexer_11_out), .sel(\单周期硬布线控制器_1_alu_src ));
  Multiplier #(.width(5)) multiplier_1 (
    .a(bit_extender_6_out), .b(5'b01000), .out(multiplier_1_out));  // open: cin, cout
  Multiplexer #(.select(1), .width(4), .disabled("Z"), .enable("false")) multiplexer_12 (
    .in0(4'b1111), .in1(decoder_1_out0), .out(RAM_Sel), .sel(sb));
  Register #(.width(2), .trigger("rising"), .Select("low")) register_9 (
    .D(\中断号 ), .en(INT), .Q(register_9_q), .clk(CLK), .clr(RST));
  Decoder #(.select(2), .tristate("false"), .disabled("Z"), .enable("false")) decoder_2 (
    .out0(decoder_2_out0), .out1(decoder_2_out1), .out2(decoder_2_out2), .out3(decoder_2_out3),
    .sel(register_9_q));
  Register #(.width(32), .trigger("rising"), .Select("low")) register_10 (
    .D(Data2), .en(update), .Q(Led2), .clk(CLK), .clr(RST));
  Register #(.width(32), .trigger("rising"), .Select("low")) register_11 (
    .D(Data6), .en(update), .Q(Led6), .clk(CLK), .clr(RST));
  Register #(.width(32), .trigger("rising"), .Select("low")) register_12 (
    .D(Data10), .en(update), .Q(Led10), .clk(CLK), .clr(RST));
  Register #(.width(32), .trigger("rising"), .Select("low")) register_13 (
    .D(Data14), .en(update), .Q(Led14), .clk(CLK), .clr(RST));
  ALU alu_1 (
    .X(R1_Data), .Y(multiplexer_11_out), .AluOP(\单周期硬布线控制器_1_alu_op ), .Equal(alu_1_equal), .Result(ALU_Res),
    .out_6(alu_1_out_6));  // open: Result_2, out_4
  Shifter #(.width(32), .shift("ll")) shifter_1 (.in(multiplexer_10_out), .\dist (5'b00001), .out(shifter_1_out));
  Shifter #(.width(32), .shift("ll")) shifter_2 (.in(MDin), .\dist (multiplier_1_out), .out(shifter_2_out));
  and and_8 (and_8_out, blt, alu_1_out_6);
  and and_9 (and_9_out, alu_1_equal, \单周期硬布线控制器_1_beq );
  and and_10 (and_10_out, ~alu_1_equal, \单周期硬布线控制器_1_bne );  // AND_Gate
  Multiplexer #(.select(1), .width(32), .disabled("Z"), .enable("false")) multiplexer_13 (
    .in0(MemData), .in1(random_Num), .out(multiplexer_13_out), .sel(random));
  Adder #(.width(32)) adder_2 (.a(PC), .b(shifter_1_out), .out(adder_2_out));  // open: cin, cout
  Multiplexer #(.select(1), .width(32), .disabled("Z"), .enable("false")) multiplexer_14 (
    .in0(MDin), .in1(shifter_2_out), .out(MemData), .sel(sb));
  and and_11 (Clr_UP, decoder_2_out0, URET);
  and and_12 (Clr_DOWN, decoder_2_out1, URET);
  and and_13 (Clr_LEFT, decoder_2_out2, URET);
  and and_14 (Clr_RIGHT, decoder_2_out3, URET);
  Register #(.width(32), .trigger("rising"), .Select("low")) register_14 (
    .D(Data3), .en(update), .Q(Led3), .clk(CLK), .clr(RST));
  Register #(.width(32), .trigger("rising"), .Select("low")) register_15 (
    .D(Data7), .en(update), .Q(Led7), .clk(CLK), .clr(RST));
  Register #(.width(32), .trigger("rising"), .Select("low")) register_16 (
    .D(Data11), .en(update), .Q(Led11), .clk(CLK), .clr(RST));
  Register #(.width(32), .trigger("rising"), .Select("low")) register_17 (
    .D(Data15), .en(update), .Q(Led15), .clk(CLK), .clr(RST));
  or or_10 (Branch, and_8_out, and_9_out, and_10_out);
  Multiplexer #(.select(1), .width(10), .disabled(0), .enable("false")) multiplexer_15 (
    .in0(ALU_Res[11:2]), .in1(bit_extender_7_out), .out(multiplexer_15_out), .sel(random));
  assign bit_extender_7_out = {{6{1'b0}}, random_Adr};  // Bit_Extender bit_extender_7
  or or_11 (or_11_out, random, MemWrite);
  Multiplexer #(.select(2), .width(32), .disabled("Z"), .enable("false")) multiplexer_16 (
    .in0(32'h3014), .in1(32'h310c), .in2(32'h3204), .in3(32'h32fc), .out(INT_Addar), .sel(\中断号 ));
  // cs3410_MIPS_RAM mips_ram_1: pin names not known; wires that end beside it: multiplexer_15_out, multiplexer_13_out, or_11_out, RAM_Sel, CLK, RST, mips_ram_1_p7
  Multiplexer #(.select(1), .width(32), .disabled("Z"), .enable("false")) multiplexer_17 (
    .in0(ALU_Res), .in1(mips_ram_1_p7), .out(multiplexer_17_out), .sel(\单周期硬布线控制器_1_memtoreg ));
  \游戏结束信号产生  \u_游戏结束信号产生_1  (
    .Led0(Led0), .Led1(Led1), .Led2(Led2), .Led3(Led3), .Led4(Led4), .Led5(Led5), .Led6(Led6), .Led7(Led7),
    .Led8(Led8), .Led9(Led9), .Led10(Led10), .Led11(Led11), .Led12(Led12), .Led13(Led13), .Led14(Led14),
    .Led15(Led15), .Win(Win), .Lost(Lost));
  or or_12 (or_12_out, J_signal, Jalr_signal);
  Multiplexer #(.select(1), .width(32), .disabled("Z"), .enable("false")) multiplexer_18 (
    .in0(multiplexer_17_out), .in1(PC_4), .out(RDin), .sel(or_12_out));
  Register #(.width(32), .trigger("falling"), .Select("low")) EPC (
    .D(Break_PC), .en(INT), .Q(RET_PC), .clk(CLK), .clr(RST));
  \随机数生成  \u_随机数生成_1  (
    .Data0(Data0), .Data1(Data1), .Data2(Data2), .Data3(Data3), .Data4(Data4), .Data5(Data5), .Data6(Data6),
    .Data7(Data7), .Data8(Data8), .Data9(Data9), .Data10(Data10), .Data11(Data11), .Data12(Data12),
    .Data13(Data13), .Data14(Data14), .Data15(Data15), .CLK(CLK), .random_Adr(random_Adr),
    .random_Num(random_Num));

  // Other names for the same wires on the sheet: Bit_Sel[1:0] = ALU_Res[1:0]

  // Notes on the sheet:
  //   中断源
  //   中断等待指示
  //   总复位信号应将除ROM以外所有存储组件全部清零
  //   戳工具选中键盘→
  //   键盘输入WASD进行游戏
  //   数码管输出
  //   数码管输出应该用寄存器锁存，否则显示数据只能一闪而过
  //   为方便自动评测，需要输出PC，IR，寄存器堆写如数据RDin
  //   RAM写使能MemWrite、RAM写入数据MDin等信号
  //   控制位
  //   暂停节拍，不能为0
  //   进行的操作是无效的
  //   戳工具置1进入计数暂停模式，ctrl+k时钟自动运行到对应节拍暂停
  //   ctrl+k关闭时钟连续运行，将控制位置零，进入单步调试模式调试
  //   用这个时钟源需要去掉电路中的其他时钟源
  //   左方红灯亮起时
  //   可计数暂停的时钟源
  //   WIN
  //   GAME OVER
  //   生成立即数选择信号
  //   存储需要更新的数据
  //   中断控制逻辑
  //   指令存储器
  //   指令探针
  //   contents of rom_1 (hex, n*v repeats v):
  //   2200893 73 2c00893 73 6f 293 1000313 393 2a403 102a483 202a903 302a983 41a63 49863 91663 99463
  //   a00006f 91a63 98863 98913 993 100393 49c63 90a63 90493 98913 993 100393 41e63 48c63 48413 90493
  //   98913 993 100393 941c63 940433 90493 98913 993 100393 1249c63 2048463 12484b3 98913 993 100393
  //   1391a63 90863 1390933 993 100393 82a023 92a823 322a023 332a823 428293 f2629ee3 100e13 1c39e63
  //   2c00893 73 2200893 73 2c00893 73 200073 293 1000313 393 2a983 102a903 202a483 302a403 41a63 49863
  //   91663 99463 a00006f 91a63 98863 98913 993 100393 49c63 90a63 90493 98913 993 100393 41e63 48c63
  //   48413 90493 98913 993 100393 941c63 940433 90493 98913 993 100393 1249c63 2048463 12484b3 98913 993
  //   100393 1391a63 90863 1390933 993 100393 132a023 122a823 292a023 282a823 428293 f2629ee3 100e13
  //   1c39e63 2c00893 73 2200893 73 2c00893 73 200073 293 4000313 393 2a403 42a483 82a903 c2a983 41a63
  //   49863 91663 99463 a00006f 91a63 98863 98913 993 100393 49c63 90a63 90493 98913 993 100393 41e63
  //   48c63 48413 90493 98913 993 100393 941c63 940433 90493 98913 993 100393 1249c63 2048463 12484b3
  //   98913 993 100393 1391a63 90863 1390933 993 100393 82a023 92a223 122a423 132a623 1028293 f2629ee3
  //   100e13 1c39e63 2c00893 73 2200893 73 2c00893 73 200073 293 4000313 393 2a983 42a903 82a483 c2a403
  //   41a63 49863 91663 99463 a00006f 91a63 98863 98913 993 100393 49c63 90a63 90493 98913 993 100393
  //   41e63 48c63 48413 90493 98913 993 100393 941c63 940433 90493 98913 993 100393 1249c63 2048463
  //   12484b3 98913 993 100393 1391a63 90863 1390933 993 100393 132a023 122a223 92a423 82a623 1028293
  //   f2629ee3 100e13 1c39e63 2c00893 73 2200893 73 2c00893 73 200073
  //   I型指令立即数
  //   S型指令立即数
  //   B型指令立即数
  //   J型指令立即数
  //   rs1
  //   rs2
  //   指令字
  //   rd
  //   生成停机信号halt和update/random信号
  //   JAL
  //   JALR
  //   URET
  //   Sltiu
  //   Sb
  //   中断使能信号产生
  //   中断请求信号产生
  //   Beq
  //   Bne
  //   MemToReg
  //   MemWrite
  //   AluOP
  //   AluSrcB
  //   RegWrite
  //   Blt
  //   存储LED显示数据
  //   中断清零信号产生
  //   计算Sb对应的MemData
  //   中断入口逻辑
  //   数据存储器
  //   CPU模块
  //   生成随机地址和随机数
  //   保护现场
endmodule

module \LED译码器  (
  input  [31:0] Num,
  output [31:0] col8,
  output [31:0] col16,
  output [31:0] col24,
  output [31:0] col0,
  output [31:0] col9,
  output [31:0] col17,
  output [31:0] col25,
  output [31:0] col1,
  output [31:0] col10,
  output [31:0] col18,
  output [31:0] col26,
  output [31:0] col2,
  output [31:0] col11,
  output [31:0] col19,
  output [31:0] col27,
  output [31:0] col3,
  output [31:0] col12,
  output [31:0] col20,
  output [31:0] col28,
  output [31:0] col4,
  output [31:0] col13,
  output [31:0] col21,
  output [31:0] col29,
  output [31:0] col5,
  output [31:0] col14,
  output [31:0] col22,
  output [31:0] col30,
  output [31:0] col6,
  output [31:0] col15,
  output [31:0] col23,
  output [31:0] col31,
  output [31:0] col7
);

  wire comparator_1_eq, comparator_2_eq, comparator_3_eq, comparator_4_eq, comparator_5_eq, comparator_6_eq,
       comparator_7_eq, comparator_8_eq, comparator_9_eq, comparator_10_eq, comparator_11_eq,
       comparator_12_eq;
  wire [7:0] Addr;

  Comparator #(.width(32), .mode("twosComplement")) comparator_1 (
    .a(Num), .b(32'h2), .eq(comparator_1_eq));  // open: gt, lt
  Comparator #(.width(32), .mode("twosComplement")) comparator_2 (
    .a(Num), .b(32'h4), .eq(comparator_2_eq));  // open: gt, lt
  Comparator #(.width(32), .mode("twosComplement")) comparator_3 (
    .a(Num), .b(32'h8), .eq(comparator_3_eq));  // open: gt, lt
  Comparator #(.width(32), .mode("twosComplement")) comparator_4 (
    .a(Num), .b(32'h10), .eq(comparator_4_eq));  // open: gt, lt
  Comparator #(.width(32), .mode("twosComplement")) comparator_5 (
    .a(Num), .b(32'h20), .eq(comparator_5_eq));  // open: gt, lt
  Comparator #(.width(32), .mode("twosComplement")) comparator_6 (
    .a(Num), .b(32'h40), .eq(comparator_6_eq));  // open: gt, lt
  Comparator #(.width(32), .mode("twosComplement")) comparator_7 (
    .a(Num), .b(32'h80), .eq(comparator_7_eq));  // open: gt, lt
  Comparator #(.width(32), .mode("twosComplement")) comparator_8 (
    .a(Num), .b(32'h100), .eq(comparator_8_eq));  // open: gt, lt
  Comparator #(.width(32), .mode("twosComplement")) comparator_9 (
    .a(Num), .b(32'h200), .eq(comparator_9_eq));  // open: gt, lt
  Comparator #(.width(32), .mode("twosComplement")) comparator_10 (
    .a(Num), .b(32'h400), .eq(comparator_10_eq));  // open: gt, lt
  Comparator #(.width(32), .mode("twosComplement")) comparator_11 (
    .a(Num), .b(32'h800), .eq(comparator_11_eq));  // open: gt, lt
  Comparator #(.width(32), .mode("twosComplement")) comparator_12 (
    .a(Num), .b({32{1'b0}}), .eq(comparator_12_eq));  // open: gt, lt
  // Probe on Addr
  assign Addr = comparator_1_eq ? {8{1'b0}} : 8'bz;  // Controlled_Buffer controlled_buffer_1
  assign Addr = comparator_2_eq ? 8'h1 : 8'bz;  // Controlled_Buffer controlled_buffer_2
  assign Addr = comparator_3_eq ? 8'h2 : 8'bz;  // Controlled_Buffer controlled_buffer_3
  assign Addr = comparator_4_eq ? 8'h3 : 8'bz;  // Controlled_Buffer controlled_buffer_4
  assign Addr = comparator_5_eq ? 8'h4 : 8'bz;  // Controlled_Buffer controlled_buffer_5
  assign Addr = comparator_6_eq ? 8'h5 : 8'bz;  // Controlled_Buffer controlled_buffer_6
  assign Addr = comparator_7_eq ? 8'h6 : 8'bz;  // Controlled_Buffer controlled_buffer_7
  assign Addr = comparator_8_eq ? 8'h7 : 8'bz;  // Controlled_Buffer controlled_buffer_8
  assign Addr = comparator_9_eq ? 8'h8 : 8'bz;  // Controlled_Buffer controlled_buffer_9
  assign Addr = comparator_10_eq ? 8'h9 : 8'bz;  // Controlled_Buffer controlled_buffer_10
  assign Addr = comparator_11_eq ? 8'ha : 8'bz;  // Controlled_Buffer controlled_buffer_11
  assign Addr = comparator_12_eq ? 8'hb : 8'bz;  // Controlled_Buffer controlled_buffer_12
  ROM #(.addrWidth(8), .dataWidth(32), .Select("low")) u_col0 (.addr(Addr), .data(col0));
  ROM #(.addrWidth(8), .dataWidth(32), .Select("low")) u_col1 (.addr(Addr), .data(col1));
  ROM #(.addrWidth(8), .dataWidth(32), .Select("low")) u_col2 (.addr(Addr), .data(col2));
  ROM #(.addrWidth(8), .dataWidth(32), .Select("low")) u_col3 (.addr(Addr), .data(col3));
  ROM #(.addrWidth(8), .dataWidth(32), .Select("low")) u_col4 (.addr(Addr), .data(col4));
  ROM #(.addrWidth(8), .dataWidth(32), .Select("low")) u_col5 (.addr(Addr), .data(col5));
  ROM #(.addrWidth(8), .dataWidth(32), .Select("low")) u_col6 (.addr(Addr), .data(col6));
  ROM #(.addrWidth(8), .dataWidth(32), .Select("low")) u_col7 (.addr(Addr), .data(col7));
  ROM #(.addrWidth(8), .dataWidth(32), .Select("low")) u_col8 (.addr(Addr), .data(col8));
  ROM #(.addrWidth(8), .dataWidth(32), .Select("low")) u_col9 (.addr(Addr), .data(col9));
  ROM #(.addrWidth(8), .dataWidth(32), .Select("low")) u_col10 (.addr(Addr), .data(col10));
  ROM #(.addrWidth(8), .dataWidth(32), .Select("low")) u_col11 (.addr(Addr), .data(col11));
  ROM #(.addrWidth(8), .dataWidth(32), .Select("low")) u_col12 (.addr(Addr), .data(col12));
  ROM #(.addrWidth(8), .dataWidth(32), .Select("low")) co13 (.addr(Addr), .data(col13));
  ROM #(.addrWidth(8), .dataWidth(32), .Select("low")) u_col14 (.addr(Addr), .data(col14));
  ROM #(.addrWidth(8), .dataWidth(32), .Select("low")) u_col15 (.addr(Addr), .data(col15));
  ROM #(.addrWidth(8), .dataWidth(32), .Select("low")) u_col16 (.addr(Addr), .data(col16));
  ROM #(.addrWidth(8), .dataWidth(32), .Select("low")) u_col17 (.addr(Addr), .data(col17));
  ROM #(.addrWidth(8), .dataWidth(32), .Select("low")) u_col18 (.addr(Addr), .data(col18));
  ROM #(.addrWidth(8), .dataWidth(32), .Select("low")) u_col19 (.addr(Addr), .data(col19));
  ROM #(.addrWidth(8), .dataWidth(32), .Select("low")) u_col20 (.addr(Addr), .data(col20));
  ROM #(.addrWidth(8), .dataWidth(32), .Select("low")) u_col21 (.addr(Addr), .data(col21));
  ROM #(.addrWidth(8), .dataWidth(32), .Select("low")) u_col22 (.addr(Addr), .data(col22));
  ROM #(.addrWidth(8), .dataWidth(32), .Select("low")) u_col23 (.addr(Addr), .data(col23));
  ROM #(.addrWidth(8), .dataWidth(32), .Select("low")) u_col24 (.addr(Addr), .data(col24));
  ROM #(.addrWidth(8), .dataWidth(32), .Select("low")) u_col25 (.addr(Addr), .data(col25));
  ROM #(.addrWidth(8), .dataWidth(32), .Select("low")) u_col26 (.addr(Addr), .data(col26));
  ROM #(.addrWidth(8), .dataWidth(32), .Select("low")) u_col27 (.addr(Addr), .data(col27));
  ROM #(.addrWidth(8), .dataWidth(32), .Select("low")) u_col28 (.addr(Addr), .data(col28));
  ROM #(.addrWidth(8), .dataWidth(32), .Select("low")) u_col29 (.addr(Addr), .data(col29));
  ROM #(.addrWidth(8), .dataWidth(32), .Select("low")) u_col30 (.addr(Addr), .data(col30));
  ROM #(.addrWidth(8), .dataWidth(32), .Select("low")) u_col31 (.addr(Addr), .data(col31));

  // Notes on the sheet:
  //   数字转地址信号
  //   contents of col1 (hex, n*v repeats v):
  //   5*0 f00 0 0 0 80400 e0c00
  //   contents of col2 (hex, n*v repeats v):
  //   4*0 7003c0 1fff00 0 180600 1800 80400 101400
  //   contents of col3 (hex, n*v repeats v):
  //   4*0 1f003e0 7fffc0 200200 3c0a00 7f1c00 1ffc00 102400
  //   contents of col4 (hex, n*v repeats v):
  //   0 0 0 800010 13001a0 e0c1e0 200200 401200 430200 400 104400
  //   contents of col5 (hex, n*v repeats v):
  //   0 0 0 800010 2000010 1818060 7ffe00 402200 420200 400 108400
  //   contents of col6 (hex, n*v repeats v):
  //   0 0 0 800030 2008010 3030030 7ffe00 404200 420200 0 f0c00
  //   contents of col7 (hex, n*v repeats v):
  //   0 0 0 1fffff0 2008010 2020010 200 618200 430600
  //   contents of col8 (hex, n*v repeats v):
  //   0 0 0 3fffff0 2008010 2020010 200 3f0600 41fc00 7f000
  //   contents of col9 (hex, n*v repeats v):
  //   0 c00 700 30 301c030 2020010 0 1c0c00 40f800 80800 7f000
  //   contents of col10 (hex, n*v repeats v):
  //   780070 3c00 7c1fc0 10 1874030 3030030 0 0 0 100400 80800
  //   contents of col11 (hex, n*v repeats v):
  //   f801f0 6400 1fe38e0 10 1fe79e0 3c38060 0 0 0 100400 100400
  //   contents of col12 (hex, n*v repeats v):
  //   1980330 1c400 1876020 10 7c3fc0 1c1ffc0 180600 1800 0 80800 100400
  //   contents of co13 (hex, n*v repeats v):
  //   3000630 30400 303c030 0 1f80 7f80 3c0a00 7f1c00 200200 7f000 80800
  //   contents of col14 (hex, n*v repeats v):
  //   2000c30 c0410 2038010 0 0 0 401200 430200 200200 0 7f000
  //   contents of col15 (hex, n*v repeats v):
  //   2001830 380410 2018010 0 0 0 402200 420200 7ffe00
  //   contents of col16 (hex, n*v repeats v):
  //   2003030 600410 201c010 0 0 0 404200 420200 7ffe00 e0c00
  //   contents of col17 (hex, n*v repeats v):
  //   2006030 1fffff0 201e010 f00 0 c00 618200 430600 200 101400 6000
  //   contents of col18 (hex, n*v repeats v):
  //   301c030 3fffff0 301e030 1fff00 780070 3c00 3f0600 41fc00 200 102400 1a000
  //   contents of col19 (hex, n*v repeats v):
  //   1ef8030 3fffff0 1877860 7fffc0 f801f0 6400 1c0c00 40f800 0 104400 22400
  //   contents of col20 (hex, n*v repeats v):
  //   ff0070 410 fe3fc0 e0c1e0 1980330 1c400 0 0 0 108400 c2400
  //   contents of col21 (hex, n*v repeats v):
  //   7c01e0 410 781f80 1818060 3000630 30400 0 0 0 f0c00 1ffc00
  //   contents of col22 (hex, n*v repeats v):
  //   0 0 0 3030030 2000c30 c0410 1c7800 ff800 180600 0 2400
  //   contents of col23 (hex, n*v repeats v):
  //   0 0 0 2020010 2001830 380410 36c400 1ffc00 3c0a00 0 2400
  //   contents of col24 (hex, n*v repeats v):
  //   0 0 0 2020010 2003030 600410 430200 210600 401200 6000
  //   contents of col25 (hex, n*v repeats v):
  //   0 0 0 2020010 2006030 1fffff0 410200 420200 402200 1a000 e3800
  //   contents of col26 (hex, n*v repeats v):
  //   0 0 0 3030030 301c030 3fffff0 418200 420200 404200 22400 114400
  //   contents of col27 (hex, n*v repeats v):
  //   0 0 0 3c38060 1ef8030 3fffff0 61c600 420200 618200 c2400 108400
  //   contents of col28 (hex, n*v repeats v):
  //   0 0 0 1c1ffc0 ff0070 410 3eec00 738c00 3f0600 1ffc00 108400
  //   contents of col29 (hex, n*v repeats v):
  //   0 0 0 7f80 7c01e0 410 1c3800 f800 1c0c00 2400 114400
  //   contents of col30 (hex, n*v repeats v):
  //   9*0 2400 e3800
endmodule

module \_16格数据存储  (
  input  CLK,
  input  [31:0] Din,
  input  RST,
  input  MenWrite,
  input  [3:0] Byte_Adr,
  output [31:0] Data0,
  output [31:0] Data1,
  output [31:0] Data2,
  output [31:0] Data3,
  output [31:0] Data4,
  output [31:0] Data5,
  output [31:0] Data6,
  output [31:0] Data7,
  output [31:0] Data8,
  output [31:0] Data9,
  output [31:0] Data10,
  output [31:0] Data11,
  output [31:0] Data12,
  output [31:0] Data13,
  output [31:0] Data14,
  output [31:0] Data15
);

  wire decoder_1_out0, decoder_1_out1, decoder_1_out2, decoder_1_out3, decoder_1_out4, decoder_1_out5,
       decoder_1_out6, decoder_1_out7, decoder_1_out8, decoder_1_out9, decoder_1_out10, decoder_1_out11,
       decoder_1_out12, decoder_1_out13, decoder_1_out14, decoder_1_out15;

  Decoder #(.select(4), .tristate("false"), .disabled(0), .enable("true")) decoder_1 (
    .out0(decoder_1_out0), .out1(decoder_1_out1), .out2(decoder_1_out2), .out3(decoder_1_out3),
    .out4(decoder_1_out4), .out5(decoder_1_out5), .out6(decoder_1_out6), .out7(decoder_1_out7),
    .out8(decoder_1_out8), .out9(decoder_1_out9), .out10(decoder_1_out10), .out11(decoder_1_out11),
    .out12(decoder_1_out12), .out13(decoder_1_out13), .out14(decoder_1_out14), .out15(decoder_1_out15),
    .sel(Byte_Adr), .en(MenWrite));
  // cs3410_MIPS_RAM mips_ram_1: pin names not known; wires that end beside it: {10{1'b0}}, Din, decoder_1_out0, CLK, RST, Data0, {10{1'b0}}, Din
  // cs3410_MIPS_RAM mips_ram_2: pin names not known; wires that end beside it: {10{1'b0}}, Din, decoder_1_out4, CLK, RST, Data4
  // cs3410_MIPS_RAM mips_ram_3: pin names not known; wires that end beside it: {10{1'b0}}, Din, decoder_1_out8, CLK, RST, Data8
  // cs3410_MIPS_RAM mips_ram_4: pin names not known; wires that end beside it: {10{1'b0}}, Din, decoder_1_out12, CLK, RST, Data12
  // cs3410_MIPS_RAM mips_ram_5: pin names not known; wires that end beside it: decoder_1_out1, CLK, RST, Data1
  // cs3410_MIPS_RAM mips_ram_6: pin names not known; wires that end beside it: {10{1'b0}}, Din, decoder_1_out5, CLK, RST, Data5
  // cs3410_MIPS_RAM mips_ram_7: pin names not known; wires that end beside it: {10{1'b0}}, Din, decoder_1_out9, CLK, RST, Data9
  // cs3410_MIPS_RAM mips_ram_8: pin names not known; wires that end beside it: {10{1'b0}}, Din, decoder_1_out13, CLK, RST, Data13
  // cs3410_MIPS_RAM mips_ram_9: pin names not known; wires that end beside it: {10{1'b0}}, Din, decoder_1_out2, CLK, RST, Data2
  // cs3410_MIPS_RAM mips_ram_10: pin names not known; wires that end beside it: {10{1'b0}}, Din, decoder_1_out6, CLK, RST, Data6
  // cs3410_MIPS_RAM mips_ram_11: pin names not known; wires that end beside it: {10{1'b0}}, Din, decoder_1_out10, CLK, RST, Data10
  // cs3410_MIPS_RAM mips_ram_12: pin names not known; wires that end beside it: {10{1'b0}}, Din, decoder_1_out14, CLK, RST, Data14
  // cs3410_MIPS_RAM mips_ram_13: pin names not known; wires that end beside it: {10{1'b0}}, Din, decoder_1_out3, CLK, RST, Data3
  // cs3410_MIPS_RAM mips_ram_14: pin names not known; wires that end beside it: {10{1'b0}}, Din, decoder_1_out7, CLK, RST, Data7
  // cs3410_MIPS_RAM mips_ram_15: pin names not known; wires that end beside it: {10{1'b0}}, Din, decoder_1_out11, CLK, RST, Data11
  // cs3410_MIPS_RAM mips_ram_16: pin names not known; wires that end beside it: {10{1'b0}}, Din, decoder_1_out15, CLK, RST, Data15
endmodule

module \按键中断控制器  (
  input  UP,
  input  Clr_UP,
  input  DOWN,
  input  Clr_DOWN,
  input  LEFT,
  input  Clr_LEFT,
  input  RIGHT,
  input  Clr_RIGHT,
  input  CLK,
  input  RST,
  output UP_2,
  output [1:0] \中断号 ,
  output \中断请求 ,
  output DOWN_2,
  output LEFT_2,
  output RIGHT_2
);

  wire and_1_out, and_2_out, and_3_out, and_4_out, not_1_out, not_2_out, not_3_out, not_4_out, not_5_out,
       or_1_out, or_2_out, or_3_out, or_4_out, or_6_out, or_8_out, or_10_out, or_12_out, register_1_q,
       register_2_q, register_3_q, register_4_q, register_5_q, register_6_q, register_7_q, register_8_q;

  Register #(.width(1), .trigger("rising"), .Select("low")) register_1 (
    .D(1'b1), .en(not_5_out), .Q(register_1_q), .clk(UP), .clr(or_1_out));
  or or_1 (or_1_out, register_5_q, RST);
  Register #(.width(1), .trigger("rising"), .Select("low")) register_2 (
    .D(1'b1), .en(not_5_out), .Q(register_2_q), .clk(DOWN), .clr(or_2_out));
  or or_2 (or_2_out, register_6_q, RST);
  Register #(.width(1), .trigger("rising"), .Select("low")) register_3 (
    .D(1'b1), .en(not_5_out), .Q(register_3_q), .clk(LEFT), .clr(or_3_out));
  or or_3 (or_3_out, register_7_q, RST);
  Register #(.width(1), .trigger("rising"), .Select("low")) register_4 (
    .D(1'b1), .en(not_5_out), .Q(register_4_q), .clk(RIGHT), .clr(or_4_out));
  or or_4 (or_4_out, register_8_q, RST);
  or or_5 (UP_2, register_1_q, register_5_q);
  or or_6 (or_6_out, register_1_q, register_5_q);
  not not_1 (not_1_out, Clr_UP);
  or or_7 (DOWN_2, register_2_q, register_6_q);
  or or_8 (or_8_out, register_2_q, register_6_q);
  not not_2 (not_2_out, Clr_DOWN);
  or or_9 (LEFT_2, register_3_q, register_7_q);
  or or_10 (or_10_out, register_3_q, register_7_q);
  not not_3 (not_3_out, Clr_LEFT);
  or or_11 (RIGHT_2, register_4_q, register_8_q);
  or or_12 (or_12_out, register_4_q, register_8_q);
  not not_4 (not_4_out, Clr_RIGHT);
  and and_1 (and_1_out, or_6_out, not_1_out);
  and and_2 (and_2_out, or_8_out, not_2_out);
  and and_3 (and_3_out, or_10_out, not_3_out);
  and and_4 (and_4_out, or_12_out, not_4_out);
  Register #(.width(1), .trigger("rising"), .Select("low")) register_5 (
    .D(and_1_out), .Q(register_5_q), .clk(CLK), .clr(RST));  // open: en
  Register #(.width(1), .trigger("rising"), .Select("low")) register_6 (
    .D(and_2_out), .Q(register_6_q), .clk(CLK), .clr(RST));  // open: en
  Register #(.width(1), .trigger("rising"), .Select("low")) register_7 (
    .D(and_3_out), .Q(register_7_q), .clk(CLK), .clr(RST));  // open: en
  Register #(.width(1), .trigger("rising"), .Select("low")) register_8 (
    .D(and_4_out), .Q(register_8_q), .clk(CLK), .clr(RST));  // open: en
  Priority_Encoder #(.select(2), .disabled(0)) priority_encoder_1 (
    .in0(register_5_q), .in1(register_6_q), .in2(register_7_q), .in3(register_8_q), .out(\中断号 ));  // open: gs, en_out, en_in
  or or_13 (\中断请求 , register_5_q, register_6_q, register_7_q, register_8_q);
  not not_5 (not_5_out, \中断请求 );
endmodule

module \随机数生成  (
  input  [31:0] Data0,
  input  [31:0] Data1,
  input  [31:0] Data2,
  input  [31:0] Data3,
  input  [31:0] Data4,
  input  [31:0] Data5,
  input  [31:0] Data6,
  input  [31:0] Data7,
  input  [31:0] Data8,
  input  [31:0] Data9,
  input  [31:0] Data10,
  input  [31:0] Data11,
  input  [31:0] Data12,
  input  [31:0] Data13,
  input  [31:0] Data14,
  input  [31:0] Data15,
  input  CLK,
  output [3:0] random_Adr,
  output [31:0] random_Num
);

  wire and_1_out, and_2_out, and_3_out, and_4_out, and_5_out, and_6_out, and_7_out, and_8_out, and_9_out,
       and_10_out, and_11_out, and_12_out, and_13_out, comparator_1_eq, comparator_2_eq, comparator_3_eq,
       comparator_4_eq, comparator_5_eq, comparator_6_eq, comparator_7_eq, comparator_8_eq, comparator_9_eq,
       comparator_10_eq, comparator_11_eq, comparator_12_eq, comparator_13_eq, comparator_14_eq,
       comparator_15_eq, comparator_16_eq, comparator_17_lt, multiplexer_1_out, multiplexer_2_out,
       multiplexer_3_out, multiplexer_4_out, multiplexer_5_out, multiplexer_6_out, multiplexer_7_out,
       multiplexer_8_out, multiplexer_17_out, multiplexer_18_out, multiplexer_19_out, multiplexer_20_out,
       multiplexer_25_out, multiplexer_26_out, multiplexer_29_out, nand_1_out, nand_2_out, nor_1_out,
       nor_2_out, nor_3_out, nor_4_out, nor_5_out, nor_6_out, nor_7_out, nor_8_out, nor_9_out, nor_10_out,
       nor_11_out, nor_12_out, nor_13_out, nor_14_out, not_1_out, random_1_out, random_2_out, random_3_out,
       random_4_out, random_5_out, random_6_out, random_7_out, random_8_out, random_9_out, random_10_out,
       random_11_out, random_12_out, random_13_out, random_14_out, random_15_out;
  wire [3:0] multiplexer_9_out, multiplexer_10_out, multiplexer_11_out, multiplexer_12_out,
       multiplexer_13_out, multiplexer_14_out, multiplexer_15_out, multiplexer_16_out, multiplexer_21_out,
       multiplexer_22_out, multiplexer_23_out, multiplexer_24_out, multiplexer_27_out, multiplexer_28_out,
       random_16_out;

  Comparator #(.width(32), .mode("twosComplement")) comparator_1 (
    .a(Data0), .b({32{1'b0}}), .eq(comparator_1_eq));  // open: gt, lt
  Comparator #(.width(32), .mode("twosComplement")) comparator_2 (
    .a(Data1), .b({32{1'b0}}), .eq(comparator_2_eq));  // open: gt, lt
  Comparator #(.width(32), .mode("twosComplement")) comparator_3 (
    .a(Data2), .b({32{1'b0}}), .eq(comparator_3_eq));  // open: gt, lt
  Comparator #(.width(32), .mode("twosComplement")) comparator_4 (
    .a(Data3), .b({32{1'b0}}), .eq(comparator_4_eq));  // open: gt, lt
  Comparator #(.width(32), .mode("twosComplement")) comparator_5 (
    .a(Data4), .b({32{1'b0}}), .eq(comparator_5_eq));  // open: gt, lt
  Comparator #(.width(32), .mode("twosComplement")) comparator_6 (
    .a(Data5), .b({32{1'b0}}), .eq(comparator_6_eq));  // open: gt, lt
  Comparator #(.width(32), .mode("twosComplement")) comparator_7 (
    .a(Data6), .b({32{1'b0}}), .eq(comparator_7_eq));  // open: gt, lt
  Comparator #(.width(32), .mode("twosComplement")) comparator_8 (
    .a(Data7), .b({32{1'b0}}), .eq(comparator_8_eq));  // open: gt, lt
  Comparator #(.width(32), .mode("twosComplement")) comparator_9 (
    .a(Data8), .b({32{1'b0}}), .eq(comparator_9_eq));  // open: gt, lt
  Comparator #(.width(32), .mode("twosComplement")) comparator_10 (
    .a(Data9), .b({32{1'b0}}), .eq(comparator_10_eq));  // open: gt, lt
  Comparator #(.width(32), .mode("twosComplement")) comparator_11 (
    .a(Data10), .b({32{1'b0}}), .eq(comparator_11_eq));  // open: gt, lt
  Comparator #(.width(32), .mode("twosComplement")) comparator_12 (
    .a(Data11), .b({32{1'b0}}), .eq(comparator_12_eq));  // open: gt, lt
  Comparator #(.width(32), .mode("twosComplement")) comparator_13 (
    .a(Data12), .b({32{1'b0}}), .eq(comparator_13_eq));  // open: gt, lt
  Comparator #(.width(32), .mode("twosComplement")) comparator_14 (
    .a(Data13), .b({32{1'b0}}), .eq(comparator_14_eq));  // open: gt, lt
  Comparator #(.width(32), .mode("twosComplement")) comparator_15 (
    .a(Data14), .b({32{1'b0}}), .eq(comparator_15_eq));  // open: gt, lt
  Comparator #(.width(32), .mode("twosComplement")) comparator_16 (
    .a(Data15), .b({32{1'b0}}), .eq(comparator_16_eq));  // open: gt, lt
  and and_1 (and_1_out, comparator_1_eq, comparator_2_eq);
  Multiplexer #(.select(1), .width(1), .disabled("Z"), .enable("false")) multiplexer_1 (
    .in0(comparator_2_eq), .in1(random_1_out), .out(multiplexer_1_out), .sel(and_1_out));
  Random #(.width(1), .seed(0), .trigger("rising")) random_1 (.clk(CLK), .out(random_1_out));  // open: next, clr
  and and_2 (and_2_out, comparator_3_eq, comparator_4_eq);
  Multiplexer #(.select(1), .width(1), .disabled("Z"), .enable("false")) multiplexer_2 (
    .in0(comparator_4_eq), .in1(random_2_out), .out(multiplexer_2_out), .sel(and_2_out));
  Random #(.width(1), .seed(100), .trigger("rising")) random_2 (.clk(CLK), .out(random_2_out));  // open: next, clr
  and and_3 (and_3_out, comparator_5_eq, comparator_6_eq);
  Multiplexer #(.select(1), .width(1), .disabled("Z"), .enable("false")) multiplexer_3 (
    .in0(comparator_6_eq), .in1(random_3_out), .out(multiplexer_3_out), .sel(and_3_out));
  Random #(.width(1), .seed(2), .trigger("rising")) random_3 (.clk(CLK), .out(random_3_out));  // open: next, clr
  and and_4 (and_4_out, comparator_7_eq, comparator_8_eq);
  Multiplexer #(.select(1), .width(1), .disabled("Z"), .enable("false")) multiplexer_4 (
    .in0(comparator_8_eq), .in1(random_4_out), .out(multiplexer_4_out), .sel(and_4_out));
  Random #(.width(1), .seed(3), .trigger("rising")) random_4 (.clk(CLK), .out(random_4_out));  // open: next, clr
  and and_5 (and_5_out, comparator_9_eq, comparator_10_eq);
  Multiplexer #(.select(1), .width(1), .disabled("Z"), .enable("false")) multiplexer_5 (
    .in0(comparator_10_eq), .in1(random_5_out), .out(multiplexer_5_out), .sel(and_5_out));
  Random #(.width(1), .seed(4), .trigger("rising")) random_5 (.clk(CLK), .out(random_5_out));  // open: next, clr
  and and_6 (and_6_out, comparator_11_eq, comparator_12_eq);
  Multiplexer #(.select(1), .width(1), .disabled("Z"), .enable("false")) multiplexer_6 (
    .in0(comparator_12_eq), .in1(random_6_out), .out(multiplexer_6_out), .sel(and_6_out));
  Random #(.width(1), .seed(5), .trigger("rising")) random_6 (.clk(CLK), .out(random_6_out));  // open: next, clr
  and and_7 (and_7_out, comparator_13_eq, comparator_14_eq);
  Multiplexer #(.select(1), .width(1), .disabled("Z"), .enable("false")) multiplexer_7 (
    .in0(comparator_14_eq), .in1(random_7_out), .out(multiplexer_7_out), .sel(and_7_out));
  Random #(.width(1), .seed(6), .trigger("rising")) random_7 (.clk(CLK), .out(random_7_out));  // open: next, clr
  and and_8 (and_8_out, comparator_15_eq, comparator_16_eq);
  Multiplexer #(.select(1), .width(1), .disabled("Z"), .enable("false")) multiplexer_8 (
    .in0(comparator_16_eq), .in1(random_8_out), .out(multiplexer_8_out), .sel(and_8_out));
  Random #(.width(1), .seed(7), .trigger("rising")) random_8 (.clk(CLK), .out(random_8_out));  // open: next, clr
  Multiplexer #(.select(1), .width(4), .disabled(0), .enable("false")) multiplexer_9 (
    .in0(4'b0000), .in1(4'b0001), .out(multiplexer_9_out), .sel(multiplexer_1_out));
  Multiplexer #(.select(1), .width(4), .disabled(0), .enable("false")) multiplexer_10 (
    .in0(4'b0010), .in1(4'b0011), .out(multiplexer_10_out), .sel(multiplexer_2_out));
  Multiplexer #(.select(1), .width(4), .disabled(0), .enable("false")) multiplexer_11 (
    .in0(4'b0100), .in1(4'b0101), .out(multiplexer_11_out), .sel(multiplexer_3_out));
  Multiplexer #(.select(1), .width(4), .disabled(0), .enable("false")) multiplexer_12 (
    .in0(4'b0110), .in1(4'b0111), .out(multiplexer_12_out), .sel(multiplexer_4_out));
  Multiplexer #(.select(1), .width(4), .disabled(0), .enable("false")) multiplexer_13 (
    .in0(4'b1000), .in1(4'b1001), .out(multiplexer_13_out), .sel(multiplexer_5_out));
  Multiplexer #(.select(1), .width(4), .disabled(0), .enable("false")) multiplexer_14 (
    .in0(4'b1010), .in1(4'b1011), .out(multiplexer_14_out), .sel(multiplexer_6_out));
  Multiplexer #(.select(1), .width(4), .disabled(0), .enable("false")) multiplexer_15 (
    .in0(4'b1100), .in1(4'b1101), .out(multiplexer_15_out), .sel(multiplexer_7_out));
  Multiplexer #(.select(1), .width(4), .disabled(0), .enable("false")) multiplexer_16 (
    .in0(4'b1110), .in1(4'b1111), .out(multiplexer_16_out), .sel(multiplexer_8_out));
  nor nor_1 (nor_1_out, comparator_1_eq, comparator_2_eq);
  nor nor_2 (nor_2_out, comparator_3_eq, comparator_4_eq);
  nor nor_3 (nor_3_out, comparator_5_eq, comparator_6_eq);
  nor nor_4 (nor_4_out, comparator_7_eq, comparator_8_eq);
  nor nor_5 (nor_5_out, comparator_9_eq, comparator_10_eq);
  nor nor_6 (nor_6_out, comparator_11_eq, comparator_12_eq);
  nor nor_7 (nor_7_out, comparator_13_eq, comparator_14_eq);
  nor nor_8 (nor_8_out, comparator_15_eq, comparator_16_eq);
  nor nor_9 (nor_9_out, nor_1_out, nor_2_out);
  Multiplexer #(.select(1), .width(1), .disabled("Z"), .enable("false")) multiplexer_17 (
    .in0(nor_1_out), .in1(random_9_out), .out(multiplexer_17_out), .sel(nor_9_out));
  Random #(.width(1), .seed(8), .trigger("rising")) random_9 (.clk(CLK), .out(random_9_out));  // open: next, clr
  nor nor_10 (nor_10_out, nor_3_out, nor_4_out);
  Multiplexer #(.select(1), .width(1), .disabled("Z"), .enable("false")) multiplexer_18 (
    .in0(nor_3_out), .in1(random_10_out), .out(multiplexer_18_out), .sel(nor_10_out));
  Random #(.width(1), .seed(9), .trigger("rising")) random_10 (.clk(CLK), .out(random_10_out));  // open: next, clr
  nor nor_11 (nor_11_out, nor_5_out, nor_6_out);
  Multiplexer #(.select(1), .width(1), .disabled("Z"), .enable("false")) multiplexer_19 (
    .in0(nor_5_out), .in1(random_11_out), .out(multiplexer_19_out), .sel(nor_11_out));
  Random #(.width(1), .seed(10), .trigger("rising")) random_11 (.clk(CLK), .out(random_11_out));  // open: next, clr
  nor nor_12 (nor_12_out, nor_7_out, nor_8_out);
  Multiplexer #(.select(1), .width(1), .disabled("Z"), .enable("false")) multiplexer_20 (
    .in0(nor_7_out), .in1(random_12_out), .out(multiplexer_20_out), .sel(nor_12_out));
  Random #(.width(1), .seed(11), .trigger("rising")) random_12 (.clk(CLK), .out(random_12_out));  // open: next, clr
  and and_9 (and_9_out, nor_1_out, nor_2_out);
  Multiplexer #(.select(1), .width(4), .disabled(0), .enable("false")) multiplexer_21 (
    .in0(multiplexer_9_out), .in1(multiplexer_10_out), .out(multiplexer_21_out), .sel(multiplexer_17_out));
  and and_10 (and_10_out, nor_3_out, nor_4_out);
  Multiplexer #(.select(1), .width(4), .disabled(0), .enable("false")) multiplexer_22 (
    .in0(multiplexer_11_out), .in1(multiplexer_12_out), .out(multiplexer_22_out), .sel(multiplexer_18_out));
  and and_11 (and_11_out, nor_5_out, nor_6_out);
  Multiplexer #(.select(1), .width(4), .disabled(0), .enable("false")) multiplexer_23 (
    .in0(multiplexer_13_out), .in1(multiplexer_14_out), .out(multiplexer_23_out), .sel(multiplexer_19_out));
  and and_12 (and_12_out, nor_7_out, nor_8_out);
  Multiplexer #(.select(1), .width(4), .disabled(0), .enable("false")) multiplexer_24 (
    .in0(multiplexer_15_out), .in1(multiplexer_16_out), .out(multiplexer_24_out), .sel(multiplexer_20_out));
  nor nor_13 (nor_13_out, and_9_out, and_10_out);
  Random #(.width(1), .seed(12), .trigger("rising")) random_13 (.clk(CLK), .out(random_13_out));  // open: next, clr
  nor nor_14 (nor_14_out, and_11_out, and_12_out);
  Random #(.width(1), .seed(13), .trigger("rising")) random_14 (.clk(CLK), .out(random_14_out));  // open: next, clr
  Multiplexer #(.select(1), .width(1), .disabled("Z"), .enable("false")) multiplexer_25 (
    .in0(and_9_out), .in1(random_13_out), .out(multiplexer_25_out), .sel(nor_13_out));
  Multiplexer #(.select(1), .width(1), .disabled("Z"), .enable("false")) multiplexer_26 (
    .in0(and_11_out), .in1(random_14_out), .out(multiplexer_26_out), .sel(nor_14_out));
  nand nand_1 (nand_1_out, and_9_out, and_10_out);
  Multiplexer #(.select(1), .width(4), .disabled(0), .enable("false")) multiplexer_27 (
    .in0(multiplexer_21_out), .in1(multiplexer_22_out), .out(multiplexer_27_out), .sel(multiplexer_25_out));
  nand nand_2 (nand_2_out, and_11_out, and_12_out);
  Multiplexer #(.select(1), .width(4), .disabled(0), .enable("false")) multiplexer_28 (
    .in0(multiplexer_23_out), .in1(multiplexer_24_out), .out(multiplexer_28_out), .sel(multiplexer_26_out));
  and and_13 (and_13_out, nand_1_out, nand_2_out);
  not not_1 (not_1_out, nand_1_out);
  Random #(.width(1), .seed(14), .trigger("rising")) random_15 (.clk(CLK), .out(random_15_out));  // open: next, clr
  Multiplexer #(.select(1), .width(1), .disabled("Z"), .enable("false")) multiplexer_29 (
    .in0(not_1_out), .in1(random_15_out), .out(multiplexer_29_out), .sel(and_13_out));
  Random #(.width(4), .seed(999), .trigger("rising")) random_16 (.clk(CLK), .out(random_16_out));  // open: next, clr
  Multiplexer #(.select(1), .width(4), .disabled(0), .enable("false")) multiplexer_30 (
    .in0(multiplexer_27_out), .in1(multiplexer_28_out), .out(random_Adr), .sel(multiplexer_29_out));
  Comparator #(.width(4), .mode("unsigned")) comparator_17 (
    .a(random_16_out), .b(4'b1100), .lt(comparator_17_lt));  // open: gt, eq
  Multiplexer #(.select(1), .width(32), .disabled("Z"), .enable("false")) multiplexer_31 (
    .in0(32'h4), .in1(32'h2), .out(random_Num), .sel(comparator_17_lt));

  // Notes on the sheet:
  //   生成随机数的位置
  //   在空格处随机生成2、4
  //   25%生成4，75%生成2
endmodule

module \游戏结束信号产生  (
  input  [31:0] Led0,
  input  [31:0] Led1,
  input  [31:0] Led2,
  input  [31:0] Led3,
  input  [31:0] Led4,
  input  [31:0] Led5,
  input  [31:0] Led6,
  input  [31:0] Led7,
  input  [31:0] Led8,
  input  [31:0] Led9,
  input  [31:0] Led10,
  input  [31:0] Led11,
  input  [31:0] Led12,
  input  [31:0] Led13,
  input  [31:0] Led14,
  input  [31:0] Led15,
  output Win,
  output Lost
);

  wire comparator_1_eq, comparator_2_eq, comparator_3_eq, comparator_4_eq, comparator_5_eq, comparator_6_eq,
       comparator_7_eq, comparator_8_eq, comparator_9_eq, comparator_10_eq, comparator_11_eq,
       comparator_12_eq, comparator_13_eq, comparator_14_eq, comparator_15_eq, comparator_16_eq,
       comparator_17_eq, comparator_18_eq, comparator_19_eq, comparator_20_eq, comparator_21_eq,
       comparator_22_eq, comparator_23_eq, comparator_24_eq, comparator_25_eq, comparator_26_eq,
       comparator_27_eq, comparator_28_eq, comparator_29_eq, comparator_30_eq, comparator_31_eq,
       comparator_32_eq, comparator_33_eq, comparator_34_eq, comparator_35_eq, comparator_36_eq,
       comparator_37_eq, comparator_38_eq, comparator_39_eq, comparator_40_eq, comparator_41_eq,
       comparator_42_eq, comparator_43_eq, comparator_44_eq, comparator_45_eq, comparator_46_eq,
       comparator_47_eq, comparator_48_eq, comparator_49_eq, comparator_50_eq, comparator_51_eq,
       comparator_52_eq, comparator_53_eq, comparator_54_eq, comparator_55_eq, comparator_56_eq, nor_1_out,
       nor_2_out, nor_3_out;

  Comparator #(.width(32), .mode("twosComplement")) comparator_1 (
    .a(Led0), .b({32{1'b0}}), .eq(comparator_1_eq));  // open: gt, lt
  Comparator #(.width(32), .mode("twosComplement")) comparator_2 (
    .a(Led1), .b({32{1'b0}}), .eq(comparator_2_eq));  // open: gt, lt
  Comparator #(.width(32), .mode("twosComplement")) comparator_3 (
    .a(Led2), .b({32{1'b0}}), .eq(comparator_3_eq));  // open: gt, lt
  Comparator #(.width(32), .mode("twosComplement")) comparator_4 (
    .a(Led3), .b({32{1'b0}}), .eq(comparator_4_eq));  // open: gt, lt
  Comparator #(.width(32), .mode("twosComplement")) comparator_5 (
    .a(Led4), .b({32{1'b0}}), .eq(comparator_5_eq));  // open: gt, lt
  Comparator #(.width(32), .mode("twosComplement")) comparator_6 (
    .a(Led5), .b({32{1'b0}}), .eq(comparator_6_eq));  // open: gt, lt
  Comparator #(.width(32), .mode("twosComplement")) comparator_7 (
    .a(Led6), .b({32{1'b0}}), .eq(comparator_7_eq));  // open: gt, lt
  Comparator #(.width(32), .mode("twosComplement")) comparator_8 (
    .a(Led7), .b({32{1'b0}}), .eq(comparator_8_eq));  // open: gt, lt
  Comparator #(.width(32), .mode("twosComplement")) comparator_9 (
    .a(Led8), .b({32{1'b0}}), .eq(comparator_9_eq));  // open: gt, lt
  Comparator #(.width(32), .mode("twosComplement")) comparator_10 (
    .a(Led9), .b({32{1'b0}}), .eq(comparator_10_eq));  // open: gt, lt
  Comparator #(.width(32), .mode("twosComplement")) comparator_11 (
    .a(Led10), .b({32{1'b0}}), .eq(comparator_11_eq));  // open: gt, lt
  Comparator #(.width(32), .mode("twosComplement")) comparator_12 (
    .a(Led11), .b({32{1'b0}}), .eq(comparator_12_eq));  // open: gt, lt
  Comparator #(.width(32), .mode("twosComplement")) comparator_13 (
    .a(Led12), .b({32{1'b0}}), .eq(comparator_13_eq));  // open: gt, lt
  Comparator #(.width(32), .mode("twosComplement")) comparator_14 (
    .a(Led13), .b({32{1'b0}}), .eq(comparator_14_eq));  // open: gt, lt
  Comparator #(.width(32), .mode("twosComplement")) comparator_15 (
    .a(Led14), .b({32{1'b0}}), .eq(comparator_15_eq));  // open: gt, lt
  Comparator #(.width(32), .mode("twosComplement")) comparator_16 (
    .a(Led15), .b({32{1'b0}}), .eq(comparator_16_eq));  // open: gt, lt
  Comparator #(.width(32), .mode("twosComplement")) comparator_17 (
    .a(Led0), .b(Led1), .eq(comparator_17_eq));  // open: gt, lt
  Comparator #(.width(32), .mode("twosComplement")) comparator_18 (
    .a(Led1), .b(Led2), .eq(comparator_18_eq));  // open: gt, lt
  Comparator #(.width(32), .mode("twosComplement")) comparator_19 (
    .a(Led2), .b(Led3), .eq(comparator_19_eq));  // open: gt, lt
  Comparator #(.width(32), .mode("twosComplement")) comparator_20 (
    .a(Led4), .b(Led5), .eq(comparator_20_eq));  // open: gt, lt
  Comparator #(.width(32), .mode("twosComplement")) comparator_21 (
    .a(Led5), .b(Led6), .eq(comparator_21_eq));  // open: gt, lt
  Comparator #(.width(32), .mode("twosComplement")) comparator_22 (
    .a(Led6), .b(Led7), .eq(comparator_22_eq));  // open: gt, lt
  Comparator #(.width(32), .mode("twosComplement")) comparator_23 (
    .a(Led8), .b(Led9), .eq(comparator_23_eq));  // open: gt, lt
  Comparator #(.width(32), .mode("twosComplement")) comparator_24 (
    .a(Led9), .b(Led10), .eq(comparator_24_eq));  // open: gt, lt
  Comparator #(.width(32), .mode("twosComplement")) comparator_25 (
    .a(Led10), .b(Led11), .eq(comparator_25_eq));  // open: gt, lt
  Comparator #(.width(32), .mode("twosComplement")) comparator_26 (
    .a(Led12), .b(Led13), .eq(comparator_26_eq));  // open: gt, lt
  Comparator #(.width(32), .mode("twosComplement")) comparator_27 (
    .a(Led13), .b(Led14), .eq(comparator_27_eq));  // open: gt, lt
  Comparator #(.width(32), .mode("twosComplement")) comparator_28 (
    .a(Led14), .b(Led15), .eq(comparator_28_eq));  // open: gt, lt
  nor nor_1 (nor_1_out, comparator_16_eq, comparator_15_eq, comparator_14_eq, comparator_13_eq, comparator_12_eq, comparator_11_eq, comparator_10_eq, comparator_9_eq, comparator_8_eq, comparator_7_eq, comparator_6_eq, comparator_5_eq, comparator_4_eq, comparator_3_eq, comparator_2_eq, comparator_1_eq);
  Comparator #(.width(32), .mode("twosComplement")) comparator_29 (
    .a(Led0), .b(Led4), .eq(comparator_29_eq));  // open: gt, lt
  Comparator #(.width(32), .mode("twosComplement")) comparator_30 (
    .a(Led1), .b(Led5), .eq(comparator_30_eq));  // open: gt, lt
  Comparator #(.width(32), .mode("twosComplement")) comparator_31 (
    .a(Led2), .b(Led6), .eq(comparator_31_eq));  // open: gt, lt
  Comparator #(.width(32), .mode("twosComplement")) comparator_32 (
    .a(Led3), .b(Led7), .eq(comparator_32_eq));  // open: gt, lt
  Comparator #(.width(32), .mode("twosComplement")) comparator_33 (
    .a(Led4), .b(Led8), .eq(comparator_33_eq));  // open: gt, lt
  nor nor_2 (nor_2_out, comparator_17_eq, comparator_18_eq, comparator_19_eq, comparator_20_eq, comparator_21_eq, comparator_22_eq, comparator_23_eq, comparator_24_eq, comparator_25_eq, comparator_26_eq, comparator_27_eq, comparator_28_eq);
  Comparator #(.width(32), .mode("twosComplement")) comparator_34 (
    .a(Led5), .b(Led9), .eq(comparator_34_eq));  // open: gt, lt
  Comparator #(.width(32), .mode("twosComplement")) comparator_35 (
    .a(Led6), .b(Led10), .eq(comparator_35_eq));  // open: gt, lt
  Comparator #(.width(32), .mode("twosComplement")) comparator_36 (
    .a(Led7), .b(Led11), .eq(comparator_36_eq));  // open: gt, lt
  Comparator #(.width(32), .mode("twosComplement")) comparator_37 (
    .a(Led8), .b(Led12), .eq(comparator_37_eq));  // open: gt, lt
  Comparator #(.width(32), .mode("twosComplement")) comparator_38 (
    .a(Led9), .b(Led13), .eq(comparator_38_eq));  // open: gt, lt
  Comparator #(.width(32), .mode("twosComplement")) comparator_39 (
    .a(Led10), .b(Led14), .eq(comparator_39_eq));  // open: gt, lt
  Comparator #(.width(32), .mode("twosComplement")) comparator_40 (
    .a(Led11), .b(Led15), .eq(comparator_40_eq));  // open: gt, lt
  nor nor_3 (nor_3_out, comparator_29_eq, comparator_30_eq, comparator_31_eq, comparator_32_eq, comparator_33_eq, comparator_34_eq, comparator_35_eq, comparator_36_eq, comparator_37_eq, comparator_38_eq, comparator_39_eq, comparator_40_eq);
  Comparator #(.width(32), .mode("twosComplement")) comparator_41 (
    .a(Led0), .b(32'h800), .eq(comparator_41_eq));  // open: gt, lt
  Comparator #(.width(32), .mode("twosComplement")) comparator_42 (
    .a(Led1), .b(32'h800), .eq(comparator_42_eq));  // open: gt, lt
  Comparator #(.width(32), .mode("twosComplement")) comparator_43 (
    .a(Led2), .b(32'h800), .eq(comparator_43_eq));  // open: gt, lt
  Comparator #(.width(32), .mode("twosComplement")) comparator_44 (
    .a(Led3), .b(32'h800), .eq(comparator_44_eq));  // open: gt, lt
  Comparator #(.width(32), .mode("twosComplement")) comparator_45 (
    .a(Led4), .b(32'h800), .eq(comparator_45_eq));  // open: gt, lt
  Comparator #(.width(32), .mode("twosComplement")) comparator_46 (
    .a(Led5), .b(32'h800), .eq(comparator_46_eq));  // open: gt, lt
  Comparator #(.width(32), .mode("twosComplement")) comparator_47 (
    .a(Led6), .b(32'h800), .eq(comparator_47_eq));  // open: gt, lt
  Comparator #(.width(32), .mode("twosComplement")) comparator_48 (
    .a(Led7), .b(32'h800), .eq(comparator_48_eq));  // open: gt, lt
  Comparator #(.width(32), .mode("twosComplement")) comparator_49 (
    .a(Led8), .b(32'h800), .eq(comparator_49_eq));  // open: gt, lt
  Comparator #(.width(32), .mode("twosComplement")) comparator_50 (
    .a(Led9), .b(32'h800), .eq(comparator_50_eq));  // open: gt, lt
  Comparator #(.width(32), .mode("twosComplement")) comparator_51 (
    .a(Led10), .b(32'h800), .eq(comparator_51_eq));  // open: gt, lt
  Comparator #(.width(32), .mode("twosComplement")) comparator_52 (
    .a(Led11), .b(32'h800), .eq(comparator_52_eq));  // open: gt, lt
  Comparator #(.width(32), .mode("twosComplement")) comparator_53 (
    .a(Led12), .b(32'h800), .eq(comparator_53_eq));  // open: gt, lt
  Comparator #(.width(32), .mode("twosComplement")) comparator_54 (
    .a(Led13), .b(32'h800), .eq(comparator_54_eq));  // open: gt, lt
  Comparator #(.width(32), .mode("twosComplement")) comparator_55 (
    .a(Led14), .b(32'h800), .eq(comparator_55_eq));  // open: gt, lt
  Comparator #(.width(32), .mode("twosComplement")) comparator_56 (
    .a(Led15), .b(32'h800), .eq(comparator_56_eq));  // open: gt, lt
  and and_1 (Lost, nor_3_out, nor_2_out, nor_1_out);
  or or_1 (Win, comparator_41_eq, comparator_42_eq, comparator_43_eq, comparator_44_eq, comparator_45_eq, comparator_46_eq, comparator_47_eq, comparator_48_eq, comparator_49_eq, comparator_50_eq, comparator_51_eq, comparator_52_eq, comparator_53_eq, comparator_54_eq, comparator_55_eq, comparator_56_eq);
endmodule
